// Logisim project data.circ as structural Verilog: 26 circuits, main circuit ◆海明传输测试1
module \国标转区位码  (
  input  [15:0] GB2312,
  output [6:0] \区号 ,
  output [6:0] \位号 
);

  wire adder_1_cout;
  wire [7:7] adder_1_out, adder_2_out;

  // Probe on GB2312
  // Probe on \区号 
  Adder adder_1 (.a(GB2312[7:0]), .b(8'h60), .out({adder_1_out[7], \位号 }), .cout(adder_1_cout));  // open: cin
  Adder adder_2 (.a(GB2312[15:8]), .b(8'h5f), .out({adder_2_out[7], \区号 }), .cin(adder_1_cout));  // open: cout
  // Probe on \位号 
  // Probe on {adder_2_out[7], \区号 , adder_1_out[7], \位号 }

  // Notes on the sheet:
  //   请勿增改引脚，请勿修改子电路封装
  //   输入引脚区
  //   请在下方利用上方输入输出引脚的隧道标签信号构建电路，ctrl+d复制选择组件
  //   华中科技大学计算机学院 计算机组成原理课程组
  //   要求用加法器完成
  //   输出引脚区
  //   探测区
endmodule

module \汉字显示  (
);

  wire \时钟_out ;
  wire [6:0] \国标转区位码_1_位号 , \国标转区位码_1_区号 ;
  wire [7:0] counter_1_q;
  wire [15:0] rom_1_data;
  wire [31:0] \字库_1_out_3 , \字库_1_out_4 , \字库_1_out_5 , \字库_1_out_6 , \字库_1_out_7 , \字库_1_out_8 ,
       \字库_1_out_9 , \字库_1_out_10 , \字库_1_out_11 , \字库_1_out_12 , \字库_1_out_13 , \字库_1_out_14 ,
       \字库_1_out_15 , \字库_1_out_16 , \字库_1_out_17 , \字库_1_out_18 , \字库_1_out_19 , \字库_1_out_20 ,
       \字库_1_out_21 , \字库_1_out_22 , \字库_1_out_23 , \字库_1_out_24 , \字库_1_out_25 , \字库_1_out_26 ,
       \字库_1_out_27 , \字库_1_out_28 , \字库_1_out_29 , \字库_1_out_30 , \字库_1_out_31 , \字库_1_out_32 ,
       \字库_1_out_33 , \字库_1_out_34 ;

  Counter counter_1 (.Q(counter_1_q), .clk(\时钟_out ));  // open: load, D, count, carry, clr
  Clock \u_时钟  (.out(\时钟_out ));
  ROM #(.dataWidth(16)) rom_1 (.addr(counter_1_q), .data(rom_1_data));  // open: sel
  \国标转区位码  \u_国标转区位码_1  (.\位号 (\国标转区位码_1_位号 ), .\区号 (\国标转区位码_1_区号 ), .GB2312(rom_1_data));
  \字库  \u_字库_1  (
    .out_3(\字库_1_out_3 ), .out_4(\字库_1_out_4 ), .out_5(\字库_1_out_5 ), .out_6(\字库_1_out_6 ),
    .out_7(\字库_1_out_7 ), .out_8(\字库_1_out_8 ), .out_9(\字库_1_out_9 ), .out_10(\字库_1_out_10 ),
    .out_11(\字库_1_out_11 ), .out_12(\字库_1_out_12 ), .out_13(\字库_1_out_13 ), .out_14(\字库_1_out_14 ),
    .out_15(\字库_1_out_15 ), .out_16(\字库_1_out_16 ), .out_17(\字库_1_out_17 ), .out_18(\字库_1_out_18 ),
    .out_19(\字库_1_out_19 ), .out_20(\字库_1_out_20 ), .out_21(\字库_1_out_21 ), .out_22(\字库_1_out_22 ),
    .out_23(\字库_1_out_23 ), .out_24(\字库_1_out_24 ), .out_25(\字库_1_out_25 ), .out_26(\字库_1_out_26 ),
    .out_27(\字库_1_out_27 ), .out_28(\字库_1_out_28 ), .out_29(\字库_1_out_29 ), .out_30(\字库_1_out_30 ),
    .out_31(\字库_1_out_31 ), .out_32(\字库_1_out_32 ), .out_33(\字库_1_out_33 ), .out_34(\字库_1_out_34 ),
    .\区号 (\国标转区位码_1_区号 ), .\位号 (\国标转区位码_1_位号 ));
  DotMatrix #(.inputtype("row"), .matrixcols(32), .matrixrows(32), .dotshape("circle")) dotmatrix_1 (
    .row0(\字库_1_out_3 ), .row1(\字库_1_out_4 ), .row2(\字库_1_out_5 ), .row3(\字库_1_out_6 ), .row4(\字库_1_out_7 ),
    .row5(\字库_1_out_8 ), .row6(\字库_1_out_9 ), .row7(\字库_1_out_10 ), .row8(\字库_1_out_11 ),
    .row9(\字库_1_out_12 ), .row10(\字库_1_out_13 ), .row11(\字库_1_out_14 ), .row12(\字库_1_out_15 ),
    .row13(\字库_1_out_16 ), .row14(\字库_1_out_17 ), .row15(\字库_1_out_18 ), .row16(\字库_1_out_19 ),
    .row17(\字库_1_out_20 ), .row18(\字库_1_out_21 ), .row19(\字库_1_out_22 ), .row20(\字库_1_out_23 ),
    .row21(\字库_1_out_24 ), .row22(\字库_1_out_25 ), .row23(\字库_1_out_26 ), .row24(\字库_1_out_27 ),
    .row25(\字库_1_out_28 ), .row26(\字库_1_out_29 ), .row27(\字库_1_out_30 ), .row28(\字库_1_out_31 ),
    .row29(\字库_1_out_32 ), .row30(\字库_1_out_33 ), .row31(\字库_1_out_34 ));

  // Notes on the sheet:
  //   计数器
  //   GB2312
  //   请在上面的ROM存储器中存100个成句的汉字
  //   实现国标转区位码电路，使得系统每个时钟正确显示一个汉字
  //   contents of rom_1 (hex, n*v repeats v):
  //   cef7 c4cf d2bd bfc6 b4f3 d1a7 a1a1 c1d9 b4b2 d2a9 d1a7 a3b1 b0e0 a1a1 c0ee c8d9 c9fd a1a1 a3e3 a3ec
  //   a3e9 a3ee a3e9 a3e3 a3e1 a3ec a1a1 a3f0 a3e8 a3e1 a3f2 a3ed a3e1 a3f2 a3e3 a3f9
endmodule

// 偶校验编码
module \偶校验编码  (
  input  [15:0] \原始数据 ,
  output [16:0] \偶校验编码 
);

  xor xor_1 (\偶校验编码 [16], \原始数据 [0], \原始数据 [1], \原始数据 [2], \原始数据 [3], \原始数据 [4], \原始数据 [5], \原始数据 [6], \原始数据 [7], \原始数据 [8], \原始数据 [9], \原始数据 [10], \原始数据 [11], \原始数据 [12], \原始数据 [13], \原始数据 [14], \原始数据 [15]);

  assign \偶校验编码 [15:0] = \原始数据 ;

  // Other names for the same wires on the sheet: D1 = \原始数据 [0]; Data[15:0] = \原始数据 ;
  //   校验码[16:0] = {\偶校验编码 [16], \原始数据 }; D2 = \原始数据 [1]; D3 = \原始数据 [2]; D4 = \原始数据 [3]; D5 = \原始数据 [4];
  //   D6 = \原始数据 [5]; D7 = \原始数据 [6]; D8 = \原始数据 [7]; D9 = \原始数据 [8]; D10 = \原始数据 [9]; D11 = \原始数据 [10];
  //   D12 = \原始数据 [11]; D13 = \原始数据 [12]; D14 = \原始数据 [13]; D15 = \原始数据 [14]; D16 = \原始数据 [15]

  // Notes on the sheet:
  //   输入引脚区
  //   请勿增改引脚，请勿修改子电路封装
  //   电路功能：实现16位数据位的偶校验编码，输入：16位数据；输出：17位校验码（数据位+校验位）
  //   请在下方利用上方输入输出引脚的隧道信号构建电路，ctrl+d复制选择部件
  //   输出引脚区
endmodule

// 偶校验检错
module \偶校验检错  (
  input  [16:0] \偶校验编码 ,
  output \检错位 ,
  output [15:0] \数据位 
);

  wire xor_1_out;

  xor xor_1 (xor_1_out, \偶校验编码 [0], \偶校验编码 [1], \偶校验编码 [2], \偶校验编码 [3], \偶校验编码 [4], \偶校验编码 [5], \偶校验编码 [6], \偶校验编码 [7], \偶校验编码 [8], \偶校验编码 [9], \偶校验编码 [10], \偶校验编码 [11], \偶校验编码 [12], \偶校验编码 [13], \偶校验编码 [14], \偶校验编码 [15]);
  xor xor_2 (\检错位 , xor_1_out, \偶校验编码 [16]);

  assign \数据位  = \偶校验编码 [15:0];

  // Other names for the same wires on the sheet: D1 = \偶校验编码 [0]; 偶校验码[16:0] = \偶校验编码 ; D2 = \偶校验编码 [1];
  //   D3 = \偶校验编码 [2]; D4 = \偶校验编码 [3]; D5 = \偶校验编码 [4]; D6 = \偶校验编码 [5]; D7 = \偶校验编码 [6]; D8 = \偶校验编码 [7];
  //   D9 = \偶校验编码 [8]; D10 = \偶校验编码 [9]; D11 = \偶校验编码 [10]; D12 = \偶校验编码 [11]; D13 = \偶校验编码 [12]; D14 = \偶校验编码 [13];
  //   D15 = \偶校验编码 [14]; D16 = \偶校验编码 [15]; P1 = \偶校验编码 [16]

  // Notes on the sheet:
  //   输入引脚区
  //   请勿增改引脚，请勿修改子电路封装
  //   电路功能：实现17位偶校验编码的检错以及数据提取。输入：17位校验码；输出：检错位、数据位
  //   请在下方利用上方输入输出引脚的隧道信号构建电路，ctrl+d复制选择部件
  //   输出引脚区
endmodule

// 海明编码
module \海明编码  (
  input  [15:0] \原始数据 ,
  output [21:0] \海明码 
);

  xor xor_1 (\海明码 [0], \原始数据 [0], \原始数据 [1], \原始数据 [3], \原始数据 [4], \原始数据 [6], \原始数据 [8], \原始数据 [10], \原始数据 [11], \原始数据 [13], \原始数据 [15]);
  xor xor_2 (\海明码 [1], \原始数据 [0], \原始数据 [2], \原始数据 [3], \原始数据 [5], \原始数据 [6], \原始数据 [9], \原始数据 [10], \原始数据 [12], \原始数据 [13]);
  xor xor_3 (\海明码 [3], \原始数据 [1], \原始数据 [2], \原始数据 [3], \原始数据 [7], \原始数据 [8], \原始数据 [9], \原始数据 [10], \原始数据 [14], \原始数据 [15]);
  xor xor_4 (\海明码 [7], \原始数据 [4], \原始数据 [5], \原始数据 [6], \原始数据 [7], \原始数据 [8], \原始数据 [9], \原始数据 [10]);
  xor xor_5 (\海明码 [15], \原始数据 [11], \原始数据 [12], \原始数据 [13], \原始数据 [14], \原始数据 [15]);
  xor xor_6 (\海明码 [21], \海明码 [0], \海明码 [1], \原始数据 [0], \原始数据 [1], \原始数据 [2], \原始数据 [3], \原始数据 [4], \原始数据 [5], \原始数据 [6], \原始数据 [7], \海明码 [3], \原始数据 [8], \原始数据 [9], \原始数据 [10], \原始数据 [11], \原始数据 [12], \原始数据 [13], \原始数据 [14], \原始数据 [15], \海明码 [7], \海明码 [15]);

  assign {\海明码 [20:16], \海明码 [14:8], \海明码 [6:4], \海明码 [2]} = \原始数据 ;

  // Other names for the same wires on the sheet: D12 = \原始数据 [11]; Data[15:0] = \原始数据 ; D14 = \原始数据 [13];
  //   D15 = \原始数据 [14]; D16 = \原始数据 [15]; P1 = \海明码 [0]; P2 = \海明码 [1]; D1 = \原始数据 [0]; P3 = \海明码 [3]; D2 = \原始数据 [1];
  //   D3 = \原始数据 [2]; D4 = \原始数据 [3]; P4 = \海明码 [7]; D5 = \原始数据 [4]; D6 = \原始数据 [5]; D7 = \原始数据 [6]; D8 = \原始数据 [7];
  //   D9 = \原始数据 [8]; D10 = \原始数据 [9]; D11 = \原始数据 [10]; P5 = \海明码 [15]; D13 = \原始数据 [12]; P6 = \海明码 [21]

  // Notes on the sheet:
  //   输入引脚区
  //   请勿增改引脚，请勿修改子电路封装
  //   电路功能：海明编码电路，可检两位错同时纠一位错，输入：16位数据；输出：22位海明码（数据位+校验位）
  //   请在下方利用上方输入输出引脚的隧道信号构建电路，ctrl+d复制选择部件
  //   输出引脚区
endmodule

// 海明解码
module \海明解码  (
  input  [21:0] \海明码 ,
  output \无错误 ,
  output \_1位错 ,
  output \_2位错 ,
  output [15:0] \纠错后数据 
);

  wire and_1_out, and_2_out, and_3_out, and_4_out, and_5_out, and_6_out, and_7_out, and_8_out, and_9_out,
       and_10_out, G1, G2, G3, G4, G5, G6, not_1_out, not_2_out, not_3_out, not_4_out, not_5_out, not_6_out,
       not_7_out, not_8_out, not_9_out, not_10_out, or_3_out;
  wire [15:0] decoder_1_out3, multiplexer_1_out, multiplexer_2_out, xor_7_out;

  xor xor_1 (G6, \海明码 [0], \海明码 [1], \海明码 [2], \海明码 [3], \海明码 [4], \海明码 [5], \海明码 [6], \海明码 [7], \海明码 [8], \海明码 [9], \海明码 [10], \海明码 [12], \海明码 [13], \海明码 [14], \海明码 [15], \海明码 [16], \海明码 [17], \海明码 [18], \海明码 [19], \海明码 [20], \海明码 [21], \海明码 [11]);
  not not_1 (not_1_out, G6);
  not not_2 (not_2_out, G6);
  not not_3 (not_3_out, G6);
  not not_4 (not_4_out, G6);
  not not_5 (not_5_out, G6);
  and and_1 (and_1_out, G5, G6);
  and and_2 (and_2_out, G4, G6);
  and and_3 (and_3_out, G3, G6);
  and and_4 (and_4_out, G2, G6);
  and and_5 (and_5_out, G1, G6);
  not not_6 (not_6_out, G1);
  not not_7 (not_7_out, G2);
  not not_8 (not_8_out, G3);
  not not_9 (not_9_out, G4);
  not not_10 (not_10_out, G5);
  and and_6 (and_6_out, G5, not_1_out);
  and and_7 (and_7_out, G4, not_2_out);
  and and_8 (and_8_out, G3, not_3_out);
  and and_9 (and_9_out, G2, not_4_out);
  and and_10 (and_10_out, G1, not_5_out);
  or or_1 (\_1位错 , and_1_out, and_2_out, and_3_out, and_4_out, and_5_out);
  and and_11 (\无错误 , not_6_out, not_7_out, not_8_out, not_9_out, not_10_out);
  or or_2 (\_2位错 , and_6_out, and_7_out, and_8_out, and_9_out, and_10_out);
  xor xor_2 (G1, \海明码 [2], \海明码 [4], \海明码 [6], \海明码 [8], \海明码 [10], \海明码 [0], \海明码 [12], \海明码 [14], \海明码 [16], \海明码 [18], \海明码 [20]);
  xor xor_3 (G2, \海明码 [2], \海明码 [5], \海明码 [6], \海明码 [9], \海明码 [10], \海明码 [1], \海明码 [13], \海明码 [14], \海明码 [17], \海明码 [18]);
  xor xor_4 (G3, \海明码 [4], \海明码 [5], \海明码 [6], \海明码 [11], \海明码 [12], \海明码 [3], \海明码 [13], \海明码 [14], \海明码 [19], \海明码 [20]);
  xor xor_5 (G4, \海明码 [8], \海明码 [9], \海明码 [11], \海明码 [12], \海明码 [7], \海明码 [13], \海明码 [14], \海明码 [10]);
  xor xor_6 (G5, \海明码 [16], \海明码 [17], \海明码 [18], \海明码 [15], \海明码 [19], \海明码 [20]);
  or or_3 (or_3_out, \_2位错 , \无错误 );
  Decoder #(.select(5)) decoder_1 (
    .out3(decoder_1_out3[0]), .out5(decoder_1_out3[1]), .out6(decoder_1_out3[2]), .out7(decoder_1_out3[3]),
    .out9(decoder_1_out3[4]), .out10(decoder_1_out3[5]), .out11(decoder_1_out3[6]),
    .out12(decoder_1_out3[7]), .out13(decoder_1_out3[8]), .out14(decoder_1_out3[9]),
    .out15(decoder_1_out3[10]), .out17(decoder_1_out3[11]), .out18(decoder_1_out3[12]),
    .out19(decoder_1_out3[13]), .out20(decoder_1_out3[14]), .out21(decoder_1_out3[15]),
    .sel({G5, G4, G3, G2, G1}));  // open: out0, out1, out2, out4, out8, out16, out22, out23, out24, out25, out26, out27, out28, out29, out30, out31, en
  Multiplexer #(.width(16)) multiplexer_1 (
    .in0({16{1'b0}}), .in1({\海明码 [20:16], \海明码 [14:8], \海明码 [6:4], \海明码 [2]}), .out(multiplexer_1_out),
    .sel(or_3_out));  // open: en
  assign xor_7_out = {\海明码 [20:16], \海明码 [14:8], \海明码 [6:4], \海明码 [2]} ^ decoder_1_out3;  // XOR_Gate xor_7, 16 bits wide
  assign \纠错后数据  = multiplexer_1_out | multiplexer_2_out;  // OR_Gate or_4, 16 bits wide
  Multiplexer #(.width(16)) multiplexer_2 (
    .in0({16{1'b0}}), .in1(xor_7_out), .out(multiplexer_2_out), .sel(\_1位错 ));  // open: en

  // Other names for the same wires on the sheet: D1 = \海明码 [2];
  //   传输数据[15:0] = {\海明码 [20:16], \海明码 [14:8], \海明码 [6:4], \海明码 [2]}; D2 = \海明码 [4]; D3 = \海明码 [5]; D4 = \海明码 [6];
  //   D5 = \海明码 [8]; D6 = \海明码 [9]; D7 = \海明码 [10]; D8 = \海明码 [11]; D9 = \海明码 [12]; D10 = \海明码 [13]; D11 = \海明码 [14];
  //   D12 = \海明码 [16]; D13 = \海明码 [17]; D14 = \海明码 [18]; D15 = \海明码 [19]; D16 = \海明码 [20]; P1 = \海明码 [0];
  //   P2 = \海明码 [1]; P3 = \海明码 [3]; P4 = \海明码 [7]; P5 = \海明码 [15]; P6 = \海明码 [21]

  // Notes on the sheet:
  //   输入引脚区
  //   输出引脚区
  //   总偶校验检错位
  //   请勿增改引脚，请勿修改子电路封装
  //   输入：22位海明码；输出：纠错后的数据、错误模式
  //   请在下方利用上方输入输出引脚的隧道信号构建电路，ctrl+d复制选择部件
  //   电路功能：实现22位海明码的数据解码，能判断1位错，2位错，无错误，1位错自动纠错。
endmodule

// CRC编码
module \CRC编码  (
  input  [15:0] \原始数据 ,
  output [21:0] \CRC校验码 
);

  wire [4:0] T1, T2, T3, T4, T5, T6, T7, T8, T9, T10, T11, T12, T13, T14, T15, T16;

  Multiplexer #(.width(5)) multiplexer_1 (.in0({5{1'b0}}), .in1(5'b01010), .out(T2), .sel(\原始数据 [1]));  // open: en
  Multiplexer #(.width(5)) multiplexer_2 (.in0({5{1'b0}}), .in1(5'b00101), .out(T1), .sel(\原始数据 [0]));  // open: en
  Multiplexer #(.width(5)) multiplexer_3 (.in0({5{1'b0}}), .in1(5'b10100), .out(T3), .sel(\原始数据 [2]));  // open: en
  Multiplexer #(.width(5)) multiplexer_4 (.in0({5{1'b0}}), .in1(5'b01101), .out(T4), .sel(\原始数据 [3]));  // open: en
  Multiplexer #(.width(5)) multiplexer_5 (.in0({5{1'b0}}), .in1(5'b11010), .out(T5), .sel(\原始数据 [4]));  // open: en
  Multiplexer #(.width(5)) multiplexer_6 (.in0({5{1'b0}}), .in1(5'b10001), .out(T6), .sel(\原始数据 [5]));  // open: en
  Multiplexer #(.width(5)) multiplexer_7 (.in0({5{1'b0}}), .in1(5'b01110), .out(T8), .sel(\原始数据 [7]));  // open: en
  Multiplexer #(.width(5)) multiplexer_8 (.in0({5{1'b0}}), .in1(5'b00111), .out(T7), .sel(\原始数据 [6]));  // open: en
  Multiplexer #(.width(5)) multiplexer_9 (.in0({5{1'b0}}), .in1(5'b11100), .out(T9), .sel(\原始数据 [8]));  // open: en
  Multiplexer #(.width(5)) multiplexer_10 (.in0({5{1'b0}}), .in1(5'b11101), .out(T10), .sel(\原始数据 [9]));  // open: en
  Multiplexer #(.width(5)) multiplexer_11 (.in0({5{1'b0}}), .in1({5{1'b1}}), .out(T11), .sel(\原始数据 [10]));  // open: en
  Multiplexer #(.width(5)) multiplexer_12 (.in0({5{1'b0}}), .in1(5'b11011), .out(T12), .sel(\原始数据 [11]));  // open: en
  Multiplexer #(.width(5)) multiplexer_13 (.in0({5{1'b0}}), .in1(5'b10011), .out(T13), .sel(\原始数据 [12]));  // open: en
  Multiplexer #(.width(5)) multiplexer_14 (.in0({5{1'b0}}), .in1(5'b00011), .out(T14), .sel(\原始数据 [13]));  // open: en
  assign \CRC校验码 [4:0] = T1 ^ T2 ^ T3 ^ T4 ^ T5 ^ T6 ^ T7 ^ T8 ^ T9 ^ T10 ^ T11 ^ T12 ^ T13 ^ T14 ^ T15 ^ T16;  // XOR_Gate xor_1, 5 bits wide
  Multiplexer #(.width(5)) multiplexer_15 (.in0({5{1'b0}}), .in1(5'b00110), .out(T15), .sel(\原始数据 [14]));  // open: en
  // Probe on \CRC校验码 [4:0]
  Multiplexer #(.width(5)) multiplexer_16 (.in0({5{1'b0}}), .in1(5'b01100), .out(T16), .sel(\原始数据 [15]));  // open: en
  xor xor_2 (\CRC校验码 [21], \CRC校验码 [0], \CRC校验码 [1], \原始数据 [0], \原始数据 [1], \原始数据 [2], \原始数据 [3], \原始数据 [4], \原始数据 [5], \原始数据 [6], \原始数据 [7], \CRC校验码 [2], \原始数据 [8], \原始数据 [9], \原始数据 [10], \原始数据 [11], \原始数据 [12], \原始数据 [13], \原始数据 [14], \原始数据 [15], \CRC校验码 [3], \CRC校验码 [4]);

  assign \CRC校验码 [20:5] = \原始数据 ;

  // Other names for the same wires on the sheet: CRC编码[21:0] = {\CRC校验码 [21], \原始数据 , \CRC校验码 [4:0]};
  //   P1 = \CRC校验码 [0]; P2 = \CRC校验码 [1]; P3 = \CRC校验码 [2]; P4 = \CRC校验码 [3]; P5 = \CRC校验码 [4]; D1 = \原始数据 [0];
  //   Data[15:0] = \原始数据 ; D2 = \原始数据 [1]; D3 = \原始数据 [2]; D4 = \原始数据 [3]; D5 = \原始数据 [4]; D6 = \原始数据 [5];
  //   D7 = \原始数据 [6]; D8 = \原始数据 [7]; D9 = \原始数据 [8]; D10 = \原始数据 [9]; D13 = \原始数据 [12]; P6 = \CRC校验码 [21];
  //   D11 = \原始数据 [10]; D12 = \原始数据 [11]; D14 = \原始数据 [13]; D15 = \原始数据 [14]; D16 = \原始数据 [15]

  // Notes on the sheet:
  //   输入引脚区
  //   请勿增改引脚，请勿修改子电路封装
  //   G(x) = x^5 + x^2 + 1
  //   电路功能：CRC编码电路，可检两位错同时纠一位错，输入：16位数据；输出：22位CRC编码（数据位+校验位）
  //   请在下方利用上方输入输出引脚的隧道信号构建电路，ctrl+d复制选择部件
  //   输出引脚区
endmodule

// CRC解码
module \CRC解码  (
  input  [21:0] \CRC编码 ,
  output \无错误 ,
  output \_1位错 ,
  output \_2位错 ,
  output [15:0] \纠错后数据 
);

  wire and_1_out, and_2_out, and_3_out, and_4_out, and_5_out, and_6_out, and_7_out, and_8_out, and_9_out,
       and_10_out, comparator_1_eq, comparator_2_eq, comparator_3_eq, comparator_4_eq, comparator_5_eq,
       comparator_6_eq, comparator_7_eq, comparator_8_eq, comparator_9_eq, comparator_10_eq,
       comparator_11_eq, comparator_12_eq, comparator_13_eq, comparator_14_eq, comparator_15_eq,
       comparator_16_eq, not_1_out, not_2_out, not_3_out, not_4_out, not_5_out, not_6_out, not_7_out,
       not_8_out, not_9_out, not_10_out, \总校验位错 ;
  wire [4:0] G, T1, T2, T3, T4, T5, T6, T7, T8, T9, T10, T11, T12, T13, T14, T15, T16;

  xor xor_1 (\总校验位错 , \CRC编码 [0], \CRC编码 [1], \CRC编码 [2], \CRC编码 [3], \CRC编码 [4], \CRC编码 [5], \CRC编码 [6], \CRC编码 [7], \CRC编码 [8], \CRC编码 [9], \CRC编码 [10], \CRC编码 [12], \CRC编码 [11], \CRC编码 [14], \CRC编码 [13], \CRC编码 [16], \CRC编码 [15], \CRC编码 [18], \CRC编码 [17], \CRC编码 [20], \CRC编码 [19], \CRC编码 [21]);
  // Probe on G
  assign G = T1 ^ T2 ^ T3 ^ T4 ^ T5 ^ T6 ^ T7 ^ T8 ^ \CRC编码 [4:0] ^ T9 ^ T10 ^ T11 ^ T12 ^ T13 ^ T14 ^ T15 ^ T16;  // XOR_Gate xor_2, 5 bits wide
  Multiplexer #(.width(5)) multiplexer_1 (.in0({5{1'b0}}), .in1(5'b00101), .out(T1), .sel(\CRC编码 [5]));  // open: en
  and and_1 (and_1_out, G[4], not_1_out);
  not not_1 (not_1_out, \总校验位错 );
  and and_2 (and_2_out, G[3], not_2_out);
  not not_2 (not_2_out, \总校验位错 );
  and and_3 (and_3_out, G[2], not_3_out);
  not not_3 (not_3_out, \总校验位错 );
  and and_4 (and_4_out, G[1], not_4_out);
  not not_4 (not_4_out, \总校验位错 );
  and and_5 (and_5_out, G[0], not_5_out);
  not not_5 (not_5_out, \总校验位错 );
  and and_6 (and_6_out, G[4], \总校验位错 );
  and and_7 (and_7_out, G[3], \总校验位错 );
  and and_8 (and_8_out, G[2], \总校验位错 );
  and and_9 (and_9_out, G[1], \总校验位错 );
  and and_10 (and_10_out, G[0], \总校验位错 );
  not not_6 (not_6_out, G[0]);
  not not_7 (not_7_out, G[1]);
  not not_8 (not_8_out, G[2]);
  not not_9 (not_9_out, G[3]);
  not not_10 (not_10_out, G[4]);
  Multiplexer #(.width(5)) multiplexer_2 (.in0({5{1'b0}}), .in1(5'b01010), .out(T2), .sel(\CRC编码 [6]));  // open: en
  Multiplexer #(.width(5)) multiplexer_3 (.in0({5{1'b0}}), .in1(5'b10100), .out(T3), .sel(\CRC编码 [7]));  // open: en
  or or_1 (\_2位错 , and_1_out, and_2_out, and_3_out, and_4_out, and_5_out);
  or or_2 (\_1位错 , and_6_out, and_7_out, and_8_out, and_9_out, and_10_out);
  and and_11 (\无错误 , not_6_out, not_7_out, not_8_out, not_9_out, not_10_out);
  Multiplexer #(.width(5)) multiplexer_4 (.in0({5{1'b0}}), .in1(5'b01101), .out(T4), .sel(\CRC编码 [8]));  // open: en
  Multiplexer #(.width(5)) multiplexer_5 (.in0({5{1'b0}}), .in1(5'b11010), .out(T5), .sel(\CRC编码 [9]));  // open: en
  Multiplexer #(.width(5)) multiplexer_6 (.in0({5{1'b0}}), .in1(5'b10001), .out(T6), .sel(\CRC编码 [10]));  // open: en
  Multiplexer #(.width(5)) multiplexer_7 (.in0({5{1'b0}}), .in1(5'b00111), .out(T7), .sel(\CRC编码 [11]));  // open: en
  Comparator #(.width(5)) comparator_1 (.a(5'b00101), .b(G), .eq(comparator_1_eq));  // open: gt, lt
  Comparator #(.width(5)) comparator_2 (.a(5'b01010), .b(G), .eq(comparator_2_eq));  // open: gt, lt
  Comparator #(.width(5)) comparator_3 (.a(5'b10100), .b(G), .eq(comparator_3_eq));  // open: gt, lt
  Comparator #(.width(5)) comparator_4 (.a(5'b01101), .b(G), .eq(comparator_4_eq));  // open: gt, lt
  Comparator #(.width(5)) comparator_5 (.a(5'b11010), .b(G), .eq(comparator_5_eq));  // open: gt, lt
  Comparator #(.width(5)) comparator_6 (.a(5'b10001), .b(G), .eq(comparator_6_eq));  // open: gt, lt
  Comparator #(.width(5)) comparator_7 (.a(5'b00111), .b(G), .eq(comparator_7_eq));  // open: gt, lt
  Comparator #(.width(5)) comparator_8 (.a(5'b01110), .b(G), .eq(comparator_8_eq));  // open: gt, lt
  Comparator #(.width(5)) comparator_9 (.a(5'b11100), .b(G), .eq(comparator_9_eq));  // open: gt, lt
  Comparator #(.width(5)) comparator_10 (.a(5'b11101), .b(G), .eq(comparator_10_eq));  // open: gt, lt
  Comparator #(.width(5)) comparator_11 (.a({5{1'b1}}), .b(G), .eq(comparator_11_eq));  // open: gt, lt
  Comparator #(.width(5)) comparator_12 (.a(5'b11011), .b(G), .eq(comparator_12_eq));  // open: gt, lt
  Comparator #(.width(5)) comparator_13 (.a(5'b10011), .b(G), .eq(comparator_13_eq));  // open: gt, lt
  Comparator #(.width(5)) comparator_14 (.a(5'b00011), .b(G), .eq(comparator_14_eq));  // open: gt, lt
  Comparator #(.width(5)) comparator_15 (.a(5'b00110), .b(G), .eq(comparator_15_eq));  // open: gt, lt
  Comparator #(.width(5)) comparator_16 (.a(5'b01100), .b(G), .eq(comparator_16_eq));  // open: gt, lt
  Multiplexer #(.width(5)) multiplexer_8 (.in0({5{1'b0}}), .in1(5'b01110), .out(T8), .sel(\CRC编码 [12]));  // open: en
  Multiplexer #(.width(5)) multiplexer_9 (.in0({5{1'b0}}), .in1(5'b11100), .out(T9), .sel(\CRC编码 [13]));  // open: en
  xor xor_3 (\纠错后数据 [0], comparator_1_eq, \CRC编码 [5]);
  xor xor_4 (\纠错后数据 [1], comparator_2_eq, \CRC编码 [6]);
  xor xor_5 (\纠错后数据 [2], comparator_3_eq, \CRC编码 [7]);
  xor xor_6 (\纠错后数据 [3], comparator_4_eq, \CRC编码 [8]);
  xor xor_7 (\纠错后数据 [4], comparator_5_eq, \CRC编码 [9]);
  xor xor_8 (\纠错后数据 [5], comparator_6_eq, \CRC编码 [10]);
  xor xor_9 (\纠错后数据 [6], comparator_7_eq, \CRC编码 [11]);
  xor xor_10 (\纠错后数据 [7], comparator_8_eq, \CRC编码 [12]);
  xor xor_11 (\纠错后数据 [8], comparator_9_eq, \CRC编码 [13]);
  xor xor_12 (\纠错后数据 [9], comparator_10_eq, \CRC编码 [14]);
  xor xor_13 (\纠错后数据 [10], comparator_11_eq, \CRC编码 [15]);
  xor xor_14 (\纠错后数据 [11], comparator_12_eq, \CRC编码 [16]);
  xor xor_15 (\纠错后数据 [12], comparator_13_eq, \CRC编码 [17]);
  xor xor_16 (\纠错后数据 [13], comparator_14_eq, \CRC编码 [18]);
  xor xor_17 (\纠错后数据 [14], comparator_15_eq, \CRC编码 [19]);
  xor xor_18 (\纠错后数据 [15], comparator_16_eq, \CRC编码 [20]);
  Multiplexer #(.width(5)) multiplexer_10 (.in0({5{1'b0}}), .in1(5'b11101), .out(T10), .sel(\CRC编码 [14]));  // open: en
  Multiplexer #(.width(5)) multiplexer_11 (.in0({5{1'b0}}), .in1(5'b11011), .out(T12), .sel(\CRC编码 [16]));  // open: en
  Multiplexer #(.width(5)) multiplexer_12 (.in0({5{1'b0}}), .in1({5{1'b1}}), .out(T11), .sel(\CRC编码 [15]));  // open: en
  Multiplexer #(.width(5)) multiplexer_13 (.in0({5{1'b0}}), .in1(5'b10011), .out(T13), .sel(\CRC编码 [17]));  // open: en
  Multiplexer #(.width(5)) multiplexer_14 (.in0({5{1'b0}}), .in1(5'b00110), .out(T15), .sel(\CRC编码 [19]));  // open: en
  Multiplexer #(.width(5)) multiplexer_15 (.in0({5{1'b0}}), .in1(5'b00011), .out(T14), .sel(\CRC编码 [18]));  // open: en
  Multiplexer #(.width(5)) multiplexer_16 (.in0({5{1'b0}}), .in1(5'b01100), .out(T16), .sel(\CRC编码 [20]));  // open: en

  // Other names for the same wires on the sheet: CRC[21:0] = \CRC编码 ; P1 = \CRC编码 [0]; P2 = \CRC编码 [1];
  //   P3 = \CRC编码 [2]; P4 = \CRC编码 [3]; P5 = \CRC编码 [4]; D1 = \CRC编码 [5]; D2 = \CRC编码 [6]; D3 = \CRC编码 [7];
  //   D4 = \CRC编码 [8]; D5 = \CRC编码 [9]; D6 = \CRC编码 [10]; D7 = \CRC编码 [11]; D8 = \CRC编码 [12]; D9 = \CRC编码 [13];
  //   D10 = \CRC编码 [14]; D11 = \CRC编码 [15]; D12 = \CRC编码 [16]; D13 = \CRC编码 [17]; D14 = \CRC编码 [18];
  //   D15 = \CRC编码 [19]; D16 = \CRC编码 [20]; P6 = \CRC编码 [21]; G1 = G[0]; G2 = G[1]; G3 = G[2]; G4 = G[3]; G5 = G[4]

  // Notes on the sheet:
  //   输入引脚区
  //   输出引脚区
  //   请勿增改引脚，请勿修改子电路封装
  //   输入：22位CRC编码；输出：纠错后的数据、错误模式
  //   请在下方利用上方输入输出引脚的隧道信号构建电路，ctrl+d复制选择部件
  //   电路功能：实现22位海CRC编码的数据解码，能判断1位错，2位错，无错误，1位错自动纠错。
endmodule

module \偶校验传输测试  (
);

  wire and_1_out, comparator_1_eq, \偶校验检错_1_检错位 , \时钟_out ;
  wire [6:0] \国标转区位码_1_位号 , \国标转区位码_1_区号 , \国标转区位码_2_位号 , \国标转区位码_2_区号 ;
  wire [7:0] counter_1_q;
  wire [15:0] \发送 , \接收 ;
  wire [16:0] \n17位随机干扰_1_加扰后数据 , \n17位随机干扰_1_随机加扰屏蔽字 , \偶校验编码_1_偶校验编码 ;
  wire [31:0] \字库_1_out_3 , \字库_1_out_4 , \字库_1_out_5 , \字库_1_out_6 , \字库_1_out_7 , \字库_1_out_8 ,
       \字库_1_out_9 , \字库_1_out_10 , \字库_1_out_11 , \字库_1_out_12 , \字库_1_out_13 , \字库_1_out_14 ,
       \字库_1_out_15 , \字库_1_out_16 , \字库_1_out_17 , \字库_1_out_18 , \字库_1_out_19 , \字库_1_out_20 ,
       \字库_1_out_21 , \字库_1_out_22 , \字库_1_out_23 , \字库_1_out_24 , \字库_1_out_25 , \字库_1_out_26 ,
       \字库_1_out_27 , \字库_1_out_28 , \字库_1_out_29 , \字库_1_out_30 , \字库_1_out_31 , \字库_1_out_32 ,
       \字库_1_out_33 , \字库_1_out_34 , \字库_2_out_3 , \字库_2_out_4 , \字库_2_out_5 , \字库_2_out_6 , \字库_2_out_7 ,
       \字库_2_out_8 , \字库_2_out_9 , \字库_2_out_10 , \字库_2_out_11 , \字库_2_out_12 , \字库_2_out_13 , \字库_2_out_14 ,
       \字库_2_out_15 , \字库_2_out_16 , \字库_2_out_17 , \字库_2_out_18 , \字库_2_out_19 , \字库_2_out_20 ,
       \字库_2_out_21 , \字库_2_out_22 , \字库_2_out_23 , \字库_2_out_24 , \字库_2_out_25 , \字库_2_out_26 ,
       \字库_2_out_27 , \字库_2_out_28 , \字库_2_out_29 , \字库_2_out_30 , \字库_2_out_31 , \字库_2_out_32 ,
       \字库_2_out_33 , \字库_2_out_34 ;

  Counter counter_1 (.Q(counter_1_q), .clk(\时钟_out ));  // open: load, D, count, carry, clr
  Clock \u_时钟  (.out(\时钟_out ));
  \国标转区位码  \u_国标转区位码_1  (.\位号 (\国标转区位码_1_位号 ), .\区号 (\国标转区位码_1_区号 ), .GB2312(\发送 ));
  ROM #(.dataWidth(16)) rom_1 (.addr(counter_1_q), .data(\发送 ));  // open: sel
  DotMatrix #(.inputtype("row"), .matrixcols(32), .matrixrows(32), .dotshape("circle")) dotmatrix_1 (
    .row0(\字库_1_out_3 ), .row1(\字库_1_out_4 ), .row2(\字库_1_out_5 ), .row3(\字库_1_out_6 ), .row4(\字库_1_out_7 ),
    .row5(\字库_1_out_8 ), .row6(\字库_1_out_9 ), .row7(\字库_1_out_10 ), .row8(\字库_1_out_11 ),
    .row9(\字库_1_out_12 ), .row10(\字库_1_out_13 ), .row11(\字库_1_out_14 ), .row12(\字库_1_out_15 ),
    .row13(\字库_1_out_16 ), .row14(\字库_1_out_17 ), .row15(\字库_1_out_18 ), .row16(\字库_1_out_19 ),
    .row17(\字库_1_out_20 ), .row18(\字库_1_out_21 ), .row19(\字库_1_out_22 ), .row20(\字库_1_out_23 ),
    .row21(\字库_1_out_24 ), .row22(\字库_1_out_25 ), .row23(\字库_1_out_26 ), .row24(\字库_1_out_27 ),
    .row25(\字库_1_out_28 ), .row26(\字库_1_out_29 ), .row27(\字库_1_out_30 ), .row28(\字库_1_out_31 ),
    .row29(\字库_1_out_32 ), .row30(\字库_1_out_33 ), .row31(\字库_1_out_34 ));
  \字库  \u_字库_1  (
    .out_3(\字库_1_out_3 ), .out_4(\字库_1_out_4 ), .out_5(\字库_1_out_5 ), .out_6(\字库_1_out_6 ),
    .out_7(\字库_1_out_7 ), .out_8(\字库_1_out_8 ), .out_9(\字库_1_out_9 ), .out_10(\字库_1_out_10 ),
    .out_11(\字库_1_out_11 ), .out_12(\字库_1_out_12 ), .out_13(\字库_1_out_13 ), .out_14(\字库_1_out_14 ),
    .out_15(\字库_1_out_15 ), .out_16(\字库_1_out_16 ), .out_17(\字库_1_out_17 ), .out_18(\字库_1_out_18 ),
    .out_19(\字库_1_out_19 ), .out_20(\字库_1_out_20 ), .out_21(\字库_1_out_21 ), .out_22(\字库_1_out_22 ),
    .out_23(\字库_1_out_23 ), .out_24(\字库_1_out_24 ), .out_25(\字库_1_out_25 ), .out_26(\字库_1_out_26 ),
    .out_27(\字库_1_out_27 ), .out_28(\字库_1_out_28 ), .out_29(\字库_1_out_29 ), .out_30(\字库_1_out_30 ),
    .out_31(\字库_1_out_31 ), .out_32(\字库_1_out_32 ), .out_33(\字库_1_out_33 ), .out_34(\字库_1_out_34 ),
    .\区号 (\国标转区位码_1_区号 ), .\位号 (\国标转区位码_1_位号 ));
  // Probe on \发送 
  \偶校验编码  \u_偶校验编码_1  (.\原始数据 (\发送 ), .\偶校验编码 (\偶校验编码_1_偶校验编码 ));
  // Probe on \偶校验编码_1_偶校验编码 
  // Probe on \偶校验编码_1_偶校验编码 
  // Probe on \n17位随机干扰_1_随机加扰屏蔽字 
  \_17位随机干扰  \u_17位随机干扰_1  (.\_17位输入 (\偶校验编码_1_偶校验编码 ), .\随机加扰屏蔽字 (\n17位随机干扰_1_随机加扰屏蔽字 ), .\加扰后数据 (\n17位随机干扰_1_加扰后数据 ));
  // Probe on \n17位随机干扰_1_加扰后数据 
  // Probe on \n17位随机干扰_1_加扰后数据 
  \国标转区位码  \u_国标转区位码_2  (.\位号 (\国标转区位码_2_位号 ), .\区号 (\国标转区位码_2_区号 ), .GB2312(\接收 ));
  DotMatrix #(.inputtype("row"), .matrixcols(32), .matrixrows(32), .dotshape("circle")) dotmatrix_2 (
    .row0(\字库_2_out_3 ), .row1(\字库_2_out_4 ), .row2(\字库_2_out_5 ), .row3(\字库_2_out_6 ), .row4(\字库_2_out_7 ),
    .row5(\字库_2_out_8 ), .row6(\字库_2_out_9 ), .row7(\字库_2_out_10 ), .row8(\字库_2_out_11 ),
    .row9(\字库_2_out_12 ), .row10(\字库_2_out_13 ), .row11(\字库_2_out_14 ), .row12(\字库_2_out_15 ),
    .row13(\字库_2_out_16 ), .row14(\字库_2_out_17 ), .row15(\字库_2_out_18 ), .row16(\字库_2_out_19 ),
    .row17(\字库_2_out_20 ), .row18(\字库_2_out_21 ), .row19(\字库_2_out_22 ), .row20(\字库_2_out_23 ),
    .row21(\字库_2_out_24 ), .row22(\字库_2_out_25 ), .row23(\字库_2_out_26 ), .row24(\字库_2_out_27 ),
    .row25(\字库_2_out_28 ), .row26(\字库_2_out_29 ), .row27(\字库_2_out_30 ), .row28(\字库_2_out_31 ),
    .row29(\字库_2_out_32 ), .row30(\字库_2_out_33 ), .row31(\字库_2_out_34 ));
  \字库  \u_字库_2  (
    .out_3(\字库_2_out_3 ), .out_4(\字库_2_out_4 ), .out_5(\字库_2_out_5 ), .out_6(\字库_2_out_6 ),
    .out_7(\字库_2_out_7 ), .out_8(\字库_2_out_8 ), .out_9(\字库_2_out_9 ), .out_10(\字库_2_out_10 ),
    .out_11(\字库_2_out_11 ), .out_12(\字库_2_out_12 ), .out_13(\字库_2_out_13 ), .out_14(\字库_2_out_14 ),
    .out_15(\字库_2_out_15 ), .out_16(\字库_2_out_16 ), .out_17(\字库_2_out_17 ), .out_18(\字库_2_out_18 ),
    .out_19(\字库_2_out_19 ), .out_20(\字库_2_out_20 ), .out_21(\字库_2_out_21 ), .out_22(\字库_2_out_22 ),
    .out_23(\字库_2_out_23 ), .out_24(\字库_2_out_24 ), .out_25(\字库_2_out_25 ), .out_26(\字库_2_out_26 ),
    .out_27(\字库_2_out_27 ), .out_28(\字库_2_out_28 ), .out_29(\字库_2_out_29 ), .out_30(\字库_2_out_30 ),
    .out_31(\字库_2_out_31 ), .out_32(\字库_2_out_32 ), .out_33(\字库_2_out_33 ), .out_34(\字库_2_out_34 ),
    .\区号 (\国标转区位码_2_区号 ), .\位号 (\国标转区位码_2_位号 ));
  LED \u_检错位  (.in(\偶校验检错_1_检错位 ));
  \偶校验检错  \u_偶校验检错_1  (.\检错位 (\偶校验检错_1_检错位 ), .\偶校验编码 (\n17位随机干扰_1_加扰后数据 ), .\数据位 (\接收 ));
  Comparator #(.width(16)) comparator_1 (.a(\发送 ), .b(\接收 ), .eq(comparator_1_eq));  // open: gt, lt
  // Probe on \接收 
  and and_1 (and_1_out, ~comparator_1_eq, ~\偶校验检错_1_检错位 );  // AND_Gate
  LED \u_数据正确  (.in(comparator_1_eq));
  LED \u_误报  (.in(and_1_out));

  // Notes on the sheet:
  //   发送方
  //   计数器
  //   发送方
  //   汉字显示
  //   GB2312
  //   contents of rom_1 (hex, n*v repeats v):
  //   bbaa d6d0 bfc6 bcbc b4f3 d1a7 cac7 b9fa bcd2 bdcc d3fd b2bf d6b1 caf4 b5c4 c8ab b9fa d6d8 b5e3 b4f3
  //   d1a7 a3ac d3c9 d4ad bbaa d6d0 c0ed b9a4 b4f3 d1a7 a1a2 cdac bcc3 d2bd bfc6 b4f3 d1a7 a1a2 cee4 baba
  //   b3c7 cad0 bda8 c9e8 d1a7 d4ba d3da a3b2 a3b0 a3b0 a3b0 c4ea a3b5 d4c2 a3b2 a3b6 c8d5 bacf b2a2 b3c9
  //   c1a2 a3ac cac7 cad7 c5fa c1d0 c8eb b9fa bcd2 a1b0 a3b2 a3b1 a3b1 b9a4 b3cc a1b1 d6d8 b5e3 bda8 c9e8
  //   bacd b9fa bcd2 a1b0 a3b9 a3b8 a3b5 b9a4 b3cc a1b1 bda8 c9e8 b8df d0a3 d6ae d2bb a1a3 d1a7 d0a3 d0a3
  //   d4b0 d5bc b5d8 c6df c7a7 d3e0 c4b6 a3ac d4b0 c4da caf7 c4be b4d0 dcd7 a3ac b1cc b2dd c8e7 d2f0 a3ac
  //   bbb7 beb3 d3c5 d1c5 a3ac beb0 c9ab d0e3 c0f6 a3ac c2cc bbaf b8b2 b8c7 c2ca 3732 25a3 acb1 bbd3 fece
  //   aaa1 b0c9 adc1 d6ca bdb4 f3d1 a7a1 b1a1
  //   电路功能：测试偶校验编解码电路正确性，仿真时设置加扰控制位和原始数据，按CTRL+T触发不同的干扰，检验编解码电路功能
  //   发送方在ROM预存了一段中文文字，通过计数器驱动电路每个时钟传输一个汉字到接收方
  //   用户实现了国标转区位码电路后，可在中间窗口观察发送方和接收方汉字显示是否一致以观察检错性能
  //   偶校验编解码传输电路
  //   接收方
  //   汉字显示
  //   Ctrl+T Ctrl+K驱动时钟触发随机干扰变化
  //   接收方
  //   请将时钟频率调到8Hz
endmodule

module \海明传输测试1  (
  input  [15:0] \原始数据 ,
  input  [1:0] \加扰控制 
);

  wire comparator_1_eq, \海明解码_1__1位错 , \海明解码_1__2位错 , \海明解码_1_无错误 ;
  wire [15:0] \海明解码_1_纠错后数据 ;
  wire [21:0] \n22位随机干扰_1_加扰后数据 , \n22位随机干扰_1_随机加扰屏蔽字 , \海明编码_1_海明码 ;

  // Probe on \原始数据 
  // Probe on \海明编码_1_海明码 
  \海明编码  \u_海明编码_1  (.\原始数据 (\原始数据 ), .\海明码 (\海明编码_1_海明码 ));
  // Probe on \海明编码_1_海明码 
  // Probe on \n22位随机干扰_1_随机加扰屏蔽字 
  // Probe on \n22位随机干扰_1_加扰后数据 
  \_22位随机干扰  \u_22位随机干扰_1  (
    .\加扰模式 (\加扰控制 ), .\随机加扰屏蔽字 (\n22位随机干扰_1_随机加扰屏蔽字 ), .\_22位输入 (\海明编码_1_海明码 ), .\加扰后数据 (\n22位随机干扰_1_加扰后数据 ));  // open: 增加三位错
  // Probe on \n22位随机干扰_1_加扰后数据 
  LED \u_无错误  (.in(\海明解码_1_无错误 ));
  LED \u_一位错  (.in(\海明解码_1__1位错 ));
  LED \u_两位错  (.in(\海明解码_1__2位错 ));
  \海明解码  \u_海明解码_1  (
    .\_1位错 (\海明解码_1__1位错 ), .\_2位错 (\海明解码_1__2位错 ), .\无错误 (\海明解码_1_无错误 ), .\海明码 (\n22位随机干扰_1_加扰后数据 ),
    .\纠错后数据 (\海明解码_1_纠错后数据 ));
  // Probe on \海明解码_1_纠错后数据 
  LED \u_数据正确  (.in(comparator_1_eq));
  Comparator #(.width(16)) comparator_1 (.a(\原始数据 ), .b(\海明解码_1_纠错后数据 ), .eq(comparator_1_eq));  // open: gt, lt

  // Notes on the sheet:
  //   发送方
  //   电路功能：测试海明编解码电路正确性，仿真时设置加扰控制位和原始数据，按CTRL+T触发不同的干扰，检验编解码电路功能
  //   Ctrl+T 驱动时钟触发随机干扰变化
  //   海明编解码传输电路
  //   加扰控制00：不加扰  01:1位加扰 10:2位加扰 11：随机加扰
  //   接收方
endmodule

module \海明传输测试2  (
  input  [1:0] \加扰控制 
);

  wire comparator_1_eq, \时钟_out , \海明解码_1__1位错 , \海明解码_1__2位错 , \海明解码_1_无错误 ;
  wire [6:0] \国标转区位码_1_位号 , \国标转区位码_1_区号 , \国标转区位码_2_位号 , \国标转区位码_2_区号 ;
  wire [7:0] counter_1_q;
  wire [15:0] \发送 , \接收 ;
  wire [21:0] \n22位随机干扰_1_加扰后数据 , \n22位随机干扰_1_随机加扰屏蔽字 , \海明编码_1_海明码 ;
  wire [31:0] \字库_1_out_3 , \字库_1_out_4 , \字库_1_out_5 , \字库_1_out_6 , \字库_1_out_7 , \字库_1_out_8 ,
       \字库_1_out_9 , \字库_1_out_10 , \字库_1_out_11 , \字库_1_out_12 , \字库_1_out_13 , \字库_1_out_14 ,
       \字库_1_out_15 , \字库_1_out_16 , \字库_1_out_17 , \字库_1_out_18 , \字库_1_out_19 , \字库_1_out_20 ,
       \字库_1_out_21 , \字库_1_out_22 , \字库_1_out_23 , \字库_1_out_24 , \字库_1_out_25 , \字库_1_out_26 ,
       \字库_1_out_27 , \字库_1_out_28 , \字库_1_out_29 , \字库_1_out_30 , \字库_1_out_31 , \字库_1_out_32 ,
       \字库_1_out_33 , \字库_1_out_34 , \字库_2_out_3 , \字库_2_out_4 , \字库_2_out_5 , \字库_2_out_6 , \字库_2_out_7 ,
       \字库_2_out_8 , \字库_2_out_9 , \字库_2_out_10 , \字库_2_out_11 , \字库_2_out_12 , \字库_2_out_13 , \字库_2_out_14 ,
       \字库_2_out_15 , \字库_2_out_16 , \字库_2_out_17 , \字库_2_out_18 , \字库_2_out_19 , \字库_2_out_20 ,
       \字库_2_out_21 , \字库_2_out_22 , \字库_2_out_23 , \字库_2_out_24 , \字库_2_out_25 , \字库_2_out_26 ,
       \字库_2_out_27 , \字库_2_out_28 , \字库_2_out_29 , \字库_2_out_30 , \字库_2_out_31 , \字库_2_out_32 ,
       \字库_2_out_33 , \字库_2_out_34 ;

  Clock \u_时钟  (.out(\时钟_out ));
  Counter counter_1 (.Q(counter_1_q), .clk(\时钟_out ));  // open: load, D, count, carry, clr
  \国标转区位码  \u_国标转区位码_1  (.\位号 (\国标转区位码_1_位号 ), .\区号 (\国标转区位码_1_区号 ), .GB2312(\发送 ));
  \字库  \u_字库_1  (
    .out_3(\字库_1_out_3 ), .out_4(\字库_1_out_4 ), .out_5(\字库_1_out_5 ), .out_6(\字库_1_out_6 ),
    .out_7(\字库_1_out_7 ), .out_8(\字库_1_out_8 ), .out_9(\字库_1_out_9 ), .out_10(\字库_1_out_10 ),
    .out_11(\字库_1_out_11 ), .out_12(\字库_1_out_12 ), .out_13(\字库_1_out_13 ), .out_14(\字库_1_out_14 ),
    .out_15(\字库_1_out_15 ), .out_16(\字库_1_out_16 ), .out_17(\字库_1_out_17 ), .out_18(\字库_1_out_18 ),
    .out_19(\字库_1_out_19 ), .out_20(\字库_1_out_20 ), .out_21(\字库_1_out_21 ), .out_22(\字库_1_out_22 ),
    .out_23(\字库_1_out_23 ), .out_24(\字库_1_out_24 ), .out_25(\字库_1_out_25 ), .out_26(\字库_1_out_26 ),
    .out_27(\字库_1_out_27 ), .out_28(\字库_1_out_28 ), .out_29(\字库_1_out_29 ), .out_30(\字库_1_out_30 ),
    .out_31(\字库_1_out_31 ), .out_32(\字库_1_out_32 ), .out_33(\字库_1_out_33 ), .out_34(\字库_1_out_34 ),
    .\区号 (\国标转区位码_1_区号 ), .\位号 (\国标转区位码_1_位号 ));
  DotMatrix #(.inputtype("row"), .matrixcols(32), .matrixrows(32), .dotshape("circle")) dotmatrix_1 (
    .row0(\字库_1_out_3 ), .row1(\字库_1_out_4 ), .row2(\字库_1_out_5 ), .row3(\字库_1_out_6 ), .row4(\字库_1_out_7 ),
    .row5(\字库_1_out_8 ), .row6(\字库_1_out_9 ), .row7(\字库_1_out_10 ), .row8(\字库_1_out_11 ),
    .row9(\字库_1_out_12 ), .row10(\字库_1_out_13 ), .row11(\字库_1_out_14 ), .row12(\字库_1_out_15 ),
    .row13(\字库_1_out_16 ), .row14(\字库_1_out_17 ), .row15(\字库_1_out_18 ), .row16(\字库_1_out_19 ),
    .row17(\字库_1_out_20 ), .row18(\字库_1_out_21 ), .row19(\字库_1_out_22 ), .row20(\字库_1_out_23 ),
    .row21(\字库_1_out_24 ), .row22(\字库_1_out_25 ), .row23(\字库_1_out_26 ), .row24(\字库_1_out_27 ),
    .row25(\字库_1_out_28 ), .row26(\字库_1_out_29 ), .row27(\字库_1_out_30 ), .row28(\字库_1_out_31 ),
    .row29(\字库_1_out_32 ), .row30(\字库_1_out_33 ), .row31(\字库_1_out_34 ));
  ROM #(.dataWidth(16)) rom_1 (.addr(counter_1_q), .data(\发送 ));  // open: sel
  // Probe on \发送 
  // Probe on \海明编码_1_海明码 
  \海明编码  \u_海明编码_1  (.\原始数据 (\发送 ), .\海明码 (\海明编码_1_海明码 ));
  // Probe on \海明编码_1_海明码 
  // Probe on \n22位随机干扰_1_随机加扰屏蔽字 
  \_22位随机干扰  \u_22位随机干扰_1  (
    .\加扰模式 (\加扰控制 ), .\随机加扰屏蔽字 (\n22位随机干扰_1_随机加扰屏蔽字 ), .\_22位输入 (\海明编码_1_海明码 ), .\加扰后数据 (\n22位随机干扰_1_加扰后数据 ));  // open: 增加三位错
  // Probe on \n22位随机干扰_1_加扰后数据 
  // Probe on \n22位随机干扰_1_加扰后数据 
  \字库  \u_字库_2  (
    .out_3(\字库_2_out_3 ), .out_4(\字库_2_out_4 ), .out_5(\字库_2_out_5 ), .out_6(\字库_2_out_6 ),
    .out_7(\字库_2_out_7 ), .out_8(\字库_2_out_8 ), .out_9(\字库_2_out_9 ), .out_10(\字库_2_out_10 ),
    .out_11(\字库_2_out_11 ), .out_12(\字库_2_out_12 ), .out_13(\字库_2_out_13 ), .out_14(\字库_2_out_14 ),
    .out_15(\字库_2_out_15 ), .out_16(\字库_2_out_16 ), .out_17(\字库_2_out_17 ), .out_18(\字库_2_out_18 ),
    .out_19(\字库_2_out_19 ), .out_20(\字库_2_out_20 ), .out_21(\字库_2_out_21 ), .out_22(\字库_2_out_22 ),
    .out_23(\字库_2_out_23 ), .out_24(\字库_2_out_24 ), .out_25(\字库_2_out_25 ), .out_26(\字库_2_out_26 ),
    .out_27(\字库_2_out_27 ), .out_28(\字库_2_out_28 ), .out_29(\字库_2_out_29 ), .out_30(\字库_2_out_30 ),
    .out_31(\字库_2_out_31 ), .out_32(\字库_2_out_32 ), .out_33(\字库_2_out_33 ), .out_34(\字库_2_out_34 ),
    .\区号 (\国标转区位码_2_区号 ), .\位号 (\国标转区位码_2_位号 ));
  \国标转区位码  \u_国标转区位码_2  (.\位号 (\国标转区位码_2_位号 ), .\区号 (\国标转区位码_2_区号 ), .GB2312(\接收 ));
  LED \u_无错误  (.in(\海明解码_1_无错误 ));
  LED \u_两位错  (.in(\海明解码_1__2位错 ));
  LED \u_一位错  (.in(\海明解码_1__1位错 ));
  DotMatrix #(.inputtype("row"), .matrixcols(32), .matrixrows(32), .dotshape("circle")) dotmatrix_2 (
    .row0(\字库_2_out_3 ), .row1(\字库_2_out_4 ), .row2(\字库_2_out_5 ), .row3(\字库_2_out_6 ), .row4(\字库_2_out_7 ),
    .row5(\字库_2_out_8 ), .row6(\字库_2_out_9 ), .row7(\字库_2_out_10 ), .row8(\字库_2_out_11 ),
    .row9(\字库_2_out_12 ), .row10(\字库_2_out_13 ), .row11(\字库_2_out_14 ), .row12(\字库_2_out_15 ),
    .row13(\字库_2_out_16 ), .row14(\字库_2_out_17 ), .row15(\字库_2_out_18 ), .row16(\字库_2_out_19 ),
    .row17(\字库_2_out_20 ), .row18(\字库_2_out_21 ), .row19(\字库_2_out_22 ), .row20(\字库_2_out_23 ),
    .row21(\字库_2_out_24 ), .row22(\字库_2_out_25 ), .row23(\字库_2_out_26 ), .row24(\字库_2_out_27 ),
    .row25(\字库_2_out_28 ), .row26(\字库_2_out_29 ), .row27(\字库_2_out_30 ), .row28(\字库_2_out_31 ),
    .row29(\字库_2_out_32 ), .row30(\字库_2_out_33 ), .row31(\字库_2_out_34 ));
  \海明解码  \u_海明解码_1  (
    .\_1位错 (\海明解码_1__1位错 ), .\_2位错 (\海明解码_1__2位错 ), .\无错误 (\海明解码_1_无错误 ), .\海明码 (\n22位随机干扰_1_加扰后数据 ),
    .\纠错后数据 (\接收 ));
  // Probe on \接收 
  Comparator #(.width(16)) comparator_1 (.a(\发送 ), .b(\接收 ), .eq(comparator_1_eq));  // open: gt, lt
  LED \u_数据正确  (.in(comparator_1_eq));

  // Notes on the sheet:
  //   发送方
  //   计数器
  //   发送方
  //   汉字显示
  //   GB2312
  //   Ctrl+T 驱动时钟触发随机干扰变化
  //   contents of rom_1 (hex, n*v repeats v):
  //   cef7 c4cf d2bd bfc6 b4f3 d1a7 cac7 cbc4 b4a8 caa1 caa1 caf4 c6d5 cda8 b8df b5c8 d4ba d0a3 a3ac d7f8
  //   c2e4 d4da b4a8 d3e5 b5e1 c7ad bde1 bacf c7f8 d3f2 b5c4 b9fa bcd2 c0fa cab7 cec4 bbaf c3fb b3c7 a1a2
  //   c8ab b9fa cec4 c3f7 b3c7 cad0 a1aa a1aa e3f2 d6dd cad0 a1a3 d1a7 d0a3 cabc bda8 d3da a3b1 a3b9 a3b5
  //   a3b1 c4ea a3ac c7b0 c9ed cac7 cef7 c4cf c7f8 b4a8 c4cf d2bd cabf d1a7 d0a3 a3ac a3b1 a3b9 a3b5 a3b9
  //   c4ea c9fd b8f1 ceaa e3f2 d6dd d2bd d1a7 d7a8 bfc6 d1a7 d0a3 a3ac a3b1 a3b9 a3b7 a3b8 c4ea c9fd b8f1
  //   ceaa b1be bfc6 d4ba d0a3 b2a2 b8fc c3fb ceaa e3f2 d6dd d2bd d1a7 d4ba a3ac a3b1 a3b9 a3b8 a3b2 c4ea
  //   bbf1 b5c3 d1a7 cabf d1a7 cebb cada d3e8 c8a8 a3ac a3b1 a3b9 a3b9 a3b3 c4ea b3c9 ceaa cbb6 cabf d1a7
  //   cebb cada d3e8 b5a5 cebb a3ac a3b2 a3b0 a3b0 a3b1 c4ea bfaa cabc c1aa bacf c5e0 d1f8 b2a9 cabf a3ac
  //   a3b2 a3b0 a3b0 a3b4 c4ea c6f0 bfaa d5b9 c1f4 d1a7 b1be bfc6 c9fa d1a7 c0fa bdcc d3fd a3ac a3b2 a3b0
  //   a3b1 a3b0 c4ea bbf1 d7bc c9e8 c1a2 b2a9 cabf baf3 bfc6 d1d0 b9a4 d7f7 d5be a3ac a3b2 a3b0 a3b1 a3b5
  //   c4ea b8fc c3fb ceaa cef7 c4cf d2bd bfc6 b4f3 d1a7 a1a3 d1a7 d0a3 cac7 cdc6 bcf6 d3c5 d0e3 d3a6 bdec
  //   b1be bfc6 b1cf d2b5 c9fa c3e2 cad4 b9a5 b6c1 cbb6 cabf d1d0 bebf c9fa d7ca b8f1 b5a5 cebb a3ac cac7
  //   cbc4 b4a8 caa1 d2c0 b7a8 d6ce d0a3 cabe b7b6 d1a7 d0a3 a1a2 cbc4 b4a8 caa1 cec4
  //   电路功能：测试海明编解码电路正确性，仿真时设置加扰控制位和原始数据，按CTRL+T触发不同的干扰，检验编解码电路功能
  //   发送方在ROM预存了一段中文文字，通过计数器驱动电路每个时钟传输一个汉字到接收方
  //   用户实现了国标转区位码电路后，可在中间窗口观察发送方和接收方汉字显示是否一致以观察海明检错纠错性能
  //   海明编解码传输电路
  //   接收方
  //   汉字显示
  //   Ctrl+T 驱动时钟触发随机干扰变化
  //   加扰控制00：不加扰  01:1位加扰 10:2位加扰 11：随机加扰
  //   加扰控制00：不加扰  01:1位加扰 10:2位加扰 11：随机加扰
  //   接收方
  //   请将时钟频率调到8Hz
endmodule

module \海明编码流水传输  (
  input  [1:0] in_1,
  input  \加噪 
);

  wire \_2位错 , \_2位错且有效 , \_4阶段有效性 , \n16位流水接口_1_传输状态out_表明当前传输数据有效 , \n22位流水接口_1_传输状态out_表明当前传输数据有效 ,
       or_1_out, xor_1_out, xor_2_out, \时钟_out , \流水暂停信号 , \海明解码_1__1位错 , \海明解码_1_无错误 ;
  wire [6:0] \国标转区位码_1_位号 , \国标转区位码_1_区号 , \国标转区位码_2_位号 , \国标转区位码_2_区号 ;
  wire [7:0] adder_1_out, adder_2_out, multiplexer_1_out, multiplexer_2_out, register_1_q;
  wire [15:0] \n16位流水接口_1_dout16 , \发送 , \接收 , \海明解码_1_纠错后数据 ;
  wire [21:0] \n22位流水接口_1_dout22 , \n22位流水接口_2_dout22 , \n22位随机干扰_1_加扰后数据 , \海明编码_1_海明码 ;
  wire [31:0] \字库_1_out_3 , \字库_1_out_4 , \字库_1_out_5 , \字库_1_out_6 , \字库_1_out_7 , \字库_1_out_8 ,
       \字库_1_out_9 , \字库_1_out_10 , \字库_1_out_11 , \字库_1_out_12 , \字库_1_out_13 , \字库_1_out_14 ,
       \字库_1_out_15 , \字库_1_out_16 , \字库_1_out_17 , \字库_1_out_18 , \字库_1_out_19 , \字库_1_out_20 ,
       \字库_1_out_21 , \字库_1_out_22 , \字库_1_out_23 , \字库_1_out_24 , \字库_1_out_25 , \字库_1_out_26 ,
       \字库_1_out_27 , \字库_1_out_28 , \字库_1_out_29 , \字库_1_out_30 , \字库_1_out_31 , \字库_1_out_32 ,
       \字库_1_out_33 , \字库_1_out_34 , \字库_2_out_3 , \字库_2_out_4 , \字库_2_out_5 , \字库_2_out_6 , \字库_2_out_7 ,
       \字库_2_out_8 , \字库_2_out_9 , \字库_2_out_10 , \字库_2_out_11 , \字库_2_out_12 , \字库_2_out_13 , \字库_2_out_14 ,
       \字库_2_out_15 , \字库_2_out_16 , \字库_2_out_17 , \字库_2_out_18 , \字库_2_out_19 , \字库_2_out_20 ,
       \字库_2_out_21 , \字库_2_out_22 , \字库_2_out_23 , \字库_2_out_24 , \字库_2_out_25 , \字库_2_out_26 ,
       \字库_2_out_27 , \字库_2_out_28 , \字库_2_out_29 , \字库_2_out_30 , \字库_2_out_31 , \字库_2_out_32 ,
       \字库_2_out_33 , \字库_2_out_34 ;

  Multiplexer #(.width(8)) multiplexer_1 (
    .in0(8'h1), .in1(8'hfe), .out(multiplexer_1_out), .sel(\_2位错且有效 ));  // open: en
  Register register_1 (.D(adder_1_out), .Q(register_1_q), .clk(\时钟_out ));  // open: en, clr
  Clock \u_时钟  (.out(\时钟_out ));
  \国标转区位码  \u_国标转区位码_1  (.\位号 (\国标转区位码_1_位号 ), .\区号 (\国标转区位码_1_区号 ), .GB2312(\发送 ));
  Adder adder_1 (.a(multiplexer_1_out), .b(register_1_q), .out(adder_1_out));  // open: cin, cout
  Multiplexer #(.width(8)) multiplexer_2 (
    .in0(register_1_q), .in1(adder_2_out), .out(multiplexer_2_out), .sel(\_2位错且有效 ));  // open: en
  Adder adder_2 (.a(register_1_q), .b(8'hfd), .out(adder_2_out));  // open: cin, cout
  \字库  \u_字库_1  (
    .out_3(\字库_1_out_3 ), .out_4(\字库_1_out_4 ), .out_5(\字库_1_out_5 ), .out_6(\字库_1_out_6 ),
    .out_7(\字库_1_out_7 ), .out_8(\字库_1_out_8 ), .out_9(\字库_1_out_9 ), .out_10(\字库_1_out_10 ),
    .out_11(\字库_1_out_11 ), .out_12(\字库_1_out_12 ), .out_13(\字库_1_out_13 ), .out_14(\字库_1_out_14 ),
    .out_15(\字库_1_out_15 ), .out_16(\字库_1_out_16 ), .out_17(\字库_1_out_17 ), .out_18(\字库_1_out_18 ),
    .out_19(\字库_1_out_19 ), .out_20(\字库_1_out_20 ), .out_21(\字库_1_out_21 ), .out_22(\字库_1_out_22 ),
    .out_23(\字库_1_out_23 ), .out_24(\字库_1_out_24 ), .out_25(\字库_1_out_25 ), .out_26(\字库_1_out_26 ),
    .out_27(\字库_1_out_27 ), .out_28(\字库_1_out_28 ), .out_29(\字库_1_out_29 ), .out_30(\字库_1_out_30 ),
    .out_31(\字库_1_out_31 ), .out_32(\字库_1_out_32 ), .out_33(\字库_1_out_33 ), .out_34(\字库_1_out_34 ),
    .\区号 (\国标转区位码_1_区号 ), .\位号 (\国标转区位码_1_位号 ));
  DotMatrix #(.inputtype("row"), .matrixcols(32), .matrixrows(32)) dotmatrix_1 (
    .row0(\字库_1_out_3 ), .row1(\字库_1_out_4 ), .row2(\字库_1_out_5 ), .row3(\字库_1_out_6 ), .row4(\字库_1_out_7 ),
    .row5(\字库_1_out_8 ), .row6(\字库_1_out_9 ), .row7(\字库_1_out_10 ), .row8(\字库_1_out_11 ),
    .row9(\字库_1_out_12 ), .row10(\字库_1_out_13 ), .row11(\字库_1_out_14 ), .row12(\字库_1_out_15 ),
    .row13(\字库_1_out_16 ), .row14(\字库_1_out_17 ), .row15(\字库_1_out_18 ), .row16(\字库_1_out_19 ),
    .row17(\字库_1_out_20 ), .row18(\字库_1_out_21 ), .row19(\字库_1_out_22 ), .row20(\字库_1_out_23 ),
    .row21(\字库_1_out_24 ), .row22(\字库_1_out_25 ), .row23(\字库_1_out_26 ), .row24(\字库_1_out_27 ),
    .row25(\字库_1_out_28 ), .row26(\字库_1_out_29 ), .row27(\字库_1_out_30 ), .row28(\字库_1_out_31 ),
    .row29(\字库_1_out_32 ), .row30(\字库_1_out_33 ), .row31(\字库_1_out_34 ));
  ROM #(.dataWidth(16)) rom_1 (.addr(multiplexer_2_out), .data(\发送 ));  // open: sel
  \流水暂停时序电路  \u_流水暂停时序电路_1  (.CLK(\时钟_out ), .out(\流水暂停信号 ), .en(\_2位错且有效 ));
  \_16位流水接口  \u_16位流水接口_1  (
    .Din16(\发送 ), .\传输状态In_表明当前传输数据有效 (1'b1), .CLK(\时钟_out ), .Dout16(\n16位流水接口_1_dout16 ),
    .\传输状态Out_表明当前传输数据有效 (\n16位流水接口_1_传输状态out_表明当前传输数据有效 ));  // open: 同步清零_气泡_高电平有效, 使能端_低电平有效_stall_高电平有效
  \海明编码  \u_海明编码_1  (.\原始数据 (\n16位流水接口_1_dout16 ), .\海明码 (\海明编码_1_海明码 ));
  xor xor_1 (xor_1_out, \n16位流水接口_1_传输状态out_表明当前传输数据有效 , \_2位错且有效 );
  \_22位流水接口  \u_22位流水接口_1  (
    .Din22(\海明编码_1_海明码 ), .\传输状态In_表明当前传输数据有效 (xor_1_out), .CLK(\时钟_out ), .Dout22(\n22位流水接口_1_dout22 ),
    .\传输状态Out_表明当前传输数据有效 (\n22位流水接口_1_传输状态out_表明当前传输数据有效 ));  // open: 同步清零_气泡_高电平有效, 使能端_低电平有效_stall_高电平有效
  \_22位随机干扰  \u_22位随机干扰_1  (
    .\加扰模式 (in_1), .\_22位输入 (\n22位流水接口_1_dout22 ), .\加扰后数据 (\n22位随机干扰_1_加扰后数据 ), .\增加三位错 (\加噪 ));  // open: 随机加扰屏蔽字
  \字库  \u_字库_2  (
    .out_3(\字库_2_out_3 ), .out_4(\字库_2_out_4 ), .out_5(\字库_2_out_5 ), .out_6(\字库_2_out_6 ),
    .out_7(\字库_2_out_7 ), .out_8(\字库_2_out_8 ), .out_9(\字库_2_out_9 ), .out_10(\字库_2_out_10 ),
    .out_11(\字库_2_out_11 ), .out_12(\字库_2_out_12 ), .out_13(\字库_2_out_13 ), .out_14(\字库_2_out_14 ),
    .out_15(\字库_2_out_15 ), .out_16(\字库_2_out_16 ), .out_17(\字库_2_out_17 ), .out_18(\字库_2_out_18 ),
    .out_19(\字库_2_out_19 ), .out_20(\字库_2_out_20 ), .out_21(\字库_2_out_21 ), .out_22(\字库_2_out_22 ),
    .out_23(\字库_2_out_23 ), .out_24(\字库_2_out_24 ), .out_25(\字库_2_out_25 ), .out_26(\字库_2_out_26 ),
    .out_27(\字库_2_out_27 ), .out_28(\字库_2_out_28 ), .out_29(\字库_2_out_29 ), .out_30(\字库_2_out_30 ),
    .out_31(\字库_2_out_31 ), .out_32(\字库_2_out_32 ), .out_33(\字库_2_out_33 ), .out_34(\字库_2_out_34 ),
    .\区号 (\国标转区位码_2_区号 ), .\位号 (\国标转区位码_2_位号 ));
  \国标转区位码  \u_国标转区位码_2  (.\位号 (\国标转区位码_2_位号 ), .\区号 (\国标转区位码_2_区号 ), .GB2312(\接收 ));
  and and_1 (\_2位错且有效 , \_2位错 , \_4阶段有效性 );
  \_22位流水接口  \u_22位流水接口_2  (
    .Din22(\n22位随机干扰_1_加扰后数据 ), .\传输状态In_表明当前传输数据有效 (xor_2_out), .CLK(\时钟_out ),
    .Dout22(\n22位流水接口_2_dout22 ), .\传输状态Out_表明当前传输数据有效 (\_4阶段有效性 ));  // open: 同步清零_气泡_高电平有效, 使能端_低电平有效_stall_高电平有效
  xor xor_2 (xor_2_out, \n22位流水接口_1_传输状态out_表明当前传输数据有效 , \_2位错且有效 );
  DotMatrix #(.inputtype("row"), .matrixcols(32), .matrixrows(32)) dotmatrix_2 (
    .row0(\字库_2_out_3 ), .row1(\字库_2_out_4 ), .row2(\字库_2_out_5 ), .row3(\字库_2_out_6 ), .row4(\字库_2_out_7 ),
    .row5(\字库_2_out_8 ), .row6(\字库_2_out_9 ), .row7(\字库_2_out_10 ), .row8(\字库_2_out_11 ),
    .row9(\字库_2_out_12 ), .row10(\字库_2_out_13 ), .row11(\字库_2_out_14 ), .row12(\字库_2_out_15 ),
    .row13(\字库_2_out_16 ), .row14(\字库_2_out_17 ), .row15(\字库_2_out_18 ), .row16(\字库_2_out_19 ),
    .row17(\字库_2_out_20 ), .row18(\字库_2_out_21 ), .row19(\字库_2_out_22 ), .row20(\字库_2_out_23 ),
    .row21(\字库_2_out_24 ), .row22(\字库_2_out_25 ), .row23(\字库_2_out_26 ), .row24(\字库_2_out_27 ),
    .row25(\字库_2_out_28 ), .row26(\字库_2_out_29 ), .row27(\字库_2_out_30 ), .row28(\字库_2_out_31 ),
    .row29(\字库_2_out_32 ), .row30(\字库_2_out_33 ), .row31(\字库_2_out_34 ));
  LED \u_两位错  (.in(\_2位错 ));
  LED \u_一位错  (.in(\海明解码_1__1位错 ));
  LED \u_无错误  (.in(\海明解码_1_无错误 ));
  \海明解码  \u_海明解码_1  (
    .\_1位错 (\海明解码_1__1位错 ), .\_2位错 (\_2位错 ), .\无错误 (\海明解码_1_无错误 ), .\海明码 (\n22位流水接口_2_dout22 ),
    .\纠错后数据 (\海明解码_1_纠错后数据 ));
  or or_1 (or_1_out, \_2位错且有效 , \流水暂停信号 );
  \_16位流水接口  \u_16位流水接口_2  (
    .Din16(\海明解码_1_纠错后数据 ), .\传输状态In_表明当前传输数据有效 (\_4阶段有效性 ), .CLK(\时钟_out ), .Dout16(\接收 ),
    .\使能端_低电平有效_stall_高电平有效 (or_1_out));  // open: 传输状态Out_表明当前传输数据有效, 同步清零_气泡_高电平有效
  // Probe on \接收 

  // Notes on the sheet:
  //   海明码流水传输电路
  //   寄存器
  //   发送方
  //   汉字显示
  //   加法器
  //   GB2312
  //   1.取数阶段
  //   contents of rom_1 (hex, n*v repeats v):
  //   bbaa d6d0 bfc6 bcbc b4f3 d1a7 cac7 b9fa bcd2 bdcc d3fd b2bf d6b1 caf4 b5c4 c8ab b9fa d6d8 b5e3 b4f3
  //   d1a7 a3ac d3c9 d4ad bbaa d6d0 c0ed b9a4 b4f3 d1a7 a1a2 cdac bcc3 d2bd bfc6 b4f3 d1a7 a1a2 cee4 baba
  //   b3c7 cad0 bda8 c9e8 d1a7 d4ba d3da a3b2 a3b0 a3b0 a3b0 c4ea a3b5 d4c2 a3b2 a3b6 c8d5 bacf b2a2 b3c9
  //   c1a2 a3ac cac7 cad7 c5fa c1d0 c8eb b9fa bcd2 a1b0 a3b2 a3b1 a3b1 b9a4 b3cc a1b1 d6d8 b5e3 bda8 c9e8
  //   bacd b9fa bcd2 a1b0 a3b9 a3b8 a3b5 b9a4 b3cc a1b1 bda8 c9e8 b8df d0a3 d6ae d2bb a1a3 d1a7 d0a3 d0a3
  //   d4b0 d5bc b5d8 c6df c7a7 d3e0 c4b6 a3ac d4b0 c4da caf7 c4be b4d0 dcd7 a3ac b1cc b2dd c8e7 d2f0 a3ac
  //   bbb7 beb3 d3c5 d1c5 a3ac beb0 c9ab d0e3 c0f6 a3ac c2cc bbaf b8b2 b8c7 c2ca 3732 25a3 acb1 bbd3 fece
  //   aaa1 b0c9 adc1 d6ca bdb4 f3d1 a7a1 b1a1
  //   ~使能/Stall
  //   发送方在ROM预存了一段中文文字，通过计数器驱动电路每个时钟传输一个汉字
  //   同步清零信号，气泡
  //   用户实现了国标转区位码电路后，可在中间窗口观察发送方和接收方汉字显示是否一致以观察海明检错纠错性能
  //   数据状态：高电平有效
  //   2.编码阶段
  //   电路功能：采用流水分段方式进行数据编码传输，测试海明编码检错纠错能力，当出现2位错时，发送重传信号要求发送方重传，保证接收方按ROM中的地址顺序接受所有汉字
  //   接收方
  //   汉字显示
  //   3.传输阶段
  //   4.解码阶段
  //   此电路可帮助学生理解指令流水线工作原理，重传类似指令流水线中的分支指令
  //   5.显示阶段
  //   请将时钟频率调到8Hz
  //   Ctrl+ K启动电路自动仿真
endmodule

module \CRC传输测试1  (
  input  [15:0] \原始数据 ,
  input  [1:0] \加扰控制 
);

  wire comparator_1_eq, \crc解码_1__1位错 , \crc解码_1__2位错 , \crc解码_1_无错误 ;
  wire [15:0] \crc解码_1_纠错后数据 ;
  wire [21:0] \crc编码_1_crc校验码 , \n22位随机干扰_1_加扰后数据 , \n22位随机干扰_1_随机加扰屏蔽字 ;

  // Probe on \原始数据 
  // Probe on \crc编码_1_crc校验码 
  \CRC编码  \crc编码_1  (.\原始数据 (\原始数据 ), .\CRC校验码 (\crc编码_1_crc校验码 ));
  // Probe on \crc编码_1_crc校验码 
  // Probe on \n22位随机干扰_1_随机加扰屏蔽字 
  // Probe on \n22位随机干扰_1_加扰后数据 
  \_22位随机干扰  \u_22位随机干扰_1  (
    .\加扰模式 (\加扰控制 ), .\随机加扰屏蔽字 (\n22位随机干扰_1_随机加扰屏蔽字 ), .\_22位输入 (\crc编码_1_crc校验码 ),
    .\加扰后数据 (\n22位随机干扰_1_加扰后数据 ));  // open: 增加三位错
  // Probe on \n22位随机干扰_1_加扰后数据 
  LED \u_一位错  (.in(\crc解码_1__1位错 ));
  LED \u_无错误  (.in(\crc解码_1_无错误 ));
  LED \u_两位错  (.in(\crc解码_1__2位错 ));
  \CRC解码  \crc解码_1  (
    .\CRC编码 (\n22位随机干扰_1_加扰后数据 ), .\无错误 (\crc解码_1_无错误 ), .\_1位错 (\crc解码_1__1位错 ), .\_2位错 (\crc解码_1__2位错 ),
    .\纠错后数据 (\crc解码_1_纠错后数据 ));
  // Probe on \crc解码_1_纠错后数据 
  Comparator #(.width(16)) comparator_1 (.a(\原始数据 ), .b(\crc解码_1_纠错后数据 ), .eq(comparator_1_eq));  // open: gt, lt
  LED \u_数据正确  (.in(comparator_1_eq));

  // Notes on the sheet:
  //   发送方
  //   电路功能：测试CRC编解码电路正确性，仿真时设置加扰控制位和原始数据，按CTRL+T触发不同的干扰，检验编解码电路功能
  //   Ctrl+T 驱动时钟触发随机干扰变化
  //   CRC编解码传输电路
  //   加扰控制00：不加扰  01:1位加扰 10:2位加扰 11：随机加扰
  //   接收方
endmodule

module \CRC传输测试2  (
  input  [1:0] \加扰控制 
);

  wire comparator_1_eq, \crc解码_1__1位错 , \crc解码_1__2位错 , \crc解码_1_无错误 , \时钟_out ;
  wire [6:0] \国标转区位码_1_位号 , \国标转区位码_1_区号 , \国标转区位码_2_位号 , \国标转区位码_2_区号 ;
  wire [7:0] counter_1_q;
  wire [15:0] \发送 , \接收 ;
  wire [21:0] \crc编码_1_crc校验码 , \n22位随机干扰_1_加扰后数据 , \n22位随机干扰_1_随机加扰屏蔽字 ;
  wire [31:0] \字库_1_out_3 , \字库_1_out_4 , \字库_1_out_5 , \字库_1_out_6 , \字库_1_out_7 , \字库_1_out_8 ,
       \字库_1_out_9 , \字库_1_out_10 , \字库_1_out_11 , \字库_1_out_12 , \字库_1_out_13 , \字库_1_out_14 ,
       \字库_1_out_15 , \字库_1_out_16 , \字库_1_out_17 , \字库_1_out_18 , \字库_1_out_19 , \字库_1_out_20 ,
       \字库_1_out_21 , \字库_1_out_22 , \字库_1_out_23 , \字库_1_out_24 , \字库_1_out_25 , \字库_1_out_26 ,
       \字库_1_out_27 , \字库_1_out_28 , \字库_1_out_29 , \字库_1_out_30 , \字库_1_out_31 , \字库_1_out_32 ,
       \字库_1_out_33 , \字库_1_out_34 , \字库_2_out_3 , \字库_2_out_4 , \字库_2_out_5 , \字库_2_out_6 , \字库_2_out_7 ,
       \字库_2_out_8 , \字库_2_out_9 , \字库_2_out_10 , \字库_2_out_11 , \字库_2_out_12 , \字库_2_out_13 , \字库_2_out_14 ,
       \字库_2_out_15 , \字库_2_out_16 , \字库_2_out_17 , \字库_2_out_18 , \字库_2_out_19 , \字库_2_out_20 ,
       \字库_2_out_21 , \字库_2_out_22 , \字库_2_out_23 , \字库_2_out_24 , \字库_2_out_25 , \字库_2_out_26 ,
       \字库_2_out_27 , \字库_2_out_28 , \字库_2_out_29 , \字库_2_out_30 , \字库_2_out_31 , \字库_2_out_32 ,
       \字库_2_out_33 , \字库_2_out_34 ;

  Clock \u_时钟  (.out(\时钟_out ));
  Counter counter_1 (.Q(counter_1_q), .clk(\时钟_out ));  // open: load, D, count, carry, clr
  \国标转区位码  \u_国标转区位码_1  (.\位号 (\国标转区位码_1_位号 ), .\区号 (\国标转区位码_1_区号 ), .GB2312(\发送 ));
  \字库  \u_字库_1  (
    .out_3(\字库_1_out_3 ), .out_4(\字库_1_out_4 ), .out_5(\字库_1_out_5 ), .out_6(\字库_1_out_6 ),
    .out_7(\字库_1_out_7 ), .out_8(\字库_1_out_8 ), .out_9(\字库_1_out_9 ), .out_10(\字库_1_out_10 ),
    .out_11(\字库_1_out_11 ), .out_12(\字库_1_out_12 ), .out_13(\字库_1_out_13 ), .out_14(\字库_1_out_14 ),
    .out_15(\字库_1_out_15 ), .out_16(\字库_1_out_16 ), .out_17(\字库_1_out_17 ), .out_18(\字库_1_out_18 ),
    .out_19(\字库_1_out_19 ), .out_20(\字库_1_out_20 ), .out_21(\字库_1_out_21 ), .out_22(\字库_1_out_22 ),
    .out_23(\字库_1_out_23 ), .out_24(\字库_1_out_24 ), .out_25(\字库_1_out_25 ), .out_26(\字库_1_out_26 ),
    .out_27(\字库_1_out_27 ), .out_28(\字库_1_out_28 ), .out_29(\字库_1_out_29 ), .out_30(\字库_1_out_30 ),
    .out_31(\字库_1_out_31 ), .out_32(\字库_1_out_32 ), .out_33(\字库_1_out_33 ), .out_34(\字库_1_out_34 ),
    .\区号 (\国标转区位码_1_区号 ), .\位号 (\国标转区位码_1_位号 ));
  DotMatrix #(.inputtype("row"), .matrixcols(32), .matrixrows(32), .dotshape("circle")) dotmatrix_1 (
    .row0(\字库_1_out_3 ), .row1(\字库_1_out_4 ), .row2(\字库_1_out_5 ), .row3(\字库_1_out_6 ), .row4(\字库_1_out_7 ),
    .row5(\字库_1_out_8 ), .row6(\字库_1_out_9 ), .row7(\字库_1_out_10 ), .row8(\字库_1_out_11 ),
    .row9(\字库_1_out_12 ), .row10(\字库_1_out_13 ), .row11(\字库_1_out_14 ), .row12(\字库_1_out_15 ),
    .row13(\字库_1_out_16 ), .row14(\字库_1_out_17 ), .row15(\字库_1_out_18 ), .row16(\字库_1_out_19 ),
    .row17(\字库_1_out_20 ), .row18(\字库_1_out_21 ), .row19(\字库_1_out_22 ), .row20(\字库_1_out_23 ),
    .row21(\字库_1_out_24 ), .row22(\字库_1_out_25 ), .row23(\字库_1_out_26 ), .row24(\字库_1_out_27 ),
    .row25(\字库_1_out_28 ), .row26(\字库_1_out_29 ), .row27(\字库_1_out_30 ), .row28(\字库_1_out_31 ),
    .row29(\字库_1_out_32 ), .row30(\字库_1_out_33 ), .row31(\字库_1_out_34 ));
  ROM #(.dataWidth(16)) rom_1 (.addr(counter_1_q), .data(\发送 ));  // open: sel
  // Probe on \发送 
  // Probe on \crc编码_1_crc校验码 
  \CRC编码  \crc编码_1  (.\原始数据 (\发送 ), .\CRC校验码 (\crc编码_1_crc校验码 ));
  // Probe on \crc编码_1_crc校验码 
  // Probe on \n22位随机干扰_1_随机加扰屏蔽字 
  \_22位随机干扰  \u_22位随机干扰_1  (
    .\加扰模式 (\加扰控制 ), .\随机加扰屏蔽字 (\n22位随机干扰_1_随机加扰屏蔽字 ), .\_22位输入 (\crc编码_1_crc校验码 ),
    .\加扰后数据 (\n22位随机干扰_1_加扰后数据 ));  // open: 增加三位错
  // Probe on \n22位随机干扰_1_加扰后数据 
  // Probe on \n22位随机干扰_1_加扰后数据 
  \字库  \u_字库_2  (
    .out_3(\字库_2_out_3 ), .out_4(\字库_2_out_4 ), .out_5(\字库_2_out_5 ), .out_6(\字库_2_out_6 ),
    .out_7(\字库_2_out_7 ), .out_8(\字库_2_out_8 ), .out_9(\字库_2_out_9 ), .out_10(\字库_2_out_10 ),
    .out_11(\字库_2_out_11 ), .out_12(\字库_2_out_12 ), .out_13(\字库_2_out_13 ), .out_14(\字库_2_out_14 ),
    .out_15(\字库_2_out_15 ), .out_16(\字库_2_out_16 ), .out_17(\字库_2_out_17 ), .out_18(\字库_2_out_18 ),
    .out_19(\字库_2_out_19 ), .out_20(\字库_2_out_20 ), .out_21(\字库_2_out_21 ), .out_22(\字库_2_out_22 ),
    .out_23(\字库_2_out_23 ), .out_24(\字库_2_out_24 ), .out_25(\字库_2_out_25 ), .out_26(\字库_2_out_26 ),
    .out_27(\字库_2_out_27 ), .out_28(\字库_2_out_28 ), .out_29(\字库_2_out_29 ), .out_30(\字库_2_out_30 ),
    .out_31(\字库_2_out_31 ), .out_32(\字库_2_out_32 ), .out_33(\字库_2_out_33 ), .out_34(\字库_2_out_34 ),
    .\区号 (\国标转区位码_2_区号 ), .\位号 (\国标转区位码_2_位号 ));
  \国标转区位码  \u_国标转区位码_2  (.\位号 (\国标转区位码_2_位号 ), .\区号 (\国标转区位码_2_区号 ), .GB2312(\接收 ));
  LED \u_两位错  (.in(\crc解码_1__2位错 ));
  LED \u_无错误  (.in(\crc解码_1_无错误 ));
  LED \u_一位错  (.in(\crc解码_1__1位错 ));
  DotMatrix #(.inputtype("row"), .matrixcols(32), .matrixrows(32), .dotshape("circle")) dotmatrix_2 (
    .row0(\字库_2_out_3 ), .row1(\字库_2_out_4 ), .row2(\字库_2_out_5 ), .row3(\字库_2_out_6 ), .row4(\字库_2_out_7 ),
    .row5(\字库_2_out_8 ), .row6(\字库_2_out_9 ), .row7(\字库_2_out_10 ), .row8(\字库_2_out_11 ),
    .row9(\字库_2_out_12 ), .row10(\字库_2_out_13 ), .row11(\字库_2_out_14 ), .row12(\字库_2_out_15 ),
    .row13(\字库_2_out_16 ), .row14(\字库_2_out_17 ), .row15(\字库_2_out_18 ), .row16(\字库_2_out_19 ),
    .row17(\字库_2_out_20 ), .row18(\字库_2_out_21 ), .row19(\字库_2_out_22 ), .row20(\字库_2_out_23 ),
    .row21(\字库_2_out_24 ), .row22(\字库_2_out_25 ), .row23(\字库_2_out_26 ), .row24(\字库_2_out_27 ),
    .row25(\字库_2_out_28 ), .row26(\字库_2_out_29 ), .row27(\字库_2_out_30 ), .row28(\字库_2_out_31 ),
    .row29(\字库_2_out_32 ), .row30(\字库_2_out_33 ), .row31(\字库_2_out_34 ));
  \CRC解码  \crc解码_1  (
    .\CRC编码 (\n22位随机干扰_1_加扰后数据 ), .\无错误 (\crc解码_1_无错误 ), .\_1位错 (\crc解码_1__1位错 ), .\_2位错 (\crc解码_1__2位错 ),
    .\纠错后数据 (\接收 ));
  // Probe on \接收 
  Comparator #(.width(16)) comparator_1 (.a(\发送 ), .b(\接收 ), .eq(comparator_1_eq));  // open: gt, lt
  LED \u_数据正确  (.in(comparator_1_eq));

  // Notes on the sheet:
  //   发送方
  //   计数器
  //   发送方
  //   汉字显示
  //   GB2312
  //   Ctrl+T 驱动时钟触发随机干扰变化
  //   contents of rom_1 (hex, n*v repeats v):
  //   bbaa d6d0 bfc6 bcbc b4f3 d1a7 cac7 b9fa bcd2 bdcc d3fd b2bf d6b1 caf4 b5c4 c8ab b9fa d6d8 b5e3 b4f3
  //   d1a7 a3ac d3c9 d4ad bbaa d6d0 c0ed b9a4 b4f3 d1a7 a1a2 cdac bcc3 d2bd bfc6 b4f3 d1a7 a1a2 cee4 baba
  //   b3c7 cad0 bda8 c9e8 d1a7 d4ba d3da a3b2 a3b0 a3b0 a3b0 c4ea a3b5 d4c2 a3b2 a3b6 c8d5 bacf b2a2 b3c9
  //   c1a2 a3ac cac7 cad7 c5fa c1d0 c8eb b9fa bcd2 a1b0 a3b2 a3b1 a3b1 b9a4 b3cc a1b1 d6d8 b5e3 bda8 c9e8
  //   bacd b9fa bcd2 a1b0 a3b9 a3b8 a3b5 b9a4 b3cc a1b1 bda8 c9e8 b8df d0a3 d6ae d2bb a1a3 d1a7 d0a3 d0a3
  //   d4b0 d5bc b5d8 c6df c7a7 d3e0 c4b6 a3ac d4b0 c4da caf7 c4be b4d0 dcd7 a3ac b1cc b2dd c8e7 d2f0 a3ac
  //   bbb7 beb3 d3c5 d1c5 a3ac beb0 c9ab d0e3 c0f6 a3ac c2cc bbaf b8b2 b8c7 c2ca 3732 25a3 acb1 bbd3 fece
  //   aaa1 b0c9 adc1 d6ca bdb4 f3d1 a7a1 b1a1
  //   电路功能：测试CRC编解码电路正确性，仿真时设置加扰控制位和原始数据，按CTRL+T触发不同的干扰，检验编解码电路功能
  //   发送方在ROM预存了一段中文文字，通过计数器驱动电路每个时钟传输一个汉字到接收方
  //   用户实现了国标转区位码电路后，可在中间窗口观察发送方和接收方汉字显示是否一致以观察海明检错纠错性能
  //   CRC编解码传输电路
  //   接收方
  //   汉字显示
  //   Ctrl+T 驱动时钟触发随机干扰变化
  //   加扰控制00：不加扰  01:1位加扰 10:2位加扰 11：随机加扰
  //   加扰控制00：不加扰  01:1位加扰 10:2位加扰 11：随机加扰
  //   接收方
  //   请将时钟频率调到8Hz
endmodule

module \CRC编码流水传输  (
  input  \加噪 
);

  wire \crc解码_1__1位错 , \crc解码_1__2位错 , \crc解码_1_无错误 , \n16位流水接口_1_传输状态out_表明当前传输数据有效 ,
       \n22位流水接口_1_传输状态out_表明当前传输数据有效 , \n22位流水接口_2_传输状态out_表明当前传输数据有效 , undriven, \时钟_out ;
  wire [6:0] \国标转区位码_1_位号 , \国标转区位码_1_区号 , \国标转区位码_2_位号 , \国标转区位码_2_区号 ;
  wire [7:0] adder_1_out, register_1_q;
  wire [15:0] \crc解码_1_纠错后数据 , \n16位流水接口_1_dout16 , \发送 , \接收 ;
  wire [21:0] \crc编码_1_crc校验码 , \n22位流水接口_1_dout22 , \n22位流水接口_2_dout22 , \n22位随机干扰_1_加扰后数据 ;
  wire [31:0] \字库_1_out_3 , \字库_1_out_4 , \字库_1_out_5 , \字库_1_out_6 , \字库_1_out_7 , \字库_1_out_8 ,
       \字库_1_out_9 , \字库_1_out_10 , \字库_1_out_11 , \字库_1_out_12 , \字库_1_out_13 , \字库_1_out_14 ,
       \字库_1_out_15 , \字库_1_out_16 , \字库_1_out_17 , \字库_1_out_18 , \字库_1_out_19 , \字库_1_out_20 ,
       \字库_1_out_21 , \字库_1_out_22 , \字库_1_out_23 , \字库_1_out_24 , \字库_1_out_25 , \字库_1_out_26 ,
       \字库_1_out_27 , \字库_1_out_28 , \字库_1_out_29 , \字库_1_out_30 , \字库_1_out_31 , \字库_1_out_32 ,
       \字库_1_out_33 , \字库_1_out_34 , \字库_2_out_3 , \字库_2_out_4 , \字库_2_out_5 , \字库_2_out_6 , \字库_2_out_7 ,
       \字库_2_out_8 , \字库_2_out_9 , \字库_2_out_10 , \字库_2_out_11 , \字库_2_out_12 , \字库_2_out_13 , \字库_2_out_14 ,
       \字库_2_out_15 , \字库_2_out_16 , \字库_2_out_17 , \字库_2_out_18 , \字库_2_out_19 , \字库_2_out_20 ,
       \字库_2_out_21 , \字库_2_out_22 , \字库_2_out_23 , \字库_2_out_24 , \字库_2_out_25 , \字库_2_out_26 ,
       \字库_2_out_27 , \字库_2_out_28 , \字库_2_out_29 , \字库_2_out_30 , \字库_2_out_31 , \字库_2_out_32 ,
       \字库_2_out_33 , \字库_2_out_34 ;

  Register register_1 (.D(adder_1_out), .Q(register_1_q), .clk(\时钟_out ));  // open: en, clr
  Clock \u_时钟  (.out(\时钟_out ));
  \国标转区位码  \u_国标转区位码_1  (.\位号 (\国标转区位码_1_位号 ), .\区号 (\国标转区位码_1_区号 ), .GB2312(\发送 ));
  Adder adder_1 (.a(8'h1), .b(register_1_q), .out(adder_1_out));  // open: cin, cout
  DotMatrix #(.inputtype("row"), .matrixcols(32), .matrixrows(32), .dotshape("circle")) dotmatrix_1 (
    .row0(\字库_1_out_3 ), .row1(\字库_1_out_4 ), .row2(\字库_1_out_5 ), .row3(\字库_1_out_6 ), .row4(\字库_1_out_7 ),
    .row5(\字库_1_out_8 ), .row6(\字库_1_out_9 ), .row7(\字库_1_out_10 ), .row8(\字库_1_out_11 ),
    .row9(\字库_1_out_12 ), .row10(\字库_1_out_13 ), .row11(\字库_1_out_14 ), .row12(\字库_1_out_15 ),
    .row13(\字库_1_out_16 ), .row14(\字库_1_out_17 ), .row15(\字库_1_out_18 ), .row16(\字库_1_out_19 ),
    .row17(\字库_1_out_20 ), .row18(\字库_1_out_21 ), .row19(\字库_1_out_22 ), .row20(\字库_1_out_23 ),
    .row21(\字库_1_out_24 ), .row22(\字库_1_out_25 ), .row23(\字库_1_out_26 ), .row24(\字库_1_out_27 ),
    .row25(\字库_1_out_28 ), .row26(\字库_1_out_29 ), .row27(\字库_1_out_30 ), .row28(\字库_1_out_31 ),
    .row29(\字库_1_out_32 ), .row30(\字库_1_out_33 ), .row31(\字库_1_out_34 ));
  \字库  \u_字库_1  (
    .out_3(\字库_1_out_3 ), .out_4(\字库_1_out_4 ), .out_5(\字库_1_out_5 ), .out_6(\字库_1_out_6 ),
    .out_7(\字库_1_out_7 ), .out_8(\字库_1_out_8 ), .out_9(\字库_1_out_9 ), .out_10(\字库_1_out_10 ),
    .out_11(\字库_1_out_11 ), .out_12(\字库_1_out_12 ), .out_13(\字库_1_out_13 ), .out_14(\字库_1_out_14 ),
    .out_15(\字库_1_out_15 ), .out_16(\字库_1_out_16 ), .out_17(\字库_1_out_17 ), .out_18(\字库_1_out_18 ),
    .out_19(\字库_1_out_19 ), .out_20(\字库_1_out_20 ), .out_21(\字库_1_out_21 ), .out_22(\字库_1_out_22 ),
    .out_23(\字库_1_out_23 ), .out_24(\字库_1_out_24 ), .out_25(\字库_1_out_25 ), .out_26(\字库_1_out_26 ),
    .out_27(\字库_1_out_27 ), .out_28(\字库_1_out_28 ), .out_29(\字库_1_out_29 ), .out_30(\字库_1_out_30 ),
    .out_31(\字库_1_out_31 ), .out_32(\字库_1_out_32 ), .out_33(\字库_1_out_33 ), .out_34(\字库_1_out_34 ),
    .\区号 (\国标转区位码_1_区号 ), .\位号 (\国标转区位码_1_位号 ));
  ROM #(.dataWidth(16)) rom_1 (.addr(register_1_q), .data(\发送 ));  // open: sel
  \_16位流水接口  \u_16位流水接口_1  (
    .Din16(\发送 ), .\传输状态In_表明当前传输数据有效 (1'b1), .CLK(\时钟_out ), .Dout16(\n16位流水接口_1_dout16 ),
    .\传输状态Out_表明当前传输数据有效 (\n16位流水接口_1_传输状态out_表明当前传输数据有效 ), .\使能端_低电平有效_stall_高电平有效 (undriven));  // open: 同步清零_气泡_高电平有效
  \CRC编码  \crc编码_1  (.\原始数据 (\n16位流水接口_1_dout16 ), .\CRC校验码 (\crc编码_1_crc校验码 ));
  \_22位流水接口  \u_22位流水接口_1  (
    .Din22(\crc编码_1_crc校验码 ), .\传输状态In_表明当前传输数据有效 (\n16位流水接口_1_传输状态out_表明当前传输数据有效 ), .CLK(\时钟_out ),
    .Dout22(\n22位流水接口_1_dout22 ), .\传输状态Out_表明当前传输数据有效 (\n22位流水接口_1_传输状态out_表明当前传输数据有效 ));  // open: 同步清零_气泡_高电平有效, 使能端_低电平有效_stall_高电平有效
  \_22位随机干扰  \u_22位随机干扰_1  (
    .\加扰模式 (2'b11), .\_22位输入 (\n22位流水接口_1_dout22 ), .\加扰后数据 (\n22位随机干扰_1_加扰后数据 ), .\增加三位错 (\加噪 ));  // open: 随机加扰屏蔽字
  \字库  \u_字库_2  (
    .out_3(\字库_2_out_3 ), .out_4(\字库_2_out_4 ), .out_5(\字库_2_out_5 ), .out_6(\字库_2_out_6 ),
    .out_7(\字库_2_out_7 ), .out_8(\字库_2_out_8 ), .out_9(\字库_2_out_9 ), .out_10(\字库_2_out_10 ),
    .out_11(\字库_2_out_11 ), .out_12(\字库_2_out_12 ), .out_13(\字库_2_out_13 ), .out_14(\字库_2_out_14 ),
    .out_15(\字库_2_out_15 ), .out_16(\字库_2_out_16 ), .out_17(\字库_2_out_17 ), .out_18(\字库_2_out_18 ),
    .out_19(\字库_2_out_19 ), .out_20(\字库_2_out_20 ), .out_21(\字库_2_out_21 ), .out_22(\字库_2_out_22 ),
    .out_23(\字库_2_out_23 ), .out_24(\字库_2_out_24 ), .out_25(\字库_2_out_25 ), .out_26(\字库_2_out_26 ),
    .out_27(\字库_2_out_27 ), .out_28(\字库_2_out_28 ), .out_29(\字库_2_out_29 ), .out_30(\字库_2_out_30 ),
    .out_31(\字库_2_out_31 ), .out_32(\字库_2_out_32 ), .out_33(\字库_2_out_33 ), .out_34(\字库_2_out_34 ),
    .\区号 (\国标转区位码_2_区号 ), .\位号 (\国标转区位码_2_位号 ));
  \国标转区位码  \u_国标转区位码_2  (.\位号 (\国标转区位码_2_位号 ), .\区号 (\国标转区位码_2_区号 ), .GB2312(\接收 ));
  \_22位流水接口  \u_22位流水接口_2  (
    .Din22(\n22位随机干扰_1_加扰后数据 ), .\传输状态In_表明当前传输数据有效 (\n22位流水接口_1_传输状态out_表明当前传输数据有效 ), .CLK(\时钟_out ),
    .Dout22(\n22位流水接口_2_dout22 ), .\传输状态Out_表明当前传输数据有效 (\n22位流水接口_2_传输状态out_表明当前传输数据有效 ));  // open: 同步清零_气泡_高电平有效, 使能端_低电平有效_stall_高电平有效
  DotMatrix #(.inputtype("row"), .matrixcols(32), .matrixrows(32), .dotshape("circle")) dotmatrix_2 (
    .row0(\字库_2_out_3 ), .row1(\字库_2_out_4 ), .row2(\字库_2_out_5 ), .row3(\字库_2_out_6 ), .row4(\字库_2_out_7 ),
    .row5(\字库_2_out_8 ), .row6(\字库_2_out_9 ), .row7(\字库_2_out_10 ), .row8(\字库_2_out_11 ),
    .row9(\字库_2_out_12 ), .row10(\字库_2_out_13 ), .row11(\字库_2_out_14 ), .row12(\字库_2_out_15 ),
    .row13(\字库_2_out_16 ), .row14(\字库_2_out_17 ), .row15(\字库_2_out_18 ), .row16(\字库_2_out_19 ),
    .row17(\字库_2_out_20 ), .row18(\字库_2_out_21 ), .row19(\字库_2_out_22 ), .row20(\字库_2_out_23 ),
    .row21(\字库_2_out_24 ), .row22(\字库_2_out_25 ), .row23(\字库_2_out_26 ), .row24(\字库_2_out_27 ),
    .row25(\字库_2_out_28 ), .row26(\字库_2_out_29 ), .row27(\字库_2_out_30 ), .row28(\字库_2_out_31 ),
    .row29(\字库_2_out_32 ), .row30(\字库_2_out_33 ), .row31(\字库_2_out_34 ));
  LED \u_两位错  (.in(\crc解码_1__2位错 ));
  LED \u_一位错  (.in(\crc解码_1__1位错 ));
  LED \u_无错误  (.in(\crc解码_1_无错误 ));
  \CRC解码  \crc解码_1  (
    .\CRC编码 (\n22位流水接口_2_dout22 ), .\无错误 (\crc解码_1_无错误 ), .\_1位错 (\crc解码_1__1位错 ), .\_2位错 (\crc解码_1__2位错 ),
    .\纠错后数据 (\crc解码_1_纠错后数据 ));
  \_16位流水接口  \u_16位流水接口_2  (
    .Din16(\crc解码_1_纠错后数据 ), .\传输状态In_表明当前传输数据有效 (\n22位流水接口_2_传输状态out_表明当前传输数据有效 ), .CLK(\时钟_out ),
    .Dout16(\接收 ));  // open: 传输状态Out_表明当前传输数据有效, 同步清零_气泡_高电平有效, 使能端_低电平有效_stall_高电平有效
  // Probe on \接收 

  // Notes on the sheet:
  //   CRC编码流水传输电路
  //   寄存器
  //   发送方
  //   汉字显示
  //   加法器
  //   GB2312
  //   1.取数阶段
  //   contents of rom_1 (hex, n*v repeats v):
  //   bbaa d6d0 bfc6 bcbc b4f3 d1a7 cac7 b9fa bcd2 bdcc d3fd b2bf d6b1 caf4 b5c4 c8ab b9fa d6d8 b5e3 b4f3
  //   d1a7 a3ac d3c9 d4ad bbaa d6d0 c0ed b9a4 b4f3 d1a7 a1a2 cdac bcc3 d2bd bfc6 b4f3 d1a7 a1a2 cee4 baba
  //   b3c7 cad0 bda8 c9e8 d1a7 d4ba d3da a3b2 a3b0 a3b0 a3b0 c4ea a3b5 d4c2 a3b2 a3b6 c8d5 bacf b2a2 b3c9
  //   c1a2 a3ac cac7 cad7 c5fa c1d0 c8eb b9fa bcd2 a1b0 a3b2 a3b1 a3b1 b9a4 b3cc a1b1 d6d8 b5e3 bda8 c9e8
  //   bacd b9fa bcd2 a1b0 a3b9 a3b8 a3b5 b9a4 b3cc a1b1 bda8 c9e8 b8df d0a3 d6ae d2bb a1a3 d1a7 d0a3 d0a3
  //   d4b0 d5bc b5d8 c6df c7a7 d3e0 c4b6 a3ac d4b0 c4da caf7 c4be b4d0 dcd7 a3ac b1cc b2dd c8e7 d2f0 a3ac
  //   bbb7 beb3 d3c5 d1c5 a3ac beb0 c9ab d0e3 c0f6 a3ac c2cc bbaf b8b2 b8c7 c2ca 3732 25a3 acb1 bbd3 fece
  //   aaa1 b0c9 adc1 d6ca bdb4 f3d1 a7a1 b1a1
  //   ~使能/Stall
  //   发送方在ROM预存了一段中文文字，通过计数器驱动电路每个时钟传输一个汉字
  //   同步清零信号，气泡
  //   用户实现了国标转区位码电路后，可在中间窗口观察发送方和接收方汉字显示是否一致以观察海明检错纠错性能
  //   数据状态：高电平有效
  //   2.编码阶段
  //   电路功能：采用流水分段方式进行数据编码传输，测试海明编码检错纠错能力，当出现2位错时，发送重传信号要求发送方重传，保证接收方按ROM中的地址顺序接受所有汉字
  //   接收方
  //   汉字显示
  //   3.传输阶段
  //   此电路可帮助学生理解指令流水线工作原理，重传类似指令流水线中的分支指令
  //   4.解码阶段
  //   5.显示阶段
  //   请将时钟频率调到8Hz
  //   Ctrl+ K启动电路自动仿真
endmodule

// 随机干扰
module \_22位随机干扰  (
  input  [21:0] \_22位输入 ,
  input  [1:0] \加扰模式 ,
  input  \增加三位错 ,
  output [21:0] \随机加扰屏蔽字 ,
  output [21:0] \加扰后数据 
);

  wire clock_1_out, comparator_1_eq, not_1_out, \随机信号_5_out ;
  wire [1:0] \随机信号_4_out ;
  wire [3:0] \随机信号_2_out , \随机信号_3_out , \随机信号_out ;
  wire [15:0] \_1位加扰A ;
  wire [21:0] \_1位加扰 , \_2位加扰 , \_3位加扰 , multiplexer_1_out, multiplexer_4_out, \随机加扰 ;
  wire [21:6] \_1位加扰B , \_1位加扰C ;

  Clock clock_1 (.out(clock_1_out));
  Random #(.width(4)) \u_随机信号  (.clk(clock_1_out), .out(\随机信号_out ));  // open: next, clr
  Decoder #(.select(4), .enable("false")) decoder_1 (
    .out0(\_1位加扰A [0]), .out1(\_1位加扰A [1]), .out2(\_1位加扰A [2]), .out3(\_1位加扰A [3]), .out4(\_1位加扰A [4]),
    .out5(\_1位加扰A [5]), .out6(\_1位加扰A [6]), .out7(\_1位加扰A [7]), .out8(\_1位加扰A [8]), .out9(\_1位加扰A [9]),
    .out10(\_1位加扰A [10]), .out11(\_1位加扰A [11]), .out12(\_1位加扰A [12]), .out13(\_1位加扰A [13]),
    .out14(\_1位加扰A [14]), .out15(\_1位加扰A [15]), .sel(\随机信号_out ));
  Random #(.width(4), .seed(18)) \u_随机信号_2  (.clk(clock_1_out), .out(\随机信号_2_out ));  // open: next, clr
  Decoder #(.select(4), .enable("false")) decoder_2 (
    .out0(\_1位加扰B [6]), .out1(\_1位加扰B [7]), .out2(\_1位加扰B [8]), .out3(\_1位加扰B [9]), .out4(\_1位加扰B [10]),
    .out5(\_1位加扰B [11]), .out6(\_1位加扰B [12]), .out7(\_1位加扰B [13]), .out8(\_1位加扰B [14]), .out9(\_1位加扰B [15]),
    .out10(\_1位加扰B [16]), .out11(\_1位加扰B [17]), .out12(\_1位加扰B [18]), .out13(\_1位加扰B [19]),
    .out14(\_1位加扰B [20]), .out15(\_1位加扰B [21]), .sel(\随机信号_2_out ));
  Random #(.width(4), .seed(3)) \u_随机信号_3  (.clk(clock_1_out), .out(\随机信号_3_out ));  // open: next, clr
  Random #(.width(2), .seed(21)) \u_随机信号_4  (.clk(clock_1_out), .out(\随机信号_4_out ));  // open: next, clr
  Random #(.width(1), .seed(31)) \u_随机信号_5  (.clk(clock_1_out), .out(\随机信号_5_out ));  // open: next, clr
  Decoder #(.select(4), .enable("false")) decoder_3 (
    .out0(\_1位加扰C [6]), .out1(\_1位加扰C [7]), .out2(\_1位加扰C [8]), .out3(\_1位加扰C [9]), .out4(\_1位加扰C [10]),
    .out5(\_1位加扰C [11]), .out6(\_1位加扰C [12]), .out7(\_1位加扰C [13]), .out8(\_1位加扰C [14]), .out9(\_1位加扰C [15]),
    .out10(\_1位加扰C [16]), .out11(\_1位加扰C [17]), .out12(\_1位加扰C [18]), .out13(\_1位加扰C [19]),
    .out14(\_1位加扰C [20]), .out15(\_1位加扰C [21]), .sel(\随机信号_3_out ));
  Pull_Resistor pull_resistor_1 (.node(\增加三位错 ));
  Multiplexer #(.width(22), .enable("false")) multiplexer_1 (
    .in0({\_1位加扰B , {6{1'b0}}}), .in1(\_3位加扰 ), .out(multiplexer_1_out), .sel(\增加三位错 ));
  Multiplexer #(.select(2), .width(22), .enable("false")) multiplexer_2 (
    .in0({22{1'b0}}), .in1({{6{1'b0}}, \_1位加扰A }), .in2(\_2位加扰 ), .in3(multiplexer_1_out), .out(\随机加扰 ),
    .sel(\随机信号_4_out ));
  Pull_Resistor #(.pull(1)) pull_resistor_2 (.node(\加扰模式 ));
  Comparator #(.width(22), .mode("unsigned")) comparator_1 (
    .a({{6{1'b0}}, \_1位加扰A }), .b({\_1位加扰B , {6{1'b0}}}), .eq(comparator_1_eq));  // open: gt, lt
  Multiplexer #(.select(2), .width(22), .enable("false")) multiplexer_3 (
    .in0({22{1'b0}}), .in1(\_1位加扰 ), .in2(\_2位加扰 ), .in3(\随机加扰 ), .out(\随机加扰屏蔽字 ), .sel(\加扰模式 ));
  Multiplexer #(.width(22), .enable("false")) multiplexer_4 (
    .in0(22'h1), .in1({{6{1'b0}}, \_1位加扰A }), .out(multiplexer_4_out), .sel(not_1_out));
  not not_1 (not_1_out, comparator_1_eq);
  assign \_2位加扰  = multiplexer_4_out ^ {\_1位加扰B , {6{1'b0}}};  // XOR_Gate xor_1, 22 bits wide
  assign \_3位加扰  = \_2位加扰  ^ {\_1位加扰C , {6{1'b0}}};  // XOR_Gate xor_2, 22 bits wide
  Multiplexer #(.width(22), .enable("false")) multiplexer_5 (
    .in0(multiplexer_4_out), .in1({\_1位加扰B , {6{1'b0}}}), .out(\_1位加扰 ), .sel(\随机信号_5_out ));
  assign \加扰后数据  = \随机加扰屏蔽字  ^ \_22位输入 ;  // XOR_Gate xor_3, 22 bits wide

  // Notes on the sheet:
  //   在随机加扰模式中增加三位错
  //   两个随机信号分别负责高16位和第16位
  //   22位信道加扰屏蔽字生成电路，加扰模式引脚00：不加扰  01:1位加扰 10:2位加扰 11：0-2位随机加扰
  //   如果两个信号相同，换一个信号
endmodule

// 随机加扰
module \_17位随机干扰  (
  input  [16:0] \_17位输入 ,
  output [16:0] \随机加扰屏蔽字 ,
  output [16:0] \加扰后数据 
);

  wire clock_1_out;
  wire [4:0] \随机数_2_out , \随机数_3_out , \随机数_out ;
  wire [16:0] or_1_out;
  wire [31:0] decoder_1_out31, decoder_2_out31, decoder_3_out31;

  Clock clock_1 (.out(clock_1_out));
  Random #(.width(5)) \u_随机数  (.clk(clock_1_out), .out(\随机数_out ));  // open: next, clr
  Decoder #(.select(5), .enable("false")) decoder_1 (
    .out0(decoder_1_out31[31]), .out1(decoder_1_out31[30]), .out2(decoder_1_out31[29]),
    .out3(decoder_1_out31[28]), .out4(decoder_1_out31[27]), .out5(decoder_1_out31[26]),
    .out6(decoder_1_out31[25]), .out7(decoder_1_out31[24]), .out8(decoder_1_out31[23]),
    .out9(decoder_1_out31[22]), .out10(decoder_1_out31[21]), .out11(decoder_1_out31[20]),
    .out12(decoder_1_out31[19]), .out13(decoder_1_out31[18]), .out14(decoder_1_out31[17]),
    .out15(decoder_1_out31[16]), .out16(decoder_1_out31[15]), .out17(decoder_1_out31[14]),
    .out18(decoder_1_out31[13]), .out19(decoder_1_out31[12]), .out20(decoder_1_out31[11]),
    .out21(decoder_1_out31[10]), .out22(decoder_1_out31[9]), .out23(decoder_1_out31[8]),
    .out24(decoder_1_out31[7]), .out25(decoder_1_out31[6]), .out26(decoder_1_out31[5]),
    .out27(decoder_1_out31[4]), .out28(decoder_1_out31[3]), .out29(decoder_1_out31[2]),
    .out30(decoder_1_out31[1]), .out31(decoder_1_out31[0]), .sel(\随机数_out ));
  Decoder #(.select(5), .enable("false")) decoder_2 (
    .out0(decoder_2_out31[31]), .out1(decoder_2_out31[30]), .out2(decoder_2_out31[29]),
    .out3(decoder_2_out31[28]), .out4(decoder_2_out31[27]), .out5(decoder_2_out31[26]),
    .out6(decoder_2_out31[25]), .out7(decoder_2_out31[24]), .out8(decoder_2_out31[23]),
    .out9(decoder_2_out31[22]), .out10(decoder_2_out31[21]), .out11(decoder_2_out31[20]),
    .out12(decoder_2_out31[19]), .out13(decoder_2_out31[18]), .out14(decoder_2_out31[17]),
    .out15(decoder_2_out31[16]), .out16(decoder_2_out31[15]), .out17(decoder_2_out31[14]),
    .out18(decoder_2_out31[13]), .out19(decoder_2_out31[12]), .out20(decoder_2_out31[11]),
    .out21(decoder_2_out31[10]), .out22(decoder_2_out31[9]), .out23(decoder_2_out31[8]),
    .out24(decoder_2_out31[7]), .out25(decoder_2_out31[6]), .out26(decoder_2_out31[5]),
    .out27(decoder_2_out31[4]), .out28(decoder_2_out31[3]), .out29(decoder_2_out31[2]),
    .out30(decoder_2_out31[1]), .out31(decoder_2_out31[0]), .sel(\随机数_2_out ));
  Random #(.width(5), .seed(18)) \u_随机数_2  (.clk(clock_1_out), .out(\随机数_2_out ));  // open: next, clr
  Random #(.width(5), .seed(3)) \u_随机数_3  (.clk(clock_1_out), .out(\随机数_3_out ));  // open: next, clr
  Decoder #(.select(5), .enable("false")) decoder_3 (
    .out0(decoder_3_out31[31]), .out1(decoder_3_out31[30]), .out2(decoder_3_out31[29]),
    .out3(decoder_3_out31[28]), .out4(decoder_3_out31[27]), .out5(decoder_3_out31[26]),
    .out6(decoder_3_out31[25]), .out7(decoder_3_out31[24]), .out8(decoder_3_out31[23]),
    .out9(decoder_3_out31[22]), .out10(decoder_3_out31[21]), .out11(decoder_3_out31[20]),
    .out12(decoder_3_out31[19]), .out13(decoder_3_out31[18]), .out14(decoder_3_out31[17]),
    .out15(decoder_3_out31[16]), .out16(decoder_3_out31[15]), .out17(decoder_3_out31[14]),
    .out18(decoder_3_out31[13]), .out19(decoder_3_out31[12]), .out20(decoder_3_out31[11]),
    .out21(decoder_3_out31[10]), .out22(decoder_3_out31[9]), .out23(decoder_3_out31[8]),
    .out24(decoder_3_out31[7]), .out25(decoder_3_out31[6]), .out26(decoder_3_out31[5]),
    .out27(decoder_3_out31[4]), .out28(decoder_3_out31[3]), .out29(decoder_3_out31[2]),
    .out30(decoder_3_out31[1]), .out31(decoder_3_out31[0]), .sel(\随机数_3_out ));
  assign or_1_out = decoder_1_out31[16:0] | decoder_2_out31[16:0];  // OR_Gate or_1, 17 bits wide
  assign \随机加扰屏蔽字  = or_1_out | decoder_3_out31[16:0];  // OR_Gate or_2, 17 bits wide
  assign \加扰后数据  = \随机加扰屏蔽字  ^ \_17位输入 ;  // XOR_Gate xor_1, 17 bits wide
endmodule
// 字库
module \字库  (
  input  [6:0] \区号 ,
  input  [6:0] \位号 ,
  output [31:0] out_3,
  output [31:0] out_4,
  output [31:0] out_5,
  output [31:0] out_6,
  output [31:0] out_7,
  output [31:0] out_8,
  output [31:0] out_9,
  output [31:0] out_10,
  output [31:0] out_11,
  output [31:0] out_12,
  output [31:0] out_13,
  output [31:0] out_14,
  output [31:0] out_15,
  output [31:0] out_16,
  output [31:0] out_17,
  output [31:0] out_18,
  output [31:0] out_19,
  output [31:0] out_20,
  output [31:0] out_21,
  output [31:0] out_22,
  output [31:0] out_23,
  output [31:0] out_24,
  output [31:0] out_25,
  output [31:0] out_26,
  output [31:0] out_27,
  output [31:0] out_28,
  output [31:0] out_29,
  output [31:0] out_30,
  output [31:0] out_31,
  output [31:0] out_32,
  output [31:0] out_33,
  output [31:0] out_34
);

  wire [6:0] multiplier_1_cout, multiplier_1_out, subtractor_1_out;
  wire [13:0] adder_1_out, bit_extender_1_out, subtractor_2_out;

  ROM #(.addrWidth(14), .dataWidth(32)) rom_1 (.addr(subtractor_2_out), .data(out_3));  // open: sel
  ROM #(.addrWidth(14), .dataWidth(32)) rom_2 (.addr(subtractor_2_out), .data(out_4));  // open: sel
  ROM #(.addrWidth(14), .dataWidth(32)) rom_3 (.addr(subtractor_2_out), .data(out_5));  // open: sel
  ROM #(.addrWidth(14), .dataWidth(32)) rom_4 (.addr(subtractor_2_out), .data(out_6));  // open: sel
  ROM #(.addrWidth(14), .dataWidth(32)) rom_5 (.addr(subtractor_2_out), .data(out_7));  // open: sel
  ROM #(.addrWidth(14), .dataWidth(32)) rom_6 (.addr(subtractor_2_out), .data(out_8));  // open: sel
  ROM #(.addrWidth(14), .dataWidth(32)) rom_7 (.addr(subtractor_2_out), .data(out_9));  // open: sel
  ROM #(.addrWidth(14), .dataWidth(32)) rom_8 (.addr(subtractor_2_out), .data(out_10));  // open: sel
  Subtractor #(.width(7)) subtractor_1 (.a(\区号 ), .b(7'b0000001), .out(subtractor_1_out));  // open: bin, bout
  Multiplier #(.width(7)) multiplier_1 (
    .a(subtractor_1_out), .b(7'b1011110), .out(multiplier_1_out), .cout(multiplier_1_cout));  // open: cin
  ROM #(.addrWidth(14), .dataWidth(32)) rom_9 (.addr(subtractor_2_out), .data(out_11));  // open: sel
  ROM #(.addrWidth(14), .dataWidth(32)) rom_10 (.addr(subtractor_2_out), .data(out_12));  // open: sel
  ROM #(.addrWidth(14), .dataWidth(32)) rom_11 (.addr(subtractor_2_out), .data(out_13));  // open: sel
  ROM #(.addrWidth(14), .dataWidth(32)) rom_12 (.addr(subtractor_2_out), .data(out_14));  // open: sel
  ROM #(.addrWidth(14), .dataWidth(32)) rom_13 (.addr(subtractor_2_out), .data(out_15));  // open: sel
  ROM #(.addrWidth(14), .dataWidth(32)) rom_14 (.addr(subtractor_2_out), .data(out_16));  // open: sel
  ROM #(.addrWidth(14), .dataWidth(32)) rom_15 (.addr(subtractor_2_out), .data(out_17));  // open: sel
  ROM #(.addrWidth(14), .dataWidth(32)) rom_16 (.addr(subtractor_2_out), .data(out_18));  // open: sel
  assign bit_extender_1_out = {{7{1'b0}}, \位号 };  // Bit_Extender bit_extender_1
  Adder #(.width(14)) adder_1 (
    .a({multiplier_1_cout, multiplier_1_out}), .b(bit_extender_1_out), .out(adder_1_out));  // open: cin, cout
  ROM #(.addrWidth(14), .dataWidth(32)) rom_17 (.addr(subtractor_2_out), .data(out_19));  // open: sel
  ROM #(.addrWidth(14), .dataWidth(32)) rom_18 (.addr(subtractor_2_out), .data(out_20));  // open: sel
  ROM #(.addrWidth(14), .dataWidth(32)) rom_19 (.addr(subtractor_2_out), .data(out_21));  // open: sel
  ROM #(.addrWidth(14), .dataWidth(32)) rom_20 (.addr(subtractor_2_out), .data(out_22));  // open: sel
  ROM #(.addrWidth(14), .dataWidth(32)) rom_21 (.addr(subtractor_2_out), .data(out_23));  // open: sel
  ROM #(.addrWidth(14), .dataWidth(32)) rom_22 (.addr(subtractor_2_out), .data(out_24));  // open: sel
  ROM #(.addrWidth(14), .dataWidth(32)) rom_23 (.addr(subtractor_2_out), .data(out_25));  // open: sel
  ROM #(.addrWidth(14), .dataWidth(32)) rom_24 (.addr(subtractor_2_out), .data(out_26));  // open: sel
  Subtractor #(.width(14)) subtractor_2 (.a(adder_1_out), .b(14'h1), .out(subtractor_2_out));  // open: bin, bout
  ROM #(.addrWidth(14), .dataWidth(32)) rom_25 (.addr(subtractor_2_out), .data(out_27));  // open: sel
  ROM #(.addrWidth(14), .dataWidth(32)) rom_26 (.addr(subtractor_2_out), .data(out_28));  // open: sel
  ROM #(.addrWidth(14), .dataWidth(32)) rom_27 (.addr(subtractor_2_out), .data(out_29));  // open: sel
  ROM #(.addrWidth(14), .dataWidth(32)) rom_28 (.addr(subtractor_2_out), .data(out_30));  // open: sel
  ROM #(.addrWidth(14), .dataWidth(32)) rom_29 (.addr(subtractor_2_out), .data(out_31));  // open: sel
  ROM #(.addrWidth(14), .dataWidth(32)) rom_30 (.addr(subtractor_2_out), .data(out_32));  // open: sel
  ROM #(.addrWidth(14), .dataWidth(32)) rom_31 (.addr(subtractor_2_out), .data(out_33));  // open: sel
  ROM #(.addrWidth(14), .dataWidth(32)) rom_32 (.addr(subtractor_2_out), .data(out_34));  // open: sel
  DotMatrix #(.inputtype("row"), .matrixcols(32), .matrixrows(32), .dotshape("circle")) dotmatrix_1 (
    .row0(out_3), .row1(out_4), .row2(out_5), .row3(out_6), .row4(out_7), .row5(out_8), .row6(out_9),
    .row7(out_10), .row8(out_11), .row9(out_12), .row10(out_13), .row11(out_14), .row12(out_15),
    .row13(out_16), .row14(out_17), .row15(out_18), .row16(out_19), .row17(out_20), .row18(out_21),
    .row19(out_22), .row20(out_23), .row21(out_24), .row22(out_25), .row23(out_26), .row24(out_27),
    .row25(out_28), .row26(out_29), .row27(out_30), .row28(out_31), .row29(out_32), .row30(out_33),
    .row31(out_34));

  // Other names for the same wires on the sheet: D0[31:0] = out_3; D1[31:0] = out_4; D2[31:0] = out_5;
  //   D3[31:0] = out_6; D4[31:0] = out_7; D5[31:0] = out_8; D6[31:0] = out_9; D7[31:0] = out_10; D8[31:0] = out_11;
  //   D9[31:0] = out_12; D10[31:0] = out_13; D11[31:0] = out_14; D12[31:0] = out_15; D13[31:0] = out_16;
  //   D14[31:0] = out_17; D15[31:0] = out_18; D16[31:0] = out_19; D17[31:0] = out_20; D18[31:0] = out_21;
  //   D19[31:0] = out_22; D20[31:0] = out_23; D21[31:0] = out_24; D22[31:0] = out_25; D23[31:0] = out_26;
  //   D24[31:0] = out_27; D25[31:0] = out_28; D26[31:0] = out_29; D27[31:0] = out_30; D28[31:0] = out_31;
  //   D29[31:0] = out_32; D30[31:0] = out_33; D31[31:0] = out_34

  // Notes on the sheet:
  //   contents of rom_1 (hex, n*v repeats v):
  //   281*0 ffffffff 272*0 60000000 202*0 18000 3c000 0 0 18000 3c000 0 0 18000 3c000 8*0 18000 18000
  //   3c000 3c000 18000 18000 3c000 3c000 18000 18000 3c000 18000 3c000 3c000 18000 3c000 18000 18000
  //   3c000 18000 3c000 3c000 18000 3c000 8*0 4*18000 4*3c000 4*18000 3c000 18000 3c000 3c000 3c000 18000
  //   18000 3c000 18000 3c000 3c000 3c000
  //   contents of rom_2 (hex, n*v repeats v):
  //   150*0 1c000 9*18000 121*0 ffffffff 269*0 10000 0 60000000 60000000 202*0 3c000 3c000 0 0 3c000 3c000
  //   0 0 3c000 3c000 8*0 24*3c000 8*0 24*3c000 587*0 8000 11*0 2000 124*0 8000 28*0 8000 291*0 400000
  //   742*0 1000 189*0 80 822*0 10000 654*0 40000 50*0 20000 64*0 4000 252*0 20000 56*0 40000 51*0 2000
  //   74*0 1000000 18*0 8000 74*0 2000 8*0 800000 400*0 40000 676*0 20 393*0 20000 31*0 2000 547*0 100
  //   58*0 800000 200 1000000 200200 387*0 1000000 5*0 800000 26*0 800000 22*0 8000 22*0 10000 0 8000 10*0
  //   10000 241*0 800000 0 0 1000000 7*0 1000000 1000000 10*0 1000000 9*0 20000 41*0 1000 301*0 20000 18*0
  //   800000 800000
  //   contents of rom_3 (hex, n*v repeats v):
  //   150*0 1ffc00 9*3ffc00 59*0 ff000 26*0 7ff0 0 ffe0000 30*0 10000 109*0 1c0000 144*0 60000006 0
  //   60000006 13*0 40000002 38000 0 60000000 e0000000 15*0 181800 0 0 0 e6000 182*0 3c000 3c000 0 0 3c000
  //   3c000 0 0 3c000 3c000 8*0 24*3c000 8*0 24*3c000 581*0 1800 1801800 8100 3000 60000 c00 c000 383800
  //   7000020 181800 0 e0 0 c200c00 1800000 30000 c06000 1003000 3000 1c000 1000 70000 2000 0 18000 0
  //   600c00 e00800 e00000 3000020 1040300 60000 6007000 6000 181800 3000018 1800000 0 0 3801800 0 8000 0
  //   3006000 2000 6100000 1800000 1800000 3000000 80 0 100800 20000 1800c00 0 3000000 800000 1800 80000
  //   301800 0 8000 30000 1800020 c00000 8 3800040 e00020 1000400 1801800 603000 c000100 30000 60000 1c00
  //   700000 300000 3818000 3803800 1800 18000 3803800 1800 1000c00 6003800 c06000 3000 181000 4000 200000
  //   30000 10 181c00 80 e00000 0 300c000 60000 3006000 1000000 100 181800 3001800 6040020 c00000 1c00
  //   1c3800 60000 102000 c3000 182000 0 2000000 602000 0 180000 c0000 2002000 6000c00 30000 380c00 18000
  //   1003000 1c000 0 8 0 c00 40180 0 70000 4000 0 1801000 1001c00 600 383000 381800 600c000 6004000
  //   c00c000 c0 18000 e000 1800000 400600 600c00 0 1800 c00 c00 200 400 c606000 3000 3000 30 18000 800000
  //   70000 40000 600c200 6000300 4018200 3000 3800000 300000 0 30000 c00800 400800 20 e000 180c000 200
  //   70000 3000 30000 3001000 0 2000 3000000 0 380 60000c0 2000000 c000 400400 c00 101000 10000c0 1001800
  //   3001800 1c00 4003300 e00e00 3801b80 3000c00 1800c00 c03000 30000 c00600 c00 1900 30100 0 0 3001000
  //   60000 3000 1000800 1c00 0 30000 1c000 3803000 c00000 2000000 3003000 1c00 603800 1c001c0 3000 1c0 20
  //   0 1e0 1c000 183000 1c1c00 300000 20000 c0 3000 6020000 6006000 1000c00 301800 800800 18000 6000
  //   183000 2000000 3000300 3806300 c3000 181800 0 c01800 1800000 0 0 0 c0 3000000 0 101800 301c00 1c000
  //   1800 1018300 38000 6000 800400 2000 3000020 202000 100180 380c000 3803000 30080c0 2004000 8000 1800
  //   3001800 30000 6000000 c00000 100 0 3000000 18000 18200 800000 1803000 0 0 600700 1800000 0 400000
  //   c00000 1800800 2000600 600000 30000 40000 60c080 1c00 3000800 60000 1000800 2020080 1380030 1040000
  //   40100 2010000 0 0 18000 1000080 6001800 0 3000 c00c00 2000180 3000c00 3000 600 3000000 8000 0 380
  //   100000 400000 0 c00 0 0 c00 100000 6000 c000 3001800 0 8000000 0 0 c00 300 1c000 403000 0 1c000
  //   3000000 180 3800000 60000 1800 18000 1c000 70000 3000800 10 1c00 c00 100000 1c00 1c00c00 0 800000 0
  //   0 60000 3000000 10000 7000000 10 c180 180 3000400 8000400 1800 600e00 400 800 18000 3006000 1800200
  //   0 3800c00 0 30000 3006000 601000 c00000 1800 18000 c000 38000 2003000 18000 0 400000 6000 1002000
  //   3000000 2000040 100 70000 3807000 800 0 6000 1800 70000 600 1800 c000 101000 c0 3200 1800 200c00
  //   18000 0 3800 300010 0 c000 80 181800 30000 200000 401000 201800 4000 1c00000 30c0 1c00800 c00000
  //   1800 1801800 30000 1000800 18000 c01c00 6000 c000 1803000 6000 60 1c001c0 70000 1800 8080 2000000
  //   1000080 300c300 3001000 200e100 1008100 4003000 1801800 6000 800000 38000 0 0 806000 300c00 418400
  //   c00 600000 e1ee00 408000 c03800 3000 30000 1800 1000000 800100 600c00 60000 3810180 0 0 1800000 0
  //   2020180 0 0 10180 20 10000 1000800 18000 181800 3801800 0 3003000 30 1800000 e0000 3000c00 100 10
  //   100010 2001800 8060180 c000 1001800 400000 c01800 0 1000000 0 1800c00 0 4100 0 2000000 c00000 e000
  //   1000 1800 800800 1000 8000 20020 3003000 1000000 30000 1800 381c00 1801800 30000 400c00 20100 3000
  //   e00000 1001000 1000 6600 38000 c6000 1800800 c03000 30000 400000 600000 18000 6001800 300c00 6000 0
  //   0 0 100 0 0 3001800 0 1000 0 c00 181800 1880 3001840 1000 3180 200 0 0 0 2000000 8 200 3001800 20000
  //   0 100 30000 80000 183800 300c700 800 3801000 1800000 6000000 2000 8000000 10000 1800100 1000 1c00 0
  //   0 c000 600000 600000 38000 1801c00 800 3000 3000 3000 1800 1800000 3001800 800 18000 2000 1800800
  //   c00 3000000 6002000 40000 300000 1000000 2000c00 400c00 1000 0 20300c0 1000 8080 c00e00 1800008 0
  //   3000c00 180 c0 3000000 1000 18000 30000 2000000 e00000 0 0 c00 0 3007000 3000 600 200 200600 1800c00
  //   1800008 8600 3000700 0 0 1000000 0 0 6000200 4*0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
  //   contents of rom_4 (hex, n*v repeats v):
  //   11*0 c3000 5*0 40 2000000 10 8000000 80 0 1ff0 100000 1ff0 f80000 1fff0 fff8000 1ffe0 7ff0000 18*0
  //   800 3800 13*0 10000 18000 0 c00000 c20000 0 18000 0 0 0 400 3e000 0 10000 10000 13*0 18000 57*0
  //   10*f00f00 34*0 c00000 24*0 3ffe00 26*0 7ff0 1800000 ffe0000 0 0 300 26*0 1c0 18000 3c00000 49*0 1c0
  //   57*0 80000 1e0380 0 0 0 180 11*0 70 11*0 20000 0 0 18000 0 0 80 0 0 0 3c0 0 0 1e0 5*0 c0 18*0 6000 0
  //   0 0 e0000 74*0 3800001c 0 7000000e 13*0 60000006 38000 0 60000000 e0000000 15*0 1c1c00 0 0 0 e7000
  //   104*0 200000 18180000 6000000 13*0 60000 0 0 300000 0 0 6000 6*0 30000 3000 0 0 0 20000 0 300 0
  //   38000 3000 0 0 30000 0 0 2000000 60000 31*0 3c000 3c000 0 0 3c000 3c000 0 0 3c000 3c000 8*0 24*3c000
  //   8*0 24*3c000 579*0 218008 30600008 3801c00 1c01c00 e380 3800 38000 1800e00 6000 383010 78001f0
  //   1c1c00 18030 1ff0 2301c0 e380600 3c00000 18000 e07000 3c01800 1800 301e000 1800 38000 8103000
  //   3ffff80 1c000 0 700e00 e00e00 e00000 18000f0 1ce0700 70000 7007000 800e000 1c1c00 380001c 1c00700
  //   600 0 3803c00 2000 e000 0 3807200 3800 7180000 1c00000 1c00000 3800000 3ffffc0 6000060 380f00 38000
  //   1c00e00 10 3840010 1e00000 83c00 3c0000 f83800 60000 e000 3038000 1c000e0 c04080 41fffc 38001e0
  //   e00070 1c00600 1c01c00 703800 6000180 38000 70000 1801c00 601008 300010 3818000 3801c00 8200c00
  //   3018000 3803800 e00 1c00e00 7001c00 e03800 8003800 1c3800 7000 780000 18000 1001c 1c1c00 3ffffc0
  //   e40040 e40080 780f000 38000 380f000 1c30060 1ffff80 3c3800 3801c00 70ffff0 e00000 1c00 1c3800 70000
  //   3c3800 c3810 1c3800 800080 3800000 f03000 180000 1c0000 1e0200 3803800 3000c00 38000 380e00 1c000
  //   3c03800 381c060 1800008 18 18 10230c30 c0301c0 8000030 60200 6007000 c018808 1c01c00 1801c00 600
  //   383800 381c00 700e000 700e000 e00e000 fe0 c000 7000 1c00000 700700 8710e00 c0000 e00 e00 8040600
  //   8000380 10270700 e706000 6003800 1801c00 800f0 1c000 e00008 38000 70000 300e380 3000380 701c380
  //   c003800 3800000 380000 8 38000 8e60c00 8720c00 4010038 7000 1c0e000 4000380 18060008 c001800 18000
  //   3801c00 700 10003800 3800000 10 1f80 70180e0 3800000 e000 300e00 c00 1c1c00 18007e0 1c01c00 7801c00
  //   c001c00 70039c0 e00e00 3801dc0 3800e00 1c01e00 f03c00 30000 e00700 8000e00 c201cc0 18030180 4001c00
  //   180070 3801d00 70000 3b00 1801c00 3801c00 18 38000 1c000 3803800 600000 7807000 3801800 301c00
  //   703c00 1e001e0 3800 100c01c0 1f0 f0 7ff0 fe030 183800 181c00 380000 70000 7ffffe0 3800 7070008
  //   7007000 1c00e00 381c00 e01e00 3c000 c007000 1c3000 7020100 3000380 3007380 c3800 1c1c00 4000008
  //   e01c00 1c00018 2040040 c202038 6000060 c0e0 38000e0 80 381c00 381c00 1c000 1c00 381c380 1c000 c2000
  //   600f00 8003800 38000e0 303800 3801c0 380e000 3807000 38060e0 700e000 601c000 1000c00 3800e00 38000
  //   3000000 e00018 ffff80 180000 3800180 1c100 c18300 e00300 1e03800 c1000c0 18 700700 1c00040 20020
  //   700000 e00000 1c00e00 3800700 700000 30400 18060000 70e1c0 1e00 3800e00 f0000 1c00e00 30301c0
  //   1b80038 3870000 8060180 3018000 4000030 20 1c000 1ffffc0 7001c00 c000000 10203800 e00e00 18001c0
  //   3800e00 383800 3800680 3004840 e600 1800100 7fc0 790010 e00020 c004840 6000ec0 300 c0600c0 e00
  //   380000 7000 e000 3801c00 6061000 e003800 4000000 1c00 e00 380 1c000 603800 0 1c000 3800000 7c0
  //   3c00000 30000 1c00 1c000 301c060 38000 3800e00 301c 1e00 18180e00 7a0008 381e00 1c01e00 71c000
  //   1e00008 6180 0 70000 1c00000 1c000 7000000 6000038 e180 60001c0 7806700 c000700 10203800 700e00 700
  //   1c01c00 38030 3803800 1c00380 c00c00 3c00e00 1c00070 1c000 3806000 701c00 e06040 1c00 18000 e000
  //   1c000 3801800 1c000 1800000 f00018 7800 1c07800 38000e0 38001e0 1f80 78000 3007800 e00 30 8007000
  //   3801c00 70040 c0c700 3801c00 6000 1c1c00 80e0 3303b00 180c00 380e00 c01c000 c000010 383c00 300038
  //   10118030 1800f000 880e0 1c1c00 38000 380000 701c00 701c00 f000 1c00000 38c0 1c01c00 e00040 10300c00
  //   1c03c00 18000 3800e00 301c040 1ec1c00 7000 e000 1c01800 3000 ffe7ff0 1e001c0 78000 1c00 c1c0 383ffe0
  //   38081c0 380e380 3801c00 380e380 381c380 6003800 1c01c00 7000 1c00000 38000 1ffff80 10 e07000 380e80
  //   71c700 e00 706000 f0c780 e0ee00 1e03800 c003800 78000 41c00 1c00000 ffff00 300e00 3070000 381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
  //   contents of rom_5 (hex, n*v repeats v):
  //   8*0 40000 0 0 c3000 0 20 3c00000 1820 3c70000 e0 6000000 30 18000000 198 19800000 1800 100000 1830
  //   d80000 1ffe0 7ff8000 1ffc0 7ff0000 18000 0 0 0 18000 12*0 7e000 3c00 7c00 6*0 30000 c000 10 4000000
  //   0 0 0 18000 ff000 800000 1c00000 1c70000 2000000 18000 18000018 0 c000 7000c00 ff800 0 18000 18000
  //   3c000 7e000 7e000 18000 18000 0 0 18000 18000 0 0 0 18000 18000 3ffffff8 18000 301c00 4008060
  //   3000000 0 180 820 8000 2000000 7*0 4000 1c000 c000 0 c0e00 0 0 8000 0 1000 0 1000 0 0 10300 0 1ff00
  //   3000 0 1c01000 7*1000080 1000180 12*1000080 1c00180 9*1c00380 0 0 10*1000080 0 0 1ff800 1fe7fc0
  //   7fdffbfe 1fffc0fc 7f81fe0 7fc1fffc 7f07fffe 7e0ffffe 3fffc1fc 7fc1fc0 1fe0fffc 7f83fffe 7*0 1f8000
  //   1c00000 20 4000000 5*0 c00 16*0 f80700 26*0 7000 c00000 e0000 18000 0 700 9*0 38000 16*0 780 18000
  //   e00000 0 30000 70000 0 0 0 80000 18*0 1c000 30000 0 0 0 e000 0 0 c0000 180000 0 0 180 0 0 0 80000 0
  //   0 0 300000 0 0 180 260 12*0 30000 19*0 10000 14*0 c000 3000 0 20000 4*0 c000 0 e0000 e0980 70000
  //   601c0 40000 1800c0 0 c0 7000 6040 0 0 0 180 0 300 600 38 38000 100 7000 6000 0 e0400 30 c00 30 e0000
  //   0 38000 0 0 1e000 2000 0 60 0 300000 0 240 0 60 120 0 100 200 18000 40180 1e0 0 f0000 30000 3000 c00
  //   0 780000 6*0 18000 0 0 0 c00 7000 0 c00 3c0000 700c0 18000 e0000 41*0 10000 0 7f000 28*0 1e000078 0
  //   3000000c 13*0 3000000c 38000 0 60000000 60000000 15*0 181c00 0 0 0 7e000 104*0 600000 c300000
  //   7000000 12*0 300000 70000 0 0 380000 60000 3000 7000 100400 0 0 3800 10000 0 38000 3000 400 0 200
  //   38000 18000 300 0 1c000 c03c00 7f0 0 38000 0 7c00 3800000 78000 60000 c000 70000 300 27*0 3c000
  //   3c000 0 0 3c000 3c000 0 0 3c000 3c000 8*0 24*3c000 8*0 24*3c000 579*0 3ffffc 3ff3fffc 3803800
  //   1803800 c380 7000 1c000 3800c00 7010 383038 7003ff0 181c00 dfff8 7ffff0 1ff181c0 c300700 3800020
  //   1c000 c0e000 3801c00 1c00 381c070 1fe00c00 18000 ff81c00 3ffffc0 18000 10 600e00 e10c00 c00000
  //   1c007f0 38e0700 40000 7006000 600c000 181800 38c1018 1c08600 8600 60 3023810 103000 6000 0 3806380
  //   8183300 6184010 1800010 1818030 383fff0 18000 7fffff0 7003c0 78000 1800c00 1ffffff8 387fff8 1c00018
  //   1ffc3800 1fc0018 7f83000 330018 30c008 3030420 18003f0 1807fc0 221fffc 3800ff0 18c003f0 1804600
  //   1801800 e03000 70030c0 38000 60000 1c01c20 601ffc 309ff8 3018618 3000c00 1ff00e08 3818010 3803000
  //   100e10 1800c00 7000c00 1c01800 6001c10 1c3800 c10e000 700000 1c018 fff8018 181c08 3ffffc0 c7ffe0
  //   e7ffc0 700e000 38000 300e000 183fff0 1c00180 703800 3003800 70e0060 c00018 181800 1c3000 c0000
  //   383800 c3ff8 1c3070 ffffc0 383fff0 e01800 101d0018 380200 1fff00 3801800 3800c00 30000 380c00 18000
  //   3803800 381c070 38ff7fc 1ffffffc 3ffffffc 1ff30c38 7018380 c1ffff8 ffff00 7007000 fffcffc 3803808
  //   3c01800 6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
  //   contents of rom_6 (hex, n*v repeats v):
  //   4*0 1ff800 300c00 181800 0 70000 0 0 c3000 0 c0 3c00000 20c0 3cf8000 1c0 3000000 30 c000000 1b0
  //   18c00000 1800 100000 1bf0 d80000 180c0 3018000 1ffc0 3ff0000 18000 0 0 0 18000 c000030 7ffff80
  //   1ffffff8 4*0 180 18000 8060 0 0 3ffc00 6e00 ce00 5*0 300 30000 c000 70 7800000 0 0 0 18000 1e7800
  //   7e00000 1c0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
  //   contents of rom_7 (hex, n*v repeats v):
  //   4*0 3ffc00 1c3800 3c3c00 0 60000 0 0 c3000 0 180 3c00000 6180 3cf8000 180 1800000 60 c000000 330
  //   cc00000 1800 100000 1be0 d80000 18180 1818000 1ff80 1ff0000 18000 80 38000 18000 3c000 c000030
  //   3ffff80 ffffff0 0 3c000 0 1800180 180 18000 c060 18 0 780e00 ce00 cc00 5*0 300 30000 c000 3e0
  //   3e00000 0 1c00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
  //   contents of rom_8 (hex, n*v repeats v):
  //   5*0 77000 3c3c00 0 60000 0 0 c3000 0 180 3c00000 c180 3c78000 300 c00000 60 6000000 320 c600000 1800
  //   100000 1a00 d80000 18180 1c18000 1ff00 ff0000 18000 30001c0 7c000 3c000 3c000 6000060 3800380
  //   1c00380 1800180 1ff800 0 3c003c0 180 18000 180c0 70 0 1c00300 c000 c000 5*0 600 30000 c000 1f00
  //   7c0000 0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
  //   contents of rom_9 (hex, n*v repeats v):
  //   5*0 3c000 181800 0 c0000 0 0 c3000 0 300 c00000 1c300 c30000 600 600000 c0 6000000 660 6600000 1800
  //   100000 1a00 d80000 18300 c18000 1ff00 ff0000 18000 1800380 7c000 7e000 66000 6000060 1c00080 1c00380
  //   1800180 7ffe00 3fffc0 3e007c0 300 18000 380c0 e0 7e000 3800180 c000 c000 0 1800f80 0 0 0 c00 30038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
  //   contents of rom_10 (hex, n*v repeats v):
  //   5*0 18000 0 0 c0300 0 0 c3000 0 3c0 1800000 1e3c0 1830000 400 600000 c0 3000000 660 6300000 1800
  //   100000 1a00 d80000 18600 618000 1fe00 7f0000 18000 c00700 7c000 3c000 66000 30000c0 e000c0 1c00380
  //   1800180 e00700 7fffc0 3e007c0 300 18000 30180 1c0 3ffc00 30000c0 18000 1c000 0 7803fe0 0 0 0 c00
  //   301f0 f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
  //   contents of rom_11 (hex, n*v repeats v):
  //   8*0 187f80 0 0 c3000 0 7c0 1000000 1f7c0 1060000 400 600000 180 3000000 cc0 3300000 1800 100000 1a00
  //   d80000 18600 618000 1fc00 7f0000 18000 600e00 38000 3c000 63000 30000c0 e00040 1c00380 1800180
  //   c00300 e00000 3c003c0 300 18000 60180 380 f00f00 6000060 18000 1c000 ffffff0 e007070 f00000 0 0 1800
  //   30f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
  //   contents of rom_12 (hex, n*v repeats v):
  //   7*0 31c00 1ff700 0 0 c3000 0 3c0 2000000 1f3c0 20c0000 400 600000 180 1800000 cc0 3180000 1800
  //   100000 1a00 d80000 18c00 318000 1fc00 3f0000 18000 301c00 0 0 c3000 1800180 700000 1c00380 1800180
  //   1c00380 1800000 800100 600 18000 60300 700 1c00380 e000060 18000 1c000 1ffffff8 c00c030 3fc0000
  //   800700 f00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
  //   contents of rom_13 (hex, n*v repeats v):
  //   7*0 71c00 360600 0 0 c3000 0 3c0 4000000 1e3c0 4180000 400 600000 300 1800000 1980 1980000 1800
  //   100000 1a00 d80000 18c00 318000 1fc00 3f0000 18000 183800 0 0 c1800 1800180 780000 1c00380 1800180
  //   1800180 3800000 0 600 18000 c0300 e00 38001c0 c000030 18000 7f000 0 1c018038 70f0018 7803fc0 3fc07f0
  //   1fff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
  //   contents of rom_14 (hex, n*v repeats v):
  //   0 0 0 3c000 0 0 0 73800 200600 0 1e00000 c3000 0 80 0 4080 0 400 600000 300 c00000 1980 18c0000 1800
  //   100000 1a00 d80000 18800 318000 1f800 3f0000 18000 c7000 0 0 181800 c00300 380000 1c00380 1800180
  //   1800180 3000000 0 600 18000 c0600 1c00 60000e0 c000030 18000 fb800 0 1c030038 c03c030 e0070e0
  //   70f1e00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
  //   contents of rom_15 (hex, n*v repeats v):
  //   0 0 0 7e000 0 0 0 63800 400c00 0 7f80008 c3000 e03c070 4*0 400 600000 600 c00000 3300 cc0000 1800
  //   100000 1a00 d80000 19800 118000 1f800 3f0000 7ffffe0 6e000 0 0 181800 c00300 1c0000 1c00380 1800180
  //   1800180 3000000 0 c00 18000 180600 3800 e000070 1c038030 18000 198c00 0 c070030 1800f0e0 c00c030
  //   c03b0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
  //   contents of rom_16 (hex, n*v repeats v):
  //   0 0 0 ff000 0 0 0 e3000 800c00 0 e1f0018 c3000 1f07c0f8 4*0 400 600000 600 600000 3300 c60000 1800
  //   100000 1a00 d80000 19800 198000 1f800 3f0000 7ffffe0 3c000 0 0 300c00 600600 1e0000 1c00380 1800180
  //   1800180 3ffff80 0 c00 18000 180c00 6000 c000030 1807c030 18000 198c00 0 e0e0070 3fc0 1801c030
  //   1801e00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
  //   contents of rom_17 (hex, n*v repeats v):
  //   0 0 0 ff000 0 0 0 c7000 1800 ffffffff 1803e030 c3000 1f07e1f8 4*0 400 600000 c00 600000 6600 460000
  //   1800 100000 1a00 d80000 19800 198000 1f800 3f0000 18000 38000 ffffff0 0 300c00 600600 e0000 1c00380
  //   1800180 1800180 3ffffc0 0 c00 18000 301c00 c000 18000018 1807e038 18000 198c00 1ffffff8 7fc01e0 f00f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
  //   contents of rom_18 (hex, n*v repeats v):
  //   0 0 0 ff000 0 0 0 c6000 1000 0 10007fe0 c3000 1f07c0f8 4*0 400 600000 600 600000 3300 c60000 1800
  //   100000 1a00 d80000 19800 198000 1f800 3f0000 18000 3c000 7ffffe0 0 600600 300c00 70000 1c00380
  //   1800180 1800180 3ffff80 0 1800 18000 301800 18000 18000018 1807c030 18000 198c00 0 1f00180 3fc0000
  //   1c030030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
  //   contents of rom_19 (hex, n*v repeats v):
  //   0 0 0 fe000 0 0 0 186000 3000 0 20000fc0 c3000 e03c0f0 4*0 400 600000 600 c00000 3300 cc0000 1800
  //   100000 1a00 d80000 19800 118000 1f800 3f0000 18000 6e000 0 0 600600 300c00 60000 1c00380 1800180
  //   1800180 3000000 0 181800 18000 603800 30000 10000008 1c03c030 18000 199c00 0 0 70f0018 c0e0070
  //   e03b800 30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
  //   contents of rom_20 (hex, n*v repeats v):
  //   0 0 0 7e000 0 0 0 18c000 42000 0 100 c3000 5*0 400 600000 300 c00000 3180 18c0000 1800 100000 1a00
  //   d80000 18800 318000 1f800 3f0000 18000 c7000 0 0 c00300 181c00 c0000 1c00380 1800180 1800180 3000000
  //   0 3c1800 18000 603000 60000 0 c000030 18000 db800 0 0 c03c030 7bc01e0 7ff1ff0 1ffffff0 3f0000 f800 1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
  //   contents of rom_21 (hex, n*v repeats v):
  //   7*0 10c000 36000 0 0 c3000 5*0 400 600000 300 1800000 1980 1980000 1800 100000 1a00 d80000 18c00
  //   318000 1fc00 3f0000 18000 183800 0 0 c00300 181800 180000 1c00380 1800180 1800180 3800000 0 6e3000
  //   18000 c06000 c0000 0 c000030 18000 7f000 0 1ffffff8 1800f0e0 3f803c0 3fc07e0 1ffffff0 7e000 7c000
  //   f8001f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
  //   contents of rom_22 (hex, n*v repeats v):
  //   0 1c000000 3c00000 4*0 308000 1c000 0 0 c3000 5*0 400 600000 180 1800000 18c0 3180000 1800 100000
  //   1a00 d80000 18c00 218000 1fc00 7f0000 18000 301c00 0 0 1800180 c3800 380000 1c00380 1800300 1800180
  //   1800000 0 73000 18000 c06000 180000 0 c000070 18000 3c000 1ffffff8 ffffff0 3fc0 0 0 c0000 3fc00
  //   3ec000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
  //   contents of rom_23 (hex, n*v repeats v):
  //   0 f000000 7e00000 4*0 200000 e000 0 0 c3000 5*0 400 600000 180 3000000 cc0 3300000 1800 100000 1a00
  //   d80000 18600 618000 1fc00 7f0000 18000 600e00 38000 38000 1800180 c3000 300000 1c00380 c00300
  //   1800180 e00000 3c003c0 73000 18000 180c000 300000 0 6000060 18000 18000 ffffff0 0 f00 0 0 180000
  //   31f80 1f0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
  //   contents of rom_24 (hex, n*v repeats v):
  //   0 3c00000 c200000 5*0 7000 0 0 c3000 5*0 400 600000 c0 3000000 c60 6300000 1800 100000 1a00 d80000
  //   18600 e18000 1fe00 7f0000 18000 c00700 7c000 7c000 1000180 67000 600040 1c00380 e00600 1800180
  //   7fff80 3c007c0 3f000 18000 180c000 600000 0 70000e0 38000 18000 5*0 300000 303f0 f80c000 fc000 3f000
  //   0 7e0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
  //   contents of rom_25 (hex, n*v repeats v):
  //   0 1e00000 c300000 5*0 7800 0 0 c3000 5*0 400 600000 c0 6000000 660 6600000 1800 100000 1a00 d80000
  //   18300 c18000 1fe00 ff0000 18000 1800380 7c000 7c000 30000c0 66000 c000c0 1c00380 7c3c00 1800180
  //   3fffc0 7e007c0 1e000 18000 3018000 c00000 0 38001c0 30000 18000 5*0 300000 30078 1e00c000 1f800
  //   f8000 0 7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
  //   contents of rom_26 (hex, n*v repeats v):
  //   0 e00000 c300000 5*0 3800 0 0 c3000 5*0 600 c00000 60 6000000 660 c600000 1800 100000 1a00 d80000
  //   18300 1818000 1ff00 1ff0000 0 30001c0 7c000 3c000 30000c0 3e000 1c00180 1c00380 1ff800 1800180 0
  //   3c007c0 e000 18000 7018000 3800000 0 1c00380 30000 30000 0 ffffff0 0 0 0 600000 30000 c000 3f00
  //   7c0000 0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
  //   contents of rom_27 (hex, n*v repeats v):
  //   0 e00000 6600000 5*0 1000 0 0 c3000 5*0 300 1800000 60 c000000 330 cc00000 1800 100000 1a00 fd80000
  //   18180 3818000 1ff80 1ff0000 0 80 38000 38000 6000060 3c000 1ffff80 1c00380 7c000 1800180 0 1800380
  //   e000 18000 6030000 7000000 0 f00f00 330000 3b0000 0 ffffff0 0 0 0 c00000 30000 c000 7e0 3e00000 0
  //   3c0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
  //   contents of rom_28 (hex, n*v repeats v):
  //   0 600000 3c00000 8*0 c3000 5*0 180 3000000 60 c000000 330 18c00000 1800 100000 1a00 fd80000 180c0
  //   3018000 1ff80 3ff0000 7ffffe0 0 0 0 6000060 1c000 3ffff80 ff01ff0 4*0 4000 ffffff0 6030000 fffffe0 0
  //   3ffc00 330000 3f0000 5*0 400000 30000 c000 f0 7000000 0 0 0 1ff800 18000 0 0 0 1fc00 dff800 c1ff830
  //   1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
  //   contents of rom_29 (hex, n*v repeats v):
  //   0 600000 1000000 8*0 c3000 5*0 c0 6000000 30 18000000 198 19800000 1800 100000 1a00 c180000 18060
  //   7ff8000 1ffc0 7ff0000 7ffffe0 0 0 0 c000030 18000 7ffff80 ff01ff0 9*0 ff000 3e0000 3e0000 6*0 30000
  //   c000 10 4*0 fe000 18000 4*0 7e000 18018010 0 0 3c0f0 1c7000 0 1800180 1800180 7e000 3c000 3c000
  //   18000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
  //   contents of rom_30 (hex, n*v repeats v):
  //   11*0 c3000 5*0 40 0 10 8000000 108 10800000 1800 ff00000 1e00 ff80000 1fff0 fff8000 1ffe0 7ff0000
  //   4*0 20 8000 12*0 80000 14*0 18000 5*0 18000 4*0 fe000 0 1000080 1000080 12*0 18000 58*0 f00700
  //   9*e00f00 39*0 8000000 0 0 200000 11*0 3000000 4*0 1ffc00 16*0 700 9*0 7ff0 380 7fe0000 9*0 3ff800 0
  //   0 ff000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
  //   contents of rom_31 (hex, n*v repeats v):
  //   24*0 7f00000 e00 7f00000 0 0 ffe0 7fe0000 119*0 10*3ffc00 54*0 6000000 4*0 3c000 26*0 7ff0 0 ffe0000
  //   9*0 1fe000 0 0 7e0000 5*0 7e0000 7f00 7*0 3c0000 0 0 10000 271*0 38000 0 60000000 70000000 77*0
  //   300000 56*0 38700000 22*0 80000 44*0 3c000 3c000 0 0 3c000 3c000 0 0 10*3c000 8*0 24*3c000 8*0
  //   16*3c000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
  //   contents of rom_32 (hex, n*v repeats v):
  //   150*0 10*7e000 88*0 7fc0000 0 ffffffff 16*0 7e0000 3e00 282*0 10000 0 60000000 70000000 134*0
  //   1fe00000 67*0 3c000 3c000 0 0 3c000 3c000 0 0 10*3c000 8*0 24*3c000 8*0 16*3c000 25*0 3c00 fc0ffff
  //   556*0 1000000 11*0 4 17*0 800000 800000 10*0 80000 4*0 400000 29*0 200000 20*0 20000 0 0 2000 19*0
  //   40000 22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
endmodule

module \_22位流水接口  (
  input  [21:0] Din22,
  input  \传输状态In_表明当前传输数据有效 ,
  input  CLK,
  input  \同步清零_气泡_高电平有效 ,
  input  \使能端_低电平有效_stall_高电平有效 ,
  output [21:0] Dout22,
  output \传输状态Out_表明当前传输数据有效 
);

  wire multiplexer_2_out, pull_resistor_2_node;
  wire [21:0] multiplexer_1_out;

  Multiplexer #(.width(22), .enable("false")) multiplexer_1 (
    .in0(Din22), .in1({22{1'b0}}), .out(multiplexer_1_out), .sel(\同步清零_气泡_高电平有效 ));
  Multiplexer #(.enable("false")) multiplexer_2 (
    .in0(\传输状态In_表明当前传输数据有效 ), .in1(1'b0), .out(multiplexer_2_out), .sel(\同步清零_气泡_高电平有效 ));
  Pull_Resistor pull_resistor_1 (.node(\同步清零_气泡_高电平有效 ));
  Register #(.width(22)) register_1 (
    .D(multiplexer_1_out), .en(pull_resistor_2_node), .Q(Dout22), .clk(CLK));  // open: clr
  Register #(.width(1)) register_2 (
    .D(multiplexer_2_out), .en(pull_resistor_2_node), .Q(\传输状态Out_表明当前传输数据有效 ), .clk(CLK));  // open: clr
  Pull_Resistor pull_resistor_2 (.node(pull_resistor_2_node));
  not not_1 (pull_resistor_2_node, \使能端_低电平有效_stall_高电平有效 );

  // Notes on the sheet:
  //   同步清零_气泡_高电平有效: pull=down
  //   使能端_低电平有效_stall_高电平有效: pull=down
endmodule

module \_16位流水接口  (
  input  [15:0] Din16,
  input  \传输状态In_表明当前传输数据有效 ,
  input  CLK,
  input  \同步清零_气泡_高电平有效 ,
  input  \使能端_低电平有效_stall_高电平有效 ,
  output [15:0] Dout16,
  output \传输状态Out_表明当前传输数据有效 
);

  wire multiplexer_2_out, pull_resistor_2_node;
  wire [15:0] multiplexer_1_out;

  Multiplexer #(.width(16), .enable("false")) multiplexer_1 (
    .in0(Din16), .in1({16{1'b0}}), .out(multiplexer_1_out), .sel(\同步清零_气泡_高电平有效 ));
  Multiplexer #(.enable("false")) multiplexer_2 (
    .in0(\传输状态In_表明当前传输数据有效 ), .in1(1'b0), .out(multiplexer_2_out), .sel(\同步清零_气泡_高电平有效 ));
  Pull_Resistor pull_resistor_1 (.node(\同步清零_气泡_高电平有效 ));
  Register #(.width(16)) register_1 (
    .D(multiplexer_1_out), .en(pull_resistor_2_node), .Q(Dout16), .clk(CLK));  // open: clr
  Register #(.width(1)) register_2 (
    .D(multiplexer_2_out), .en(pull_resistor_2_node), .Q(\传输状态Out_表明当前传输数据有效 ), .clk(CLK));  // open: clr
  Pull_Resistor pull_resistor_2 (.node(pull_resistor_2_node));
  not not_1 (pull_resistor_2_node, \使能端_低电平有效_stall_高电平有效 );
endmodule

module \流水模拟  (
);

  wire \时钟_out ;
  wire [15:0] counter_1_q, \n16位流水接口_1_dout16 , \n16位流水接口_2_dout16 , \n16位流水接口_3_dout16 ,
       \n16位流水接口_4_dout16 , \组合逻辑_1_out_2 , \组合逻辑_2_out_2 , \组合逻辑_3_out_2 ;

  Clock \u_时钟  (.out(\时钟_out ));
  Counter #(.width(16), .max('hffff)) counter_1 (.Q(counter_1_q), .clk(\时钟_out ));  // open: load, D, count, carry, clr
  // Probe on counter_1_q
  \_16位流水接口  \u_16位流水接口_1  (
    .Din16(counter_1_q), .CLK(\时钟_out ), .Dout16(\n16位流水接口_1_dout16 ));  // open: 传输状态In_表明当前传输数据有效, 传输状态Out_表明当前传输数据有效, 同步清零_气泡_高电平有效, 使能端_低电平有效_stall_高电平有效
  // Probe on \n16位流水接口_1_dout16 
  \组合逻辑  \u_组合逻辑_1  (.in_1(\n16位流水接口_1_dout16 ), .out_2(\组合逻辑_1_out_2 ));
  \_16位流水接口  \u_16位流水接口_2  (
    .Din16(\组合逻辑_1_out_2 ), .CLK(\时钟_out ), .Dout16(\n16位流水接口_2_dout16 ));  // open: 传输状态In_表明当前传输数据有效, 传输状态Out_表明当前传输数据有效, 同步清零_气泡_高电平有效, 使能端_低电平有效_stall_高电平有效
  // Probe on \n16位流水接口_2_dout16 
  \组合逻辑  \u_组合逻辑_2  (.in_1(\n16位流水接口_2_dout16 ), .out_2(\组合逻辑_2_out_2 ));
  \_16位流水接口  \u_16位流水接口_3  (
    .Din16(\组合逻辑_2_out_2 ), .CLK(\时钟_out ), .Dout16(\n16位流水接口_3_dout16 ));  // open: 传输状态In_表明当前传输数据有效, 传输状态Out_表明当前传输数据有效, 同步清零_气泡_高电平有效, 使能端_低电平有效_stall_高电平有效
  // Probe on \n16位流水接口_3_dout16 
  \组合逻辑  \u_组合逻辑_3  (.in_1(\n16位流水接口_3_dout16 ), .out_2(\组合逻辑_3_out_2 ));
  \_16位流水接口  \u_16位流水接口_4  (
    .Din16(\组合逻辑_3_out_2 ), .CLK(\时钟_out ), .Dout16(\n16位流水接口_4_dout16 ));  // open: 传输状态In_表明当前传输数据有效, 传输状态Out_表明当前传输数据有效, 同步清零_气泡_高电平有效, 使能端_低电平有效_stall_高电平有效
  // Probe on \n16位流水接口_4_dout16 

  // Notes on the sheet:
  //   计数器
  //   阶段1
  //   阶段2
  //   阶段3
  //   利用ctrl+T驱动该电路时钟，观察数据在流水线中传递的过程
  //   阶段4
  //   阶段5
endmodule

module \组合逻辑  (
  input  [15:0] in_1,
  output [15:0] out_2
);


  assign out_2 = in_1;
endmodule

module \海明解码自动生成电路  (
  input  G1,
  input  G2,
  input  G3,
  input  G4,
  input  G5,
  input  G6,
  output O1,
  output O2,
  output O3
);

  wire and_1_out, and_2_out, and_3_out, and_4_out, and_5_out, and_6_out, and_7_out, and_8_out, and_9_out,
       and_10_out, not_1_out, not_2_out, not_3_out, not_4_out, not_5_out, not_6_out, not_7_out, not_8_out,
       not_9_out, not_10_out;

  not not_1 (not_1_out, G6);
  not not_2 (not_2_out, G6);
  not not_3 (not_3_out, G6);
  not not_4 (not_4_out, G6);
  not not_5 (not_5_out, G6);
  and and_1 (and_1_out, G5, G6);
  and and_2 (and_2_out, G4, G6);
  and and_3 (and_3_out, G3, G6);
  and and_4 (and_4_out, G2, G6);
  and and_5 (and_5_out, G1, G6);
  not not_6 (not_6_out, G1);
  not not_7 (not_7_out, G2);
  not not_8 (not_8_out, G3);
  not not_9 (not_9_out, G4);
  not not_10 (not_10_out, G5);
  and and_6 (and_6_out, G5, not_1_out);
  and and_7 (and_7_out, G4, not_2_out);
  and and_8 (and_8_out, G3, not_3_out);
  and and_9 (and_9_out, G2, not_4_out);
  and and_10 (and_10_out, G1, not_5_out);
  or or_1 (O2, and_1_out, and_2_out, and_3_out, and_4_out, and_5_out);
  and and_11 (O3, not_6_out, not_7_out, not_8_out, not_9_out, not_10_out);
  or or_2 (O1, and_6_out, and_7_out, and_8_out, and_9_out, and_10_out);
endmodule

module \串行模2余数计算  (
);

  wire clock_1_out, rom_1_data, xor_1_out, xor_2_out;
  wire [4:0] d_ff_5_q;
  wire [7:0] counter_1_q;

  Clock clock_1 (.out(clock_1_out));
  D_Flip_Flop d_ff_1 (.clk(clock_1_out), .D(d_ff_5_q[3]), .Q(d_ff_5_q[4]));  // open: Qn, preset, en, reset
  D_Flip_Flop d_ff_2 (.clk(clock_1_out), .D(d_ff_5_q[2]), .Q(d_ff_5_q[3]));  // open: Qn, preset, en, reset
  D_Flip_Flop d_ff_3 (.clk(clock_1_out), .D(xor_1_out), .Q(d_ff_5_q[2]));  // open: Qn, preset, en, reset
  xor xor_1 (xor_1_out, d_ff_5_q[4], d_ff_5_q[1]);
  D_Flip_Flop d_ff_4 (.clk(clock_1_out), .D(d_ff_5_q[0]), .Q(d_ff_5_q[1]));  // open: Qn, preset, en, reset
  D_Flip_Flop d_ff_5 (.clk(clock_1_out), .D(xor_2_out), .Q(d_ff_5_q[0]));  // open: Qn, preset, en, reset
  xor xor_2 (xor_2_out, d_ff_5_q[4], rom_1_data);
  // Probe on d_ff_5_q
  Counter counter_1 (.Q(counter_1_q), .clk(clock_1_out));  // open: load, D, count, carry, clr
  ROM #(.dataWidth(1)) rom_1 (.addr(counter_1_q), .data(rom_1_data));  // open: sel

  // Notes on the sheet:
  //   G(x) = x^5 + x^2 + 1
  //   contents of rom_1 (hex, n*v repeats v):
  //   1
endmodule

module \流水暂停时序电路  (
  input  en,
  input  CLK,
  output out
);

  wire and_1_out, and_2_out, bit_0_q, bit_1_q, not_1_out, not_2_out, not_3_out;

  not not_1 (not_1_out, bit_1_q);
  not not_2 (not_2_out, bit_0_q);
  not not_3 (not_3_out, bit_1_q);
  and and_1 (and_1_out, not_1_out, not_2_out, en);
  and and_2 (and_2_out, not_3_out, bit_0_q);
  D_Flip_Flop bit_0 (.clk(CLK), .D(and_1_out), .Q(bit_0_q));  // open: Qn, preset, en, reset
  D_Flip_Flop bit_1 (.clk(CLK), .D(and_2_out), .Q(bit_1_q));  // open: Qn, preset, en, reset
  or or_1 (out, bit_0_q, bit_1_q);
endmodule

module \海明编码流水传输RAM改造  (
  input  [1:0] in_1,
  input  \加噪 
);

  wire \_2位错 , \_2位错且有效 , \_4阶段有效性 , and_2_out, \n16位流水接口_1_传输状态out_表明当前传输数据有效 ,
       \n16位流水接口_2_传输状态out_表明当前传输数据有效 , \n22位流水接口_1_传输状态out_表明当前传输数据有效 , not_1_out, or_1_out, xor_1_out,
       xor_2_out, \时钟_out , \流水暂停信号 , \海明解码_1__1位错 , \海明解码_1_无错误 ;
  wire [6:0] \国标转区位码_1_位号 , \国标转区位码_1_区号 , \国标转区位码_2_位号 , \国标转区位码_2_区号 ;
  wire [7:0] adder_1_out, adder_2_out, counter_1_q, multiplexer_1_out, multiplexer_2_out, register_1_q;
  wire [15:0] \n16位流水接口_1_dout16 , \发送 , \接收 , \海明解码_1_纠错后数据 ;
  wire [21:0] \n22位流水接口_1_dout22 , \n22位流水接口_2_dout22 , \n22位随机干扰_1_加扰后数据 , \海明编码_1_海明码 ;
  wire [31:0] \字库_1_out_3 , \字库_1_out_4 , \字库_1_out_5 , \字库_1_out_6 , \字库_1_out_7 , \字库_1_out_8 ,
       \字库_1_out_9 , \字库_1_out_10 , \字库_1_out_11 , \字库_1_out_12 , \字库_1_out_13 , \字库_1_out_14 ,
       \字库_1_out_15 , \字库_1_out_16 , \字库_1_out_17 , \字库_1_out_18 , \字库_1_out_19 , \字库_1_out_20 ,
       \字库_1_out_21 , \字库_1_out_22 , \字库_1_out_23 , \字库_1_out_24 , \字库_1_out_25 , \字库_1_out_26 ,
       \字库_1_out_27 , \字库_1_out_28 , \字库_1_out_29 , \字库_1_out_30 , \字库_1_out_31 , \字库_1_out_32 ,
       \字库_1_out_33 , \字库_1_out_34 , \字库_2_out_3 , \字库_2_out_4 , \字库_2_out_5 , \字库_2_out_6 , \字库_2_out_7 ,
       \字库_2_out_8 , \字库_2_out_9 , \字库_2_out_10 , \字库_2_out_11 , \字库_2_out_12 , \字库_2_out_13 , \字库_2_out_14 ,
       \字库_2_out_15 , \字库_2_out_16 , \字库_2_out_17 , \字库_2_out_18 , \字库_2_out_19 , \字库_2_out_20 ,
       \字库_2_out_21 , \字库_2_out_22 , \字库_2_out_23 , \字库_2_out_24 , \字库_2_out_25 , \字库_2_out_26 ,
       \字库_2_out_27 , \字库_2_out_28 , \字库_2_out_29 , \字库_2_out_30 , \字库_2_out_31 , \字库_2_out_32 ,
       \字库_2_out_33 , \字库_2_out_34 ;

  Multiplexer #(.width(8)) multiplexer_1 (
    .in0(8'h1), .in1(8'hfe), .out(multiplexer_1_out), .sel(\_2位错且有效 ));  // open: en
  Register register_1 (.D(adder_1_out), .Q(register_1_q), .clk(\时钟_out ));  // open: en, clr
  Clock \u_时钟  (.out(\时钟_out ));
  \国标转区位码  \u_国标转区位码_1  (.\位号 (\国标转区位码_1_位号 ), .\区号 (\国标转区位码_1_区号 ), .GB2312(\发送 ));
  Adder adder_1 (.a(multiplexer_1_out), .b(register_1_q), .out(adder_1_out));  // open: cin, cout
  Multiplexer #(.width(8)) multiplexer_2 (
    .in0(register_1_q), .in1(adder_2_out), .out(multiplexer_2_out), .sel(\_2位错且有效 ));  // open: en
  Adder adder_2 (.a(register_1_q), .b(8'hfd), .out(adder_2_out));  // open: cin, cout
  \字库  \u_字库_1  (
    .out_3(\字库_1_out_3 ), .out_4(\字库_1_out_4 ), .out_5(\字库_1_out_5 ), .out_6(\字库_1_out_6 ),
    .out_7(\字库_1_out_7 ), .out_8(\字库_1_out_8 ), .out_9(\字库_1_out_9 ), .out_10(\字库_1_out_10 ),
    .out_11(\字库_1_out_11 ), .out_12(\字库_1_out_12 ), .out_13(\字库_1_out_13 ), .out_14(\字库_1_out_14 ),
    .out_15(\字库_1_out_15 ), .out_16(\字库_1_out_16 ), .out_17(\字库_1_out_17 ), .out_18(\字库_1_out_18 ),
    .out_19(\字库_1_out_19 ), .out_20(\字库_1_out_20 ), .out_21(\字库_1_out_21 ), .out_22(\字库_1_out_22 ),
    .out_23(\字库_1_out_23 ), .out_24(\字库_1_out_24 ), .out_25(\字库_1_out_25 ), .out_26(\字库_1_out_26 ),
    .out_27(\字库_1_out_27 ), .out_28(\字库_1_out_28 ), .out_29(\字库_1_out_29 ), .out_30(\字库_1_out_30 ),
    .out_31(\字库_1_out_31 ), .out_32(\字库_1_out_32 ), .out_33(\字库_1_out_33 ), .out_34(\字库_1_out_34 ),
    .\区号 (\国标转区位码_1_区号 ), .\位号 (\国标转区位码_1_位号 ));
  DotMatrix #(.inputtype("row"), .matrixcols(32), .matrixrows(32), .dotshape("circle")) dotmatrix_1 (
    .row0(\字库_1_out_3 ), .row1(\字库_1_out_4 ), .row2(\字库_1_out_5 ), .row3(\字库_1_out_6 ), .row4(\字库_1_out_7 ),
    .row5(\字库_1_out_8 ), .row6(\字库_1_out_9 ), .row7(\字库_1_out_10 ), .row8(\字库_1_out_11 ),
    .row9(\字库_1_out_12 ), .row10(\字库_1_out_13 ), .row11(\字库_1_out_14 ), .row12(\字库_1_out_15 ),
    .row13(\字库_1_out_16 ), .row14(\字库_1_out_17 ), .row15(\字库_1_out_18 ), .row16(\字库_1_out_19 ),
    .row17(\字库_1_out_20 ), .row18(\字库_1_out_21 ), .row19(\字库_1_out_22 ), .row20(\字库_1_out_23 ),
    .row21(\字库_1_out_24 ), .row22(\字库_1_out_25 ), .row23(\字库_1_out_26 ), .row24(\字库_1_out_27 ),
    .row25(\字库_1_out_28 ), .row26(\字库_1_out_29 ), .row27(\字库_1_out_30 ), .row28(\字库_1_out_31 ),
    .row29(\字库_1_out_32 ), .row30(\字库_1_out_33 ), .row31(\字库_1_out_34 ));
  ROM #(.dataWidth(16)) rom_1 (.addr(multiplexer_2_out), .data(\发送 ));  // open: sel
  \流水暂停时序电路  \u_流水暂停时序电路_1  (.CLK(\时钟_out ), .out(\流水暂停信号 ), .en(\_2位错且有效 ));
  \_16位流水接口  \u_16位流水接口_1  (
    .Din16(\发送 ), .\传输状态In_表明当前传输数据有效 (1'b1), .CLK(\时钟_out ), .Dout16(\n16位流水接口_1_dout16 ),
    .\传输状态Out_表明当前传输数据有效 (\n16位流水接口_1_传输状态out_表明当前传输数据有效 ));  // open: 同步清零_气泡_高电平有效, 使能端_低电平有效_stall_高电平有效
  \海明编码  \u_海明编码_1  (.\原始数据 (\n16位流水接口_1_dout16 ), .\海明码 (\海明编码_1_海明码 ));
  xor xor_1 (xor_1_out, \n16位流水接口_1_传输状态out_表明当前传输数据有效 , \_2位错且有效 );
  \_22位流水接口  \u_22位流水接口_1  (
    .Din22(\海明编码_1_海明码 ), .\传输状态In_表明当前传输数据有效 (xor_1_out), .CLK(\时钟_out ), .Dout22(\n22位流水接口_1_dout22 ),
    .\传输状态Out_表明当前传输数据有效 (\n22位流水接口_1_传输状态out_表明当前传输数据有效 ));  // open: 同步清零_气泡_高电平有效, 使能端_低电平有效_stall_高电平有效
  \_22位随机干扰  \u_22位随机干扰_1  (
    .\加扰模式 (in_1), .\_22位输入 (\n22位流水接口_1_dout22 ), .\加扰后数据 (\n22位随机干扰_1_加扰后数据 ), .\增加三位错 (\加噪 ));  // open: 随机加扰屏蔽字
  \字库  \u_字库_2  (
    .out_3(\字库_2_out_3 ), .out_4(\字库_2_out_4 ), .out_5(\字库_2_out_5 ), .out_6(\字库_2_out_6 ),
    .out_7(\字库_2_out_7 ), .out_8(\字库_2_out_8 ), .out_9(\字库_2_out_9 ), .out_10(\字库_2_out_10 ),
    .out_11(\字库_2_out_11 ), .out_12(\字库_2_out_12 ), .out_13(\字库_2_out_13 ), .out_14(\字库_2_out_14 ),
    .out_15(\字库_2_out_15 ), .out_16(\字库_2_out_16 ), .out_17(\字库_2_out_17 ), .out_18(\字库_2_out_18 ),
    .out_19(\字库_2_out_19 ), .out_20(\字库_2_out_20 ), .out_21(\字库_2_out_21 ), .out_22(\字库_2_out_22 ),
    .out_23(\字库_2_out_23 ), .out_24(\字库_2_out_24 ), .out_25(\字库_2_out_25 ), .out_26(\字库_2_out_26 ),
    .out_27(\字库_2_out_27 ), .out_28(\字库_2_out_28 ), .out_29(\字库_2_out_29 ), .out_30(\字库_2_out_30 ),
    .out_31(\字库_2_out_31 ), .out_32(\字库_2_out_32 ), .out_33(\字库_2_out_33 ), .out_34(\字库_2_out_34 ),
    .\区号 (\国标转区位码_2_区号 ), .\位号 (\国标转区位码_2_位号 ));
  \国标转区位码  \u_国标转区位码_2  (.\位号 (\国标转区位码_2_位号 ), .\区号 (\国标转区位码_2_区号 ), .GB2312(\接收 ));
  and and_1 (\_2位错且有效 , \_2位错 , \_4阶段有效性 );
  \_22位流水接口  \u_22位流水接口_2  (
    .Din22(\n22位随机干扰_1_加扰后数据 ), .\传输状态In_表明当前传输数据有效 (xor_2_out), .CLK(\时钟_out ),
    .Dout22(\n22位流水接口_2_dout22 ), .\传输状态Out_表明当前传输数据有效 (\_4阶段有效性 ));  // open: 同步清零_气泡_高电平有效, 使能端_低电平有效_stall_高电平有效
  xor xor_2 (xor_2_out, \n22位流水接口_1_传输状态out_表明当前传输数据有效 , \_2位错且有效 );
  DotMatrix #(.inputtype("row"), .matrixcols(32), .matrixrows(32), .dotshape("circle")) dotmatrix_2 (
    .row0(\字库_2_out_3 ), .row1(\字库_2_out_4 ), .row2(\字库_2_out_5 ), .row3(\字库_2_out_6 ), .row4(\字库_2_out_7 ),
    .row5(\字库_2_out_8 ), .row6(\字库_2_out_9 ), .row7(\字库_2_out_10 ), .row8(\字库_2_out_11 ),
    .row9(\字库_2_out_12 ), .row10(\字库_2_out_13 ), .row11(\字库_2_out_14 ), .row12(\字库_2_out_15 ),
    .row13(\字库_2_out_16 ), .row14(\字库_2_out_17 ), .row15(\字库_2_out_18 ), .row16(\字库_2_out_19 ),
    .row17(\字库_2_out_20 ), .row18(\字库_2_out_21 ), .row19(\字库_2_out_22 ), .row20(\字库_2_out_23 ),
    .row21(\字库_2_out_24 ), .row22(\字库_2_out_25 ), .row23(\字库_2_out_26 ), .row24(\字库_2_out_27 ),
    .row25(\字库_2_out_28 ), .row26(\字库_2_out_29 ), .row27(\字库_2_out_30 ), .row28(\字库_2_out_31 ),
    .row29(\字库_2_out_32 ), .row30(\字库_2_out_33 ), .row31(\字库_2_out_34 ));
  LED \u_两位错  (.in(\_2位错 ));
  LED \u_一位错  (.in(\海明解码_1__1位错 ));
  LED \u_无错误  (.in(\海明解码_1_无错误 ));
  \海明解码  \u_海明解码_1  (
    .\_1位错 (\海明解码_1__1位错 ), .\_2位错 (\_2位错 ), .\无错误 (\海明解码_1_无错误 ), .\海明码 (\n22位流水接口_2_dout22 ),
    .\纠错后数据 (\海明解码_1_纠错后数据 ));
  or or_1 (or_1_out, \_2位错且有效 , \流水暂停信号 );
  \_16位流水接口  \u_16位流水接口_2  (
    .Din16(\海明解码_1_纠错后数据 ), .\传输状态In_表明当前传输数据有效 (\_4阶段有效性 ), .CLK(\时钟_out ), .Dout16(\接收 ),
    .\传输状态Out_表明当前传输数据有效 (\n16位流水接口_2_传输状态out_表明当前传输数据有效 ), .\使能端_低电平有效_stall_高电平有效 (or_1_out));  // open: 同步清零_气泡_高电平有效
  // Probe on \接收 
  not not_1 (not_1_out, or_1_out);
  and and_2 (and_2_out, \n16位流水接口_2_传输状态out_表明当前传输数据有效 , not_1_out);
  Counter counter_1 (.count(and_2_out), .Q(counter_1_q), .clk(\时钟_out ));  // open: load, D, carry, clr
  RAM #(.dataWidth(16), .bus("separate")) ram_1 (
    .addr(counter_1_q), .din(\接收 ), .clk(\时钟_out ), .ld(\n16位流水接口_2_传输状态out_表明当前传输数据有效 ));  // open: data, str, sel, clr

  // Notes on the sheet:
  //   海明码流水传输电路
  //   寄存器
  //   发送方
  //   汉字显示
  //   加法器
  //   GB2312
  //   1.取数阶段
  //   contents of rom_1 (hex, n*v repeats v):
  //   bbaa d6d0 bfc6 bcbc b4f3 d1a7 cac7 b9fa bcd2 bdcc d3fd b2bf d6b1 caf4 b5c4 c8ab b9fa d6d8 b5e3 b4f3
  //   d1a7 a3ac d3c9 d4ad bbaa d6d0 c0ed b9a4 b4f3 d1a7 a1a2 cdac bcc3 d2bd bfc6 b4f3 d1a7 a1a2 cee4 baba
  //   b3c7 cad0 bda8 c9e8 d1a7 d4ba d3da a3b2 a3b0 a3b0 a3b0 c4ea a3b5 d4c2 a3b2 a3b6 c8d5 bacf b2a2 b3c9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
  //   ~使能/Stall
  //   发送方在ROM预存了一段中文文字，通过计数器驱动电路每个时钟传输一个汉字
  //   同步清零信号，气泡
  //   用户实现了国标转区位码电路后，可在中间窗口观察发送方和接收方汉字显示是否一致以观察海明检错纠错性能
  //   数据状态：高电平有效
  //   2.编码阶段
  //   电路功能：采用流水分段方式进行数据编码传输，测试海明编码检错纠错能力，当出现2位错时，发送重传信号要求发送方重传，保证接收方按ROM中的地址顺序接受所有汉字
  //   接收方
  //   汉字显示
  //   3.传输阶段
  //   4.解码阶段
  //   5.显示阶段
  //   请将时钟频率调到8Hz
  //   Ctrl+ K启动电路自动仿真
endmodule
