// Logisim project alu.circ as structural Verilog
// CAS
module \_8位可控加减法器  (
  input  [7:0] X,
  input  [7:0] Y,
  input  Sub,
  output [7:0] S,
  output Cout,
  output Overflow
);

  wire xor_2_out, xor_3_out, xor_4_out, xor_5_out, xor_6_out, xor_7_out, xor_8_out, xor_9_out,
       \一位全加器fa封装1_1_cout , \一位全加器fa封装1_3_cout , \一位全加器fa封装1_4_cout , \一位全加器fa封装1_5_cout ,
       \一位全加器fa封装1_6_cout , \一位全加器fa封装1_7_cout , \一位全加器fa封装1_8_cout ;
  wire [8:0] \运算指示 ;

  xor xor_1 (Overflow, Cout, \一位全加器fa封装1_1_cout );
  \一位全加器FA封装1  \u_一位全加器fa封装1_1  (
    .Cout(\一位全加器fa封装1_1_cout ), .Si(S[6]), .Cin(\一位全加器fa封装1_3_cout ), .Xi(X[6]), .Yi(xor_4_out));
  \一位全加器FA封装1  \u_一位全加器fa封装1_2  (.Cout(Cout), .Si(S[7]), .Cin(\一位全加器fa封装1_1_cout ), .Xi(X[7]), .Yi(xor_2_out));
  \一位全加器FA封装1  \u_一位全加器fa封装1_3  (
    .Cout(\一位全加器fa封装1_3_cout ), .Si(S[5]), .Cin(\一位全加器fa封装1_4_cout ), .Xi(X[5]), .Yi(xor_3_out));
  \一位全加器FA封装1  \u_一位全加器fa封装1_4  (
    .Cout(\一位全加器fa封装1_4_cout ), .Si(S[4]), .Cin(\一位全加器fa封装1_5_cout ), .Xi(X[4]), .Yi(xor_7_out));
  \一位全加器FA封装1  \u_一位全加器fa封装1_5  (
    .Cout(\一位全加器fa封装1_5_cout ), .Si(S[3]), .Cin(\一位全加器fa封装1_6_cout ), .Xi(X[3]), .Yi(xor_6_out));
  xor xor_2 (xor_2_out, Y[7], Sub);
  xor xor_3 (xor_3_out, Y[5], Sub);
  xor xor_4 (xor_4_out, Y[6], Sub);
  \一位全加器FA封装1  \u_一位全加器fa封装1_6  (
    .Cout(\一位全加器fa封装1_6_cout ), .Si(S[2]), .Cin(\一位全加器fa封装1_7_cout ), .Xi(X[2]), .Yi(xor_5_out));
  xor xor_5 (xor_5_out, Y[2], Sub);
  xor xor_6 (xor_6_out, Y[3], Sub);
  xor xor_7 (xor_7_out, Y[4], Sub);
  // Probe on X
  // Probe on Y
  // Probe on S
  \一位全加器FA封装1  \u_一位全加器fa封装1_7  (
    .Cout(\一位全加器fa封装1_7_cout ), .Si(S[1]), .Cin(\一位全加器fa封装1_8_cout ), .Xi(X[1]), .Yi(xor_9_out));
  xor xor_8 (xor_8_out, Y[0], Sub);
  xor xor_9 (xor_9_out, Y[1], Sub);
  DotMatrix #(.matrixcols(3), .matrixrows(3)) dotmatrix_1 (.col0(\运算指示 [8:6]), .col1(\运算指示 [5:3]), .col2(\运算指示 [2:0]));
  \一位全加器FA封装1  \u_一位全加器fa封装1_8  (.Cout(\一位全加器fa封装1_8_cout ), .Si(S[0]), .Cin(Sub), .Xi(X[0]), .Yi(xor_8_out));
  // Probe on X
  // Probe on Y
  // Probe on S
  Multiplexer #(.width(9), .enable("false")) multiplexer_1 (.in0(9'hba), .in1(9'h92), .out(\运算指示 ), .sel(Sub));

  // Other names for the same wires on the sheet: OF = Overflow

  // Notes on the sheet:
  //   Cout: pull=down
  //   S: pull=down
  //   Sub: pull=down
  //   X: pull=down
  //   Overflow: pull=down
  //   Y: pull=down
  //   8位可控加减法器
  //   输入引脚区
  //   输出引脚区
  //   功能说明：  8位可控加减法器    Sub=0: S = X＋Y  Sub=1:S = X－Y   Cout为最高位进位位，Overflow为有符号溢出标志
  //   =
  //   有符号
  //   =
  //   无符号
endmodule

// CLA74182
module \_4位先行进位74182  (
  input  G4,
  input  P4,
  input  G3,
  input  P3,
  input  G2,
  input  P2,
  input  G1,
  input  P1,
  input  Cin,
  output C4,
  output C3,
  output C2,
  output C1,
  output G_star,
  output P_star
);

  wire and_1_out, and_2_out, and_3_out, and_4_out, and_5_out, and_6_out, and_7_out, and_8_out, and_9_out,
       and_10_out, and_11_out, and_12_out, and_13_out;

  and and_1 (and_1_out, P4, G3);
  and and_2 (and_2_out, P4, P3, G2);
  and and_3 (and_3_out, P4, P3, P2, G1);
  and and_4 (and_4_out, P4, P3, P2, P1, Cin);
  and and_5 (and_5_out, P3, G2);
  and and_6 (and_6_out, P3, P2, G1);
  and and_7 (and_7_out, P3, P2, P1, Cin);
  and and_8 (and_8_out, P2, G1);
  and and_9 (and_9_out, P2, P1, Cin);
  and and_10 (and_10_out, P1, Cin);
  and and_11 (and_11_out, P4, G3);
  and and_12 (and_12_out, P4, P3, G2);
  and and_13 (and_13_out, P4, P3, P2, G1);
  and and_14 (P_star, P4, P3, P2, P1);
  or or_1 (C4, G4, and_1_out, and_2_out, and_3_out, and_4_out);
  or or_2 (C3, G3, and_5_out, and_6_out, and_7_out);
  or or_3 (C2, G2, and_8_out, and_9_out);
  or or_4 (C1, G1, and_10_out);
  or or_5 (G_star, G4, and_11_out, and_12_out, and_13_out);

  // Notes on the sheet:
  //   G1: pull=down
  //   G4: pull=down
  //   G2: pull=down
  //   Cin: pull=down
  //   P4: pull=down
  //   P2: pull=down
  //   P3: pull=down
  //   G3: pull=down
  //   P1: pull=down
  //   输入引脚区
  //   4位先行进位电路
  //   请根据以上引脚以及隧道信号设计完成74LS182先行进位电路，尽可能使用多输入逻辑门，并分析电路延迟
  //   输出引脚区
endmodule

// 4位快速加法器
module \_4位快速加法器  (
  input  [3:0] X,
  input  [3:0] Y,
  input  C0,
  output [3:0] S,
  output C4,
  output C3,
  output G_star,
  output P_star
);

  wire and_1_out, and_2_out, and_3_out, and_4_out, \n4位先行进位74182_1_c1 , \n4位先行进位74182_1_c2 , or_1_out,
       or_2_out, or_3_out, or_4_out;

  \_4位先行进位74182  \u_4位先行进位74182_1  (
    .G4(and_1_out), .P4(or_1_out), .G3(and_2_out), .P3(or_2_out), .G2(and_3_out), .P2(or_3_out),
    .G1(and_4_out), .P1(or_4_out), .Cin(C0), .C4(C4), .C3(C3), .C2(\n4位先行进位74182_1_c2 ),
    .C1(\n4位先行进位74182_1_c1 ), .G_star(G_star), .P_star(P_star));
  or or_1 (or_1_out, X[3], Y[3]);
  and and_1 (and_1_out, X[3], Y[3]);
  \一位全加器FA封装1  \u_一位全加器fa封装1_1  (.Si(S[3]), .Cin(C3), .Xi(X[3]), .Yi(Y[3]));  // open: Cout
  \一位全加器FA封装1  \u_一位全加器fa封装1_2  (.Si(S[2]), .Cin(\n4位先行进位74182_1_c2 ), .Xi(X[2]), .Yi(Y[2]));  // open: Cout
  or or_2 (or_2_out, X[2], Y[2]);
  and and_2 (and_2_out, X[2], Y[2]);
  and and_3 (and_3_out, X[1], Y[1]);
  \一位全加器FA封装1  \u_一位全加器fa封装1_3  (.Si(S[1]), .Cin(\n4位先行进位74182_1_c1 ), .Xi(X[1]), .Yi(Y[1]));  // open: Cout
  or or_3 (or_3_out, X[1], Y[1]);
  \一位全加器FA封装1  \u_一位全加器fa封装1_4  (.Si(S[0]), .Cin(C0), .Xi(X[0]), .Yi(Y[0]));  // open: Cout
  or or_4 (or_4_out, X[0], Y[0]);
  and and_4 (and_4_out, X[0], Y[0]);
  // Probe on X
  // Probe on Y
  // Probe on S
  // Probe on X
  // Probe on Y
  // Probe on S

  // Notes on the sheet:
  //   Y: pull=down
  //   X: pull=down
  //   C0: pull=down
  //   输入引脚区
  //   4位快速加法器
  //   输出引脚区
  //   功能说明:4位Adder  S=X+Y，C4、C3分别为最高位、次高位进位位，C0为进位输入， G* P*为成组进位生成传递函数
  //   +
  //   =
  //   有符号加法
  //   +
  //   =
  //   无符号加法
  //   共8级门延迟，其中P,G信号一级，CLA74182两级，FA两级，模块两级*2，FA的模块延迟只能观察到1级
endmodule

// 16位快速加法器
module \_16位快速加法器  (
  input  [15:0] X,
  input  [15:0] Y,
  input  C0,
  output C16,
  output C15,
  output G_star,
  output P_star,
  output [15:0] S
);

  wire C4, C8, C12, \n4位快速加法器_1_g_star , \n4位快速加法器_1_p_star , \n4位快速加法器_2_g_star , \n4位快速加法器_2_p_star ,
       \n4位快速加法器_3_g_star , \n4位快速加法器_3_p_star , \n4位快速加法器_4_g_star , \n4位快速加法器_4_p_star ;

  \_4位先行进位74182  \u_4位先行进位74182_1  (
    .G4(\n4位快速加法器_1_g_star ), .P4(\n4位快速加法器_1_p_star ), .G3(\n4位快速加法器_2_g_star ), .P3(\n4位快速加法器_2_p_star ),
    .G2(\n4位快速加法器_3_g_star ), .P2(\n4位快速加法器_3_p_star ), .G1(\n4位快速加法器_4_g_star ), .P1(\n4位快速加法器_4_p_star ),
    .Cin(C0), .C4(C16), .C3(C12), .C2(C8), .C1(C4), .G_star(G_star), .P_star(P_star));
  \_4位快速加法器  \u_4位快速加法器_1  (
    .X(X[15:12]), .Y(Y[15:12]), .C0(C12), .S(S[15:12]), .G_star(\n4位快速加法器_1_g_star ),
    .P_star(\n4位快速加法器_1_p_star ), .C3(C15));  // open: C4
  \_4位快速加法器  \u_4位快速加法器_2  (
    .X(X[11:8]), .Y(Y[11:8]), .C0(C8), .S(S[11:8]), .G_star(\n4位快速加法器_2_g_star ), .P_star(\n4位快速加法器_2_p_star ));  // open: C4, C3
  \_4位快速加法器  \u_4位快速加法器_3  (
    .X(X[7:4]), .Y(Y[7:4]), .C0(C4), .S(S[7:4]), .G_star(\n4位快速加法器_3_g_star ), .P_star(\n4位快速加法器_3_p_star ));  // open: C4, C3
  // Probe on X
  // Probe on Y
  // Probe on S
  \_4位快速加法器  \u_4位快速加法器_4  (
    .X(X[3:0]), .Y(Y[3:0]), .C0(C0), .S(S[3:0]), .G_star(\n4位快速加法器_4_g_star ), .P_star(\n4位快速加法器_4_p_star ));  // open: C4, C3
  // Probe on X
  // Probe on Y
  // Probe on S

  // Other names for the same wires on the sheet: S0[3:0] = S[3:0]; S1[3:0] = S[7:4]; S2[3:0] = S[11:8];
  //   S3[3:0] = S[15:12]; X0[3:0] = X[3:0]; X1[3:0] = X[7:4]; X2[3:0] = X[11:8]; X3[3:0] = X[15:12]; Y0[3:0] = Y[3:0];
  //   Y1[3:0] = Y[7:4]; Y2[3:0] = Y[11:8]; Y3[3:0] = Y[15:12]

  // Notes on the sheet:
  //   Y: pull=down
  //   X: pull=down
  //   C0: pull=down
  //   输入引脚区
  //   16位快速加法器
  //   输出引脚区
  //   功能说明：16位Adder  S=X＋Y，C16、C15分别为最高位、次高位进位位，C0为进位输入， G* P*为成组进位生成传递函数
  //   +
  //   =
  //   有符号加法
  //   +
  //   =
  //   无符号加法
endmodule

// 32位加法器
module \_32位快速加法器  (
  input  C0,
  input  [31:0] X,
  input  [31:0] Y,
  output C32,
  output C31,
  output [31:0] S
);

  wire \n4位先行进位74182_1_c1 , \n4位先行进位74182_1_c2 , \n4位先行进位74182_1_c3 , \n4位先行进位74182_2_c1 ,
       \n4位先行进位74182_2_c2 , \n4位先行进位74182_2_c3 , \n4位先行进位74182_2_c4 , \n4位快速加法器_1_g_star ,
       \n4位快速加法器_1_p_star , \n4位快速加法器_2_g_star , \n4位快速加法器_2_p_star , \n4位快速加法器_3_g_star ,
       \n4位快速加法器_3_p_star , \n4位快速加法器_4_g_star , \n4位快速加法器_4_p_star , \n4位快速加法器_5_g_star ,
       \n4位快速加法器_5_p_star , \n4位快速加法器_6_g_star , \n4位快速加法器_6_p_star , \n4位快速加法器_7_g_star ,
       \n4位快速加法器_7_p_star , \n4位快速加法器_8_g_star , \n4位快速加法器_8_p_star ;

  \_4位先行进位74182  \u_4位先行进位74182_1  (
    .G4(\n4位快速加法器_1_g_star ), .P4(\n4位快速加法器_1_p_star ), .G3(\n4位快速加法器_2_g_star ), .P3(\n4位快速加法器_2_p_star ),
    .G2(\n4位快速加法器_3_g_star ), .P2(\n4位快速加法器_3_p_star ), .G1(\n4位快速加法器_4_g_star ), .P1(\n4位快速加法器_4_p_star ),
    .Cin(\n4位先行进位74182_2_c4 ), .C4(C32), .C3(\n4位先行进位74182_1_c3 ), .C2(\n4位先行进位74182_1_c2 ),
    .C1(\n4位先行进位74182_1_c1 ));  // open: G_star, P_star
  \_4位快速加法器  \u_4位快速加法器_1  (
    .X(X[31:28]), .Y(Y[31:28]), .C0(\n4位先行进位74182_1_c3 ), .S(S[31:28]), .G_star(\n4位快速加法器_1_g_star ),
    .P_star(\n4位快速加法器_1_p_star ), .C3(C31));  // open: C4
  \_4位快速加法器  \u_4位快速加法器_2  (
    .X(X[27:24]), .Y(Y[27:24]), .C0(\n4位先行进位74182_1_c2 ), .S(S[27:24]), .G_star(\n4位快速加法器_2_g_star ),
    .P_star(\n4位快速加法器_2_p_star ));  // open: C4, C3
  \_4位快速加法器  \u_4位快速加法器_3  (
    .X(X[23:20]), .Y(Y[23:20]), .C0(\n4位先行进位74182_1_c1 ), .S(S[23:20]), .G_star(\n4位快速加法器_3_g_star ),
    .P_star(\n4位快速加法器_3_p_star ));  // open: C4, C3
  // Probe on X
  // Probe on Y
  // Probe on S
  \_4位快速加法器  \u_4位快速加法器_4  (
    .X(X[19:16]), .Y(Y[19:16]), .C0(\n4位先行进位74182_2_c4 ), .S(S[19:16]), .G_star(\n4位快速加法器_4_g_star ),
    .P_star(\n4位快速加法器_4_p_star ));  // open: C4, C3
  \_4位先行进位74182  \u_4位先行进位74182_2  (
    .G4(\n4位快速加法器_5_g_star ), .P4(\n4位快速加法器_5_p_star ), .G3(\n4位快速加法器_6_g_star ), .P3(\n4位快速加法器_6_p_star ),
    .G2(\n4位快速加法器_7_g_star ), .P2(\n4位快速加法器_7_p_star ), .G1(\n4位快速加法器_8_g_star ), .P1(\n4位快速加法器_8_p_star ),
    .Cin(C0), .C4(\n4位先行进位74182_2_c4 ), .C3(\n4位先行进位74182_2_c3 ), .C2(\n4位先行进位74182_2_c2 ),
    .C1(\n4位先行进位74182_2_c1 ));  // open: G_star, P_star
  // Probe on X
  // Probe on Y
  // Probe on S
  \_4位快速加法器  \u_4位快速加法器_5  (
    .X(X[15:12]), .Y(Y[15:12]), .C0(\n4位先行进位74182_2_c3 ), .S(S[15:12]), .G_star(\n4位快速加法器_5_g_star ),
    .P_star(\n4位快速加法器_5_p_star ));  // open: C4, C3
  \_4位快速加法器  \u_4位快速加法器_6  (
    .X(X[11:8]), .Y(Y[11:8]), .C0(\n4位先行进位74182_2_c2 ), .S(S[11:8]), .G_star(\n4位快速加法器_6_g_star ),
    .P_star(\n4位快速加法器_6_p_star ));  // open: C4, C3
  \_4位快速加法器  \u_4位快速加法器_7  (
    .X(X[7:4]), .Y(Y[7:4]), .C0(\n4位先行进位74182_2_c1 ), .S(S[7:4]), .G_star(\n4位快速加法器_7_g_star ),
    .P_star(\n4位快速加法器_7_p_star ));  // open: C4, C3
  \_4位快速加法器  \u_4位快速加法器_8  (
    .X(X[3:0]), .Y(Y[3:0]), .C0(C0), .S(S[3:0]), .G_star(\n4位快速加法器_8_g_star ), .P_star(\n4位快速加法器_8_p_star ));  // open: C4, C3

  // Other names for the same wires on the sheet: S0[3:0] = S[3:0]; S1[3:0] = S[7:4]; S2[3:0] = S[11:8];
  //   S3[3:0] = S[15:12]; S4[3:0] = S[19:16]; S5[3:0] = S[23:20]; S6[3:0] = S[27:24]; S7[3:0] = S[31:28];
  //   X0[3:0] = X[3:0]; X1[3:0] = X[7:4]; X2[3:0] = X[11:8]; X3[3:0] = X[15:12]; X4[3:0] = X[19:16];
  //   X5[3:0] = X[23:20]; X6[3:0] = X[27:24]; X7[3:0] = X[31:28]; Y0[3:0] = Y[3:0]; Y1[3:0] = Y[7:4];
  //   Y2[3:0] = Y[11:8]; Y3[3:0] = Y[15:12]; Y4[3:0] = Y[19:16]; Y5[3:0] = Y[23:20]; Y6[3:0] = Y[27:24];
  //   Y7[3:0] = Y[31:28]

  // Notes on the sheet:
  //   C0: pull=down
  //   X: pull=down
  //   Y: pull=down
  //   输入引脚区
  //   32位快速加法器
  //   功能说明：利用已完成的74182以及4位快速加法器构建速度最快的32位加法器 S = X ＋ Y，并分析电路延迟；
  //   输出引脚区
  //   +
  //   =
  //   有符号加法
  //   +
  //   =
  //   无符号加法
  //   C32、C31分别为最高位、次高位进位位，C0为进位输入
endmodule

// 5位阵列乘法器
module \_5位阵列乘法器  (
  input  [4:0] X,
  input  [4:0] Y,
  output [9:0] \乘积 
);

  wire X0Y1, X0Y2, X0Y3, X0Y4, X1Y0, X1Y1, X1Y2, X1Y3, X1Y4, X2Y0, X2Y1, X2Y2, X2Y3, X2Y4, X3Y0, X3Y1, X3Y2,
       X3Y3, X3Y4, X4Y0, X4Y1, X4Y2, X4Y3, X4Y4, \一位全加器fa封装3_2_cout , \一位全加器fa封装3_2_si , \一位全加器fa封装3_3_cout ,
       \一位全加器fa封装3_4_cout , \一位全加器fa封装3_4_si , \一位全加器fa封装3_5_cout , \一位全加器fa封装3_5_si , \一位全加器fa封装3_6_cout ,
       \一位全加器fa封装3_7_cout , \一位全加器fa封装3_7_si , \一位全加器fa封装3_8_cout , \一位全加器fa封装3_8_si , \一位全加器fa封装3_9_cout ,
       \一位全加器fa封装3_9_si , \一位全加器fa封装3_10_cout , \一位全加器fa封装3_11_cout , \一位全加器fa封装3_11_si ,
       \一位全加器fa封装3_12_cout , \一位全加器fa封装3_12_si , \一位全加器fa封装3_13_cout , \一位全加器fa封装3_13_si ,
       \一位全加器fa封装3_14_cout , \一位全加器fa封装3_15_cout , \一位全加器fa封装3_15_si , \一位全加器fa封装3_16_cout ,
       \一位全加器fa封装3_16_si , \一位全加器fa封装3_17_cout , \一位全加器fa封装3_18_cout , \一位全加器fa封装3_18_si ,
       \一位全加器fa封装3_19_cout , \一位全加器fa封装3_20_cout ;

  // Probe on X
  \一位全加器FA封装3  \u_一位全加器fa封装3_1  (
    .Cout(\乘积 [9]), .Si(\乘积 [8]), .Cin(\一位全加器fa封装3_2_cout ), .Xi(\一位全加器fa封装3_3_cout ), .Yi(X4Y4));
  \一位全加器FA封装3  \u_一位全加器fa封装3_2  (
    .Cout(\一位全加器fa封装3_2_cout ), .Si(\一位全加器fa封装3_2_si ), .Cin(\一位全加器fa封装3_4_cout ), .Xi(X3Y4), .Yi(X4Y3));
  \一位全加器FA封装3  \u_一位全加器fa封装3_3  (
    .Cout(\一位全加器fa封装3_3_cout ), .Si(\乘积 [7]), .Cin(\一位全加器fa封装3_5_cout ), .Xi(\一位全加器fa封装3_6_cout ),
    .Yi(\一位全加器fa封装3_2_si ));
  // Probe on Y
  \一位全加器FA封装3  \u_一位全加器fa封装3_4  (
    .Cout(\一位全加器fa封装3_4_cout ), .Si(\一位全加器fa封装3_4_si ), .Cin(\一位全加器fa封装3_7_cout ), .Xi(X3Y3), .Yi(X4Y2));
  \一位全加器FA封装3  \u_一位全加器fa封装3_5  (
    .Cout(\一位全加器fa封装3_5_cout ), .Si(\一位全加器fa封装3_5_si ), .Cin(\一位全加器fa封装3_8_cout ), .Xi(X2Y4),
    .Yi(\一位全加器fa封装3_4_si ));
  \一位全加器FA封装3  \u_一位全加器fa封装3_6  (
    .Cout(\一位全加器fa封装3_6_cout ), .Si(\乘积 [6]), .Cin(\一位全加器fa封装3_9_cout ), .Xi(\一位全加器fa封装3_10_cout ),
    .Yi(\一位全加器fa封装3_5_si ));
  \一位全加器FA封装3  \u_一位全加器fa封装3_7  (
    .Cout(\一位全加器fa封装3_7_cout ), .Si(\一位全加器fa封装3_7_si ), .Cin(\一位全加器fa封装3_11_cout ), .Xi(X3Y2), .Yi(X4Y1));
  \一位全加器FA封装3  \u_一位全加器fa封装3_8  (
    .Cout(\一位全加器fa封装3_8_cout ), .Si(\一位全加器fa封装3_8_si ), .Cin(\一位全加器fa封装3_12_cout ), .Xi(X2Y3),
    .Yi(\一位全加器fa封装3_7_si ));
  \一位全加器FA封装3  \u_一位全加器fa封装3_9  (
    .Cout(\一位全加器fa封装3_9_cout ), .Si(\一位全加器fa封装3_9_si ), .Cin(\一位全加器fa封装3_13_cout ), .Xi(X1Y4),
    .Yi(\一位全加器fa封装3_8_si ));
  \一位全加器FA封装3  \u_一位全加器fa封装3_10  (
    .Cout(\一位全加器fa封装3_10_cout ), .Si(\乘积 [5]), .Cin(\一位全加器fa封装3_14_cout ), .Xi(1'b0), .Yi(\一位全加器fa封装3_9_si ));
  \一位全加器FA封装3  \u_一位全加器fa封装3_11  (
    .Cout(\一位全加器fa封装3_11_cout ), .Si(\一位全加器fa封装3_11_si ), .Cin(1'b0), .Xi(X3Y1), .Yi(X4Y0));
  \一位全加器FA封装3  \u_一位全加器fa封装3_12  (
    .Cout(\一位全加器fa封装3_12_cout ), .Si(\一位全加器fa封装3_12_si ), .Cin(\一位全加器fa封装3_15_cout ), .Xi(X2Y2),
    .Yi(\一位全加器fa封装3_11_si ));
  \一位全加器FA封装3  \u_一位全加器fa封装3_13  (
    .Cout(\一位全加器fa封装3_13_cout ), .Si(\一位全加器fa封装3_13_si ), .Cin(\一位全加器fa封装3_16_cout ), .Xi(X1Y3),
    .Yi(\一位全加器fa封装3_12_si ));
  \一位全加器FA封装3  \u_一位全加器fa封装3_14  (
    .Cout(\一位全加器fa封装3_14_cout ), .Si(\乘积 [4]), .Cin(\一位全加器fa封装3_17_cout ), .Xi(X0Y4), .Yi(\一位全加器fa封装3_13_si ));
  \一位全加器FA封装3  \u_一位全加器fa封装3_15  (
    .Cout(\一位全加器fa封装3_15_cout ), .Si(\一位全加器fa封装3_15_si ), .Cin(1'b0), .Xi(X2Y1), .Yi(X3Y0));
  \一位全加器FA封装3  \u_一位全加器fa封装3_16  (
    .Cout(\一位全加器fa封装3_16_cout ), .Si(\一位全加器fa封装3_16_si ), .Cin(\一位全加器fa封装3_18_cout ), .Xi(X1Y2),
    .Yi(\一位全加器fa封装3_15_si ));
  \一位全加器FA封装3  \u_一位全加器fa封装3_17  (
    .Cout(\一位全加器fa封装3_17_cout ), .Si(\乘积 [3]), .Cin(\一位全加器fa封装3_19_cout ), .Xi(X0Y3), .Yi(\一位全加器fa封装3_16_si ));
  // Probe on X
  // Probe on Y
  // Probe on \乘积 
  \一位全加器FA封装3  \u_一位全加器fa封装3_18  (
    .Cout(\一位全加器fa封装3_18_cout ), .Si(\一位全加器fa封装3_18_si ), .Cin(1'b0), .Xi(X1Y1), .Yi(X2Y0));
  \一位全加器FA封装3  \u_一位全加器fa封装3_19  (
    .Cout(\一位全加器fa封装3_19_cout ), .Si(\乘积 [2]), .Cin(\一位全加器fa封装3_20_cout ), .Xi(X0Y2), .Yi(\一位全加器fa封装3_18_si ));
  \一位全加器FA封装3  \u_一位全加器fa封装3_20  (.Cout(\一位全加器fa封装3_20_cout ), .Si(\乘积 [1]), .Cin(1'b0), .Xi(X0Y1), .Yi(X1Y0));
  \_5位乘法与门阵列  \u_5位乘法与门阵列_1  (
    .X(X), .XY4({X4Y4, X3Y4, X2Y4, X1Y4, X0Y4}), .XY3({X4Y3, X3Y3, X2Y3, X1Y3, X0Y3}),
    .XY2({X4Y2, X3Y2, X2Y2, X1Y2, X0Y2}), .XY1({X4Y1, X3Y1, X2Y1, X1Y1, X0Y1}),
    .XY0({X4Y0, X3Y0, X2Y0, X1Y0, \乘积 [0]}), .Y(Y));

  // Other names for the same wires on the sheet: P[9:0] = \乘积 ; P1 = \乘积 [1]; P2 = \乘积 [2]; P3 = \乘积 [3];
  //   P4 = \乘积 [4]; P5 = \乘积 [5]; P6 = \乘积 [6]; P7 = \乘积 [7]; P8 = \乘积 [8]; P9 = \乘积 [9]; P0 = \乘积 [0];
  //   X0Y0 = \乘积 [0]; XY0[4:0] = {X4Y0, X3Y0, X2Y0, X1Y0, \乘积 [0]}; XY1[4:0] = {X4Y1, X3Y1, X2Y1, X1Y1, X0Y1};
  //   XY2[4:0] = {X4Y2, X3Y2, X2Y2, X1Y2, X0Y2}; XY3[4:0] = {X4Y3, X3Y3, X2Y3, X1Y3, X0Y3};
  //   XY4[4:0] = {X4Y4, X3Y4, X2Y4, X1Y4, X0Y4}

  // Notes on the sheet:
  //   X: pull=down
  //   Y: pull=down
  //   5位无符号阵列乘法器
  //   输入引脚区
  //   功能说明：利用一位全加器构成5位×5位的无符号数阵列乘法器，乘积=X×Y，并分析电路延迟；
  //   输出引脚区
  //   ×
  //   =
endmodule

module \_6位补码阵列乘法器  (
  input  [5:0] X,
  input  [5:0] Y,
  output [10:0] \乘积 
);

  wire xor_1_out;
  wire [4:0] X_t, Y_t;
  wire [5:0] negator_1_out, negator_3_out;
  wire [9:0] \n5位阵列乘法器_1_乘积 ;
  wire [10:0] negator_2_out;

  // Probe on X
  \_5位阵列乘法器  \u_5位阵列乘法器_1  (.\乘积 (\n5位阵列乘法器_1_乘积 ), .X(X_t), .Y(Y_t));
  xor xor_1 (xor_1_out, X[5], Y[5]);
  Negator #(.width(6)) negator_1 (.in(X), .out(negator_1_out));
  Multiplexer #(.width(11)) multiplexer_1 (
    .in0({1'b0, \n5位阵列乘法器_1_乘积 }), .in1(negator_2_out), .out(\乘积 ), .sel(xor_1_out));  // open: en
  // Probe on Y
  Multiplexer #(.width(5), .enable("false")) multiplexer_2 (
    .in0(X[4:0]), .in1(negator_1_out[4:0]), .out(X_t), .sel(X[5]));
  Negator #(.width(11)) negator_2 (.in({1'b0, \n5位阵列乘法器_1_乘积 }), .out(negator_2_out));
  Negator #(.width(6)) negator_3 (.in(Y), .out(negator_3_out));
  Multiplexer #(.width(5), .enable("false")) multiplexer_3 (
    .in0(Y[4:0]), .in1(negator_3_out[4:0]), .out(Y_t), .sel(Y[5]));
  // Probe on X
  // Probe on Y
  // Probe on \乘积 

  // Other names for the same wires on the sheet: P[10:0] = \乘积 ; P0 = \乘积 [0]; P1 = \乘积 [1]; P2 = \乘积 [2];
  //   P3 = \乘积 [3]; P4 = \乘积 [4]; P5 = \乘积 [5]; P6 = \乘积 [6]; P7 = \乘积 [7]; P8 = \乘积 [8]; P9 = \乘积 [9];
  //   P10 = \乘积 [10]; X4_0[4:0] = X[4:0]; Y4_0[4:0] = Y[4:0]

  // Notes on the sheet:
  //   6位补码阵列乘法器
  //   输入引脚区
  //   功能说明：利用五位阵列乘法器6位×6位的补码阵列乘法器，乘积P = X × Y，尝试计算 －32 × 1，分析结果  
  //   输出引脚区
  //   ×
  //   =
endmodule

module \_5位无符号乘法流水线  (
);

  wire CLK, comparator_1_eq, not_1_out, \时钟信号_2_out ;
  wire [4:0] multiplier_1_cout, multiplier_1_out, \n5位乘法与门阵列_1_xy0 , \n5位乘法与门阵列_1_xy1 , \n5位乘法与门阵列_1_xy2 ,
       \n5位乘法与门阵列_1_xy3 , \n5位乘法与门阵列_1_xy4 , \乘数Y , \乘法线流水接口_1_x_prime , \乘法线流水接口_1_xy0_prime ,
       \乘法线流水接口_1_xy1_prime , \乘法线流水接口_1_xy2_prime , \乘法线流水接口_1_xy3_2 , \乘法线流水接口_1_xy4_2 ,
       \乘法线流水接口_1_y_prime , \乘法线流水接口_2_x_prime , \乘法线流水接口_2_xy0_prime , \乘法线流水接口_2_xy1_prime ,
       \乘法线流水接口_2_xy2_prime , \乘法线流水接口_2_xy3_2 , \乘法线流水接口_2_xy4_2 , \乘法线流水接口_2_y_prime , \乘法线流水接口_3_x_prime ,
       \乘法线流水接口_3_xy0_prime , \乘法线流水接口_3_xy1_prime , \乘法线流水接口_3_xy2_prime , \乘法线流水接口_3_xy3_2 ,
       \乘法线流水接口_3_xy4_2 , \乘法线流水接口_3_y_prime , \乘法线流水接口_4_x_prime , \乘法线流水接口_4_y_prime , \被乘数X ;
  wire [9:0] adder_1_out, adder_2_out, adder_3_out, adder_4_out, bit_extender_1_out, bit_extender_2_out,
       bit_extender_3_out, bit_extender_4_out, bit_extender_5_out, shifter_1_out, shifter_2_out,
       shifter_3_out, shifter_4_out, \乘法线流水接口_1_out_19 , \乘法线流水接口_2_out_19 , \乘法线流水接口_3_out_19 ,
       \乘法线流水接口_4_out_19 ;

  Clock \u_时钟信号  (.out(CLK));
  \_5位乘法与门阵列  \u_5位乘法与门阵列_1  (
    .X(\被乘数X ), .XY4(\n5位乘法与门阵列_1_xy4 ), .XY3(\n5位乘法与门阵列_1_xy3 ), .XY2(\n5位乘法与门阵列_1_xy2 ),
    .XY1(\n5位乘法与门阵列_1_xy1 ), .XY0(\n5位乘法与门阵列_1_xy0 ), .Y(\乘数Y ));
  Clock \u_时钟信号_2  (.out(\时钟信号_2_out ));
  // Probe on \被乘数X 
  assign bit_extender_1_out = {{5{1'b0}}, \n5位乘法与门阵列_1_xy0 };  // Bit_Extender bit_extender_1
  assign bit_extender_2_out = {{5{1'b0}}, \n5位乘法与门阵列_1_xy1 };  // Bit_Extender bit_extender_2
  // Probe on \乘数Y 
  Shifter #(.width(10)) shifter_1 (.in(bit_extender_2_out), .\dist (4'b0001), .out(shifter_1_out));
  Random #(.width(5), .seed(1)) random_1 (.clk(CLK), .out(\被乘数X ));  // open: next, clr
  Adder #(.width(10)) adder_1 (.a(bit_extender_1_out), .b(shifter_1_out), .out(adder_1_out));  // open: cin, cout
  \乘法线流水接口  \u_乘法线流水接口_1  (
    .X(\被乘数X ), .Y(\乘数Y ), .XY0(\n5位乘法与门阵列_1_xy0 ), .XY1(\n5位乘法与门阵列_1_xy1 ), .XY2(\n5位乘法与门阵列_1_xy2 ),
    .XY3(\n5位乘法与门阵列_1_xy3 ), .XY4(\n5位乘法与门阵列_1_xy4 ), .in_8(adder_1_out), .CLK(\时钟信号_2_out ),
    .X_prime(\乘法线流水接口_1_x_prime ), .Y_prime(\乘法线流水接口_1_y_prime ), .XY0_prime(\乘法线流水接口_1_xy0_prime ),
    .XY1_prime(\乘法线流水接口_1_xy1_prime ), .XY2_prime(\乘法线流水接口_1_xy2_prime ), .XY3_2(\乘法线流水接口_1_xy3_2 ),
    .XY4_2(\乘法线流水接口_1_xy4_2 ), .out_19(\乘法线流水接口_1_out_19 ));  // open: 同步清零_高电平有效, 使能端_低电平有效
  Random #(.width(5)) random_2 (.clk(CLK), .out(\乘数Y ));  // open: next, clr
  // Probe on \乘法线流水接口_1_x_prime 
  assign bit_extender_3_out = {{5{1'b0}}, \乘法线流水接口_1_xy2_prime };  // Bit_Extender bit_extender_3
  Shifter #(.width(10)) shifter_2 (.in(bit_extender_3_out), .\dist (4'b0010), .out(shifter_2_out));
  // Probe on \乘法线流水接口_1_y_prime 
  Adder #(.width(10)) adder_2 (.a(\乘法线流水接口_1_out_19 ), .b(shifter_2_out), .out(adder_2_out));  // open: cin, cout
  \乘法线流水接口  \u_乘法线流水接口_2  (
    .X(\乘法线流水接口_1_x_prime ), .Y(\乘法线流水接口_1_y_prime ), .XY0(\乘法线流水接口_1_xy0_prime ),
    .XY1(\乘法线流水接口_1_xy1_prime ), .XY2(\乘法线流水接口_1_xy2_prime ), .XY3(\乘法线流水接口_1_xy3_2 ),
    .XY4(\乘法线流水接口_1_xy4_2 ), .in_8(adder_2_out), .CLK(\时钟信号_2_out ), .X_prime(\乘法线流水接口_2_x_prime ),
    .Y_prime(\乘法线流水接口_2_y_prime ), .XY0_prime(\乘法线流水接口_2_xy0_prime ), .XY1_prime(\乘法线流水接口_2_xy1_prime ),
    .XY2_prime(\乘法线流水接口_2_xy2_prime ), .XY3_2(\乘法线流水接口_2_xy3_2 ), .XY4_2(\乘法线流水接口_2_xy4_2 ),
    .out_19(\乘法线流水接口_2_out_19 ));  // open: 同步清零_高电平有效, 使能端_低电平有效
  assign bit_extender_4_out = {{5{1'b0}}, \乘法线流水接口_2_xy3_2 };  // Bit_Extender bit_extender_4
  // Probe on \乘法线流水接口_2_x_prime 
  Shifter #(.width(10)) shifter_3 (.in(bit_extender_4_out), .\dist (4'b0011), .out(shifter_3_out));
  // Probe on \乘法线流水接口_2_y_prime 
  Adder #(.width(10)) adder_3 (.a(\乘法线流水接口_2_out_19 ), .b(shifter_3_out), .out(adder_3_out));  // open: cin, cout
  \乘法线流水接口  \u_乘法线流水接口_3  (
    .X(\乘法线流水接口_2_x_prime ), .Y(\乘法线流水接口_2_y_prime ), .XY0(\乘法线流水接口_2_xy0_prime ),
    .XY1(\乘法线流水接口_2_xy1_prime ), .XY2(\乘法线流水接口_2_xy2_prime ), .XY3(\乘法线流水接口_2_xy3_2 ),
    .XY4(\乘法线流水接口_2_xy4_2 ), .in_8(adder_3_out), .CLK(\时钟信号_2_out ), .X_prime(\乘法线流水接口_3_x_prime ),
    .Y_prime(\乘法线流水接口_3_y_prime ), .XY0_prime(\乘法线流水接口_3_xy0_prime ), .XY1_prime(\乘法线流水接口_3_xy1_prime ),
    .XY2_prime(\乘法线流水接口_3_xy2_prime ), .XY3_2(\乘法线流水接口_3_xy3_2 ), .XY4_2(\乘法线流水接口_3_xy4_2 ),
    .out_19(\乘法线流水接口_3_out_19 ));  // open: 同步清零_高电平有效, 使能端_低电平有效
  // Probe on \乘法线流水接口_3_x_prime 
  assign bit_extender_5_out = {{5{1'b0}}, \乘法线流水接口_3_xy4_2 };  // Bit_Extender bit_extender_5
  Shifter #(.width(10)) shifter_4 (.in(bit_extender_5_out), .\dist (4'b0100), .out(shifter_4_out));
  // Probe on \乘法线流水接口_3_y_prime 
  Adder #(.width(10)) adder_4 (.a(\乘法线流水接口_3_out_19 ), .b(shifter_4_out), .out(adder_4_out));  // open: cin, cout
  \乘法线流水接口  \u_乘法线流水接口_4  (
    .X(\乘法线流水接口_3_x_prime ), .Y(\乘法线流水接口_3_y_prime ), .XY0(\乘法线流水接口_3_xy0_prime ),
    .XY1(\乘法线流水接口_3_xy1_prime ), .XY2(\乘法线流水接口_3_xy2_prime ), .XY3(\乘法线流水接口_3_xy3_2 ),
    .XY4(\乘法线流水接口_3_xy4_2 ), .in_8(adder_4_out), .CLK(\时钟信号_2_out ), .X_prime(\乘法线流水接口_4_x_prime ),
    .Y_prime(\乘法线流水接口_4_y_prime ), .out_19(\乘法线流水接口_4_out_19 ));  // open: XY0_prime, XY1_prime, XY2_prime, XY3_2, XY4_2, 同步清零_高电平有效, 使能端_低电平有效
  // Probe on \乘法线流水接口_4_y_prime 
  // Probe on \乘法线流水接口_4_x_prime 
  // Probe on {multiplier_1_cout, multiplier_1_out}
  // Probe on \乘法线流水接口_4_out_19 
  Multiplier #(.width(5)) multiplier_1 (
    .a(\乘法线流水接口_4_x_prime ), .b(\乘法线流水接口_4_y_prime ), .out(multiplier_1_out), .cout(multiplier_1_cout));  // open: cin
  Comparator #(.width(10)) comparator_1 (
    .a({multiplier_1_cout, multiplier_1_out}), .b(\乘法线流水接口_4_out_19 ), .eq(comparator_1_eq));  // open: gt, lt
  not not_1 (not_1_out, comparator_1_eq);
  LED \u_不正确  (.in(not_1_out));

  // Notes on the sheet:
  //   第1步
  //   第2步
  //   随机产生乘法运算数据
  //   第3步
  //   第4步
endmodule

module \原码一位乘法器  (
  input  [7:0] X,
  input  [7:0] Y,
  output [15:0] \乘积 
);

  wire comparator_1_eq, comparator_2_eq, not_1_out, not_2_out, RST, \时钟_out ;
  wire [0:0] \n8位串行加法器_1_s ;
  wire [5:0] counter_1_q;
  wire [7:0] multiplexer_1_out, multiplexer_2_out, \n8位串行加法器_1_cout ;

  not not_1 (not_1_out, comparator_1_eq);
  Clock \u_时钟  (.out(\时钟_out ));
  Counter #(.width(6), .max('h3f)) counter_1 (
    .count(not_1_out), .Q(counter_1_q), .clk(\时钟_out ), .clr(RST));  // open: load, D, carry
  Comparator #(.width(6)) comparator_1 (.a(6'b001001), .b(counter_1_q), .eq(comparator_1_eq));  // open: gt, lt
  not not_2 (not_2_out, comparator_1_eq);
  Comparator #(.width(6)) comparator_2 (.a({6{1'b0}}), .b(counter_1_q), .eq(comparator_2_eq));  // open: gt, lt
  Button \u_复位  (.out(RST));
  // Probe on \乘积 [15:8]
  Register register_1 (.D(\n8位串行加法器_1_cout ), .en(not_2_out), .Q(\乘积 [15:8]), .clk(\时钟_out ), .clr(RST));
  \_8位串行加法器  \u_8位串行加法器_1  (
    .X(\乘积 [15:8]), .Y(multiplexer_1_out), .S({\n8位串行加法器_1_cout [6:0], \n8位串行加法器_1_s [0]}),
    .Cout(\n8位串行加法器_1_cout [7]));  // open: Cin, Overflow
  Multiplexer #(.width(8)) multiplexer_1 (
    .in0({8{1'b0}}), .in1(X), .out(multiplexer_1_out), .sel(\乘积 [0]));  // open: en
  // Probe on X
  // Probe on Y
  // Probe on \乘积 
  Multiplexer #(.width(8)) multiplexer_2 (
    .in0({\n8位串行加法器_1_s [0], \乘积 [7:1]}), .in1(Y), .out(multiplexer_2_out), .sel(comparator_2_eq));  // open: en
  // Probe on \乘积 [7:0]
  Register Y_2 (.D(multiplexer_2_out), .en(not_2_out), .Q(\乘积 [7:0]), .clk(\时钟_out ), .clr(RST));

  // Notes on the sheet:
  //   8位无符号一位乘法器
  //   功能说明: 原码一位乘法器   乘积=X*Y，要求采用原码一位乘法实现，最终结果能输出在乘积引脚上
  //   后续所有实验中凡是涉及存储器件，如寄存器、计数器、RAM等，必须增加统一的复位信号RST，方便系统复位
  //   ∑
  //   输入输出引脚区
  //   逻辑右移一位
  //   ∑+Yn|X|
  //   ×
  //   =
  //   核心算法：{ ∑ , Y } = { ∑ ＋ Y  |X|  , Y  } / 2
  //   n
endmodule

module \补码一位乘法器  (
  input  [7:0] X,
  input  [7:0] Y,
  output [15:0] \乘积 
);

  wire clock_1_out, comparator_1_eq, comparator_2_eq, not_1_out, RST;
  wire [0:0] Y_4_q;
  wire [5:0] counter_1_q;
  wire [7:0] multiplexer_1_out, multiplexer_2_out, negator_1_out, \newΣ ;
  wire [7:7] \n8位串行加法器_1_s ;

  Clock clock_1 (.out(clock_1_out));
  Counter #(.width(6), .max('h3f), .ongoal("load")) counter_1 (
    .count(not_1_out), .Q(counter_1_q), .clk(clock_1_out), .clr(RST));  // open: load, D, carry
  Comparator #(.width(6)) comparator_1 (.a(6'b001001), .b(counter_1_q), .eq(comparator_1_eq));  // open: gt, lt
  not not_1 (not_1_out, comparator_1_eq);
  Button \u_复位  (.out(RST));
  Comparator #(.width(6)) comparator_2 (.a({6{1'b0}}), .b(counter_1_q), .eq(comparator_2_eq));  // open: gt, lt
  // Probe on \乘积 [15:8]
  Register register (.D({{2{\newΣ [7]}}, \newΣ [5:0]}), .en(not_1_out), .Q(\乘积 [15:8]), .clk(clock_1_out), .clr(RST));
  \_8位串行加法器  \u_8位串行加法器_1  (
    .X(\乘积 [15:8]), .Y(multiplexer_1_out), .S({\newΣ [7], \newΣ [5:0], \n8位串行加法器_1_s [7]}));  // open: Cin, Cout, Overflow
  Multiplexer #(.select(2), .width(8)) multiplexer_1 (
    .in0({8{1'b0}}), .in1(X), .in2(negator_1_out), .in3({8{1'b0}}), .out(multiplexer_1_out),
    .sel({\乘积 [0], Y_4_q[0]}));  // open: en
  Multiplexer #(.width(8)) multiplexer_2 (
    .in0({\n8位串行加法器_1_s [7], \乘积 [7:1]}), .in1(Y), .out(multiplexer_2_out), .sel(comparator_2_eq));  // open: en
  Negator negator_1 (.in(X), .out(negator_1_out));
  // Probe on \乘积 [7:0]
  Register Y_2 (.D(multiplexer_2_out), .en(not_1_out), .Q(\乘积 [7:0]), .clk(clock_1_out), .clr(RST));
  // Probe on X
  // Probe on Y
  // Probe on \乘积 
  // Probe on Y_4_q[0]
  Register #(.width(1)) Y_4 (.D(\乘积 [0]), .en(not_1_out), .Q(Y_4_q[0]), .clk(clock_1_out), .clr(RST));

  // Other names for the same wires on the sheet: newΣ[6] = \newΣ [7]; Σ[7:0] = \乘积 [15:8]

  // Notes on the sheet:
  //   8位补码 Booth一位乘法器
  //   功能说明: 补码一位乘法器   乘积=X×Y，要求采用补码一位乘法实现，最终结果能输出在乘积引脚上
  //   后续所有实验中凡是涉及存储器件，如寄存器、计数器、RAM等，必须增加统一的复位信号RST，方便系统复位
  //   算术右移一位
  //   输入输出引脚区
  //   核心算法：{ ∑,Y } = { ∑ ＋（Y      －  Y  ）[X]   , Y } / 2
  //   ∑+ (Yn+1-Yn)补
  //   ×
  //   =
  //   n
  //   n+1
  //   补
  //   n+1
  //   n+1
endmodule

// ALU
module \算术逻辑运算单元ALU  (
  input  [31:0] X,
  input  [31:0] Y,
  input  [3:0] AluOP,
  output Signed_Overflow,
  output UnSigned_Overflow,
  output Equal,
  output [31:0] Result,
  output [31:0] Result_2
);

  wire and_2_out, and_3_out, and_4_out, and_5_out, and_6_out, and_7_out, comparator_1_eq, comparator_3_eq,
       comparator_5_gt, comparator_5_lt, comparator_6_gt, comparator_6_lt, comparator_7_eq, comparator_7_gt,
       comparator_7_lt, comparator_8_gt, comparator_9_lt, comparator_10_eq, comparator_11_eq, not_1_out,
       not_2_out, or_1_out, or_3_out, or_5_out, signed_cmp, signed_overflow_t, unsigned_cmp,
       unsigned_overflow_t, \自带加法器包装_3_cout , \自带加法器包装_4_cout , \自带加法器包装_6_cout , \自带加法器包装_7_cout ;
  wire [1:0] multiplexer_3_out_2;
  wire [3:0] multiplexer_3_out;
  wire [31:0] add_or_sub_result, and_result, div_remain, div_result, mul_rslt_h, mul_rslt_l, mul_rslt_x_1h,
       mul_rslt_x_1l, mul_rslt_x_y_1h, mul_rslt_x_y_1l, mul_rslt_y_1h, mul_rslt_y_1l, multiplexer_7_out,
       multiplier_1_cout, multiplier_1_out, negator_1_out, negator_2_out, negator_3_out, nor_result,
       or_result, sar, sll, slr, xor_result;

  // Probe on X
  // Probe on X
  // Probe on Y
  // Probe on Y
  Shifter #(.width(32)) shifter_1 (.in(X), .\dist (Y[4:0]), .out(sll));
  Shifter #(.width(32), .shift("ar")) shifter_2 (.in(X), .\dist (Y[4:0]), .out(sar));
  Shifter #(.width(32), .shift("lr")) shifter_3 (.in(X), .\dist (Y[4:0]), .out(slr));
  Divider #(.width(32)) divider_1 (.a(X), .b(Y), .out(div_result), .rem(div_remain));  // open: upper
  Multiplier #(.width(32)) multiplier_1 (
    .a({1'b0, X[30:0]}), .b({1'b0, Y[30:0]}), .out(multiplier_1_out), .cout(multiplier_1_cout));  // open: cin
  // Probe on multiplier_1_cout
  \自带加法器包装  \u_自带加法器包装_1  (
    .x({2'b00, Y[30:1]}), .y(multiplier_1_cout), .Out(mul_rslt_x_1h), .Cin(\自带加法器包装_3_cout ));  // open: Cout
  // Probe on AluOP
  \自带加法器包装  \u_自带加法器包装_2  (
    .x({2'b00, X[30:1]}), .y(multiplier_1_cout), .Out(mul_rslt_y_1h), .Cin(\自带加法器包装_4_cout ));  // open: Cout
  // Probe on Result
  // Probe on Result
  \自带加法器包装  \u_自带加法器包装_3  (
    .x(multiplier_1_out), .y({Y[0], {31{1'b0}}}), .Out(mul_rslt_x_1l), .Cout(\自带加法器包装_3_cout ));  // open: Cin
  \自带加法器包装  \u_自带加法器包装_4  (
    .x(multiplier_1_out), .y({X[0], {31{1'b0}}}), .Out(mul_rslt_y_1l), .Cout(\自带加法器包装_4_cout ));  // open: Cin
  Multiplexer #(.select(2), .width(32)) multiplexer_1 (
    .in0(multiplier_1_cout), .in1(mul_rslt_x_1h), .in2(mul_rslt_y_1h), .in3(mul_rslt_x_y_1h),
    .out(mul_rslt_h), .sel({Y[31], X[31]}));  // open: en
  // Probe on multiplier_1_out
  // Probe on Result_2
  Multiplexer #(.select(2), .width(32)) multiplexer_2 (
    .in0({32{1'b0}}), .in1(mul_rslt_h), .in2(div_remain), .in3({32{1'b0}}), .out(Result_2),
    .sel(multiplexer_3_out_2));  // open: en
  Multiplexer #(.width(4)) multiplexer_3 (
    .in0(4'b0000), .in1(AluOP), .out({multiplexer_3_out[3], multiplexer_3_out_2, multiplexer_3_out[0]}),
    .sel(or_1_out));  // open: en
  \自带加法器包装  \u_自带加法器包装_5  (
    .x({1'b0, X[31:1]}), .y(mul_rslt_x_1h), .Out(mul_rslt_x_y_1h), .Cin(\自带加法器包装_6_cout ));  // open: Cout
  Multiplexer #(.select(2), .width(32)) multiplexer_4 (
    .in0(multiplier_1_out), .in1(mul_rslt_x_1l), .in2(mul_rslt_y_1l), .in3(mul_rslt_x_y_1l),
    .out(mul_rslt_l), .sel({Y[31], X[31]}));  // open: en
  \自带加法器包装  \u_自带加法器包装_6  (
    .x({X[0], {31{1'b0}}}), .y(mul_rslt_x_1l), .Out(mul_rslt_x_y_1l), .Cout(\自带加法器包装_6_cout ));  // open: Cin
  or or_1 (or_1_out, comparator_1_eq, comparator_3_eq);
  Comparator #(.width(4)) comparator_1 (.a(4'b0011), .b(AluOP), .eq(comparator_1_eq));  // open: gt, lt
  Comparator #(.width(32)) comparator_2 (.a(X), .b(Y), .eq(Equal));  // open: gt, lt
  assign and_result = X & Y;  // AND_Gate and_1, 32 bits wide
  assign or_result = X | Y;  // OR_Gate or_2, 32 bits wide
  Comparator #(.width(4)) comparator_3 (.a(4'b0100), .b(AluOP), .eq(comparator_3_eq));  // open: gt, lt
  assign xor_result = X ^ Y;  // XOR_Gate xor_1, 32 bits wide
  assign nor_result = ~(X | Y);  // NOR_Gate nor_1, 32 bits wide
  Comparator #(.width(32), .mode("unsigned")) comparator_4 (.a(X), .b(Y), .lt(unsigned_cmp));  // open: gt, eq
  Comparator #(.width(32)) comparator_5 (
    .a(X), .b({32{1'b0}}), .gt(comparator_5_gt), .lt(comparator_5_lt));  // open: eq
  Comparator #(.width(32)) comparator_6 (
    .a(multiplexer_7_out), .b({32{1'b0}}), .gt(comparator_6_gt), .lt(comparator_6_lt));  // open: eq
  Comparator #(.width(32)) comparator_7 (
    .a(add_or_sub_result), .b({32{1'b0}}), .gt(comparator_7_gt), .eq(comparator_7_eq), .lt(comparator_7_lt));
  or or_3 (or_3_out, comparator_7_gt, comparator_7_eq);
  Multiplexer #(.select(4), .width(32)) multiplexer_5 (
    .in0(sll), .in1(sar), .in2(slr), .in3(mul_rslt_l), .in4(div_result), .in5(add_or_sub_result),
    .in6(add_or_sub_result), .in7(and_result), .in8(or_result), .in9(xor_result), .in10(nor_result),
    .in11({{31{1'b0}}, signed_cmp}), .in12({{31{1'b0}}, unsigned_cmp}), .in13(32'h300000), .in14(32'h300000),
    .in15(32'h300000), .out(Result), .sel(AluOP));  // open: en
  and and_2 (and_2_out, comparator_5_gt, comparator_6_gt, comparator_7_lt);
  and and_3 (and_3_out, comparator_5_lt, comparator_6_lt, or_3_out);
  or or_4 (signed_overflow_t, and_2_out, and_3_out);
  Negator #(.width(32)) negator_1 (.in(X), .out(negator_1_out));
  Negator #(.width(32)) negator_2 (.in(Y), .out(negator_2_out));
  Multiplexer multiplexer_6 (.in0(1'b0), .in1(signed_overflow_t), .out(Signed_Overflow), .sel(or_5_out));  // open: en
  Comparator #(.width(32)) comparator_8 (.a(negator_1_out), .b(negator_2_out), .gt(comparator_8_gt));  // open: eq, lt
  Comparator #(.width(32)) comparator_9 (
    .a({1'b0, X[30:0]}), .b({1'b0, Y[30:0]}), .lt(comparator_9_lt));  // open: gt, eq
  not not_1 (not_1_out, X[31]);
  not not_2 (not_2_out, Y[31]);
  \自带加法器包装  \u_自带加法器包装_7  (
    .x(X), .y(multiplexer_7_out), .Out(add_or_sub_result), .Cout(\自带加法器包装_7_cout ));  // open: Cin
  Comparator #(.width(4)) comparator_10 (.a(4'b0101), .b(AluOP), .eq(comparator_10_eq));  // open: gt, lt
  and and_4 (and_4_out, comparator_9_lt, not_1_out, not_2_out);
  Multiplexer #(.width(32)) multiplexer_7 (
    .in0(Y), .in1(negator_3_out), .out(multiplexer_7_out), .sel(and_7_out));  // open: en
  Negator #(.width(32)) negator_3 (.in(Y), .out(negator_3_out));
  Multiplexer multiplexer_8 (
    .in0(1'b0), .in1(unsigned_overflow_t), .out(UnSigned_Overflow), .sel(or_5_out));  // open: en
  or or_5 (or_5_out, comparator_10_eq, comparator_11_eq);
  Comparator #(.width(4)) comparator_11 (.a(4'b0110), .b(AluOP), .eq(comparator_11_eq));  // open: gt, lt
  and and_5 (and_5_out, comparator_8_gt, X[31], Y[31]);
  and and_6 (and_6_out, X[31], not_2_out);
  and and_7 (and_7_out, 1'b1, AluOP[1]);
  or or_6 (signed_cmp, and_4_out, and_5_out, and_6_out);
  xor xor_2 (unsigned_overflow_t, \自带加法器包装_7_cout , and_7_out);

  // Other names for the same wires on the sheet: OF = Signed_Overflow; Result2[31:0] = Result_2; S[3:0] = AluOP;
  //   signed_cmp32[0] = signed_cmp; unsigned_cmp32[0] = unsigned_cmp; UOF = UnSigned_Overflow

  // Notes on the sheet:
  //   X: pull=down
  //   Y: pull=down
  //   AluOP: pull=down
  //   32位MIPS运算器
  //   不要改变此引脚区域内容，也不要改变ALU封装形式
  //   输入引脚
  //   请在下方利用上方输入输出引脚的隧道信号构建ALU电路，ctrl+d复制选择部件
  //   华中科技大学计算机学院 计算机组成原理，鸣谢加州大学伯克利CS61C课程
  //   输出引脚
  //   探测区域
endmodule

module \ALU自动测试  (
  output [7:0] Test_num,
  output Equal
);

  wire ADD, AND, and_1_out, CF, CF_S, CLK, comparator_2_eq, comparator_3_eq, DIV, \EQ__标志 , EQ_OK, EQ_S,
       Halt, MUL, multiplexer_1_out, NEQ, nHalt, NOR, OF, OF_OK, OR, priority_encoder_1_gs, ROK, SAR, SCMP,
       SLL, SLR, SUB, tunnel, UCMP, UOF_OK, XOR, \与 , \乘法 , \减法 , \加法 , \异或 , \悬空检测 , \或 , \或非 , \无符号比较 ,
       \无符号溢出标志 , \有符号比较 , \有符号溢出标志 , \算术右移 , \逻辑右移 , \逻辑左移 , \除法 ;
  wire [2:2] FLAG_Standard;
  wire [3:0] ALUOP, High, Low, Mid;
  wire [7:0] adder_1_out, \单项评分_1_total , \单项评分_1_扣分 , \单项评分_1_正确条数 , \单项评分_2_total , \单项评分_2_扣分 ,
       \单项评分_2_正确条数 , \单项评分_3_total , \单项评分_3_扣分 , \单项评分_3_正确条数 , \单项评分_4_total , \单项评分_4_扣分 , \单项评分_4_正确条数 ,
       \单项评分_5_total , \单项评分_5_扣分 , \单项评分_5_正确条数 , \单项评分_6_total , \单项评分_6_扣分 , \单项评分_6_正确条数 ,
       \单项评分_7_total , \单项评分_7_扣分 , \单项评分_7_正确条数 , \单项评分_8_total , \单项评分_8_扣分 , \单项评分_8_正确条数 ,
       \单项评分_9_total , \单项评分_9_扣分 , \单项评分_9_正确条数 , \单项评分_10_total , \单项评分_10_扣分 , \单项评分_10_正确条数 ,
       \单项评分_11_total , \单项评分_11_扣分 , \单项评分_11_正确条数 , \单项评分_12_total , \单项评分_12_扣分 , \单项评分_12_正确条数 ,
       \单项评分_13_total , \单项评分_13_扣分 , \单项评分_13_正确条数 , \单项评分_14_total , \单项评分_14_扣分 , \单项评分_14_正确条数 ,
       \单项评分_15_total , \单项评分_15_扣分 , \单项评分_15_正确条数 , \单项评分_16_total , \单项评分_16_扣分 , \单项评分_16_正确条数 ,
       \总评分_result ;
  wire [9:0] counter_1_q;
  wire [31:0] bit_extender_1_out, R, R2, R2_Standard, R_Standard, X, Y;

  Clock clock_1 (.out(CLK));
  Register register_1 (.D(adder_1_out), .en(nHalt), .Q(Test_num), .clk(CLK));  // open: clr
  LED \u_测试完成  (.in(Halt));
  Counter #(.width(10), .max('h3ff)) counter_1 (
    .count(NEQ), .Q(counter_1_q), .clk(CLK), .clr(Halt));  // open: load, D, carry
  LED #(.active("false")) led_1 (.in(\逻辑左移 ));
  LED #(.active("false")) led_2 (.in(\逻辑右移 ));
  LED #(.active("false")) led_3 (.in(\EQ__标志 ));
  \单项评分  \u_单项评分_1  (
    .EQ(ROK), .EN(nHalt), .\分值 (5'b00101), .CLK(CLK), .\正确条数 (\单项评分_1_正确条数 ), .\扣分 (\单项评分_1_扣分 ),
    .Right(\逻辑左移 ), .ALU_SWITCH(SLL), .Total(\单项评分_1_total ));
  // Probe on \单项评分_1_total 
  // Probe on \单项评分_1_正确条数 
  // Probe on \单项评分_1_扣分 
  Adder adder_1 (.a(8'h1), .b(Test_num), .out(adder_1_out));  // open: cin, cout
  not not_1 (nHalt, Halt);
  Comparator #(.width(4)) comparator_1 (.a(ALUOP), .b(4'b1111), .eq(Halt));  // open: gt, lt
  and and_1 (and_1_out, ~Halt, NEQ);  // AND_Gate
  LED #(.active("false")) led_4 (.in(\算术右移 ));
  LED led_5 (.in(\悬空检测 ));
  \单项评分  \u_单项评分_2  (
    .EQ(ROK), .EN(nHalt), .\分值 (5'b00101), .CLK(CLK), .\正确条数 (\单项评分_2_正确条数 ), .\扣分 (\单项评分_2_扣分 ),
    .Right(\算术右移 ), .ALU_SWITCH(SAR), .Total(\单项评分_2_total ));
  // Probe on \单项评分_3_total 
  // Probe on \单项评分_2_total 
  // Probe on \单项评分_2_正确条数 
  // Probe on \单项评分_2_扣分 
  // Probe on X
  trace trace_1 (
    .in_1(Test_num), .X(X), .Y(Y), .AluOP(ALUOP), .R(R_Standard), .R2(R2_Standard),
    .FLAGS({FLAG_Standard[2], CF_S, EQ_S}));
  RAM #(.addrWidth(10), .dataWidth(32), .bus("separate")) ram_1 (
    .addr(counter_1_q), .din(X), .str(and_1_out), .clk(CLK));  // open: data, sel, ld, clr
  LED #(.active("false")) led_6 (.in(\与 ));
  LED #(.active("false")) led_7 (.in(\或 ));
  LED #(.active("false")) led_8 (.in(\有符号溢出标志 ));
  \单项评分  \u_单项评分_3  (
    .EQ(ROK), .EN(nHalt), .\分值 (5'b00101), .CLK(CLK), .\正确条数 (\单项评分_3_正确条数 ), .\扣分 (\单项评分_3_扣分 ),
    .Right(\逻辑右移 ), .ALU_SWITCH(SLR), .Total(\单项评分_3_total ));
  // Probe on \单项评分_4_total 
  // Probe on \单项评分_3_正确条数 
  // Probe on \单项评分_4_正确条数 
  // Probe on \单项评分_3_扣分 
  // Probe on Y
  \单项评分  \u_单项评分_4  (
    .EQ(ROK), .EN(nHalt), .\分值 (5'b00101), .CLK(CLK), .\正确条数 (\单项评分_4_正确条数 ), .\扣分 (\单项评分_4_扣分 ),
    .Right(\乘法 ), .ALU_SWITCH(MUL), .Total(\单项评分_4_total ));
  // Probe on \单项评分_6_total 
  // Probe on \单项评分_6_正确条数 
  // Probe on \单项评分_6_扣分 
  // Probe on \单项评分_4_扣分 
  // Probe on ALUOP
  RAM #(.addrWidth(10), .dataWidth(32), .bus("separate")) ram_2 (
    .addr(counter_1_q), .din(Y), .str(and_1_out), .clk(CLK));  // open: data, sel, ld, clr
  assign bit_extender_1_out = {{28{1'b0}}, ALUOP};  // Bit_Extender bit_extender_1
  LED #(.active("false")) led_9 (.in(\或非 ));
  LED #(.active("false")) led_10 (.in(\异或 ));
  \单项评分  \u_单项评分_5  (
    .EQ(ROK), .EN(nHalt), .\分值 (5'b00101), .CLK(CLK), .\正确条数 (\单项评分_5_正确条数 ), .\扣分 (\单项评分_5_扣分 ),
    .Right(\加法 ), .ALU_SWITCH(ADD), .Total(\单项评分_5_total ));
  \单项评分  \u_单项评分_6  (
    .EQ(ROK), .EN(nHalt), .\分值 (5'b00101), .CLK(CLK), .\正确条数 (\单项评分_6_正确条数 ), .\扣分 (\单项评分_6_扣分 ),
    .Right(\除法 ), .ALU_SWITCH(DIV), .Total(\单项评分_6_total ));
  // Probe on \单项评分_5_total 
  // Probe on \单项评分_5_正确条数 
  // Probe on \单项评分_5_扣分 
  // Probe on R_Standard
  \算术逻辑运算单元ALU  \u_算术逻辑运算单元alu_1  (
    .AluOP(ALUOP), .X(X), .Equal(Equal), .Result(R), .Signed_Overflow(OF), .Result_2(R2),
    .UnSigned_Overflow(CF), .Y(Y));
  LED #(.active("false")) led_11 (.in(\乘法 ));
  LED #(.active("false")) led_12 (.in(\除法 ));
  LED #(.active("false")) led_13 (.in(\无符号溢出标志 ));
  \单项评分  \u_单项评分_7  (
    .EQ(ROK), .EN(nHalt), .\分值 (5'b00101), .CLK(CLK), .\正确条数 (\单项评分_7_正确条数 ), .\扣分 (\单项评分_7_扣分 ),
    .Right(\减法 ), .ALU_SWITCH(SUB), .Total(\单项评分_7_total ));
  // Probe on \单项评分_7_total 
  // Probe on \单项评分_7_正确条数 
  // Probe on \单项评分_7_扣分 
  // Probe on R
  RAM #(.addrWidth(10), .dataWidth(32), .bus("separate")) ram_3 (
    .addr(counter_1_q), .din(bit_extender_1_out), .str(and_1_out), .clk(CLK));  // open: data, sel, ld, clr
  LED #(.active("false")) led_14 (.in(\加法 ));
  LED #(.active("false")) led_15 (.in(\减法 ));
  \单项评分  \u_单项评分_8  (
    .EQ(ROK), .EN(nHalt), .\分值 (5'b00101), .CLK(CLK), .\正确条数 (\单项评分_8_正确条数 ), .\扣分 (\单项评分_8_扣分 ),
    .Right(\与 ), .ALU_SWITCH(AND), .Total(\单项评分_8_total ));
  // Probe on \单项评分_8_total 
  // Probe on \单项评分_8_正确条数 
  // Probe on \单项评分_8_扣分 
  \总评分  \u_总评分  (
    .in_1(\单项评分_1_扣分 ), .in_2(\单项评分_2_扣分 ), .in_3(\单项评分_3_扣分 ), .in_4(\单项评分_4_扣分 ), .in_5(\单项评分_6_扣分 ),
    .in_6(\单项评分_5_扣分 ), .in_7(\单项评分_7_扣分 ), .in_8(\单项评分_8_扣分 ), .in_9(\单项评分_9_扣分 ), .in_10(\单项评分_10_扣分 ),
    .in_11(\单项评分_11_扣分 ), .in_12(\单项评分_12_扣分 ), .in_13(\单项评分_13_扣分 ), .in_14(\单项评分_14_扣分 ),
    .in_15(\单项评分_15_扣分 ), .in_16(\单项评分_16_扣分 ), .\悬空扣分 (\悬空检测 ), .Result(\总评分_result ), .High(High),
    .Low(Low), .Mid(Mid));
  Hex_Digit_Display hex_digit_display_1 (.value(High));  // open: dp
  Hex_Digit_Display hex_digit_display_2 (.value(Mid));  // open: dp
  \单项评分  \u_单项评分_9  (
    .EQ(ROK), .EN(nHalt), .\分值 (5'b00101), .CLK(CLK), .\正确条数 (\单项评分_9_正确条数 ), .\扣分 (\单项评分_9_扣分 ),
    .Right(\或 ), .ALU_SWITCH(OR), .Total(\单项评分_9_total ));
  // Probe on nothing
  // Probe on \单项评分_9_正确条数 
  // Probe on \单项评分_9_扣分 
  // Probe on \总评分_result 
  Hex_Digit_Display hex_digit_display_3 (.value(Low));  // open: dp
  LED #(.active("false")) led_16 (.in(\有符号比较 ));
  LED #(.active("false")) led_17 (.in(\无符号比较 ));
  \单项评分  \u_单项评分_10  (
    .EQ(ROK), .EN(nHalt), .\分值 (5'b00101), .CLK(CLK), .\正确条数 (\单项评分_10_正确条数 ), .\扣分 (\单项评分_10_扣分 ),
    .Right(\异或 ), .ALU_SWITCH(XOR), .Total(\单项评分_10_total ));
  // Probe on \单项评分_10_total 
  // Probe on \单项评分_11_total 
  // Probe on \单项评分_10_正确条数 
  // Probe on \单项评分_10_扣分 
  \单项评分  \u_单项评分_11  (
    .EQ(ROK), .EN(nHalt), .\分值 (5'b00101), .CLK(CLK), .\正确条数 (\单项评分_11_正确条数 ), .\扣分 (\单项评分_11_扣分 ),
    .Right(\或非 ), .ALU_SWITCH(NOR), .Total(\单项评分_11_total ));
  // Probe on \单项评分_12_total 
  // Probe on \单项评分_11_正确条数 
  // Probe on \单项评分_12_正确条数 
  // Probe on \单项评分_11_扣分 
  \单项评分  \u_单项评分_12  (
    .EQ(ROK), .EN(nHalt), .\分值 (5'b00101), .CLK(CLK), .\正确条数 (\单项评分_12_正确条数 ), .\扣分 (\单项评分_12_扣分 ),
    .Right(\有符号比较 ), .ALU_SWITCH(SCMP), .Total(\单项评分_12_total ));
  // Probe on \单项评分_13_total 
  // Probe on \单项评分_13_正确条数 
  // Probe on \单项评分_12_扣分 
  // Probe on \单项评分_13_扣分 
  \单项评分  \u_单项评分_13  (
    .EQ(ROK), .EN(nHalt), .\分值 (5'b00101), .CLK(CLK), .\正确条数 (\单项评分_13_正确条数 ), .\扣分 (\单项评分_13_扣分 ),
    .Right(\无符号比较 ), .ALU_SWITCH(UCMP), .Total(\单项评分_13_total ));
  \单项评分  \u_单项评分_14  (
    .EQ(EQ_OK), .EN(nHalt), .\分值 (5'b01000), .CLK(CLK), .\正确条数 (\单项评分_14_正确条数 ), .\扣分 (\单项评分_14_扣分 ),
    .Right(\EQ__标志 ), .ALU_SWITCH(EQ_OK), .Total(\单项评分_14_total ));
  // Probe on \单项评分_14_total 
  // Probe on \单项评分_14_正确条数 
  // Probe on \单项评分_14_扣分 
  \单项评分  \u_单项评分_15  (
    .EQ(OF_OK), .EN(nHalt), .\分值 (5'b01000), .CLK(CLK), .\正确条数 (\单项评分_15_正确条数 ), .\扣分 (\单项评分_15_扣分 ),
    .Right(\有符号溢出标志 ), .ALU_SWITCH(1'b1), .Total(\单项评分_15_total ));
  // Probe on \单项评分_15_total 
  // Probe on \单项评分_15_正确条数 
  // Probe on \单项评分_15_扣分 
  \单项评分  \u_单项评分_16  (
    .EQ(UOF_OK), .EN(nHalt), .\分值 (5'b01000), .CLK(CLK), .\正确条数 (\单项评分_16_正确条数 ), .\扣分 (\单项评分_16_扣分 ),
    .Right(\无符号溢出标志 ), .ALU_SWITCH(1'b1), .Total(\单项评分_16_total ));
  // Probe on \单项评分_16_total 
  // Probe on \单项评分_16_正确条数 
  // Probe on \单项评分_16_扣分 
  // Probe on ALUOP
  Decoder #(.select(4), .enable("false")) decoder_1 (
    .out0(SLL), .out1(SAR), .out2(SLR), .out3(MUL), .out4(DIV), .out5(ADD), .out6(SUB), .out7(AND),
    .out8(OR), .out9(XOR), .out10(NOR), .out11(SCMP), .out12(UCMP), .sel(ALUOP));  // open: out13, out14, out15
  xnor xnor_1 (EQ_OK, EQ_S, Equal);
  xnor xnor_2 (OF_OK, FLAG_Standard[2], OF);
  xnor xnor_3 (UOF_OK, CF_S, CF);
  Comparator #(.width(32)) comparator_2 (.a(R_Standard), .b(R), .eq(comparator_2_eq));  // open: gt, lt
  Comparator #(.width(32)) comparator_3 (.a(R2_Standard), .b(R2), .eq(comparator_3_eq));  // open: gt, lt
  Multiplexer #(.disabled(0), .enable("false")) multiplexer_1 (
    .in0(1'b1), .in1(1'b1), .out(multiplexer_1_out), .sel(CF));
  and and_2 (ROK, comparator_2_eq, comparator_3_eq);
  or or_1 (tunnel, ADD, SUB);
  Priority_Encoder #(.select(1)) priority_encoder_1 (
    .in0(multiplexer_1_out), .in1(multiplexer_1_out), .gs(priority_encoder_1_gs));  // open: out, en_out, en_in
  not not_2 (\悬空检测 , priority_encoder_1_gs);
  nand nand_1 (NEQ, EQ_OK, OF_OK, UOF_OK, ROK);

  // Other names for the same wires on the sheet: EQ = Equal; FLAG_Standard[1:0] = {CF_S, EQ_S};
  //   OF_S = FLAG_Standard[2]

  // Notes on the sheet:
  //   操作码为F停止
  //   错误记录X
  //   错误记录Y
  //   运算故障指示灯，红色异常
  //   错误记录ALUOP
  //   3个存储器存储的是所有错误的测试用例
  //   错误扣分值
  //   成绩
  //   ctrl+K驱动时钟自动测试
  //   华中科技大学：计算机组成课程组
  //   悬空扣5分
  //   错误扣分值
  //   各部分分值
  //   各部分扣分
  //   悬空检测
endmodule

// 与门阵列
module \_5位乘法与门阵列  (
  input  [4:0] X,
  input  [4:0] Y,
  output [4:0] XY0,
  output [4:0] XY1,
  output [4:0] XY2,
  output [4:0] XY3,
  output [4:0] XY4
);

  and and_1 (XY0[4], X[4], Y[0]);
  and and_2 (XY1[4], X[4], Y[1]);
  and and_3 (XY2[4], X[4], Y[2]);
  and and_4 (XY3[4], X[4], Y[3]);
  and and_5 (XY4[4], X[4], Y[4]);
  and and_6 (XY0[3], X[3], Y[0]);
  and and_7 (XY1[3], X[3], Y[1]);
  and and_8 (XY2[3], X[3], Y[2]);
  and and_9 (XY3[3], X[3], Y[3]);
  and and_10 (XY4[3], X[3], Y[4]);
  and and_11 (XY0[2], X[2], Y[0]);
  and and_12 (XY1[2], X[2], Y[1]);
  and and_13 (XY2[2], X[2], Y[2]);
  and and_14 (XY3[2], X[2], Y[3]);
  and and_15 (XY4[2], X[2], Y[4]);
  and and_16 (XY0[0], X[0], Y[0]);
  and and_17 (XY0[1], X[1], Y[0]);
  and and_18 (XY1[1], X[1], Y[1]);
  and and_19 (XY1[0], X[0], Y[1]);
  and and_20 (XY2[1], X[1], Y[2]);
  and and_21 (XY2[0], X[0], Y[2]);
  and and_22 (XY3[1], X[1], Y[3]);
  and and_23 (XY3[0], X[0], Y[3]);
  and and_24 (XY4[0], X[0], Y[4]);
  and and_25 (XY4[1], X[1], Y[4]);

  // Other names for the same wires on the sheet: X0Y0 = XY0[0]; X1Y0 = XY0[1]; X2Y0 = XY0[2]; X3Y0 = XY0[3];
  //   X4Y0 = XY0[4]; X0Y1 = XY1[0]; X1Y1 = XY1[1]; X2Y1 = XY1[2]; X3Y1 = XY1[3]; X4Y1 = XY1[4]; X0Y2 = XY2[0];
  //   X1Y2 = XY2[1]; X2Y2 = XY2[2]; X3Y2 = XY2[3]; X4Y2 = XY2[4]; X0Y3 = XY3[0]; X1Y3 = XY3[1]; X2Y3 = XY3[2];
  //   X3Y3 = XY3[3]; X4Y3 = XY3[4]; X0Y4 = XY4[0]; X1Y4 = XY4[1]; X2Y4 = XY4[2]; X3Y4 = XY4[3]; X4Y4 = XY4[4]
endmodule

module \乘法线流水接口  (
  input  [4:0] X,
  input  [4:0] Y,
  input  [4:0] XY0,
  input  [4:0] XY1,
  input  [4:0] XY2,
  input  [4:0] XY3,
  input  [4:0] XY4,
  input  [9:0] in_8,
  input  CLK,
  input  \同步清零_高电平有效 ,
  input  \使能端_低电平有效 ,
  output [4:0] X_prime,
  output [4:0] Y_prime,
  output [4:0] XY0_prime,
  output [4:0] XY1_prime,
  output [4:0] XY2_prime,
  output [4:0] XY3_2,
  output [4:0] XY4_2,
  output [9:0] out_19
);

  wire pull_resistor_2_node;
  wire [4:0] multiplexer_1_out, multiplexer_2_out, multiplexer_3_out, multiplexer_4_out, multiplexer_5_out,
       multiplexer_6_out, multiplexer_7_out;
  wire [9:0] multiplexer_8_out;

  Multiplexer #(.width(5), .enable("false")) multiplexer_1 (
    .in0(X), .in1({5{1'b0}}), .out(multiplexer_1_out), .sel(\同步清零_高电平有效 ));
  Multiplexer #(.width(5), .enable("false")) multiplexer_2 (
    .in0(Y), .in1({5{1'b0}}), .out(multiplexer_2_out), .sel(\同步清零_高电平有效 ));
  Multiplexer #(.width(5), .enable("false")) multiplexer_3 (
    .in0(XY0), .in1({5{1'b0}}), .out(multiplexer_3_out), .sel(\同步清零_高电平有效 ));
  Multiplexer #(.width(5), .enable("false")) multiplexer_4 (
    .in0(XY1), .in1({5{1'b0}}), .out(multiplexer_4_out), .sel(\同步清零_高电平有效 ));
  Multiplexer #(.width(5), .enable("false")) multiplexer_5 (
    .in0(XY2), .in1({5{1'b0}}), .out(multiplexer_5_out), .sel(\同步清零_高电平有效 ));
  Multiplexer #(.width(5), .enable("false")) multiplexer_6 (
    .in0(XY3), .in1({5{1'b0}}), .out(multiplexer_6_out), .sel(\同步清零_高电平有效 ));
  Multiplexer #(.width(5), .enable("false")) multiplexer_7 (
    .in0(XY4), .in1({5{1'b0}}), .out(multiplexer_7_out), .sel(\同步清零_高电平有效 ));
  Multiplexer #(.width(10), .enable("false")) multiplexer_8 (
    .in0(in_8), .in1({10{1'b0}}), .out(multiplexer_8_out), .sel(\同步清零_高电平有效 ));
  Pull_Resistor pull_resistor_1 (.node(\同步清零_高电平有效 ));
  Register #(.width(5)) register_1 (
    .D(multiplexer_1_out), .en(pull_resistor_2_node), .Q(X_prime), .clk(CLK));  // open: clr
  Register #(.width(5)) register_2 (
    .D(multiplexer_2_out), .en(pull_resistor_2_node), .Q(Y_prime), .clk(CLK));  // open: clr
  Register #(.width(5)) register_3 (
    .D(multiplexer_3_out), .en(pull_resistor_2_node), .Q(XY0_prime), .clk(CLK));  // open: clr
  Register #(.width(5)) register_4 (
    .D(multiplexer_4_out), .en(pull_resistor_2_node), .Q(XY1_prime), .clk(CLK));  // open: clr
  Register #(.width(5)) register_5 (
    .D(multiplexer_5_out), .en(pull_resistor_2_node), .Q(XY2_prime), .clk(CLK));  // open: clr
  Register #(.width(5)) register_6 (
    .D(multiplexer_6_out), .en(pull_resistor_2_node), .Q(XY3_2), .clk(CLK));  // open: clr
  Register #(.width(5)) register_7 (
    .D(multiplexer_7_out), .en(pull_resistor_2_node), .Q(XY4_2), .clk(CLK));  // open: clr
  Register #(.width(10)) register_8 (
    .D(multiplexer_8_out), .en(pull_resistor_2_node), .Q(out_19), .clk(CLK));  // open: clr
  Pull_Resistor pull_resistor_2 (.node(pull_resistor_2_node));
  not not_1 (pull_resistor_2_node, \使能端_低电平有效 );

  // Notes on the sheet:
  //   使能端_低电平有效: pull=down
  //   同步清零_高电平有效: pull=down
  //   下拉电阻使得引脚可以悬空
  //   流水接口传输XY的目的是为了测试
endmodule

// FA
module \一位全加器FA封装1  (
  input  Cin,
  input  Xi,
  input  Yi,
  output Cout,
  output Si
);

  wire AND_2_out, AND_out, XOR_2_out;

  or OR (Cout, AND_out, AND_2_out);
  and AND (AND_out, Xi, Yi);
  and AND_2 (AND_2_out, Cin, XOR_2_out);
  xor XOR (Si, Cin, XOR_2_out);
  xor XOR_2 (XOR_2_out, Xi, Yi);

  // Notes on the sheet:
  //   Yi: pull=down
  //   Xi: pull=down
  //   Cin: pull=down
  //   Si = Xi ^ Yi ^ Cin
  //   Cout = Xi Yi + Cin (Xi ^ Yi)
endmodule

module \一位全加器FA封装2  (
  input  Cin,
  input  Xi,
  input  Yi,
  output Cout,
  output Si
);

  wire AND_2_out, AND_out, XOR_2_out;

  or OR (Cout, AND_out, AND_2_out);
  and AND (AND_out, Xi, Yi);
  and AND_2 (AND_2_out, Cin, XOR_2_out);
  xor XOR (Si, Cin, XOR_2_out);
  xor XOR_2 (XOR_2_out, Xi, Yi);

  // Notes on the sheet:
  //   Si = Xi ^ Yi ^ Cin
  //   Cout = Xi Yi + Cin (Xi ^ Yi)
endmodule

module \一位全加器FA封装3  (
  input  Cin,
  input  Xi,
  input  Yi,
  output Cout,
  output Si
);

  wire AND_2_out, AND_out, XOR_2_out;

  or OR (Cout, AND_out, AND_2_out);
  and AND (AND_out, Xi, Yi);
  and AND_2 (AND_2_out, Cin, XOR_2_out);
  xor XOR (Si, Cin, XOR_2_out);
  xor XOR_2 (XOR_2_out, Xi, Yi);

  // Notes on the sheet:
  //   Si = Xi ^ Yi ^ Cin
  //   Cout = Xi Yi + Cin (Xi ^ Yi)
endmodule

module \_8位串行加法器  (
  input  [7:0] X,
  input  [7:0] Y,
  input  Cin,
  output [7:0] S,
  output Cout,
  output Overflow
);

  wire \一位全加器fa封装1_2_cout , \一位全加器fa封装1_3_cout , \一位全加器fa封装1_4_cout , \一位全加器fa封装1_5_cout ,
       \一位全加器fa封装1_6_cout , \一位全加器fa封装1_7_cout , \一位全加器fa封装1_8_cout ;

  xor xor_1 (Overflow, Cout, \一位全加器fa封装1_2_cout );
  \一位全加器FA封装1  \u_一位全加器fa封装1_1  (.Cout(Cout), .Si(S[7]), .Cin(\一位全加器fa封装1_2_cout ), .Xi(X[7]), .Yi(Y[7]));
  \一位全加器FA封装1  \u_一位全加器fa封装1_2  (
    .Cout(\一位全加器fa封装1_2_cout ), .Si(S[6]), .Cin(\一位全加器fa封装1_3_cout ), .Xi(X[6]), .Yi(Y[6]));
  \一位全加器FA封装1  \u_一位全加器fa封装1_3  (
    .Cout(\一位全加器fa封装1_3_cout ), .Si(S[5]), .Cin(\一位全加器fa封装1_4_cout ), .Xi(X[5]), .Yi(Y[5]));
  \一位全加器FA封装1  \u_一位全加器fa封装1_4  (
    .Cout(\一位全加器fa封装1_4_cout ), .Si(S[4]), .Cin(\一位全加器fa封装1_5_cout ), .Xi(X[4]), .Yi(Y[4]));
  \一位全加器FA封装1  \u_一位全加器fa封装1_5  (
    .Cout(\一位全加器fa封装1_5_cout ), .Si(S[3]), .Cin(\一位全加器fa封装1_6_cout ), .Xi(X[3]), .Yi(Y[3]));
  \一位全加器FA封装1  \u_一位全加器fa封装1_6  (
    .Cout(\一位全加器fa封装1_6_cout ), .Si(S[2]), .Cin(\一位全加器fa封装1_7_cout ), .Xi(X[2]), .Yi(Y[2]));
  // Probe on X
  // Probe on Y
  // Probe on S
  \一位全加器FA封装1  \u_一位全加器fa封装1_7  (
    .Cout(\一位全加器fa封装1_7_cout ), .Si(S[1]), .Cin(\一位全加器fa封装1_8_cout ), .Xi(X[1]), .Yi(Y[1]));
  // Probe on X
  // Probe on Y
  // Probe on S
  \一位全加器FA封装1  \u_一位全加器fa封装1_8  (.Cout(\一位全加器fa封装1_8_cout ), .Si(S[0]), .Cin(Cin), .Xi(X[0]), .Yi(Y[0]));

  // Other names for the same wires on the sheet: OF = Overflow

  // Notes on the sheet:
  //   X: pull=down
  //   Cin: pull=down
  //   Y: pull=down
  //   输入引脚区
  //   符号位
  //   输出引脚区
  //   +
  //   =
  //   有符号加法
  //   +
  //   =
  //   无符号加法
endmodule

module \华莱士树  (
);

  wire undriven, undriven_2, undriven_3, undriven_4, undriven_5, undriven_6, undriven_7, undriven_8,
       undriven_9, undriven_10, undriven_11, undriven_12, undriven_13, undriven_14, undriven_15, undriven_16,
       undriven_17, undriven_18, undriven_19, undriven_20, undriven_21, undriven_22, undriven_23,
       undriven_24, undriven_25, undriven_26, undriven_27, undriven_28, undriven_29, undriven_30,
       undriven_31, undriven_32, undriven_33, undriven_34, undriven_35, undriven_36, undriven_37,
       undriven_38, undriven_39, undriven_40, undriven_41, undriven_42, undriven_43, undriven_44,
       undriven_45, undriven_46, undriven_47, undriven_48, undriven_49, undriven_50, undriven_51,
       undriven_52, undriven_53, undriven_54, undriven_55, undriven_56, undriven_57, undriven_58,
       undriven_59, undriven_60, undriven_61, undriven_62, undriven_63, undriven_64, undriven_65,
       undriven_66, undriven_67, undriven_68, undriven_69, undriven_70, undriven_71, undriven_72,
       undriven_73, undriven_74, undriven_75, undriven_76, undriven_77, undriven_78, undriven_79,
       undriven_80, undriven_81, undriven_82, undriven_83, undriven_84, undriven_85, undriven_86,
       undriven_87, undriven_88, undriven_89, undriven_90, undriven_91, undriven_92, undriven_93,
       undriven_94, undriven_95, undriven_96, undriven_97, undriven_98, undriven_99, undriven_100,
       undriven_101, undriven_102, undriven_103, undriven_104, undriven_105, undriven_106, undriven_107,
       undriven_108, undriven_109, undriven_110, undriven_111, undriven_112, undriven_113, undriven_114,
       undriven_115, undriven_116, undriven_117, undriven_118, undriven_119, undriven_120, undriven_121,
       undriven_122, undriven_123, undriven_124, undriven_125, undriven_126, undriven_127, undriven_128,
       undriven_130, \一位全加器fa封装2_1_cout , \一位全加器fa封装2_1_si , \一位全加器fa封装2_2_si , \一位全加器fa封装2_3_cout ,
       \一位全加器fa封装2_3_si , \一位全加器fa封装2_4_si , \一位全加器fa封装2_5_si , \一位全加器fa封装2_6_si , \一位全加器fa封装2_7_si ,
       \一位全加器fa封装2_8_si , \一位全加器fa封装2_9_cout , \一位全加器fa封装2_9_si , \一位全加器fa封装2_10_si , \一位全加器fa封装2_11_cout ,
       \一位全加器fa封装2_11_si , \一位全加器fa封装2_12_si , \一位全加器fa封装2_13_si , \一位全加器fa封装2_14_si , \一位全加器fa封装2_15_cout ,
       \一位全加器fa封装2_15_si , \一位全加器fa封装2_16_si , \一位全加器fa封装2_17_cout , \一位全加器fa封装2_17_si , \一位全加器fa封装2_18_si ,
       \一位全加器fa封装2_19_si , \一位全加器fa封装2_20_si , \一位全加器fa封装2_21_si , \一位全加器fa封装2_22_si , \一位全加器fa封装2_23_cout ,
       \一位全加器fa封装2_23_si , \一位全加器fa封装2_24_si , \一位全加器fa封装2_25_cout , \一位全加器fa封装2_25_si , \一位全加器fa封装2_26_si ,
       \一位全加器fa封装2_27_si , \一位全加器fa封装2_28_si , \一位全加器fa封装2_29_cout , \一位全加器fa封装2_29_si , \一位全加器fa封装2_30_si ,
       \一位全加器fa封装2_31_cout , \一位全加器fa封装2_31_si , \一位全加器fa封装2_32_si , \一位全加器fa封装2_33_si , \一位全加器fa封装2_34_si ,
       \一位全加器fa封装2_35_si , \一位全加器fa封装2_36_si , \一位全加器fa封装2_37_cout , \一位全加器fa封装2_37_si , \一位全加器fa封装2_38_si ,
       \一位全加器fa封装2_39_cout , \一位全加器fa封装2_39_si , \一位全加器fa封装2_40_si , \一位全加器fa封装2_41_si , \一位全加器fa封装2_42_si ,
       \一位全加器fa封装2_43_cout , \一位全加器fa封装2_43_si , \一位全加器fa封装2_44_si , \一位全加器fa封装2_45_cout ,
       \一位全加器fa封装2_45_si , \一位全加器fa封装2_46_si , \一位全加器fa封装2_47_si , \一位全加器fa封装2_48_si , \一位全加器fa封装2_49_si ,
       \一位全加器fa封装2_50_si , \一位全加器fa封装2_51_cout , \一位全加器fa封装2_51_si , \一位全加器fa封装2_52_si ,
       \一位全加器fa封装2_53_cout , \一位全加器fa封装2_53_si , \一位全加器fa封装2_54_si , \一位全加器fa封装2_55_si , \一位全加器fa封装2_56_si ,
       \一位全加器fa封装2_57_cout , \一位全加器fa封装2_57_si , \一位全加器fa封装2_58_si , \一位全加器fa封装2_59_cout ,
       \一位全加器fa封装2_59_si , \一位全加器fa封装2_60_si , \一位全加器fa封装2_61_si , \一位全加器fa封装2_62_si , \一位全加器fa封装2_63_si ,
       \一位全加器fa封装2_64_si , \一位全加器fa封装2_65_cout , \一位全加器fa封装2_65_si , \一位全加器fa封装2_66_si , \一位全加器fa封装2_67_si ,
       \一位全加器fa封装2_68_cout , \一位全加器fa封装2_68_si , \一位全加器fa封装2_69_si , \一位全加器fa封装2_70_si ,
       \一位全加器fa封装2_71_cout , \一位全加器fa封装2_71_si , \一位全加器fa封装2_72_si , \一位全加器fa封装2_73_cout ,
       \一位全加器fa封装2_73_si , \一位全加器fa封装2_74_si , \一位全加器fa封装2_75_si , \一位全加器fa封装2_76_si , \一位全加器fa封装2_77_si ,
       \一位全加器fa封装2_78_si , \一位全加器fa封装2_79_cout , \一位全加器fa封装2_79_si , \一位全加器fa封装2_80_si ,
       \一位全加器fa封装2_81_cout , \一位全加器fa封装2_81_si , \一位全加器fa封装2_82_si , \一位全加器fa封装2_83_si , \一位全加器fa封装2_84_si ,
       \一位全加器fa封装2_85_cout , \一位全加器fa封装2_85_si , \一位全加器fa封装2_86_si , \一位全加器fa封装2_87_cout ,
       \一位全加器fa封装2_87_si , \一位全加器fa封装2_88_si , \一位全加器fa封装2_89_si , \一位全加器fa封装2_90_si , \一位全加器fa封装2_91_si ,
       \一位全加器fa封装2_92_si , \一位全加器fa封装2_93_cout , \一位全加器fa封装2_93_si , \一位全加器fa封装2_94_si ,
       \一位全加器fa封装2_95_cout , \一位全加器fa封装2_95_si , \一位全加器fa封装2_96_si , \一位全加器fa封装2_97_si , \一位全加器fa封装2_98_si ,
       \一位全加器fa封装2_99_cout , \一位全加器fa封装2_99_si , \一位全加器fa封装2_100_si , \一位全加器fa封装2_101_cout ,
       \一位全加器fa封装2_101_si , \一位全加器fa封装2_102_si , \一位全加器fa封装2_103_si , \一位全加器fa封装2_104_si ,
       \一位全加器fa封装2_105_si , \一位全加器fa封装2_106_si , \一位全加器fa封装2_107_cout , \一位全加器fa封装2_107_si ,
       \一位全加器fa封装2_108_si , \一位全加器fa封装2_109_cout , \一位全加器fa封装2_109_si , \一位全加器fa封装2_110_si ,
       \一位全加器fa封装2_111_si , \一位全加器fa封装2_112_si ;
  wire [1:0] undriven_131, \一位全加器fa封装2_4_cout , \一位全加器fa封装2_10_cout , \一位全加器fa封装2_16_cout ,
       \一位全加器fa封装2_22_cout , \一位全加器fa封装2_32_cout , \一位全加器fa封装2_38_cout , \一位全加器fa封装2_44_cout ,
       \一位全加器fa封装2_50_cout , \一位全加器fa封装2_60_cout , \一位全加器fa封装2_66_cout , \一位全加器fa封装2_72_cout ,
       \一位全加器fa封装2_78_cout , \一位全加器fa封装2_88_cout , \一位全加器fa封装2_94_cout , \一位全加器fa封装2_100_cout ,
       \一位全加器fa封装2_106_cout ;
  wire [2:0] undriven_129, \一位全加器fa封装2_6_cout , \一位全加器fa封装2_14_cout , \一位全加器fa封装2_21_cout ,
       \一位全加器fa封装2_28_cout , \一位全加器fa封装2_34_cout , \一位全加器fa封装2_42_cout , \一位全加器fa封装2_49_cout ,
       \一位全加器fa封装2_55_cout , \一位全加器fa封装2_63_cout , \一位全加器fa封装2_70_cout , \一位全加器fa封装2_77_cout ,
       \一位全加器fa封装2_84_cout , \一位全加器fa封装2_91_cout , \一位全加器fa封装2_98_cout , \一位全加器fa封装2_105_cout ,
       \一位全加器fa封装2_112_cout ;

  shape shape_1 ();
  \一位全加器FA封装2  \u_一位全加器fa封装2_1  (
    .Cout(\一位全加器fa封装2_1_cout ), .Si(\一位全加器fa封装2_1_si ), .Cin(\一位全加器fa封装2_6_si ), .Xi(\一位全加器fa封装2_2_si ),
    .Yi(\一位全加器fa封装2_7_si ));
  \一位全加器FA封装2  \u_一位全加器fa封装2_2  (
    .Cout(\一位全加器fa封装2_6_cout [2]), .Si(\一位全加器fa封装2_2_si ), .Cin(undriven_3), .Xi(undriven), .Yi(undriven_2));
  \一位全加器FA封装2  \u_一位全加器fa封装2_3  (
    .Cout(\一位全加器fa封装2_3_cout ), .Si(\一位全加器fa封装2_3_si ), .Cin(\一位全加器fa封装2_10_cout [0]),
    .Xi(\一位全加器fa封装2_4_si ), .Yi(\一位全加器fa封装2_10_cout [1]));
  \一位全加器FA封装2  \u_一位全加器fa封装2_4  (
    .Cout(\一位全加器fa封装2_4_cout [0]), .Si(\一位全加器fa封装2_4_si ), .Cin(\一位全加器fa封装2_11_cout ),
    .Xi(\一位全加器fa封装2_1_si ), .Yi(\一位全加器fa封装2_5_si ));
  \一位全加器FA封装2  \u_一位全加器fa封装2_5  (
    .Cout(\一位全加器fa封装2_4_cout [1]), .Si(\一位全加器fa封装2_5_si ), .Cin(\一位全加器fa封装2_14_cout [0]),
    .Xi(\一位全加器fa封装2_14_cout [2]), .Yi(\一位全加器fa封装2_14_cout [1]));
  \一位全加器FA封装2  \u_一位全加器fa封装2_6  (
    .Cout(\一位全加器fa封装2_6_cout [0]), .Si(\一位全加器fa封装2_6_si ), .Cin(1'b0), .Xi(undriven_7), .Yi(undriven_8));
  \一位全加器FA封装2  \u_一位全加器fa封装2_7  (
    .Cout(\一位全加器fa封装2_6_cout [1]), .Si(\一位全加器fa封装2_7_si ), .Cin(undriven_6), .Xi(undriven_4), .Yi(undriven_5));
  \一位全加器FA封装2  \u_一位全加器fa封装2_8  (
    .Cout(\一位全加器fa封装2_14_cout [2]), .Si(\一位全加器fa封装2_8_si ), .Cin(undriven_11), .Xi(undriven_9),
    .Yi(undriven_10));
  \一位全加器FA封装2  \u_一位全加器fa封装2_9  (
    .Cout(\一位全加器fa封装2_9_cout ), .Si(\一位全加器fa封装2_9_si ), .Cin(\一位全加器fa封装2_16_cout [0]),
    .Xi(\一位全加器fa封装2_10_si ), .Yi(\一位全加器fa封装2_16_cout [1]));
  \一位全加器FA封装2  \u_一位全加器fa封装2_10  (
    .Cout(\一位全加器fa封装2_10_cout [0]), .Si(\一位全加器fa封装2_10_si ), .Cin(\一位全加器fa封装2_17_cout ),
    .Xi(\一位全加器fa封装2_11_si ), .Yi(\一位全加器fa封装2_12_si ));
  \一位全加器FA封装2  \u_一位全加器fa封装2_11  (
    .Cout(\一位全加器fa封装2_11_cout ), .Si(\一位全加器fa封装2_11_si ), .Cin(\一位全加器fa封装2_14_si ), .Xi(\一位全加器fa封装2_8_si ),
    .Yi(\一位全加器fa封装2_13_si ));
  \一位全加器FA封装2  \u_一位全加器fa封装2_12  (
    .Cout(\一位全加器fa封装2_10_cout [1]), .Si(\一位全加器fa封装2_12_si ), .Cin(\一位全加器fa封装2_21_cout [0]),
    .Xi(\一位全加器fa封装2_21_cout [2]), .Yi(\一位全加器fa封装2_21_cout [1]));
  \一位全加器FA封装2  \u_一位全加器fa封装2_13  (
    .Cout(\一位全加器fa封装2_14_cout [1]), .Si(\一位全加器fa封装2_13_si ), .Cin(undriven_14), .Xi(undriven_12),
    .Yi(undriven_13));
  shape shape_2 ();
  \一位全加器FA封装2  \u_一位全加器fa封装2_14  (
    .Cout(\一位全加器fa封装2_14_cout [0]), .Si(\一位全加器fa封装2_14_si ), .Cin(1'b0), .Xi(undriven_15), .Yi(undriven_16));
  \一位全加器FA封装2  \u_一位全加器fa封装2_15  (
    .Cout(\一位全加器fa封装2_15_cout ), .Si(\一位全加器fa封装2_15_si ), .Cin(\一位全加器fa封装2_22_cout [0]),
    .Xi(\一位全加器fa封装2_16_si ), .Yi(\一位全加器fa封装2_22_cout [1]));
  \一位全加器FA封装2  \u_一位全加器fa封装2_16  (
    .Cout(\一位全加器fa封装2_16_cout [0]), .Si(\一位全加器fa封装2_16_si ), .Cin(\一位全加器fa封装2_23_cout ),
    .Xi(\一位全加器fa封装2_17_si ), .Yi(\一位全加器fa封装2_20_si ));
  \一位全加器FA封装2  \u_一位全加器fa封装2_17  (
    .Cout(\一位全加器fa封装2_17_cout ), .Si(\一位全加器fa封装2_17_si ), .Cin(\一位全加器fa封装2_21_si ), .Xi(\一位全加器fa封装2_18_si ),
    .Yi(\一位全加器fa封装2_19_si ));
  \一位全加器FA封装2  \u_一位全加器fa封装2_18  (
    .Cout(\一位全加器fa封装2_21_cout [2]), .Si(\一位全加器fa封装2_18_si ), .Cin(undriven_19), .Xi(undriven_17),
    .Yi(undriven_18));
  \一位全加器FA封装2  \u_一位全加器fa封装2_19  (
    .Cout(\一位全加器fa封装2_21_cout [1]), .Si(\一位全加器fa封装2_19_si ), .Cin(undriven_22), .Xi(undriven_20),
    .Yi(undriven_21));
  \一位全加器FA封装2  \u_一位全加器fa封装2_20  (
    .Cout(\一位全加器fa封装2_16_cout [1]), .Si(\一位全加器fa封装2_20_si ), .Cin(\一位全加器fa封装2_28_cout [0]),
    .Xi(\一位全加器fa封装2_28_cout [2]), .Yi(\一位全加器fa封装2_28_cout [1]));
  \一位全加器FA封装2  \u_一位全加器fa封装2_21  (
    .Cout(\一位全加器fa封装2_21_cout [0]), .Si(\一位全加器fa封装2_21_si ), .Cin(1'b0), .Xi(undriven_23), .Yi(undriven_24));
  \一位全加器FA封装2  \u_一位全加器fa封装2_22  (
    .Cout(\一位全加器fa封装2_22_cout [0]), .Si(\一位全加器fa封装2_22_si ), .Cin(\一位全加器fa封装2_29_cout ),
    .Xi(\一位全加器fa封装2_23_si ), .Yi(\一位全加器fa封装2_26_si ));
  \一位全加器FA封装2  \u_一位全加器fa封装2_23  (
    .Cout(\一位全加器fa封装2_23_cout ), .Si(\一位全加器fa封装2_23_si ), .Cin(\一位全加器fa封装2_28_si ), .Xi(\一位全加器fa封装2_24_si ),
    .Yi(\一位全加器fa封装2_27_si ));
  \一位全加器FA封装2  \u_一位全加器fa封装2_24  (
    .Cout(\一位全加器fa封装2_28_cout [2]), .Si(\一位全加器fa封装2_24_si ), .Cin(undriven_27), .Xi(undriven_25),
    .Yi(undriven_26));
  shape shape_3 ();
  \一位全加器FA封装2  \u_一位全加器fa封装2_25  (
    .Cout(\一位全加器fa封装2_25_cout ), .Si(\一位全加器fa封装2_25_si ), .Cin(\一位全加器fa封装2_32_cout [0]),
    .Xi(\一位全加器fa封装2_22_si ), .Yi(\一位全加器fa封装2_32_cout [1]));
  \一位全加器FA封装2  \u_一位全加器fa封装2_26  (
    .Cout(\一位全加器fa封装2_22_cout [1]), .Si(\一位全加器fa封装2_26_si ), .Cin(\一位全加器fa封装2_34_cout [0]),
    .Xi(\一位全加器fa封装2_34_cout [2]), .Yi(\一位全加器fa封装2_34_cout [1]));
  \一位全加器FA封装2  \u_一位全加器fa封装2_27  (
    .Cout(\一位全加器fa封装2_28_cout [1]), .Si(\一位全加器fa封装2_27_si ), .Cin(undriven_30), .Xi(undriven_28),
    .Yi(undriven_29));
  \一位全加器FA封装2  \u_一位全加器fa封装2_28  (
    .Cout(\一位全加器fa封装2_28_cout [0]), .Si(\一位全加器fa封装2_28_si ), .Cin(1'b0), .Xi(undriven_31), .Yi(undriven_32));
  \一位全加器FA封装2  \u_一位全加器fa封装2_29  (
    .Cout(\一位全加器fa封装2_29_cout ), .Si(\一位全加器fa封装2_29_si ), .Cin(\一位全加器fa封装2_34_si ), .Xi(\一位全加器fa封装2_30_si ),
    .Yi(\一位全加器fa封装2_35_si ));
  \一位全加器FA封装2  \u_一位全加器fa封装2_30  (
    .Cout(\一位全加器fa封装2_34_cout [2]), .Si(\一位全加器fa封装2_30_si ), .Cin(undriven_35), .Xi(undriven_33),
    .Yi(undriven_34));
  \一位全加器FA封装2  \u_一位全加器fa封装2_31  (
    .Cout(\一位全加器fa封装2_31_cout ), .Si(\一位全加器fa封装2_31_si ), .Cin(\一位全加器fa封装2_38_cout [0]),
    .Xi(\一位全加器fa封装2_32_si ), .Yi(\一位全加器fa封装2_38_cout [1]));
  \一位全加器FA封装2  \u_一位全加器fa封装2_32  (
    .Cout(\一位全加器fa封装2_32_cout [0]), .Si(\一位全加器fa封装2_32_si ), .Cin(\一位全加器fa封装2_39_cout ),
    .Xi(\一位全加器fa封装2_29_si ), .Yi(\一位全加器fa封装2_33_si ));
  \一位全加器FA封装2  \u_一位全加器fa封装2_33  (
    .Cout(\一位全加器fa封装2_32_cout [1]), .Si(\一位全加器fa封装2_33_si ), .Cin(\一位全加器fa封装2_42_cout [0]),
    .Xi(\一位全加器fa封装2_42_cout [2]), .Yi(\一位全加器fa封装2_42_cout [1]));
  \一位全加器FA封装2  \u_一位全加器fa封装2_34  (
    .Cout(\一位全加器fa封装2_34_cout [0]), .Si(\一位全加器fa封装2_34_si ), .Cin(1'b0), .Xi(undriven_39), .Yi(undriven_40));
  \一位全加器FA封装2  \u_一位全加器fa封装2_35  (
    .Cout(\一位全加器fa封装2_34_cout [1]), .Si(\一位全加器fa封装2_35_si ), .Cin(undriven_38), .Xi(undriven_36),
    .Yi(undriven_37));
  \一位全加器FA封装2  \u_一位全加器fa封装2_36  (
    .Cout(\一位全加器fa封装2_42_cout [2]), .Si(\一位全加器fa封装2_36_si ), .Cin(undriven_43), .Xi(undriven_41),
    .Yi(undriven_42));
  \一位全加器FA封装2  \u_一位全加器fa封装2_37  (
    .Cout(\一位全加器fa封装2_37_cout ), .Si(\一位全加器fa封装2_37_si ), .Cin(\一位全加器fa封装2_44_cout [0]),
    .Xi(\一位全加器fa封装2_38_si ), .Yi(\一位全加器fa封装2_44_cout [1]));
  \一位全加器FA封装2  \u_一位全加器fa封装2_38  (
    .Cout(\一位全加器fa封装2_38_cout [0]), .Si(\一位全加器fa封装2_38_si ), .Cin(\一位全加器fa封装2_45_cout ),
    .Xi(\一位全加器fa封装2_39_si ), .Yi(\一位全加器fa封装2_40_si ));
  \一位全加器FA封装2  \u_一位全加器fa封装2_39  (
    .Cout(\一位全加器fa封装2_39_cout ), .Si(\一位全加器fa封装2_39_si ), .Cin(\一位全加器fa封装2_42_si ), .Xi(\一位全加器fa封装2_36_si ),
    .Yi(\一位全加器fa封装2_41_si ));
  \一位全加器FA封装2  \u_一位全加器fa封装2_40  (
    .Cout(\一位全加器fa封装2_38_cout [1]), .Si(\一位全加器fa封装2_40_si ), .Cin(\一位全加器fa封装2_49_cout [0]),
    .Xi(\一位全加器fa封装2_49_cout [2]), .Yi(\一位全加器fa封装2_49_cout [1]));
  \一位全加器FA封装2  \u_一位全加器fa封装2_41  (
    .Cout(\一位全加器fa封装2_42_cout [1]), .Si(\一位全加器fa封装2_41_si ), .Cin(undriven_46), .Xi(undriven_44),
    .Yi(undriven_45));
  shape shape_4 ();
  \一位全加器FA封装2  \u_一位全加器fa封装2_42  (
    .Cout(\一位全加器fa封装2_42_cout [0]), .Si(\一位全加器fa封装2_42_si ), .Cin(1'b0), .Xi(undriven_47), .Yi(undriven_48));
  \一位全加器FA封装2  \u_一位全加器fa封装2_43  (
    .Cout(\一位全加器fa封装2_43_cout ), .Si(\一位全加器fa封装2_43_si ), .Cin(\一位全加器fa封装2_50_cout [0]),
    .Xi(\一位全加器fa封装2_44_si ), .Yi(\一位全加器fa封装2_50_cout [1]));
  \一位全加器FA封装2  \u_一位全加器fa封装2_44  (
    .Cout(\一位全加器fa封装2_44_cout [0]), .Si(\一位全加器fa封装2_44_si ), .Cin(\一位全加器fa封装2_51_cout ),
    .Xi(\一位全加器fa封装2_45_si ), .Yi(\一位全加器fa封装2_48_si ));
  \一位全加器FA封装2  \u_一位全加器fa封装2_45  (
    .Cout(\一位全加器fa封装2_45_cout ), .Si(\一位全加器fa封装2_45_si ), .Cin(\一位全加器fa封装2_49_si ), .Xi(\一位全加器fa封装2_47_si ),
    .Yi(\一位全加器fa封装2_46_si ));
  \一位全加器FA封装2  \u_一位全加器fa封装2_46  (
    .Cout(\一位全加器fa封装2_49_cout [1]), .Si(\一位全加器fa封装2_46_si ), .Cin(undriven_54), .Xi(undriven_52),
    .Yi(undriven_53));
  \一位全加器FA封装2  \u_一位全加器fa封装2_47  (
    .Cout(\一位全加器fa封装2_49_cout [2]), .Si(\一位全加器fa封装2_47_si ), .Cin(undriven_51), .Xi(undriven_49),
    .Yi(undriven_50));
  \一位全加器FA封装2  \u_一位全加器fa封装2_48  (
    .Cout(\一位全加器fa封装2_44_cout [1]), .Si(\一位全加器fa封装2_48_si ), .Cin(\一位全加器fa封装2_55_cout [0]),
    .Xi(\一位全加器fa封装2_55_cout [2]), .Yi(\一位全加器fa封装2_55_cout [1]));
  \一位全加器FA封装2  \u_一位全加器fa封装2_49  (
    .Cout(\一位全加器fa封装2_49_cout [0]), .Si(\一位全加器fa封装2_49_si ), .Cin(1'b0), .Xi(undriven_55), .Yi(undriven_56));
  \一位全加器FA封装2  \u_一位全加器fa封装2_50  (
    .Cout(\一位全加器fa封装2_50_cout [0]), .Si(\一位全加器fa封装2_50_si ), .Cin(\一位全加器fa封装2_57_cout ),
    .Xi(\一位全加器fa封装2_51_si ), .Yi(\一位全加器fa封装2_54_si ));
  \一位全加器FA封装2  \u_一位全加器fa封装2_51  (
    .Cout(\一位全加器fa封装2_51_cout ), .Si(\一位全加器fa封装2_51_si ), .Cin(\一位全加器fa封装2_55_si ), .Xi(\一位全加器fa封装2_52_si ),
    .Yi(\一位全加器fa封装2_56_si ));
  \一位全加器FA封装2  \u_一位全加器fa封装2_52  (
    .Cout(\一位全加器fa封装2_55_cout [2]), .Si(\一位全加器fa封装2_52_si ), .Cin(undriven_59), .Xi(undriven_57),
    .Yi(undriven_58));
  shape shape_5 ();
  \一位全加器FA封装2  \u_一位全加器fa封装2_53  (
    .Cout(\一位全加器fa封装2_53_cout ), .Si(\一位全加器fa封装2_53_si ), .Cin(\一位全加器fa封装2_60_cout [0]),
    .Xi(\一位全加器fa封装2_50_si ), .Yi(\一位全加器fa封装2_60_cout [1]));
  \一位全加器FA封装2  \u_一位全加器fa封装2_54  (
    .Cout(\一位全加器fa封装2_50_cout [1]), .Si(\一位全加器fa封装2_54_si ), .Cin(\一位全加器fa封装2_63_cout [0]),
    .Xi(\一位全加器fa封装2_63_cout [2]), .Yi(\一位全加器fa封装2_63_cout [1]));
  \一位全加器FA封装2  \u_一位全加器fa封装2_55  (
    .Cout(\一位全加器fa封装2_55_cout [0]), .Si(\一位全加器fa封装2_55_si ), .Cin(1'b0), .Xi(undriven_63), .Yi(undriven_64));
  \一位全加器FA封装2  \u_一位全加器fa封装2_56  (
    .Cout(\一位全加器fa封装2_55_cout [1]), .Si(\一位全加器fa封装2_56_si ), .Cin(undriven_62), .Xi(undriven_60),
    .Yi(undriven_61));
  \一位全加器FA封装2  \u_一位全加器fa封装2_57  (
    .Cout(\一位全加器fa封装2_57_cout ), .Si(\一位全加器fa封装2_57_si ), .Cin(\一位全加器fa封装2_63_si ), .Xi(\一位全加器fa封装2_58_si ),
    .Yi(\一位全加器fa封装2_62_si ));
  \一位全加器FA封装2  \u_一位全加器fa封装2_58  (
    .Cout(\一位全加器fa封装2_63_cout [2]), .Si(\一位全加器fa封装2_58_si ), .Cin(undriven_67), .Xi(undriven_65),
    .Yi(undriven_66));
  \一位全加器FA封装2  \u_一位全加器fa封装2_59  (
    .Cout(\一位全加器fa封装2_59_cout ), .Si(\一位全加器fa封装2_59_si ), .Cin(\一位全加器fa封装2_66_cout [0]),
    .Xi(\一位全加器fa封装2_60_si ), .Yi(\一位全加器fa封装2_66_cout [1]));
  \一位全加器FA封装2  \u_一位全加器fa封装2_60  (
    .Cout(\一位全加器fa封装2_60_cout [0]), .Si(\一位全加器fa封装2_60_si ), .Cin(\一位全加器fa封装2_68_cout ),
    .Xi(\一位全加器fa封装2_57_si ), .Yi(\一位全加器fa封装2_61_si ));
  \一位全加器FA封装2  \u_一位全加器fa封装2_61  (
    .Cout(\一位全加器fa封装2_60_cout [1]), .Si(\一位全加器fa封装2_61_si ), .Cin(\一位全加器fa封装2_70_cout [0]),
    .Xi(\一位全加器fa封装2_70_cout [2]), .Yi(\一位全加器fa封装2_70_cout [1]));
  \一位全加器FA封装2  \u_一位全加器fa封装2_62  (
    .Cout(\一位全加器fa封装2_63_cout [1]), .Si(\一位全加器fa封装2_62_si ), .Cin(undriven_70), .Xi(undriven_68),
    .Yi(undriven_69));
  \一位全加器FA封装2  \u_一位全加器fa封装2_63  (
    .Cout(\一位全加器fa封装2_63_cout [0]), .Si(\一位全加器fa封装2_63_si ), .Cin(1'b0), .Xi(undriven_71), .Yi(undriven_72));
  \一位全加器FA封装2  \u_一位全加器fa封装2_64  (
    .Cout(\一位全加器fa封装2_70_cout [2]), .Si(\一位全加器fa封装2_64_si ), .Cin(undriven_75), .Xi(undriven_73),
    .Yi(undriven_74));
  \一位全加器FA封装2  \u_一位全加器fa封装2_65  (
    .Cout(\一位全加器fa封装2_65_cout ), .Si(\一位全加器fa封装2_65_si ), .Cin(\一位全加器fa封装2_72_cout [0]),
    .Xi(\一位全加器fa封装2_66_si ), .Yi(\一位全加器fa封装2_72_cout [1]));
  \一位全加器FA封装2  \u_一位全加器fa封装2_66  (
    .Cout(\一位全加器fa封装2_66_cout [0]), .Si(\一位全加器fa封装2_66_si ), .Cin(\一位全加器fa封装2_73_cout ),
    .Xi(\一位全加器fa封装2_68_si ), .Yi(\一位全加器fa封装2_67_si ));
  \一位全加器FA封装2  \u_一位全加器fa封装2_67  (
    .Cout(\一位全加器fa封装2_66_cout [1]), .Si(\一位全加器fa封装2_67_si ), .Cin(\一位全加器fa封装2_77_cout [0]),
    .Xi(\一位全加器fa封装2_77_cout [2]), .Yi(\一位全加器fa封装2_77_cout [1]));
  \一位全加器FA封装2  \u_一位全加器fa封装2_68  (
    .Cout(\一位全加器fa封装2_68_cout ), .Si(\一位全加器fa封装2_68_si ), .Cin(\一位全加器fa封装2_70_si ), .Xi(\一位全加器fa封装2_64_si ),
    .Yi(\一位全加器fa封装2_69_si ));
  \一位全加器FA封装2  \u_一位全加器fa封装2_69  (
    .Cout(\一位全加器fa封装2_70_cout [1]), .Si(\一位全加器fa封装2_69_si ), .Cin(undriven_78), .Xi(undriven_76),
    .Yi(undriven_77));
  shape shape_6 ();
  \一位全加器FA封装2  \u_一位全加器fa封装2_70  (
    .Cout(\一位全加器fa封装2_70_cout [0]), .Si(\一位全加器fa封装2_70_si ), .Cin(1'b0), .Xi(undriven_79), .Yi(undriven_80));
  \一位全加器FA封装2  \u_一位全加器fa封装2_71  (
    .Cout(\一位全加器fa封装2_71_cout ), .Si(\一位全加器fa封装2_71_si ), .Cin(\一位全加器fa封装2_78_cout [0]),
    .Xi(\一位全加器fa封装2_72_si ), .Yi(\一位全加器fa封装2_78_cout [1]));
  \一位全加器FA封装2  \u_一位全加器fa封装2_72  (
    .Cout(\一位全加器fa封装2_72_cout [0]), .Si(\一位全加器fa封装2_72_si ), .Cin(\一位全加器fa封装2_79_cout ),
    .Xi(\一位全加器fa封装2_73_si ), .Yi(\一位全加器fa封装2_76_si ));
  \一位全加器FA封装2  \u_一位全加器fa封装2_73  (
    .Cout(\一位全加器fa封装2_73_cout ), .Si(\一位全加器fa封装2_73_si ), .Cin(\一位全加器fa封装2_77_si ), .Xi(\一位全加器fa封装2_75_si ),
    .Yi(\一位全加器fa封装2_74_si ));
  \一位全加器FA封装2  \u_一位全加器fa封装2_74  (
    .Cout(\一位全加器fa封装2_77_cout [1]), .Si(\一位全加器fa封装2_74_si ), .Cin(undriven_86), .Xi(undriven_84),
    .Yi(undriven_85));
  \一位全加器FA封装2  \u_一位全加器fa封装2_75  (
    .Cout(\一位全加器fa封装2_77_cout [2]), .Si(\一位全加器fa封装2_75_si ), .Cin(undriven_83), .Xi(undriven_81),
    .Yi(undriven_82));
  \一位全加器FA封装2  \u_一位全加器fa封装2_76  (
    .Cout(\一位全加器fa封装2_72_cout [1]), .Si(\一位全加器fa封装2_76_si ), .Cin(\一位全加器fa封装2_84_cout [0]),
    .Xi(\一位全加器fa封装2_84_cout [2]), .Yi(\一位全加器fa封装2_84_cout [1]));
  \一位全加器FA封装2  \u_一位全加器fa封装2_77  (
    .Cout(\一位全加器fa封装2_77_cout [0]), .Si(\一位全加器fa封装2_77_si ), .Cin(1'b0), .Xi(undriven_87), .Yi(undriven_88));
  \一位全加器FA封装2  \u_一位全加器fa封装2_78  (
    .Cout(\一位全加器fa封装2_78_cout [0]), .Si(\一位全加器fa封装2_78_si ), .Cin(\一位全加器fa封装2_85_cout ),
    .Xi(\一位全加器fa封装2_79_si ), .Yi(\一位全加器fa封装2_82_si ));
  \一位全加器FA封装2  \u_一位全加器fa封装2_79  (
    .Cout(\一位全加器fa封装2_79_cout ), .Si(\一位全加器fa封装2_79_si ), .Cin(\一位全加器fa封装2_84_si ), .Xi(\一位全加器fa封装2_80_si ),
    .Yi(\一位全加器fa封装2_83_si ));
  \一位全加器FA封装2  \u_一位全加器fa封装2_80  (
    .Cout(\一位全加器fa封装2_84_cout [2]), .Si(\一位全加器fa封装2_80_si ), .Cin(undriven_91), .Xi(undriven_89),
    .Yi(undriven_90));
  shape shape_7 ();
  \一位全加器FA封装2  \u_一位全加器fa封装2_81  (
    .Cout(\一位全加器fa封装2_81_cout ), .Si(\一位全加器fa封装2_81_si ), .Cin(\一位全加器fa封装2_88_cout [0]),
    .Xi(\一位全加器fa封装2_78_si ), .Yi(\一位全加器fa封装2_88_cout [1]));
  \一位全加器FA封装2  \u_一位全加器fa封装2_82  (
    .Cout(\一位全加器fa封装2_78_cout [1]), .Si(\一位全加器fa封装2_82_si ), .Cin(\一位全加器fa封装2_91_cout [0]),
    .Xi(\一位全加器fa封装2_91_cout [2]), .Yi(\一位全加器fa封装2_91_cout [1]));
  \一位全加器FA封装2  \u_一位全加器fa封装2_83  (
    .Cout(\一位全加器fa封装2_84_cout [1]), .Si(\一位全加器fa封装2_83_si ), .Cin(undriven_94), .Xi(undriven_92),
    .Yi(undriven_93));
  \一位全加器FA封装2  \u_一位全加器fa封装2_84  (
    .Cout(\一位全加器fa封装2_84_cout [0]), .Si(\一位全加器fa封装2_84_si ), .Cin(1'b0), .Xi(undriven_95), .Yi(undriven_96));
  \一位全加器FA封装2  \u_一位全加器fa封装2_85  (
    .Cout(\一位全加器fa封装2_85_cout ), .Si(\一位全加器fa封装2_85_si ), .Cin(\一位全加器fa封装2_91_si ), .Xi(\一位全加器fa封装2_86_si ),
    .Yi(\一位全加器fa封装2_90_si ));
  \一位全加器FA封装2  \u_一位全加器fa封装2_86  (
    .Cout(\一位全加器fa封装2_91_cout [2]), .Si(\一位全加器fa封装2_86_si ), .Cin(undriven_99), .Xi(undriven_97),
    .Yi(undriven_98));
  \一位全加器FA封装2  \u_一位全加器fa封装2_87  (
    .Cout(\一位全加器fa封装2_87_cout ), .Si(\一位全加器fa封装2_87_si ), .Cin(\一位全加器fa封装2_94_cout [0]),
    .Xi(\一位全加器fa封装2_88_si ), .Yi(\一位全加器fa封装2_94_cout [1]));
  \一位全加器FA封装2  \u_一位全加器fa封装2_88  (
    .Cout(\一位全加器fa封装2_88_cout [0]), .Si(\一位全加器fa封装2_88_si ), .Cin(\一位全加器fa封装2_95_cout ),
    .Xi(\一位全加器fa封装2_85_si ), .Yi(\一位全加器fa封装2_89_si ));
  \一位全加器FA封装2  \u_一位全加器fa封装2_89  (
    .Cout(\一位全加器fa封装2_88_cout [1]), .Si(\一位全加器fa封装2_89_si ), .Cin(\一位全加器fa封装2_98_cout [0]),
    .Xi(\一位全加器fa封装2_98_cout [2]), .Yi(\一位全加器fa封装2_98_cout [1]));
  \一位全加器FA封装2  \u_一位全加器fa封装2_90  (
    .Cout(\一位全加器fa封装2_91_cout [1]), .Si(\一位全加器fa封装2_90_si ), .Cin(undriven_102), .Xi(undriven_100),
    .Yi(undriven_101));
  \一位全加器FA封装2  \u_一位全加器fa封装2_91  (
    .Cout(\一位全加器fa封装2_91_cout [0]), .Si(\一位全加器fa封装2_91_si ), .Cin(1'b0), .Xi(undriven_103), .Yi(undriven_104));
  \一位全加器FA封装2  \u_一位全加器fa封装2_92  (
    .Cout(\一位全加器fa封装2_98_cout [2]), .Si(\一位全加器fa封装2_92_si ), .Cin(undriven_107), .Xi(undriven_105),
    .Yi(undriven_106));
  \一位全加器FA封装2  \u_一位全加器fa封装2_93  (
    .Cout(\一位全加器fa封装2_93_cout ), .Si(\一位全加器fa封装2_93_si ), .Cin(\一位全加器fa封装2_100_cout [0]),
    .Xi(\一位全加器fa封装2_94_si ), .Yi(\一位全加器fa封装2_100_cout [1]));
  \一位全加器FA封装2  \u_一位全加器fa封装2_94  (
    .Cout(\一位全加器fa封装2_94_cout [0]), .Si(\一位全加器fa封装2_94_si ), .Cin(\一位全加器fa封装2_101_cout ),
    .Xi(\一位全加器fa封装2_95_si ), .Yi(\一位全加器fa封装2_96_si ));
  \一位全加器FA封装2  \u_一位全加器fa封装2_95  (
    .Cout(\一位全加器fa封装2_95_cout ), .Si(\一位全加器fa封装2_95_si ), .Cin(\一位全加器fa封装2_98_si ), .Xi(\一位全加器fa封装2_92_si ),
    .Yi(\一位全加器fa封装2_97_si ));
  \一位全加器FA封装2  \u_一位全加器fa封装2_96  (
    .Cout(\一位全加器fa封装2_94_cout [1]), .Si(\一位全加器fa封装2_96_si ), .Cin(\一位全加器fa封装2_105_cout [0]),
    .Xi(\一位全加器fa封装2_105_cout [2]), .Yi(\一位全加器fa封装2_105_cout [1]));
  \一位全加器FA封装2  \u_一位全加器fa封装2_97  (
    .Cout(\一位全加器fa封装2_98_cout [1]), .Si(\一位全加器fa封装2_97_si ), .Cin(undriven_110), .Xi(undriven_108),
    .Yi(undriven_109));
  shape shape_8 ();
  \一位全加器FA封装2  \u_一位全加器fa封装2_98  (
    .Cout(\一位全加器fa封装2_98_cout [0]), .Si(\一位全加器fa封装2_98_si ), .Cin(1'b0), .Xi(undriven_111), .Yi(undriven_112));
  \一位全加器FA封装2  \u_一位全加器fa封装2_99  (
    .Cout(\一位全加器fa封装2_99_cout ), .Si(\一位全加器fa封装2_99_si ), .Cin(\一位全加器fa封装2_106_cout [0]),
    .Xi(\一位全加器fa封装2_100_si ), .Yi(\一位全加器fa封装2_106_cout [1]));
  \一位全加器FA封装2  \u_一位全加器fa封装2_100  (
    .Cout(\一位全加器fa封装2_100_cout [0]), .Si(\一位全加器fa封装2_100_si ), .Cin(\一位全加器fa封装2_107_cout ),
    .Xi(\一位全加器fa封装2_101_si ), .Yi(\一位全加器fa封装2_104_si ));
  \一位全加器FA封装2  \u_一位全加器fa封装2_101  (
    .Cout(\一位全加器fa封装2_101_cout ), .Si(\一位全加器fa封装2_101_si ), .Cin(\一位全加器fa封装2_105_si ),
    .Xi(\一位全加器fa封装2_103_si ), .Yi(\一位全加器fa封装2_102_si ));
  \一位全加器FA封装2  \u_一位全加器fa封装2_102  (
    .Cout(\一位全加器fa封装2_105_cout [1]), .Si(\一位全加器fa封装2_102_si ), .Cin(undriven_118), .Xi(undriven_116),
    .Yi(undriven_117));
  \一位全加器FA封装2  \u_一位全加器fa封装2_103  (
    .Cout(\一位全加器fa封装2_105_cout [2]), .Si(\一位全加器fa封装2_103_si ), .Cin(undriven_115), .Xi(undriven_113),
    .Yi(undriven_114));
  \一位全加器FA封装2  \u_一位全加器fa封装2_104  (
    .Cout(\一位全加器fa封装2_100_cout [1]), .Si(\一位全加器fa封装2_104_si ), .Cin(\一位全加器fa封装2_112_cout [0]),
    .Xi(\一位全加器fa封装2_112_cout [2]), .Yi(\一位全加器fa封装2_112_cout [1]));
  \一位全加器FA封装2  \u_一位全加器fa封装2_105  (
    .Cout(\一位全加器fa封装2_105_cout [0]), .Si(\一位全加器fa封装2_105_si ), .Cin(1'b0), .Xi(undriven_119),
    .Yi(undriven_120));
  \一位全加器FA封装2  \u_一位全加器fa封装2_106  (
    .Cout(\一位全加器fa封装2_106_cout [0]), .Si(\一位全加器fa封装2_106_si ), .Cin(undriven_125), .Xi(\一位全加器fa封装2_107_si ),
    .Yi(\一位全加器fa封装2_110_si ));
  \一位全加器FA封装2  \u_一位全加器fa封装2_107  (
    .Cout(\一位全加器fa封装2_107_cout ), .Si(\一位全加器fa封装2_107_si ), .Cin(\一位全加器fa封装2_112_si ),
    .Xi(\一位全加器fa封装2_108_si ), .Yi(\一位全加器fa封装2_111_si ));
  \一位全加器FA封装2  \u_一位全加器fa封装2_108  (
    .Cout(\一位全加器fa封装2_112_cout [2]), .Si(\一位全加器fa封装2_108_si ), .Cin(undriven_123), .Xi(undriven_121),
    .Yi(undriven_122));
  \一位全加器FA封装2  \u_一位全加器fa封装2_109  (
    .Cout(\一位全加器fa封装2_109_cout ), .Si(\一位全加器fa封装2_109_si ), .Cin(undriven_131[0]), .Xi(\一位全加器fa封装2_106_si ),
    .Yi(undriven_131[1]));
  \一位全加器FA封装2  \u_一位全加器fa封装2_110  (
    .Cout(\一位全加器fa封装2_106_cout [1]), .Si(\一位全加器fa封装2_110_si ), .Cin(undriven_129[0]), .Xi(undriven_129[2]),
    .Yi(undriven_129[1]));
  \一位全加器FA封装2  \u_一位全加器fa封装2_111  (
    .Cout(\一位全加器fa封装2_112_cout [1]), .Si(\一位全加器fa封装2_111_si ), .Cin(undriven_127), .Xi(undriven_124),
    .Yi(undriven_126));
  \一位全加器FA封装2  \u_一位全加器fa封装2_112  (
    .Cout(\一位全加器fa封装2_112_cout [0]), .Si(\一位全加器fa封装2_112_si ), .Cin(1'b0), .Xi(undriven_128),
    .Yi(undriven_130));
endmodule

// Trace
module trace (
  input  [7:0] in_1,
  output [31:0] X,
  output [31:0] Y,
  output [3:0] AluOP,
  output [31:0] R,
  output [31:0] R2,
  output [2:0] FLAGS
);

  ROM #(.dataWidth(32)) rom_1 (.addr(in_1), .data(X));  // open: sel
  ROM #(.dataWidth(32)) rom_2 (.addr(in_1), .data(Y));  // open: sel
  ROM #(.dataWidth(4)) rom_3 (.addr(in_1), .data(AluOP));  // open: sel
  ROM #(.dataWidth(32)) rom_4 (.addr(in_1), .data(R));  // open: sel
  ROM #(.dataWidth(32)) rom_5 (.addr(in_1), .data(R2));  // open: sel
  ROM #(.dataWidth(3)) rom_6 (.addr(in_1), .data(FLAGS));  // open: sel

  // Notes on the sheet:
  //   X trace
  //   Y trace
  //   ALU OP Trace
  //   Result Benchmark
  //   Result2 Benchmark
  //   FLAGS Benchmark
  //   contents of rom_1 (hex, n*v repeats v):
  //   ff00ffff ff00ffff ff000000 ff00ffff 7fffffff fffffffe ffff ffffffff 7fffffff 80000000 7ff00000 7c
  //   80000000 7fffffff ff00ffff 7fffffff 18*fffffffe
  //   contents of rom_2 (hex, n*v repeats v):
  //   7 ff00ffff 18 18 10 10 80 ffffffff c 80000000 7c 7ff00000 1 fffffffe 18 74 fffffffe 88 10 ffffffff
  //   10 ffffffff 12*10
  //   contents of rom_3 (hex, n*v repeats v):
  //   0 0 1 2 3 4 4*5 4*6 7 8 9 a b b c c f 11*9 f
  //   contents of rom_4 (hex, n*v repeats v):
  //   807fff80 80000000 ffffffff ff fffffff0 fffffff 1007f fffffffe 8000000b 0 7fefff84 8010007c 7fffffff
  //   80000001 18 7fffffff 0 1 1 1 0 1 300000 11*ffffffee 1
  //   contents of rom_5 (hex, n*v repeats v):
  //   4*0 7 e
  //   contents of rom_6 (hex, n*v repeats v):
  //   0 1 5*0 3 4 7 0 2 4 6 0 0 1 17*0 66*1
endmodule

// 单项评分
module \单项评分  (
  input  ALU_SWITCH,
  input  EQ,
  input  EN,
  input  [4:0] \分值 ,
  input  CLK,
  output [7:0] \正确条数 ,
  output [7:0] \扣分 ,
  output Right,
  output [7:0] Total
);

  wire and_1_out, and_2_out, not_1_out, priority_encoder_1_gs, priority_encoder_1_out;
  wire [7:0] bit_extender_1_out;

  and and_1 (and_1_out, ALU_SWITCH, EN);
  Priority_Encoder #(.select(1)) priority_encoder_1 (
    .in0(EQ), .in1(EQ), .out(priority_encoder_1_out), .gs(priority_encoder_1_gs));  // open: en_out, en_in
  Counter counter_1 (.count(and_1_out), .Q(Total), .clk(CLK));  // open: load, D, carry, clr
  and and_2 (and_2_out, ALU_SWITCH, priority_encoder_1_out, priority_encoder_1_gs, EN);
  Counter counter_2 (.count(and_2_out), .Q(\正确条数 ), .clk(CLK));  // open: load, D, carry, clr
  Comparator comparator_1 (.a(\正确条数 ), .b(Total), .eq(Right));  // open: gt, lt
  assign bit_extender_1_out = {{3{1'b0}}, \分值 };  // Bit_Extender bit_extender_1
  Multiplexer #(.width(8), .enable("false")) multiplexer_1 (
    .in0({8{1'b0}}), .in1(bit_extender_1_out), .out(\扣分 ), .sel(not_1_out));
  not not_1 (not_1_out, Right);

  // Notes on the sheet:
  //   只有使用优先编码器才能屏蔽掉位置状态
endmodule

module \总评分  (
  input  [7:0] in_1,
  input  [7:0] in_2,
  input  [7:0] in_3,
  input  [7:0] in_4,
  input  [7:0] in_5,
  input  [7:0] in_6,
  input  [7:0] in_7,
  input  [7:0] in_8,
  input  [7:0] in_9,
  input  [7:0] in_10,
  input  [7:0] in_11,
  input  [7:0] in_12,
  input  [7:0] in_13,
  input  [7:0] in_14,
  input  [7:0] in_15,
  input  [7:0] in_16,
  input  \悬空扣分 ,
  output [7:0] Result,
  output [3:0] High,
  output [3:0] Low,
  output [3:0] Mid
);

  wire [7:0] adder_1_out, adder_2_out, adder_3_out, adder_4_out, adder_5_out, adder_6_out, adder_7_out,
       adder_8_out, adder_9_out, adder_10_out, adder_11_out, adder_12_out, adder_13_out, adder_14_out,
       adder_15_out, divider_1_out, subtractor_1_out, subtractor_2_out;
  wire [7:4] divider_1_rem, divider_2_out, divider_2_rem;

  Adder adder_1 (.a(in_1), .b(in_2), .out(adder_1_out));  // open: cin, cout
  Adder adder_2 (.a(in_3), .b(in_4), .out(adder_2_out));  // open: cin, cout
  Adder adder_3 (.a(in_5), .b(in_6), .out(adder_3_out));  // open: cin, cout
  Adder adder_4 (.a(in_7), .b(in_8), .out(adder_4_out));  // open: cin, cout
  Adder adder_5 (.a(in_9), .b(in_10), .out(adder_5_out));  // open: cin, cout
  Adder adder_6 (.a(in_11), .b(in_12), .out(adder_6_out));  // open: cin, cout
  Adder adder_7 (.a(in_13), .b(in_14), .out(adder_7_out));  // open: cin, cout
  Adder adder_8 (.a(in_15), .b(in_16), .out(adder_8_out));  // open: cin, cout
  Adder adder_9 (.a(adder_1_out), .b(adder_2_out), .out(adder_9_out));  // open: cin, cout
  Adder adder_10 (.a(adder_3_out), .b(adder_4_out), .out(adder_10_out));  // open: cin, cout
  Adder adder_11 (.a(adder_5_out), .b(adder_6_out), .out(adder_11_out));  // open: cin, cout
  Adder adder_12 (.a(adder_7_out), .b(adder_8_out), .out(adder_12_out));  // open: cin, cout
  Adder adder_13 (.a(adder_9_out), .b(adder_10_out), .out(adder_13_out));  // open: cin, cout
  Adder adder_14 (.a(adder_11_out), .b(adder_12_out), .out(adder_14_out));  // open: cin, cout
  Adder adder_15 (.a(adder_13_out), .b(adder_14_out), .out(adder_15_out));  // open: cin, cout
  Subtractor subtractor_1 (.a(8'h64), .b(adder_15_out), .out(subtractor_1_out));  // open: bin, bout
  Subtractor subtractor_2 (.a(subtractor_1_out), .b(8'h5), .out(subtractor_2_out));  // open: bin, bout
  Multiplexer #(.width(8), .enable("false")) multiplexer_1 (
    .in0(subtractor_1_out), .in1(subtractor_2_out), .out(Result), .sel(\悬空扣分 ));
  Divider divider_1 (.a(Result), .b(8'ha), .out(divider_1_out), .rem({divider_1_rem, Low}));  // open: upper
  Divider divider_2 (
    .a(divider_1_out), .b(8'ha), .out({divider_2_out, High}), .rem({divider_2_rem, Mid}));  // open: upper
endmodule
module \移位电路  (
  input  [31:0] X,
  input  [4:0] Y,
  output [31:0] out
);

  wire full_with_1, multiplexer_1_out, multiplexer_2_out, multiplexer_3_out, multiplexer_4_out,
       multiplexer_5_out, multiplexer_6_out, multiplexer_7_out, multiplexer_8_out, multiplexer_9_out,
       multiplexer_10_out, multiplexer_11_out, multiplexer_12_out, multiplexer_13_out, multiplexer_14_out,
       multiplexer_15_out, multiplexer_16_out, multiplexer_17_out, multiplexer_18_out, multiplexer_19_out,
       multiplexer_20_out, multiplexer_21_out, multiplexer_22_out, multiplexer_23_out, multiplexer_24_out,
       multiplexer_25_out, multiplexer_26_out, multiplexer_27_out, multiplexer_28_out, multiplexer_29_out,
       multiplexer_30_out, multiplexer_31_out, multiplexer_32_out, multiplexer_33_out, multiplexer_34_out,
       multiplexer_35_out, multiplexer_36_out, multiplexer_37_out, multiplexer_38_out, multiplexer_39_out,
       multiplexer_40_out, multiplexer_41_out, multiplexer_42_out, multiplexer_43_out, multiplexer_44_out,
       multiplexer_45_out, multiplexer_46_out, multiplexer_47_out, multiplexer_48_out, multiplexer_49_out,
       multiplexer_50_out, multiplexer_51_out, multiplexer_52_out, multiplexer_53_out, multiplexer_54_out,
       multiplexer_55_out, multiplexer_56_out, multiplexer_57_out, multiplexer_58_out, multiplexer_59_out,
       multiplexer_60_out, multiplexer_61_out, multiplexer_62_out, multiplexer_63_out, multiplexer_64_out,
       multiplexer_65_out, multiplexer_66_out, multiplexer_67_out, multiplexer_68_out, multiplexer_69_out,
       multiplexer_70_out, multiplexer_71_out, multiplexer_72_out, multiplexer_73_out, multiplexer_74_out,
       multiplexer_75_out, multiplexer_76_out, multiplexer_77_out, multiplexer_78_out, multiplexer_79_out,
       multiplexer_80_out, multiplexer_81_out, multiplexer_82_out, multiplexer_83_out, multiplexer_84_out,
       multiplexer_85_out, multiplexer_86_out, multiplexer_87_out, multiplexer_88_out, multiplexer_89_out,
       multiplexer_90_out, multiplexer_91_out, multiplexer_92_out, multiplexer_93_out, multiplexer_94_out,
       multiplexer_95_out, multiplexer_96_out, multiplexer_97_out, multiplexer_98_out, multiplexer_99_out,
       multiplexer_100_out, multiplexer_101_out, multiplexer_102_out, multiplexer_103_out,
       multiplexer_104_out, multiplexer_105_out, multiplexer_106_out, multiplexer_107_out,
       multiplexer_108_out, multiplexer_109_out, multiplexer_110_out, multiplexer_111_out,
       multiplexer_112_out, multiplexer_113_out, multiplexer_114_out, multiplexer_115_out,
       multiplexer_116_out, multiplexer_117_out, multiplexer_118_out, multiplexer_119_out,
       multiplexer_120_out, multiplexer_121_out, multiplexer_122_out, multiplexer_123_out,
       multiplexer_124_out, multiplexer_125_out, multiplexer_126_out, multiplexer_127_out,
       multiplexer_128_out, multiplexer_129_out, multiplexer_130_out, multiplexer_131_out,
       multiplexer_132_out, multiplexer_133_out, multiplexer_134_out, multiplexer_135_out,
       multiplexer_136_out, multiplexer_137_out, multiplexer_138_out, multiplexer_139_out,
       multiplexer_140_out, multiplexer_141_out, multiplexer_142_out, multiplexer_143_out,
       multiplexer_144_out, multiplexer_145_out, multiplexer_146_out, multiplexer_147_out,
       multiplexer_148_out, multiplexer_149_out, multiplexer_150_out, multiplexer_151_out,
       multiplexer_152_out, multiplexer_153_out, multiplexer_154_out, multiplexer_155_out,
       multiplexer_156_out, multiplexer_157_out, multiplexer_158_out, multiplexer_159_out,
       multiplexer_160_out, multiplexer_161_out, multiplexer_162_out, multiplexer_163_out,
       multiplexer_164_out, multiplexer_165_out, multiplexer_166_out, multiplexer_167_out,
       multiplexer_168_out, multiplexer_169_out, multiplexer_170_out, multiplexer_171_out,
       multiplexer_172_out, multiplexer_173_out, multiplexer_174_out, multiplexer_175_out,
       multiplexer_176_out, multiplexer_177_out, multiplexer_178_out, multiplexer_179_out,
       multiplexer_180_out, multiplexer_181_out, multiplexer_182_out, multiplexer_183_out,
       multiplexer_184_out, multiplexer_185_out, multiplexer_186_out, multiplexer_187_out,
       multiplexer_188_out, multiplexer_189_out, multiplexer_190_out, multiplexer_191_out,
       multiplexer_192_out, multiplexer_193_out, multiplexer_194_out, multiplexer_195_out,
       multiplexer_196_out, multiplexer_197_out, multiplexer_198_out, multiplexer_199_out,
       multiplexer_200_out, multiplexer_201_out, multiplexer_202_out, multiplexer_203_out,
       multiplexer_204_out, multiplexer_205_out, multiplexer_206_out, multiplexer_207_out,
       multiplexer_208_out, multiplexer_209_out, multiplexer_210_out, multiplexer_211_out,
       multiplexer_212_out, multiplexer_213_out, multiplexer_214_out, multiplexer_215_out,
       multiplexer_216_out, multiplexer_217_out, multiplexer_218_out, multiplexer_219_out,
       multiplexer_220_out, multiplexer_221_out, multiplexer_222_out, multiplexer_223_out,
       multiplexer_224_out, multiplexer_225_out, multiplexer_226_out, multiplexer_227_out,
       multiplexer_228_out, multiplexer_229_out, multiplexer_230_out, multiplexer_231_out,
       multiplexer_232_out, multiplexer_233_out, multiplexer_234_out, multiplexer_235_out,
       multiplexer_236_out, multiplexer_237_out, multiplexer_238_out, multiplexer_239_out,
       multiplexer_240_out, multiplexer_241_out, multiplexer_242_out, multiplexer_243_out,
       multiplexer_244_out, multiplexer_245_out, multiplexer_246_out, multiplexer_247_out,
       multiplexer_248_out, multiplexer_249_out, multiplexer_250_out, multiplexer_251_out,
       multiplexer_252_out, multiplexer_253_out, multiplexer_254_out, multiplexer_255_out,
       multiplexer_256_out, multiplexer_257_out, multiplexer_258_out, multiplexer_259_out,
       multiplexer_260_out, multiplexer_261_out, multiplexer_262_out, multiplexer_263_out,
       multiplexer_264_out, multiplexer_265_out, multiplexer_266_out, multiplexer_267_out,
       multiplexer_268_out, multiplexer_269_out, multiplexer_270_out, multiplexer_271_out,
       multiplexer_272_out, multiplexer_273_out, multiplexer_274_out, multiplexer_275_out,
       multiplexer_276_out, multiplexer_277_out, multiplexer_278_out, multiplexer_279_out,
       multiplexer_280_out, multiplexer_281_out, multiplexer_282_out, multiplexer_283_out,
       multiplexer_284_out, multiplexer_285_out, multiplexer_286_out, multiplexer_287_out,
       multiplexer_288_out, multiplexer_289_out, multiplexer_290_out, multiplexer_291_out,
       multiplexer_292_out, multiplexer_293_out, multiplexer_294_out, multiplexer_295_out,
       multiplexer_296_out, multiplexer_297_out, multiplexer_298_out, multiplexer_299_out,
       multiplexer_300_out, multiplexer_301_out, multiplexer_302_out, multiplexer_303_out,
       multiplexer_304_out, multiplexer_305_out, multiplexer_306_out, multiplexer_307_out,
       multiplexer_308_out, multiplexer_309_out, multiplexer_310_out, multiplexer_311_out,
       multiplexer_312_out, multiplexer_313_out, multiplexer_314_out, multiplexer_315_out,
       multiplexer_316_out, multiplexer_317_out, multiplexer_318_out, multiplexer_319_out,
       multiplexer_320_out, multiplexer_321_out, multiplexer_322_out, multiplexer_323_out,
       multiplexer_324_out, multiplexer_325_out, multiplexer_326_out, multiplexer_327_out,
       multiplexer_328_out, multiplexer_329_out, multiplexer_330_out, multiplexer_331_out,
       multiplexer_332_out, multiplexer_333_out, multiplexer_334_out, multiplexer_335_out,
       multiplexer_336_out, multiplexer_337_out, multiplexer_338_out, multiplexer_339_out,
       multiplexer_340_out, multiplexer_341_out, multiplexer_342_out, multiplexer_343_out,
       multiplexer_344_out, multiplexer_345_out, multiplexer_346_out, multiplexer_347_out,
       multiplexer_348_out, multiplexer_349_out, multiplexer_350_out, multiplexer_351_out,
       multiplexer_352_out, multiplexer_353_out, multiplexer_354_out, multiplexer_355_out,
       multiplexer_356_out, multiplexer_357_out, multiplexer_358_out, multiplexer_359_out,
       multiplexer_360_out, multiplexer_361_out, multiplexer_362_out, multiplexer_363_out,
       multiplexer_364_out, multiplexer_365_out, multiplexer_366_out, multiplexer_367_out,
       multiplexer_368_out, multiplexer_369_out, multiplexer_370_out, multiplexer_371_out,
       multiplexer_372_out, multiplexer_373_out, multiplexer_374_out, multiplexer_375_out,
       multiplexer_376_out, multiplexer_377_out, multiplexer_378_out, multiplexer_379_out,
       multiplexer_380_out, multiplexer_381_out, multiplexer_382_out, multiplexer_383_out,
       multiplexer_384_out, multiplexer_385_out, multiplexer_386_out, multiplexer_387_out,
       multiplexer_388_out, multiplexer_389_out, multiplexer_390_out, multiplexer_391_out,
       multiplexer_392_out, multiplexer_393_out, multiplexer_394_out, multiplexer_395_out,
       multiplexer_396_out, multiplexer_397_out, multiplexer_398_out, multiplexer_399_out,
       multiplexer_400_out, multiplexer_401_out, multiplexer_402_out, multiplexer_403_out,
       multiplexer_404_out, multiplexer_405_out, multiplexer_406_out, multiplexer_407_out,
       multiplexer_408_out, multiplexer_409_out, multiplexer_410_out, multiplexer_411_out,
       multiplexer_412_out, multiplexer_413_out, multiplexer_414_out, multiplexer_415_out,
       multiplexer_416_out, multiplexer_417_out, multiplexer_418_out, multiplexer_419_out,
       multiplexer_420_out, multiplexer_421_out, multiplexer_422_out, multiplexer_423_out,
       multiplexer_424_out, multiplexer_425_out, multiplexer_426_out, multiplexer_427_out,
       multiplexer_428_out, multiplexer_429_out, multiplexer_430_out, multiplexer_431_out,
       multiplexer_432_out, multiplexer_433_out, multiplexer_434_out, multiplexer_435_out,
       multiplexer_436_out, multiplexer_437_out, multiplexer_438_out, multiplexer_439_out,
       multiplexer_440_out, multiplexer_441_out, multiplexer_442_out, multiplexer_443_out,
       multiplexer_444_out, multiplexer_445_out, multiplexer_446_out, multiplexer_447_out,
       multiplexer_448_out, multiplexer_449_out, multiplexer_450_out, multiplexer_451_out,
       multiplexer_452_out, multiplexer_453_out, multiplexer_454_out, multiplexer_455_out,
       multiplexer_456_out, multiplexer_457_out, multiplexer_458_out, multiplexer_459_out,
       multiplexer_460_out, multiplexer_461_out, multiplexer_462_out, multiplexer_463_out,
       multiplexer_464_out, multiplexer_465_out, multiplexer_466_out, multiplexer_467_out,
       multiplexer_468_out, multiplexer_469_out, multiplexer_470_out, multiplexer_471_out,
       multiplexer_472_out, multiplexer_473_out, multiplexer_474_out, multiplexer_475_out,
       multiplexer_476_out, multiplexer_477_out, multiplexer_478_out, multiplexer_479_out,
       multiplexer_480_out, multiplexer_481_out, multiplexer_482_out, multiplexer_483_out,
       multiplexer_484_out, multiplexer_485_out, multiplexer_486_out, multiplexer_487_out,
       multiplexer_488_out, multiplexer_489_out, multiplexer_490_out, multiplexer_491_out,
       multiplexer_492_out, multiplexer_493_out, multiplexer_494_out, multiplexer_495_out,
       multiplexer_496_out, multiplexer_497_out, multiplexer_498_out, multiplexer_499_out,
       multiplexer_500_out, multiplexer_501_out, multiplexer_502_out, multiplexer_503_out,
       multiplexer_504_out, multiplexer_505_out, multiplexer_506_out, multiplexer_507_out,
       multiplexer_508_out, multiplexer_509_out, multiplexer_510_out, multiplexer_511_out,
       multiplexer_512_out, multiplexer_513_out, multiplexer_514_out, multiplexer_515_out,
       multiplexer_516_out, multiplexer_517_out, multiplexer_518_out, multiplexer_519_out,
       multiplexer_520_out, multiplexer_521_out, multiplexer_522_out, multiplexer_523_out,
       multiplexer_524_out, multiplexer_525_out, multiplexer_526_out, multiplexer_527_out,
       multiplexer_528_out, swift_0, swift_1, swift_2, swift_3, swift_4, swift_5, swift_6, swift_7, swift_8,
       swift_9, swift_10, swift_11, swift_12, swift_13, swift_14, swift_15, swift_16, swift_17, swift_18,
       swift_19, swift_20, swift_21, swift_22, swift_23, swift_24, swift_25, swift_26, swift_27, swift_28,
       swift_29, swift_30, swift_31;

  Multiplexer multiplexer_1 (.in0(1'b0), .in1(1'b1), .out(multiplexer_1_out), .sel(full_with_1));  // open: en
  Multiplexer multiplexer_2 (.in0(1'b0), .in1(1'b1), .out(multiplexer_2_out), .sel(full_with_1));  // open: en
  Multiplexer multiplexer_3 (.in0(multiplexer_1_out), .in1(X[0]), .out(multiplexer_3_out), .sel(swift_31));  // open: en
  Multiplexer multiplexer_4 (.in0(1'b0), .in1(1'b1), .out(multiplexer_4_out), .sel(full_with_1));  // open: en
  Multiplexer multiplexer_5 (.in0(multiplexer_2_out), .in1(X[0]), .out(multiplexer_5_out), .sel(swift_30));  // open: en
  Multiplexer multiplexer_6 (.in0(multiplexer_3_out), .in1(X[1]), .out(multiplexer_6_out), .sel(swift_30));  // open: en
  Multiplexer multiplexer_7 (.in0(1'b0), .in1(1'b1), .out(multiplexer_7_out), .sel(full_with_1));  // open: en
  Multiplexer multiplexer_8 (.in0(multiplexer_4_out), .in1(X[0]), .out(multiplexer_8_out), .sel(swift_29));  // open: en
  Multiplexer multiplexer_9 (.in0(multiplexer_5_out), .in1(X[1]), .out(multiplexer_9_out), .sel(swift_29));  // open: en
  Multiplexer multiplexer_10 (
    .in0(multiplexer_6_out), .in1(X[2]), .out(multiplexer_10_out), .sel(swift_29));  // open: en
  Multiplexer multiplexer_11 (.in0(1'b0), .in1(1'b1), .out(multiplexer_11_out), .sel(full_with_1));  // open: en
  Multiplexer multiplexer_12 (
    .in0(multiplexer_7_out), .in1(X[0]), .out(multiplexer_12_out), .sel(swift_28));  // open: en
  Multiplexer multiplexer_13 (
    .in0(multiplexer_8_out), .in1(X[1]), .out(multiplexer_13_out), .sel(swift_28));  // open: en
  Multiplexer multiplexer_14 (
    .in0(multiplexer_9_out), .in1(X[2]), .out(multiplexer_14_out), .sel(swift_28));  // open: en
  Multiplexer multiplexer_15 (
    .in0(multiplexer_10_out), .in1(X[3]), .out(multiplexer_15_out), .sel(swift_28));  // open: en
  Multiplexer multiplexer_16 (.in0(1'b0), .in1(1'b1), .out(multiplexer_16_out), .sel(full_with_1));  // open: en
  Multiplexer multiplexer_17 (
    .in0(multiplexer_11_out), .in1(X[0]), .out(multiplexer_17_out), .sel(swift_27));  // open: en
  Multiplexer multiplexer_18 (
    .in0(multiplexer_12_out), .in1(X[1]), .out(multiplexer_18_out), .sel(swift_27));  // open: en
  Multiplexer multiplexer_19 (
    .in0(multiplexer_13_out), .in1(X[2]), .out(multiplexer_19_out), .sel(swift_27));  // open: en
  Multiplexer multiplexer_20 (
    .in0(multiplexer_14_out), .in1(X[3]), .out(multiplexer_20_out), .sel(swift_27));  // open: en
  Multiplexer multiplexer_21 (
    .in0(multiplexer_15_out), .in1(X[4]), .out(multiplexer_21_out), .sel(swift_27));  // open: en
  Multiplexer multiplexer_22 (.in0(1'b0), .in1(1'b1), .out(multiplexer_22_out), .sel(full_with_1));  // open: en
  Multiplexer multiplexer_23 (
    .in0(multiplexer_16_out), .in1(X[0]), .out(multiplexer_23_out), .sel(swift_26));  // open: en
  Multiplexer multiplexer_24 (
    .in0(multiplexer_17_out), .in1(X[1]), .out(multiplexer_24_out), .sel(swift_26));  // open: en
  Multiplexer multiplexer_25 (
    .in0(multiplexer_18_out), .in1(X[2]), .out(multiplexer_25_out), .sel(swift_26));  // open: en
  Multiplexer multiplexer_26 (
    .in0(multiplexer_19_out), .in1(X[3]), .out(multiplexer_26_out), .sel(swift_26));  // open: en
  Multiplexer multiplexer_27 (
    .in0(multiplexer_20_out), .in1(X[4]), .out(multiplexer_27_out), .sel(swift_26));  // open: en
  Multiplexer multiplexer_28 (
    .in0(multiplexer_21_out), .in1(X[5]), .out(multiplexer_28_out), .sel(swift_26));  // open: en
  Multiplexer multiplexer_29 (
    .in0(multiplexer_22_out), .in1(X[0]), .out(multiplexer_29_out), .sel(swift_25));  // open: en
  Multiplexer multiplexer_30 (
    .in0(multiplexer_23_out), .in1(X[1]), .out(multiplexer_30_out), .sel(swift_25));  // open: en
  Multiplexer multiplexer_31 (
    .in0(multiplexer_24_out), .in1(X[2]), .out(multiplexer_31_out), .sel(swift_25));  // open: en
  Multiplexer multiplexer_32 (
    .in0(multiplexer_25_out), .in1(X[3]), .out(multiplexer_32_out), .sel(swift_25));  // open: en
  Multiplexer multiplexer_33 (
    .in0(multiplexer_26_out), .in1(X[4]), .out(multiplexer_33_out), .sel(swift_25));  // open: en
  Multiplexer multiplexer_34 (
    .in0(multiplexer_27_out), .in1(X[5]), .out(multiplexer_34_out), .sel(swift_25));  // open: en
  Multiplexer multiplexer_35 (
    .in0(multiplexer_28_out), .in1(X[6]), .out(multiplexer_35_out), .sel(swift_25));  // open: en
  Multiplexer multiplexer_36 (.in0(1'b0), .in1(1'b1), .out(multiplexer_36_out), .sel(full_with_1));  // open: en
  Multiplexer multiplexer_37 (
    .in0(multiplexer_36_out), .in1(X[0]), .out(multiplexer_37_out), .sel(swift_24));  // open: en
  Multiplexer multiplexer_38 (
    .in0(multiplexer_29_out), .in1(X[1]), .out(multiplexer_38_out), .sel(swift_24));  // open: en
  Multiplexer multiplexer_39 (
    .in0(multiplexer_30_out), .in1(X[2]), .out(multiplexer_39_out), .sel(swift_24));  // open: en
  Multiplexer multiplexer_40 (
    .in0(multiplexer_31_out), .in1(X[3]), .out(multiplexer_40_out), .sel(swift_24));  // open: en
  Multiplexer multiplexer_41 (
    .in0(multiplexer_32_out), .in1(X[4]), .out(multiplexer_41_out), .sel(swift_24));  // open: en
  Multiplexer multiplexer_42 (
    .in0(multiplexer_33_out), .in1(X[5]), .out(multiplexer_42_out), .sel(swift_24));  // open: en
  Multiplexer multiplexer_43 (
    .in0(multiplexer_34_out), .in1(X[6]), .out(multiplexer_43_out), .sel(swift_24));  // open: en
  Multiplexer multiplexer_44 (
    .in0(multiplexer_35_out), .in1(X[7]), .out(multiplexer_44_out), .sel(swift_24));  // open: en
  Decoder #(.select(5)) decoder_1 (
    .out0(swift_0), .out1(swift_1), .out2(swift_2), .out3(swift_3), .out4(swift_4), .out5(swift_5),
    .out6(swift_6), .out7(swift_7), .out8(swift_8), .out9(swift_9), .out10(swift_10), .out11(swift_11),
    .out12(swift_12), .out13(swift_13), .out14(swift_14), .out15(swift_15), .out16(swift_16),
    .out17(swift_17), .out18(swift_18), .out19(swift_19), .out20(swift_20), .out21(swift_21),
    .out22(swift_22), .out23(swift_23), .out24(swift_24), .out25(swift_25), .out26(swift_26),
    .out27(swift_27), .out28(swift_28), .out29(swift_29), .out30(swift_30), .out31(swift_31), .sel(Y));  // open: en
  Multiplexer multiplexer_45 (.in0(1'b0), .in1(1'b1), .out(multiplexer_45_out), .sel(full_with_1));  // open: en
  Multiplexer multiplexer_46 (
    .in0(multiplexer_45_out), .in1(X[0]), .out(multiplexer_46_out), .sel(swift_23));  // open: en
  Multiplexer multiplexer_47 (
    .in0(multiplexer_37_out), .in1(X[1]), .out(multiplexer_47_out), .sel(swift_23));  // open: en
  Multiplexer multiplexer_48 (
    .in0(multiplexer_38_out), .in1(X[2]), .out(multiplexer_48_out), .sel(swift_23));  // open: en
  Multiplexer multiplexer_49 (
    .in0(multiplexer_39_out), .in1(X[3]), .out(multiplexer_49_out), .sel(swift_23));  // open: en
  Multiplexer multiplexer_50 (
    .in0(multiplexer_40_out), .in1(X[4]), .out(multiplexer_50_out), .sel(swift_23));  // open: en
  Multiplexer multiplexer_51 (
    .in0(multiplexer_41_out), .in1(X[5]), .out(multiplexer_51_out), .sel(swift_23));  // open: en
  Multiplexer multiplexer_52 (
    .in0(multiplexer_42_out), .in1(X[6]), .out(multiplexer_52_out), .sel(swift_23));  // open: en
  Multiplexer multiplexer_53 (
    .in0(multiplexer_43_out), .in1(X[7]), .out(multiplexer_53_out), .sel(swift_23));  // open: en
  Multiplexer multiplexer_54 (
    .in0(multiplexer_44_out), .in1(X[8]), .out(multiplexer_54_out), .sel(swift_23));  // open: en
  Multiplexer multiplexer_55 (.in0(1'b0), .in1(1'b1), .out(multiplexer_55_out), .sel(full_with_1));  // open: en
  Multiplexer multiplexer_56 (.in0(1'b0), .in1(1'b1), .out(multiplexer_56_out), .sel(full_with_1));  // open: en
  Multiplexer multiplexer_57 (
    .in0(multiplexer_55_out), .in1(X[0]), .out(multiplexer_57_out), .sel(swift_22));  // open: en
  Multiplexer multiplexer_58 (
    .in0(multiplexer_46_out), .in1(X[1]), .out(multiplexer_58_out), .sel(swift_22));  // open: en
  Multiplexer multiplexer_59 (
    .in0(multiplexer_47_out), .in1(X[2]), .out(multiplexer_59_out), .sel(swift_22));  // open: en
  Multiplexer multiplexer_60 (
    .in0(multiplexer_48_out), .in1(X[3]), .out(multiplexer_60_out), .sel(swift_22));  // open: en
  Multiplexer multiplexer_61 (
    .in0(multiplexer_49_out), .in1(X[4]), .out(multiplexer_61_out), .sel(swift_22));  // open: en
  Multiplexer multiplexer_62 (
    .in0(multiplexer_50_out), .in1(X[5]), .out(multiplexer_62_out), .sel(swift_22));  // open: en
  Multiplexer multiplexer_63 (
    .in0(multiplexer_51_out), .in1(X[6]), .out(multiplexer_63_out), .sel(swift_22));  // open: en
  Multiplexer multiplexer_64 (
    .in0(multiplexer_52_out), .in1(X[7]), .out(multiplexer_64_out), .sel(swift_22));  // open: en
  Multiplexer multiplexer_65 (
    .in0(multiplexer_53_out), .in1(X[8]), .out(multiplexer_65_out), .sel(swift_22));  // open: en
  Multiplexer multiplexer_66 (
    .in0(multiplexer_54_out), .in1(X[9]), .out(multiplexer_66_out), .sel(swift_22));  // open: en
  Multiplexer multiplexer_67 (.in0(1'b0), .in1(1'b1), .out(multiplexer_67_out), .sel(full_with_1));  // open: en
  Multiplexer multiplexer_68 (
    .in0(multiplexer_56_out), .in1(X[0]), .out(multiplexer_68_out), .sel(swift_21));  // open: en
  Multiplexer multiplexer_69 (
    .in0(multiplexer_57_out), .in1(X[1]), .out(multiplexer_69_out), .sel(swift_21));  // open: en
  Multiplexer multiplexer_70 (
    .in0(multiplexer_58_out), .in1(X[2]), .out(multiplexer_70_out), .sel(swift_21));  // open: en
  Multiplexer multiplexer_71 (
    .in0(multiplexer_59_out), .in1(X[3]), .out(multiplexer_71_out), .sel(swift_21));  // open: en
  Multiplexer multiplexer_72 (
    .in0(multiplexer_60_out), .in1(X[4]), .out(multiplexer_72_out), .sel(swift_21));  // open: en
  Multiplexer multiplexer_73 (
    .in0(multiplexer_61_out), .in1(X[5]), .out(multiplexer_73_out), .sel(swift_21));  // open: en
  Multiplexer multiplexer_74 (
    .in0(multiplexer_62_out), .in1(X[6]), .out(multiplexer_74_out), .sel(swift_21));  // open: en
  Multiplexer multiplexer_75 (
    .in0(multiplexer_63_out), .in1(X[7]), .out(multiplexer_75_out), .sel(swift_21));  // open: en
  Multiplexer multiplexer_76 (
    .in0(multiplexer_64_out), .in1(X[8]), .out(multiplexer_76_out), .sel(swift_21));  // open: en
  Multiplexer multiplexer_77 (
    .in0(multiplexer_65_out), .in1(X[9]), .out(multiplexer_77_out), .sel(swift_21));  // open: en
  Multiplexer multiplexer_78 (
    .in0(multiplexer_66_out), .in1(X[10]), .out(multiplexer_78_out), .sel(swift_21));  // open: en
  Multiplexer multiplexer_79 (.in0(1'b0), .in1(1'b1), .out(multiplexer_79_out), .sel(full_with_1));  // open: en
  Multiplexer multiplexer_80 (
    .in0(multiplexer_67_out), .in1(X[0]), .out(multiplexer_80_out), .sel(swift_20));  // open: en
  Multiplexer multiplexer_81 (
    .in0(multiplexer_68_out), .in1(X[1]), .out(multiplexer_81_out), .sel(swift_20));  // open: en
  Multiplexer multiplexer_82 (
    .in0(multiplexer_69_out), .in1(X[2]), .out(multiplexer_82_out), .sel(swift_20));  // open: en
  Multiplexer multiplexer_83 (
    .in0(multiplexer_70_out), .in1(X[3]), .out(multiplexer_83_out), .sel(swift_20));  // open: en
  Multiplexer multiplexer_84 (
    .in0(multiplexer_71_out), .in1(X[4]), .out(multiplexer_84_out), .sel(swift_20));  // open: en
  Multiplexer multiplexer_85 (
    .in0(multiplexer_72_out), .in1(X[5]), .out(multiplexer_85_out), .sel(swift_20));  // open: en
  Multiplexer multiplexer_86 (
    .in0(multiplexer_73_out), .in1(X[6]), .out(multiplexer_86_out), .sel(swift_20));  // open: en
  Multiplexer multiplexer_87 (
    .in0(multiplexer_74_out), .in1(X[7]), .out(multiplexer_87_out), .sel(swift_20));  // open: en
  Multiplexer multiplexer_88 (
    .in0(multiplexer_75_out), .in1(X[8]), .out(multiplexer_88_out), .sel(swift_20));  // open: en
  Multiplexer multiplexer_89 (
    .in0(multiplexer_76_out), .in1(X[9]), .out(multiplexer_89_out), .sel(swift_20));  // open: en
  Multiplexer multiplexer_90 (
    .in0(multiplexer_77_out), .in1(X[10]), .out(multiplexer_90_out), .sel(swift_20));  // open: en
  Multiplexer multiplexer_91 (
    .in0(multiplexer_78_out), .in1(X[11]), .out(multiplexer_91_out), .sel(swift_20));  // open: en
  Multiplexer multiplexer_92 (.in0(1'b0), .in1(1'b1), .out(multiplexer_92_out), .sel(full_with_1));  // open: en
  Multiplexer multiplexer_93 (
    .in0(multiplexer_79_out), .in1(X[0]), .out(multiplexer_93_out), .sel(swift_19));  // open: en
  Multiplexer multiplexer_94 (
    .in0(multiplexer_80_out), .in1(X[1]), .out(multiplexer_94_out), .sel(swift_19));  // open: en
  Multiplexer multiplexer_95 (
    .in0(multiplexer_81_out), .in1(X[2]), .out(multiplexer_95_out), .sel(swift_19));  // open: en
  Multiplexer multiplexer_96 (
    .in0(multiplexer_82_out), .in1(X[3]), .out(multiplexer_96_out), .sel(swift_19));  // open: en
  Multiplexer multiplexer_97 (
    .in0(multiplexer_83_out), .in1(X[4]), .out(multiplexer_97_out), .sel(swift_19));  // open: en
  Multiplexer multiplexer_98 (
    .in0(multiplexer_84_out), .in1(X[5]), .out(multiplexer_98_out), .sel(swift_19));  // open: en
  Multiplexer multiplexer_99 (
    .in0(multiplexer_85_out), .in1(X[6]), .out(multiplexer_99_out), .sel(swift_19));  // open: en
  Multiplexer multiplexer_100 (
    .in0(multiplexer_86_out), .in1(X[7]), .out(multiplexer_100_out), .sel(swift_19));  // open: en
  Multiplexer multiplexer_101 (
    .in0(multiplexer_87_out), .in1(X[8]), .out(multiplexer_101_out), .sel(swift_19));  // open: en
  Multiplexer multiplexer_102 (
    .in0(multiplexer_88_out), .in1(X[9]), .out(multiplexer_102_out), .sel(swift_19));  // open: en
  Multiplexer multiplexer_103 (
    .in0(multiplexer_89_out), .in1(X[10]), .out(multiplexer_103_out), .sel(swift_19));  // open: en
  Multiplexer multiplexer_104 (
    .in0(multiplexer_90_out), .in1(X[11]), .out(multiplexer_104_out), .sel(swift_19));  // open: en
  Multiplexer multiplexer_105 (
    .in0(multiplexer_91_out), .in1(X[12]), .out(multiplexer_105_out), .sel(swift_19));  // open: en
  Multiplexer multiplexer_106 (.in0(1'b0), .in1(1'b1), .out(multiplexer_106_out), .sel(full_with_1));  // open: en
  Multiplexer multiplexer_107 (
    .in0(multiplexer_92_out), .in1(X[0]), .out(multiplexer_107_out), .sel(swift_18));  // open: en
  Multiplexer multiplexer_108 (
    .in0(multiplexer_93_out), .in1(X[1]), .out(multiplexer_108_out), .sel(swift_18));  // open: en
  Multiplexer multiplexer_109 (
    .in0(multiplexer_94_out), .in1(X[2]), .out(multiplexer_109_out), .sel(swift_18));  // open: en
  Multiplexer multiplexer_110 (
    .in0(multiplexer_95_out), .in1(X[3]), .out(multiplexer_110_out), .sel(swift_18));  // open: en
  Multiplexer multiplexer_111 (
    .in0(multiplexer_96_out), .in1(X[4]), .out(multiplexer_111_out), .sel(swift_18));  // open: en
  Multiplexer multiplexer_112 (
    .in0(multiplexer_97_out), .in1(X[5]), .out(multiplexer_112_out), .sel(swift_18));  // open: en
  Multiplexer multiplexer_113 (
    .in0(multiplexer_98_out), .in1(X[6]), .out(multiplexer_113_out), .sel(swift_18));  // open: en
  Multiplexer multiplexer_114 (
    .in0(multiplexer_99_out), .in1(X[7]), .out(multiplexer_114_out), .sel(swift_18));  // open: en
  Multiplexer multiplexer_115 (
    .in0(multiplexer_100_out), .in1(X[8]), .out(multiplexer_115_out), .sel(swift_18));  // open: en
  Multiplexer multiplexer_116 (
    .in0(multiplexer_101_out), .in1(X[9]), .out(multiplexer_116_out), .sel(swift_18));  // open: en
  Multiplexer multiplexer_117 (
    .in0(multiplexer_102_out), .in1(X[10]), .out(multiplexer_117_out), .sel(swift_18));  // open: en
  Multiplexer multiplexer_118 (
    .in0(multiplexer_103_out), .in1(X[11]), .out(multiplexer_118_out), .sel(swift_18));  // open: en
  Multiplexer multiplexer_119 (
    .in0(multiplexer_104_out), .in1(X[12]), .out(multiplexer_119_out), .sel(swift_18));  // open: en
  Multiplexer multiplexer_120 (
    .in0(multiplexer_105_out), .in1(X[13]), .out(multiplexer_120_out), .sel(swift_18));  // open: en
  Multiplexer multiplexer_121 (
    .in0(multiplexer_106_out), .in1(X[0]), .out(multiplexer_121_out), .sel(swift_17));  // open: en
  Multiplexer multiplexer_122 (
    .in0(multiplexer_107_out), .in1(X[1]), .out(multiplexer_122_out), .sel(swift_17));  // open: en
  Multiplexer multiplexer_123 (
    .in0(multiplexer_108_out), .in1(X[2]), .out(multiplexer_123_out), .sel(swift_17));  // open: en
  Multiplexer multiplexer_124 (
    .in0(multiplexer_109_out), .in1(X[3]), .out(multiplexer_124_out), .sel(swift_17));  // open: en
  Multiplexer multiplexer_125 (
    .in0(multiplexer_110_out), .in1(X[4]), .out(multiplexer_125_out), .sel(swift_17));  // open: en
  Multiplexer multiplexer_126 (
    .in0(multiplexer_111_out), .in1(X[5]), .out(multiplexer_126_out), .sel(swift_17));  // open: en
  Multiplexer multiplexer_127 (
    .in0(multiplexer_112_out), .in1(X[6]), .out(multiplexer_127_out), .sel(swift_17));  // open: en
  Multiplexer multiplexer_128 (
    .in0(multiplexer_113_out), .in1(X[7]), .out(multiplexer_128_out), .sel(swift_17));  // open: en
  Multiplexer multiplexer_129 (
    .in0(multiplexer_114_out), .in1(X[8]), .out(multiplexer_129_out), .sel(swift_17));  // open: en
  Multiplexer multiplexer_130 (
    .in0(multiplexer_115_out), .in1(X[9]), .out(multiplexer_130_out), .sel(swift_17));  // open: en
  Multiplexer multiplexer_131 (
    .in0(multiplexer_116_out), .in1(X[10]), .out(multiplexer_131_out), .sel(swift_17));  // open: en
  Multiplexer multiplexer_132 (
    .in0(multiplexer_117_out), .in1(X[11]), .out(multiplexer_132_out), .sel(swift_17));  // open: en
  Multiplexer multiplexer_133 (
    .in0(multiplexer_118_out), .in1(X[12]), .out(multiplexer_133_out), .sel(swift_17));  // open: en
  Multiplexer multiplexer_134 (
    .in0(multiplexer_119_out), .in1(X[13]), .out(multiplexer_134_out), .sel(swift_17));  // open: en
  Multiplexer multiplexer_135 (
    .in0(multiplexer_120_out), .in1(X[14]), .out(multiplexer_135_out), .sel(swift_17));  // open: en
  Multiplexer multiplexer_136 (.in0(1'b0), .in1(1'b1), .out(multiplexer_136_out), .sel(full_with_1));  // open: en
  Multiplexer multiplexer_137 (
    .in0(multiplexer_136_out), .in1(X[0]), .out(multiplexer_137_out), .sel(swift_16));  // open: en
  Multiplexer multiplexer_138 (
    .in0(multiplexer_121_out), .in1(X[1]), .out(multiplexer_138_out), .sel(swift_16));  // open: en
  Multiplexer multiplexer_139 (
    .in0(multiplexer_122_out), .in1(X[2]), .out(multiplexer_139_out), .sel(swift_16));  // open: en
  Multiplexer multiplexer_140 (
    .in0(multiplexer_123_out), .in1(X[3]), .out(multiplexer_140_out), .sel(swift_16));  // open: en
  Multiplexer multiplexer_141 (
    .in0(multiplexer_124_out), .in1(X[4]), .out(multiplexer_141_out), .sel(swift_16));  // open: en
  Multiplexer multiplexer_142 (
    .in0(multiplexer_125_out), .in1(X[5]), .out(multiplexer_142_out), .sel(swift_16));  // open: en
  Multiplexer multiplexer_143 (
    .in0(multiplexer_126_out), .in1(X[6]), .out(multiplexer_143_out), .sel(swift_16));  // open: en
  Multiplexer multiplexer_144 (
    .in0(multiplexer_127_out), .in1(X[7]), .out(multiplexer_144_out), .sel(swift_16));  // open: en
  Multiplexer multiplexer_145 (
    .in0(multiplexer_128_out), .in1(X[8]), .out(multiplexer_145_out), .sel(swift_16));  // open: en
  Multiplexer multiplexer_146 (
    .in0(multiplexer_129_out), .in1(X[9]), .out(multiplexer_146_out), .sel(swift_16));  // open: en
  Multiplexer multiplexer_147 (
    .in0(multiplexer_130_out), .in1(X[10]), .out(multiplexer_147_out), .sel(swift_16));  // open: en
  Multiplexer multiplexer_148 (
    .in0(multiplexer_131_out), .in1(X[11]), .out(multiplexer_148_out), .sel(swift_16));  // open: en
  Multiplexer multiplexer_149 (
    .in0(multiplexer_132_out), .in1(X[12]), .out(multiplexer_149_out), .sel(swift_16));  // open: en
  Multiplexer multiplexer_150 (
    .in0(multiplexer_133_out), .in1(X[13]), .out(multiplexer_150_out), .sel(swift_16));  // open: en
  Multiplexer multiplexer_151 (
    .in0(multiplexer_134_out), .in1(X[14]), .out(multiplexer_151_out), .sel(swift_16));  // open: en
  Multiplexer multiplexer_152 (
    .in0(multiplexer_135_out), .in1(X[15]), .out(multiplexer_152_out), .sel(swift_16));  // open: en
  Multiplexer multiplexer_153 (.in0(1'b0), .in1(1'b1), .out(multiplexer_153_out), .sel(full_with_1));  // open: en
  Multiplexer multiplexer_154 (
    .in0(multiplexer_153_out), .in1(X[0]), .out(multiplexer_154_out), .sel(swift_15));  // open: en
  Multiplexer multiplexer_155 (
    .in0(multiplexer_137_out), .in1(X[1]), .out(multiplexer_155_out), .sel(swift_15));  // open: en
  Multiplexer multiplexer_156 (
    .in0(multiplexer_138_out), .in1(X[2]), .out(multiplexer_156_out), .sel(swift_15));  // open: en
  Multiplexer multiplexer_157 (
    .in0(multiplexer_139_out), .in1(X[3]), .out(multiplexer_157_out), .sel(swift_15));  // open: en
  Multiplexer multiplexer_158 (
    .in0(multiplexer_140_out), .in1(X[4]), .out(multiplexer_158_out), .sel(swift_15));  // open: en
  Multiplexer multiplexer_159 (
    .in0(multiplexer_141_out), .in1(X[5]), .out(multiplexer_159_out), .sel(swift_15));  // open: en
  Multiplexer multiplexer_160 (
    .in0(multiplexer_142_out), .in1(X[6]), .out(multiplexer_160_out), .sel(swift_15));  // open: en
  Multiplexer multiplexer_161 (
    .in0(multiplexer_143_out), .in1(X[7]), .out(multiplexer_161_out), .sel(swift_15));  // open: en
  Multiplexer multiplexer_162 (
    .in0(multiplexer_144_out), .in1(X[8]), .out(multiplexer_162_out), .sel(swift_15));  // open: en
  Multiplexer multiplexer_163 (
    .in0(multiplexer_145_out), .in1(X[9]), .out(multiplexer_163_out), .sel(swift_15));  // open: en
  Multiplexer multiplexer_164 (
    .in0(multiplexer_146_out), .in1(X[10]), .out(multiplexer_164_out), .sel(swift_15));  // open: en
  Multiplexer multiplexer_165 (
    .in0(multiplexer_147_out), .in1(X[11]), .out(multiplexer_165_out), .sel(swift_15));  // open: en
  Multiplexer multiplexer_166 (
    .in0(multiplexer_148_out), .in1(X[12]), .out(multiplexer_166_out), .sel(swift_15));  // open: en
  Multiplexer multiplexer_167 (
    .in0(multiplexer_149_out), .in1(X[13]), .out(multiplexer_167_out), .sel(swift_15));  // open: en
  Multiplexer multiplexer_168 (
    .in0(multiplexer_150_out), .in1(X[14]), .out(multiplexer_168_out), .sel(swift_15));  // open: en
  Multiplexer multiplexer_169 (
    .in0(multiplexer_151_out), .in1(X[15]), .out(multiplexer_169_out), .sel(swift_15));  // open: en
  Multiplexer multiplexer_170 (
    .in0(multiplexer_152_out), .in1(X[16]), .out(multiplexer_170_out), .sel(swift_15));  // open: en
  Multiplexer multiplexer_171 (.in0(1'b0), .in1(1'b1), .out(multiplexer_171_out), .sel(full_with_1));  // open: en
  Multiplexer multiplexer_172 (.in0(1'b0), .in1(1'b1), .out(multiplexer_172_out), .sel(full_with_1));  // open: en
  Multiplexer multiplexer_173 (
    .in0(multiplexer_171_out), .in1(X[0]), .out(multiplexer_173_out), .sel(swift_14));  // open: en
  Multiplexer multiplexer_174 (
    .in0(multiplexer_154_out), .in1(X[1]), .out(multiplexer_174_out), .sel(swift_14));  // open: en
  Multiplexer multiplexer_175 (
    .in0(multiplexer_155_out), .in1(X[2]), .out(multiplexer_175_out), .sel(swift_14));  // open: en
  Multiplexer multiplexer_176 (
    .in0(multiplexer_156_out), .in1(X[3]), .out(multiplexer_176_out), .sel(swift_14));  // open: en
  Multiplexer multiplexer_177 (
    .in0(multiplexer_157_out), .in1(X[4]), .out(multiplexer_177_out), .sel(swift_14));  // open: en
  Multiplexer multiplexer_178 (
    .in0(multiplexer_158_out), .in1(X[5]), .out(multiplexer_178_out), .sel(swift_14));  // open: en
  Multiplexer multiplexer_179 (
    .in0(multiplexer_159_out), .in1(X[6]), .out(multiplexer_179_out), .sel(swift_14));  // open: en
  Multiplexer multiplexer_180 (
    .in0(multiplexer_160_out), .in1(X[7]), .out(multiplexer_180_out), .sel(swift_14));  // open: en
  Multiplexer multiplexer_181 (
    .in0(multiplexer_161_out), .in1(X[8]), .out(multiplexer_181_out), .sel(swift_14));  // open: en
  Multiplexer multiplexer_182 (
    .in0(multiplexer_162_out), .in1(X[9]), .out(multiplexer_182_out), .sel(swift_14));  // open: en
  Multiplexer multiplexer_183 (
    .in0(multiplexer_163_out), .in1(X[10]), .out(multiplexer_183_out), .sel(swift_14));  // open: en
  Multiplexer multiplexer_184 (
    .in0(multiplexer_164_out), .in1(X[11]), .out(multiplexer_184_out), .sel(swift_14));  // open: en
  Multiplexer multiplexer_185 (
    .in0(multiplexer_165_out), .in1(X[12]), .out(multiplexer_185_out), .sel(swift_14));  // open: en
  Multiplexer multiplexer_186 (
    .in0(multiplexer_166_out), .in1(X[13]), .out(multiplexer_186_out), .sel(swift_14));  // open: en
  Multiplexer multiplexer_187 (
    .in0(multiplexer_167_out), .in1(X[14]), .out(multiplexer_187_out), .sel(swift_14));  // open: en
  Multiplexer multiplexer_188 (
    .in0(multiplexer_168_out), .in1(X[15]), .out(multiplexer_188_out), .sel(swift_14));  // open: en
  Multiplexer multiplexer_189 (
    .in0(multiplexer_169_out), .in1(X[16]), .out(multiplexer_189_out), .sel(swift_14));  // open: en
  Multiplexer multiplexer_190 (
    .in0(multiplexer_170_out), .in1(X[17]), .out(multiplexer_190_out), .sel(swift_14));  // open: en
  Multiplexer multiplexer_191 (.in0(1'b0), .in1(1'b1), .out(multiplexer_191_out), .sel(full_with_1));  // open: en
  Multiplexer multiplexer_192 (
    .in0(multiplexer_172_out), .in1(X[0]), .out(multiplexer_192_out), .sel(swift_13));  // open: en
  Multiplexer multiplexer_193 (
    .in0(multiplexer_173_out), .in1(X[1]), .out(multiplexer_193_out), .sel(swift_13));  // open: en
  Multiplexer multiplexer_194 (
    .in0(multiplexer_174_out), .in1(X[2]), .out(multiplexer_194_out), .sel(swift_13));  // open: en
  Multiplexer multiplexer_195 (
    .in0(multiplexer_175_out), .in1(X[3]), .out(multiplexer_195_out), .sel(swift_13));  // open: en
  Multiplexer multiplexer_196 (
    .in0(multiplexer_176_out), .in1(X[4]), .out(multiplexer_196_out), .sel(swift_13));  // open: en
  Multiplexer multiplexer_197 (
    .in0(multiplexer_177_out), .in1(X[5]), .out(multiplexer_197_out), .sel(swift_13));  // open: en
  Multiplexer multiplexer_198 (
    .in0(multiplexer_178_out), .in1(X[6]), .out(multiplexer_198_out), .sel(swift_13));  // open: en
  Multiplexer multiplexer_199 (
    .in0(multiplexer_179_out), .in1(X[7]), .out(multiplexer_199_out), .sel(swift_13));  // open: en
  Multiplexer multiplexer_200 (
    .in0(multiplexer_180_out), .in1(X[8]), .out(multiplexer_200_out), .sel(swift_13));  // open: en
  Multiplexer multiplexer_201 (
    .in0(multiplexer_181_out), .in1(X[9]), .out(multiplexer_201_out), .sel(swift_13));  // open: en
  Multiplexer multiplexer_202 (
    .in0(multiplexer_182_out), .in1(X[10]), .out(multiplexer_202_out), .sel(swift_13));  // open: en
  Multiplexer multiplexer_203 (
    .in0(multiplexer_183_out), .in1(X[11]), .out(multiplexer_203_out), .sel(swift_13));  // open: en
  Multiplexer multiplexer_204 (
    .in0(multiplexer_184_out), .in1(X[12]), .out(multiplexer_204_out), .sel(swift_13));  // open: en
  Multiplexer multiplexer_205 (
    .in0(multiplexer_185_out), .in1(X[13]), .out(multiplexer_205_out), .sel(swift_13));  // open: en
  Multiplexer multiplexer_206 (
    .in0(multiplexer_186_out), .in1(X[14]), .out(multiplexer_206_out), .sel(swift_13));  // open: en
  Multiplexer multiplexer_207 (
    .in0(multiplexer_187_out), .in1(X[15]), .out(multiplexer_207_out), .sel(swift_13));  // open: en
  Multiplexer multiplexer_208 (
    .in0(multiplexer_188_out), .in1(X[16]), .out(multiplexer_208_out), .sel(swift_13));  // open: en
  Multiplexer multiplexer_209 (
    .in0(multiplexer_189_out), .in1(X[17]), .out(multiplexer_209_out), .sel(swift_13));  // open: en
  Multiplexer multiplexer_210 (
    .in0(multiplexer_190_out), .in1(X[18]), .out(multiplexer_210_out), .sel(swift_13));  // open: en
  Multiplexer multiplexer_211 (.in0(1'b0), .in1(1'b1), .out(multiplexer_211_out), .sel(full_with_1));  // open: en
  Multiplexer multiplexer_212 (
    .in0(multiplexer_191_out), .in1(X[0]), .out(multiplexer_212_out), .sel(swift_12));  // open: en
  Multiplexer multiplexer_213 (
    .in0(multiplexer_192_out), .in1(X[1]), .out(multiplexer_213_out), .sel(swift_12));  // open: en
  Multiplexer multiplexer_214 (
    .in0(multiplexer_193_out), .in1(X[2]), .out(multiplexer_214_out), .sel(swift_12));  // open: en
  Multiplexer multiplexer_215 (
    .in0(multiplexer_194_out), .in1(X[3]), .out(multiplexer_215_out), .sel(swift_12));  // open: en
  Multiplexer multiplexer_216 (
    .in0(multiplexer_195_out), .in1(X[4]), .out(multiplexer_216_out), .sel(swift_12));  // open: en
  Multiplexer multiplexer_217 (
    .in0(multiplexer_196_out), .in1(X[5]), .out(multiplexer_217_out), .sel(swift_12));  // open: en
  Multiplexer multiplexer_218 (
    .in0(multiplexer_197_out), .in1(X[6]), .out(multiplexer_218_out), .sel(swift_12));  // open: en
  Multiplexer multiplexer_219 (
    .in0(multiplexer_198_out), .in1(X[7]), .out(multiplexer_219_out), .sel(swift_12));  // open: en
  Multiplexer multiplexer_220 (
    .in0(multiplexer_199_out), .in1(X[8]), .out(multiplexer_220_out), .sel(swift_12));  // open: en
  Multiplexer multiplexer_221 (
    .in0(multiplexer_200_out), .in1(X[9]), .out(multiplexer_221_out), .sel(swift_12));  // open: en
  Multiplexer multiplexer_222 (
    .in0(multiplexer_201_out), .in1(X[10]), .out(multiplexer_222_out), .sel(swift_12));  // open: en
  Multiplexer multiplexer_223 (
    .in0(multiplexer_202_out), .in1(X[11]), .out(multiplexer_223_out), .sel(swift_12));  // open: en
  Multiplexer multiplexer_224 (
    .in0(multiplexer_203_out), .in1(X[12]), .out(multiplexer_224_out), .sel(swift_12));  // open: en
  Multiplexer multiplexer_225 (
    .in0(multiplexer_204_out), .in1(X[13]), .out(multiplexer_225_out), .sel(swift_12));  // open: en
  Multiplexer multiplexer_226 (
    .in0(multiplexer_205_out), .in1(X[14]), .out(multiplexer_226_out), .sel(swift_12));  // open: en
  Multiplexer multiplexer_227 (
    .in0(multiplexer_206_out), .in1(X[15]), .out(multiplexer_227_out), .sel(swift_12));  // open: en
  Multiplexer multiplexer_228 (
    .in0(multiplexer_207_out), .in1(X[16]), .out(multiplexer_228_out), .sel(swift_12));  // open: en
  Multiplexer multiplexer_229 (
    .in0(multiplexer_208_out), .in1(X[17]), .out(multiplexer_229_out), .sel(swift_12));  // open: en
  Multiplexer multiplexer_230 (
    .in0(multiplexer_209_out), .in1(X[18]), .out(multiplexer_230_out), .sel(swift_12));  // open: en
  Multiplexer multiplexer_231 (
    .in0(multiplexer_210_out), .in1(X[19]), .out(multiplexer_231_out), .sel(swift_12));  // open: en
  Multiplexer multiplexer_232 (.in0(1'b0), .in1(1'b1), .out(multiplexer_232_out), .sel(full_with_1));  // open: en
  Multiplexer multiplexer_233 (
    .in0(multiplexer_211_out), .in1(X[0]), .out(multiplexer_233_out), .sel(swift_11));  // open: en
  Multiplexer multiplexer_234 (
    .in0(multiplexer_212_out), .in1(X[1]), .out(multiplexer_234_out), .sel(swift_11));  // open: en
  Multiplexer multiplexer_235 (
    .in0(multiplexer_213_out), .in1(X[2]), .out(multiplexer_235_out), .sel(swift_11));  // open: en
  Multiplexer multiplexer_236 (
    .in0(multiplexer_214_out), .in1(X[3]), .out(multiplexer_236_out), .sel(swift_11));  // open: en
  Multiplexer multiplexer_237 (
    .in0(multiplexer_215_out), .in1(X[4]), .out(multiplexer_237_out), .sel(swift_11));  // open: en
  Multiplexer multiplexer_238 (
    .in0(multiplexer_216_out), .in1(X[5]), .out(multiplexer_238_out), .sel(swift_11));  // open: en
  Multiplexer multiplexer_239 (
    .in0(multiplexer_217_out), .in1(X[6]), .out(multiplexer_239_out), .sel(swift_11));  // open: en
  Multiplexer multiplexer_240 (
    .in0(multiplexer_218_out), .in1(X[7]), .out(multiplexer_240_out), .sel(swift_11));  // open: en
  Multiplexer multiplexer_241 (
    .in0(multiplexer_219_out), .in1(X[8]), .out(multiplexer_241_out), .sel(swift_11));  // open: en
  Multiplexer multiplexer_242 (
    .in0(multiplexer_220_out), .in1(X[9]), .out(multiplexer_242_out), .sel(swift_11));  // open: en
  Multiplexer multiplexer_243 (
    .in0(multiplexer_221_out), .in1(X[10]), .out(multiplexer_243_out), .sel(swift_11));  // open: en
  Multiplexer multiplexer_244 (
    .in0(multiplexer_222_out), .in1(X[11]), .out(multiplexer_244_out), .sel(swift_11));  // open: en
  Multiplexer multiplexer_245 (
    .in0(multiplexer_223_out), .in1(X[12]), .out(multiplexer_245_out), .sel(swift_11));  // open: en
  Multiplexer multiplexer_246 (
    .in0(multiplexer_224_out), .in1(X[13]), .out(multiplexer_246_out), .sel(swift_11));  // open: en
  Multiplexer multiplexer_247 (
    .in0(multiplexer_225_out), .in1(X[14]), .out(multiplexer_247_out), .sel(swift_11));  // open: en
  Multiplexer multiplexer_248 (
    .in0(multiplexer_226_out), .in1(X[15]), .out(multiplexer_248_out), .sel(swift_11));  // open: en
  Multiplexer multiplexer_249 (
    .in0(multiplexer_227_out), .in1(X[16]), .out(multiplexer_249_out), .sel(swift_11));  // open: en
  Multiplexer multiplexer_250 (
    .in0(multiplexer_228_out), .in1(X[17]), .out(multiplexer_250_out), .sel(swift_11));  // open: en
  Multiplexer multiplexer_251 (
    .in0(multiplexer_229_out), .in1(X[18]), .out(multiplexer_251_out), .sel(swift_11));  // open: en
  Multiplexer multiplexer_252 (
    .in0(multiplexer_230_out), .in1(X[19]), .out(multiplexer_252_out), .sel(swift_11));  // open: en
  Multiplexer multiplexer_253 (
    .in0(multiplexer_231_out), .in1(X[20]), .out(multiplexer_253_out), .sel(swift_11));  // open: en
  Multiplexer multiplexer_254 (.in0(1'b0), .in1(1'b1), .out(multiplexer_254_out), .sel(full_with_1));  // open: en
  Multiplexer multiplexer_255 (
    .in0(multiplexer_232_out), .in1(X[0]), .out(multiplexer_255_out), .sel(swift_10));  // open: en
  Multiplexer multiplexer_256 (
    .in0(multiplexer_233_out), .in1(X[1]), .out(multiplexer_256_out), .sel(swift_10));  // open: en
  Multiplexer multiplexer_257 (
    .in0(multiplexer_234_out), .in1(X[2]), .out(multiplexer_257_out), .sel(swift_10));  // open: en
  Multiplexer multiplexer_258 (
    .in0(multiplexer_235_out), .in1(X[3]), .out(multiplexer_258_out), .sel(swift_10));  // open: en
  Multiplexer multiplexer_259 (
    .in0(multiplexer_236_out), .in1(X[4]), .out(multiplexer_259_out), .sel(swift_10));  // open: en
  Multiplexer multiplexer_260 (
    .in0(multiplexer_237_out), .in1(X[5]), .out(multiplexer_260_out), .sel(swift_10));  // open: en
  Multiplexer multiplexer_261 (
    .in0(multiplexer_238_out), .in1(X[6]), .out(multiplexer_261_out), .sel(swift_10));  // open: en
  Multiplexer multiplexer_262 (
    .in0(multiplexer_239_out), .in1(X[7]), .out(multiplexer_262_out), .sel(swift_10));  // open: en
  Multiplexer multiplexer_263 (
    .in0(multiplexer_240_out), .in1(X[8]), .out(multiplexer_263_out), .sel(swift_10));  // open: en
  Multiplexer multiplexer_264 (
    .in0(multiplexer_241_out), .in1(X[9]), .out(multiplexer_264_out), .sel(swift_10));  // open: en
  Multiplexer multiplexer_265 (
    .in0(multiplexer_242_out), .in1(X[10]), .out(multiplexer_265_out), .sel(swift_10));  // open: en
  Multiplexer multiplexer_266 (
    .in0(multiplexer_243_out), .in1(X[11]), .out(multiplexer_266_out), .sel(swift_10));  // open: en
  Multiplexer multiplexer_267 (
    .in0(multiplexer_244_out), .in1(X[12]), .out(multiplexer_267_out), .sel(swift_10));  // open: en
  Multiplexer multiplexer_268 (
    .in0(multiplexer_245_out), .in1(X[13]), .out(multiplexer_268_out), .sel(swift_10));  // open: en
  Multiplexer multiplexer_269 (
    .in0(multiplexer_246_out), .in1(X[14]), .out(multiplexer_269_out), .sel(swift_10));  // open: en
  Multiplexer multiplexer_270 (
    .in0(multiplexer_247_out), .in1(X[15]), .out(multiplexer_270_out), .sel(swift_10));  // open: en
  Multiplexer multiplexer_271 (
    .in0(multiplexer_248_out), .in1(X[16]), .out(multiplexer_271_out), .sel(swift_10));  // open: en
  Multiplexer multiplexer_272 (
    .in0(multiplexer_249_out), .in1(X[17]), .out(multiplexer_272_out), .sel(swift_10));  // open: en
  Multiplexer multiplexer_273 (
    .in0(multiplexer_250_out), .in1(X[18]), .out(multiplexer_273_out), .sel(swift_10));  // open: en
  Multiplexer multiplexer_274 (
    .in0(multiplexer_251_out), .in1(X[19]), .out(multiplexer_274_out), .sel(swift_10));  // open: en
  Multiplexer multiplexer_275 (
    .in0(multiplexer_252_out), .in1(X[20]), .out(multiplexer_275_out), .sel(swift_10));  // open: en
  Multiplexer multiplexer_276 (
    .in0(multiplexer_253_out), .in1(X[21]), .out(multiplexer_276_out), .sel(swift_10));  // open: en
  Multiplexer multiplexer_277 (
    .in0(multiplexer_254_out), .in1(X[0]), .out(multiplexer_277_out), .sel(swift_9));  // open: en
  Multiplexer multiplexer_278 (
    .in0(multiplexer_255_out), .in1(X[1]), .out(multiplexer_278_out), .sel(swift_9));  // open: en
  Multiplexer multiplexer_279 (
    .in0(multiplexer_256_out), .in1(X[2]), .out(multiplexer_279_out), .sel(swift_9));  // open: en
  Multiplexer multiplexer_280 (
    .in0(multiplexer_257_out), .in1(X[3]), .out(multiplexer_280_out), .sel(swift_9));  // open: en
  Multiplexer multiplexer_281 (
    .in0(multiplexer_258_out), .in1(X[4]), .out(multiplexer_281_out), .sel(swift_9));  // open: en
  Multiplexer multiplexer_282 (
    .in0(multiplexer_259_out), .in1(X[5]), .out(multiplexer_282_out), .sel(swift_9));  // open: en
  Multiplexer multiplexer_283 (
    .in0(multiplexer_260_out), .in1(X[6]), .out(multiplexer_283_out), .sel(swift_9));  // open: en
  Multiplexer multiplexer_284 (
    .in0(multiplexer_261_out), .in1(X[7]), .out(multiplexer_284_out), .sel(swift_9));  // open: en
  Multiplexer multiplexer_285 (
    .in0(multiplexer_262_out), .in1(X[8]), .out(multiplexer_285_out), .sel(swift_9));  // open: en
  Multiplexer multiplexer_286 (
    .in0(multiplexer_263_out), .in1(X[9]), .out(multiplexer_286_out), .sel(swift_9));  // open: en
  Multiplexer multiplexer_287 (
    .in0(multiplexer_264_out), .in1(X[10]), .out(multiplexer_287_out), .sel(swift_9));  // open: en
  Multiplexer multiplexer_288 (
    .in0(multiplexer_265_out), .in1(X[11]), .out(multiplexer_288_out), .sel(swift_9));  // open: en
  Multiplexer multiplexer_289 (
    .in0(multiplexer_266_out), .in1(X[12]), .out(multiplexer_289_out), .sel(swift_9));  // open: en
  Multiplexer multiplexer_290 (
    .in0(multiplexer_267_out), .in1(X[13]), .out(multiplexer_290_out), .sel(swift_9));  // open: en
  Multiplexer multiplexer_291 (
    .in0(multiplexer_268_out), .in1(X[14]), .out(multiplexer_291_out), .sel(swift_9));  // open: en
  Multiplexer multiplexer_292 (
    .in0(multiplexer_269_out), .in1(X[15]), .out(multiplexer_292_out), .sel(swift_9));  // open: en
  Multiplexer multiplexer_293 (
    .in0(multiplexer_270_out), .in1(X[16]), .out(multiplexer_293_out), .sel(swift_9));  // open: en
  Multiplexer multiplexer_294 (
    .in0(multiplexer_271_out), .in1(X[17]), .out(multiplexer_294_out), .sel(swift_9));  // open: en
  Multiplexer multiplexer_295 (
    .in0(multiplexer_272_out), .in1(X[18]), .out(multiplexer_295_out), .sel(swift_9));  // open: en
  Multiplexer multiplexer_296 (
    .in0(multiplexer_273_out), .in1(X[19]), .out(multiplexer_296_out), .sel(swift_9));  // open: en
  Multiplexer multiplexer_297 (
    .in0(multiplexer_274_out), .in1(X[20]), .out(multiplexer_297_out), .sel(swift_9));  // open: en
  Multiplexer multiplexer_298 (
    .in0(multiplexer_275_out), .in1(X[21]), .out(multiplexer_298_out), .sel(swift_9));  // open: en
  Multiplexer multiplexer_299 (
    .in0(multiplexer_276_out), .in1(X[22]), .out(multiplexer_299_out), .sel(swift_9));  // open: en
  Multiplexer multiplexer_300 (.in0(1'b0), .in1(1'b1), .out(multiplexer_300_out), .sel(full_with_1));  // open: en
  Multiplexer multiplexer_301 (
    .in0(multiplexer_300_out), .in1(X[0]), .out(multiplexer_301_out), .sel(swift_8));  // open: en
  Multiplexer multiplexer_302 (
    .in0(multiplexer_277_out), .in1(X[1]), .out(multiplexer_302_out), .sel(swift_8));  // open: en
  Multiplexer multiplexer_303 (
    .in0(multiplexer_278_out), .in1(X[2]), .out(multiplexer_303_out), .sel(swift_8));  // open: en
  Multiplexer multiplexer_304 (
    .in0(multiplexer_279_out), .in1(X[3]), .out(multiplexer_304_out), .sel(swift_8));  // open: en
  Multiplexer multiplexer_305 (
    .in0(multiplexer_280_out), .in1(X[4]), .out(multiplexer_305_out), .sel(swift_8));  // open: en
  Multiplexer multiplexer_306 (
    .in0(multiplexer_281_out), .in1(X[5]), .out(multiplexer_306_out), .sel(swift_8));  // open: en
  Multiplexer multiplexer_307 (
    .in0(multiplexer_282_out), .in1(X[6]), .out(multiplexer_307_out), .sel(swift_8));  // open: en
  Multiplexer multiplexer_308 (
    .in0(multiplexer_283_out), .in1(X[7]), .out(multiplexer_308_out), .sel(swift_8));  // open: en
  Multiplexer multiplexer_309 (
    .in0(multiplexer_284_out), .in1(X[8]), .out(multiplexer_309_out), .sel(swift_8));  // open: en
  Multiplexer multiplexer_310 (
    .in0(multiplexer_285_out), .in1(X[9]), .out(multiplexer_310_out), .sel(swift_8));  // open: en
  Multiplexer multiplexer_311 (
    .in0(multiplexer_286_out), .in1(X[10]), .out(multiplexer_311_out), .sel(swift_8));  // open: en
  Multiplexer multiplexer_312 (
    .in0(multiplexer_287_out), .in1(X[11]), .out(multiplexer_312_out), .sel(swift_8));  // open: en
  Multiplexer multiplexer_313 (
    .in0(multiplexer_288_out), .in1(X[12]), .out(multiplexer_313_out), .sel(swift_8));  // open: en
  Multiplexer multiplexer_314 (
    .in0(multiplexer_289_out), .in1(X[13]), .out(multiplexer_314_out), .sel(swift_8));  // open: en
  Multiplexer multiplexer_315 (
    .in0(multiplexer_290_out), .in1(X[14]), .out(multiplexer_315_out), .sel(swift_8));  // open: en
  Multiplexer multiplexer_316 (
    .in0(multiplexer_291_out), .in1(X[15]), .out(multiplexer_316_out), .sel(swift_8));  // open: en
  Multiplexer multiplexer_317 (
    .in0(multiplexer_292_out), .in1(X[16]), .out(multiplexer_317_out), .sel(swift_8));  // open: en
  Multiplexer multiplexer_318 (
    .in0(multiplexer_293_out), .in1(X[17]), .out(multiplexer_318_out), .sel(swift_8));  // open: en
  Multiplexer multiplexer_319 (
    .in0(multiplexer_294_out), .in1(X[18]), .out(multiplexer_319_out), .sel(swift_8));  // open: en
  Multiplexer multiplexer_320 (
    .in0(multiplexer_295_out), .in1(X[19]), .out(multiplexer_320_out), .sel(swift_8));  // open: en
  Multiplexer multiplexer_321 (
    .in0(multiplexer_296_out), .in1(X[20]), .out(multiplexer_321_out), .sel(swift_8));  // open: en
  Multiplexer multiplexer_322 (
    .in0(multiplexer_297_out), .in1(X[21]), .out(multiplexer_322_out), .sel(swift_8));  // open: en
  Multiplexer multiplexer_323 (
    .in0(multiplexer_298_out), .in1(X[22]), .out(multiplexer_323_out), .sel(swift_8));  // open: en
  Multiplexer multiplexer_324 (
    .in0(multiplexer_299_out), .in1(X[23]), .out(multiplexer_324_out), .sel(swift_8));  // open: en
  Multiplexer multiplexer_325 (.in0(1'b0), .in1(1'b1), .out(multiplexer_325_out), .sel(full_with_1));  // open: en
  Multiplexer multiplexer_326 (
    .in0(multiplexer_325_out), .in1(X[0]), .out(multiplexer_326_out), .sel(swift_7));  // open: en
  Multiplexer multiplexer_327 (
    .in0(multiplexer_301_out), .in1(X[1]), .out(multiplexer_327_out), .sel(swift_7));  // open: en
  Multiplexer multiplexer_328 (
    .in0(multiplexer_302_out), .in1(X[2]), .out(multiplexer_328_out), .sel(swift_7));  // open: en
  Multiplexer multiplexer_329 (
    .in0(multiplexer_303_out), .in1(X[3]), .out(multiplexer_329_out), .sel(swift_7));  // open: en
  Multiplexer multiplexer_330 (
    .in0(multiplexer_304_out), .in1(X[4]), .out(multiplexer_330_out), .sel(swift_7));  // open: en
  Multiplexer multiplexer_331 (
    .in0(multiplexer_305_out), .in1(X[5]), .out(multiplexer_331_out), .sel(swift_7));  // open: en
  Multiplexer multiplexer_332 (
    .in0(multiplexer_306_out), .in1(X[6]), .out(multiplexer_332_out), .sel(swift_7));  // open: en
  Multiplexer multiplexer_333 (
    .in0(multiplexer_307_out), .in1(X[7]), .out(multiplexer_333_out), .sel(swift_7));  // open: en
  Multiplexer multiplexer_334 (
    .in0(multiplexer_308_out), .in1(X[8]), .out(multiplexer_334_out), .sel(swift_7));  // open: en
  Multiplexer multiplexer_335 (
    .in0(multiplexer_309_out), .in1(X[9]), .out(multiplexer_335_out), .sel(swift_7));  // open: en
  Multiplexer multiplexer_336 (
    .in0(multiplexer_310_out), .in1(X[10]), .out(multiplexer_336_out), .sel(swift_7));  // open: en
  Multiplexer multiplexer_337 (
    .in0(multiplexer_311_out), .in1(X[11]), .out(multiplexer_337_out), .sel(swift_7));  // open: en
  Multiplexer multiplexer_338 (
    .in0(multiplexer_312_out), .in1(X[12]), .out(multiplexer_338_out), .sel(swift_7));  // open: en
  Multiplexer multiplexer_339 (
    .in0(multiplexer_313_out), .in1(X[13]), .out(multiplexer_339_out), .sel(swift_7));  // open: en
  Multiplexer multiplexer_340 (
    .in0(multiplexer_314_out), .in1(X[14]), .out(multiplexer_340_out), .sel(swift_7));  // open: en
  Multiplexer multiplexer_341 (
    .in0(multiplexer_315_out), .in1(X[15]), .out(multiplexer_341_out), .sel(swift_7));  // open: en
  Multiplexer multiplexer_342 (
    .in0(multiplexer_316_out), .in1(X[16]), .out(multiplexer_342_out), .sel(swift_7));  // open: en
  Multiplexer multiplexer_343 (
    .in0(multiplexer_317_out), .in1(X[17]), .out(multiplexer_343_out), .sel(swift_7));  // open: en
  Multiplexer multiplexer_344 (
    .in0(multiplexer_318_out), .in1(X[18]), .out(multiplexer_344_out), .sel(swift_7));  // open: en
  Multiplexer multiplexer_345 (
    .in0(multiplexer_319_out), .in1(X[19]), .out(multiplexer_345_out), .sel(swift_7));  // open: en
  Multiplexer multiplexer_346 (
    .in0(multiplexer_320_out), .in1(X[20]), .out(multiplexer_346_out), .sel(swift_7));  // open: en
  Multiplexer multiplexer_347 (
    .in0(multiplexer_321_out), .in1(X[21]), .out(multiplexer_347_out), .sel(swift_7));  // open: en
  Multiplexer multiplexer_348 (
    .in0(multiplexer_322_out), .in1(X[22]), .out(multiplexer_348_out), .sel(swift_7));  // open: en
  Multiplexer multiplexer_349 (
    .in0(multiplexer_323_out), .in1(X[23]), .out(multiplexer_349_out), .sel(swift_7));  // open: en
  Multiplexer multiplexer_350 (
    .in0(multiplexer_324_out), .in1(X[24]), .out(multiplexer_350_out), .sel(swift_7));  // open: en
  Multiplexer multiplexer_351 (.in0(1'b0), .in1(1'b1), .out(multiplexer_351_out), .sel(full_with_1));  // open: en
  Multiplexer multiplexer_352 (.in0(1'b0), .in1(1'b1), .out(multiplexer_352_out), .sel(full_with_1));  // open: en
  Multiplexer multiplexer_353 (
    .in0(multiplexer_351_out), .in1(X[0]), .out(multiplexer_353_out), .sel(swift_6));  // open: en
  Multiplexer multiplexer_354 (
    .in0(multiplexer_326_out), .in1(X[1]), .out(multiplexer_354_out), .sel(swift_6));  // open: en
  Multiplexer multiplexer_355 (
    .in0(multiplexer_327_out), .in1(X[2]), .out(multiplexer_355_out), .sel(swift_6));  // open: en
  Multiplexer multiplexer_356 (
    .in0(multiplexer_328_out), .in1(X[3]), .out(multiplexer_356_out), .sel(swift_6));  // open: en
  Multiplexer multiplexer_357 (
    .in0(multiplexer_329_out), .in1(X[4]), .out(multiplexer_357_out), .sel(swift_6));  // open: en
  Multiplexer multiplexer_358 (
    .in0(multiplexer_330_out), .in1(X[5]), .out(multiplexer_358_out), .sel(swift_6));  // open: en
  Multiplexer multiplexer_359 (
    .in0(multiplexer_331_out), .in1(X[6]), .out(multiplexer_359_out), .sel(swift_6));  // open: en
  Multiplexer multiplexer_360 (
    .in0(multiplexer_332_out), .in1(X[7]), .out(multiplexer_360_out), .sel(swift_6));  // open: en
  Multiplexer multiplexer_361 (
    .in0(multiplexer_333_out), .in1(X[8]), .out(multiplexer_361_out), .sel(swift_6));  // open: en
  Multiplexer multiplexer_362 (
    .in0(multiplexer_334_out), .in1(X[9]), .out(multiplexer_362_out), .sel(swift_6));  // open: en
  Multiplexer multiplexer_363 (
    .in0(multiplexer_335_out), .in1(X[10]), .out(multiplexer_363_out), .sel(swift_6));  // open: en
  Multiplexer multiplexer_364 (
    .in0(multiplexer_336_out), .in1(X[11]), .out(multiplexer_364_out), .sel(swift_6));  // open: en
  Multiplexer multiplexer_365 (
    .in0(multiplexer_337_out), .in1(X[12]), .out(multiplexer_365_out), .sel(swift_6));  // open: en
  Multiplexer multiplexer_366 (
    .in0(multiplexer_338_out), .in1(X[13]), .out(multiplexer_366_out), .sel(swift_6));  // open: en
  Multiplexer multiplexer_367 (
    .in0(multiplexer_339_out), .in1(X[14]), .out(multiplexer_367_out), .sel(swift_6));  // open: en
  Multiplexer multiplexer_368 (
    .in0(multiplexer_340_out), .in1(X[15]), .out(multiplexer_368_out), .sel(swift_6));  // open: en
  Multiplexer multiplexer_369 (
    .in0(multiplexer_341_out), .in1(X[16]), .out(multiplexer_369_out), .sel(swift_6));  // open: en
  Multiplexer multiplexer_370 (
    .in0(multiplexer_342_out), .in1(X[17]), .out(multiplexer_370_out), .sel(swift_6));  // open: en
  Multiplexer multiplexer_371 (
    .in0(multiplexer_343_out), .in1(X[18]), .out(multiplexer_371_out), .sel(swift_6));  // open: en
  Multiplexer multiplexer_372 (
    .in0(multiplexer_344_out), .in1(X[19]), .out(multiplexer_372_out), .sel(swift_6));  // open: en
  Multiplexer multiplexer_373 (
    .in0(multiplexer_345_out), .in1(X[20]), .out(multiplexer_373_out), .sel(swift_6));  // open: en
  Multiplexer multiplexer_374 (
    .in0(multiplexer_346_out), .in1(X[21]), .out(multiplexer_374_out), .sel(swift_6));  // open: en
  Multiplexer multiplexer_375 (
    .in0(multiplexer_347_out), .in1(X[22]), .out(multiplexer_375_out), .sel(swift_6));  // open: en
  Multiplexer multiplexer_376 (
    .in0(multiplexer_348_out), .in1(X[23]), .out(multiplexer_376_out), .sel(swift_6));  // open: en
  Multiplexer multiplexer_377 (
    .in0(multiplexer_349_out), .in1(X[24]), .out(multiplexer_377_out), .sel(swift_6));  // open: en
  Multiplexer multiplexer_378 (
    .in0(multiplexer_350_out), .in1(X[25]), .out(multiplexer_378_out), .sel(swift_6));  // open: en
  Multiplexer multiplexer_379 (.in0(1'b0), .in1(1'b1), .out(multiplexer_379_out), .sel(full_with_1));  // open: en
  Multiplexer multiplexer_380 (
    .in0(multiplexer_352_out), .in1(X[0]), .out(multiplexer_380_out), .sel(swift_5));  // open: en
  Multiplexer multiplexer_381 (
    .in0(multiplexer_353_out), .in1(X[1]), .out(multiplexer_381_out), .sel(swift_5));  // open: en
  Multiplexer multiplexer_382 (
    .in0(multiplexer_354_out), .in1(X[2]), .out(multiplexer_382_out), .sel(swift_5));  // open: en
  Multiplexer multiplexer_383 (
    .in0(multiplexer_355_out), .in1(X[3]), .out(multiplexer_383_out), .sel(swift_5));  // open: en
  Multiplexer multiplexer_384 (
    .in0(multiplexer_356_out), .in1(X[4]), .out(multiplexer_384_out), .sel(swift_5));  // open: en
  Multiplexer multiplexer_385 (
    .in0(multiplexer_357_out), .in1(X[5]), .out(multiplexer_385_out), .sel(swift_5));  // open: en
  Multiplexer multiplexer_386 (
    .in0(multiplexer_358_out), .in1(X[6]), .out(multiplexer_386_out), .sel(swift_5));  // open: en
  Multiplexer multiplexer_387 (
    .in0(multiplexer_359_out), .in1(X[7]), .out(multiplexer_387_out), .sel(swift_5));  // open: en
  Multiplexer multiplexer_388 (
    .in0(multiplexer_360_out), .in1(X[8]), .out(multiplexer_388_out), .sel(swift_5));  // open: en
  Multiplexer multiplexer_389 (
    .in0(multiplexer_361_out), .in1(X[9]), .out(multiplexer_389_out), .sel(swift_5));  // open: en
  Multiplexer multiplexer_390 (
    .in0(multiplexer_362_out), .in1(X[10]), .out(multiplexer_390_out), .sel(swift_5));  // open: en
  Multiplexer multiplexer_391 (
    .in0(multiplexer_363_out), .in1(X[11]), .out(multiplexer_391_out), .sel(swift_5));  // open: en
  Multiplexer multiplexer_392 (
    .in0(multiplexer_364_out), .in1(X[12]), .out(multiplexer_392_out), .sel(swift_5));  // open: en
  Multiplexer multiplexer_393 (
    .in0(multiplexer_365_out), .in1(X[13]), .out(multiplexer_393_out), .sel(swift_5));  // open: en
  Multiplexer multiplexer_394 (
    .in0(multiplexer_366_out), .in1(X[14]), .out(multiplexer_394_out), .sel(swift_5));  // open: en
  Multiplexer multiplexer_395 (
    .in0(multiplexer_367_out), .in1(X[15]), .out(multiplexer_395_out), .sel(swift_5));  // open: en
  Multiplexer multiplexer_396 (
    .in0(multiplexer_368_out), .in1(X[16]), .out(multiplexer_396_out), .sel(swift_5));  // open: en
  Multiplexer multiplexer_397 (
    .in0(multiplexer_369_out), .in1(X[17]), .out(multiplexer_397_out), .sel(swift_5));  // open: en
  Multiplexer multiplexer_398 (
    .in0(multiplexer_370_out), .in1(X[18]), .out(multiplexer_398_out), .sel(swift_5));  // open: en
  Multiplexer multiplexer_399 (
    .in0(multiplexer_371_out), .in1(X[19]), .out(multiplexer_399_out), .sel(swift_5));  // open: en
  Multiplexer multiplexer_400 (
    .in0(multiplexer_372_out), .in1(X[20]), .out(multiplexer_400_out), .sel(swift_5));  // open: en
  Multiplexer multiplexer_401 (
    .in0(multiplexer_373_out), .in1(X[21]), .out(multiplexer_401_out), .sel(swift_5));  // open: en
  Multiplexer multiplexer_402 (
    .in0(multiplexer_374_out), .in1(X[22]), .out(multiplexer_402_out), .sel(swift_5));  // open: en
  Multiplexer multiplexer_403 (
    .in0(multiplexer_375_out), .in1(X[23]), .out(multiplexer_403_out), .sel(swift_5));  // open: en
  Multiplexer multiplexer_404 (
    .in0(multiplexer_376_out), .in1(X[24]), .out(multiplexer_404_out), .sel(swift_5));  // open: en
  Multiplexer multiplexer_405 (
    .in0(multiplexer_377_out), .in1(X[25]), .out(multiplexer_405_out), .sel(swift_5));  // open: en
  Multiplexer multiplexer_406 (
    .in0(multiplexer_378_out), .in1(X[26]), .out(multiplexer_406_out), .sel(swift_5));  // open: en
  Multiplexer multiplexer_407 (.in0(1'b0), .in1(1'b1), .out(multiplexer_407_out), .sel(full_with_1));  // open: en
  Multiplexer multiplexer_408 (
    .in0(multiplexer_379_out), .in1(X[0]), .out(multiplexer_408_out), .sel(swift_4));  // open: en
  Multiplexer multiplexer_409 (
    .in0(multiplexer_380_out), .in1(X[1]), .out(multiplexer_409_out), .sel(swift_4));  // open: en
  Multiplexer multiplexer_410 (
    .in0(multiplexer_381_out), .in1(X[2]), .out(multiplexer_410_out), .sel(swift_4));  // open: en
  Multiplexer multiplexer_411 (
    .in0(multiplexer_382_out), .in1(X[3]), .out(multiplexer_411_out), .sel(swift_4));  // open: en
  Multiplexer multiplexer_412 (
    .in0(multiplexer_383_out), .in1(X[4]), .out(multiplexer_412_out), .sel(swift_4));  // open: en
  Multiplexer multiplexer_413 (
    .in0(multiplexer_384_out), .in1(X[5]), .out(multiplexer_413_out), .sel(swift_4));  // open: en
  Multiplexer multiplexer_414 (
    .in0(multiplexer_385_out), .in1(X[6]), .out(multiplexer_414_out), .sel(swift_4));  // open: en
  Multiplexer multiplexer_415 (
    .in0(multiplexer_386_out), .in1(X[7]), .out(multiplexer_415_out), .sel(swift_4));  // open: en
  Multiplexer multiplexer_416 (
    .in0(multiplexer_387_out), .in1(X[8]), .out(multiplexer_416_out), .sel(swift_4));  // open: en
  Multiplexer multiplexer_417 (
    .in0(multiplexer_388_out), .in1(X[9]), .out(multiplexer_417_out), .sel(swift_4));  // open: en
  Multiplexer multiplexer_418 (
    .in0(multiplexer_389_out), .in1(X[10]), .out(multiplexer_418_out), .sel(swift_4));  // open: en
  Multiplexer multiplexer_419 (
    .in0(multiplexer_390_out), .in1(X[11]), .out(multiplexer_419_out), .sel(swift_4));  // open: en
  Multiplexer multiplexer_420 (
    .in0(multiplexer_391_out), .in1(X[12]), .out(multiplexer_420_out), .sel(swift_4));  // open: en
  Multiplexer multiplexer_421 (
    .in0(multiplexer_392_out), .in1(X[13]), .out(multiplexer_421_out), .sel(swift_4));  // open: en
  Multiplexer multiplexer_422 (
    .in0(multiplexer_393_out), .in1(X[14]), .out(multiplexer_422_out), .sel(swift_4));  // open: en
  Multiplexer multiplexer_423 (
    .in0(multiplexer_394_out), .in1(X[15]), .out(multiplexer_423_out), .sel(swift_4));  // open: en
  Multiplexer multiplexer_424 (
    .in0(multiplexer_395_out), .in1(X[16]), .out(multiplexer_424_out), .sel(swift_4));  // open: en
  Multiplexer multiplexer_425 (
    .in0(multiplexer_396_out), .in1(X[17]), .out(multiplexer_425_out), .sel(swift_4));  // open: en
  Multiplexer multiplexer_426 (
    .in0(multiplexer_397_out), .in1(X[18]), .out(multiplexer_426_out), .sel(swift_4));  // open: en
  Multiplexer multiplexer_427 (
    .in0(multiplexer_398_out), .in1(X[19]), .out(multiplexer_427_out), .sel(swift_4));  // open: en
  Multiplexer multiplexer_428 (
    .in0(multiplexer_399_out), .in1(X[20]), .out(multiplexer_428_out), .sel(swift_4));  // open: en
  Multiplexer multiplexer_429 (
    .in0(multiplexer_400_out), .in1(X[21]), .out(multiplexer_429_out), .sel(swift_4));  // open: en
  Multiplexer multiplexer_430 (
    .in0(multiplexer_401_out), .in1(X[22]), .out(multiplexer_430_out), .sel(swift_4));  // open: en
  Multiplexer multiplexer_431 (
    .in0(multiplexer_402_out), .in1(X[23]), .out(multiplexer_431_out), .sel(swift_4));  // open: en
  Multiplexer multiplexer_432 (
    .in0(multiplexer_403_out), .in1(X[24]), .out(multiplexer_432_out), .sel(swift_4));  // open: en
  Multiplexer multiplexer_433 (
    .in0(multiplexer_404_out), .in1(X[25]), .out(multiplexer_433_out), .sel(swift_4));  // open: en
  Multiplexer multiplexer_434 (
    .in0(multiplexer_405_out), .in1(X[26]), .out(multiplexer_434_out), .sel(swift_4));  // open: en
  Multiplexer multiplexer_435 (
    .in0(multiplexer_406_out), .in1(X[27]), .out(multiplexer_435_out), .sel(swift_4));  // open: en
  Multiplexer multiplexer_436 (.in0(1'b0), .in1(1'b1), .out(multiplexer_436_out), .sel(full_with_1));  // open: en
  Multiplexer multiplexer_437 (
    .in0(multiplexer_407_out), .in1(X[0]), .out(multiplexer_437_out), .sel(swift_3));  // open: en
  Multiplexer multiplexer_438 (
    .in0(multiplexer_408_out), .in1(X[1]), .out(multiplexer_438_out), .sel(swift_3));  // open: en
  Multiplexer multiplexer_439 (
    .in0(multiplexer_409_out), .in1(X[2]), .out(multiplexer_439_out), .sel(swift_3));  // open: en
  Multiplexer multiplexer_440 (
    .in0(multiplexer_410_out), .in1(X[3]), .out(multiplexer_440_out), .sel(swift_3));  // open: en
  Multiplexer multiplexer_441 (
    .in0(multiplexer_411_out), .in1(X[4]), .out(multiplexer_441_out), .sel(swift_3));  // open: en
  Multiplexer multiplexer_442 (
    .in0(multiplexer_412_out), .in1(X[5]), .out(multiplexer_442_out), .sel(swift_3));  // open: en
  Multiplexer multiplexer_443 (
    .in0(multiplexer_413_out), .in1(X[6]), .out(multiplexer_443_out), .sel(swift_3));  // open: en
  Multiplexer multiplexer_444 (
    .in0(multiplexer_414_out), .in1(X[7]), .out(multiplexer_444_out), .sel(swift_3));  // open: en
  Multiplexer multiplexer_445 (
    .in0(multiplexer_415_out), .in1(X[8]), .out(multiplexer_445_out), .sel(swift_3));  // open: en
  Multiplexer multiplexer_446 (
    .in0(multiplexer_416_out), .in1(X[9]), .out(multiplexer_446_out), .sel(swift_3));  // open: en
  Multiplexer multiplexer_447 (
    .in0(multiplexer_417_out), .in1(X[10]), .out(multiplexer_447_out), .sel(swift_3));  // open: en
  Multiplexer multiplexer_448 (
    .in0(multiplexer_418_out), .in1(X[11]), .out(multiplexer_448_out), .sel(swift_3));  // open: en
  Multiplexer multiplexer_449 (
    .in0(multiplexer_419_out), .in1(X[12]), .out(multiplexer_449_out), .sel(swift_3));  // open: en
  Multiplexer multiplexer_450 (
    .in0(multiplexer_420_out), .in1(X[13]), .out(multiplexer_450_out), .sel(swift_3));  // open: en
  Multiplexer multiplexer_451 (
    .in0(multiplexer_421_out), .in1(X[14]), .out(multiplexer_451_out), .sel(swift_3));  // open: en
  Multiplexer multiplexer_452 (
    .in0(multiplexer_422_out), .in1(X[15]), .out(multiplexer_452_out), .sel(swift_3));  // open: en
  Multiplexer multiplexer_453 (
    .in0(multiplexer_423_out), .in1(X[16]), .out(multiplexer_453_out), .sel(swift_3));  // open: en
  Multiplexer multiplexer_454 (
    .in0(multiplexer_424_out), .in1(X[17]), .out(multiplexer_454_out), .sel(swift_3));  // open: en
  Multiplexer multiplexer_455 (
    .in0(multiplexer_425_out), .in1(X[18]), .out(multiplexer_455_out), .sel(swift_3));  // open: en
  Multiplexer multiplexer_456 (
    .in0(multiplexer_426_out), .in1(X[19]), .out(multiplexer_456_out), .sel(swift_3));  // open: en
  Multiplexer multiplexer_457 (
    .in0(multiplexer_427_out), .in1(X[20]), .out(multiplexer_457_out), .sel(swift_3));  // open: en
  Multiplexer multiplexer_458 (
    .in0(multiplexer_428_out), .in1(X[21]), .out(multiplexer_458_out), .sel(swift_3));  // open: en
  Multiplexer multiplexer_459 (
    .in0(multiplexer_429_out), .in1(X[22]), .out(multiplexer_459_out), .sel(swift_3));  // open: en
  Multiplexer multiplexer_460 (
    .in0(multiplexer_430_out), .in1(X[23]), .out(multiplexer_460_out), .sel(swift_3));  // open: en
  Multiplexer multiplexer_461 (
    .in0(multiplexer_431_out), .in1(X[24]), .out(multiplexer_461_out), .sel(swift_3));  // open: en
  Multiplexer multiplexer_462 (
    .in0(multiplexer_432_out), .in1(X[25]), .out(multiplexer_462_out), .sel(swift_3));  // open: en
  Multiplexer multiplexer_463 (
    .in0(multiplexer_433_out), .in1(X[26]), .out(multiplexer_463_out), .sel(swift_3));  // open: en
  Multiplexer multiplexer_464 (
    .in0(multiplexer_434_out), .in1(X[27]), .out(multiplexer_464_out), .sel(swift_3));  // open: en
  Multiplexer multiplexer_465 (
    .in0(multiplexer_435_out), .in1(X[28]), .out(multiplexer_465_out), .sel(swift_3));  // open: en
  Multiplexer multiplexer_466 (.in0(1'b0), .in1(1'b1), .out(multiplexer_466_out), .sel(full_with_1));  // open: en
  Multiplexer multiplexer_467 (
    .in0(multiplexer_436_out), .in1(X[0]), .out(multiplexer_467_out), .sel(swift_2));  // open: en
  Multiplexer multiplexer_468 (
    .in0(multiplexer_437_out), .in1(X[1]), .out(multiplexer_468_out), .sel(swift_2));  // open: en
  Multiplexer multiplexer_469 (
    .in0(multiplexer_438_out), .in1(X[2]), .out(multiplexer_469_out), .sel(swift_2));  // open: en
  Multiplexer multiplexer_470 (
    .in0(multiplexer_439_out), .in1(X[3]), .out(multiplexer_470_out), .sel(swift_2));  // open: en
  Multiplexer multiplexer_471 (
    .in0(multiplexer_440_out), .in1(X[4]), .out(multiplexer_471_out), .sel(swift_2));  // open: en
  Multiplexer multiplexer_472 (
    .in0(multiplexer_441_out), .in1(X[5]), .out(multiplexer_472_out), .sel(swift_2));  // open: en
  Multiplexer multiplexer_473 (
    .in0(multiplexer_442_out), .in1(X[6]), .out(multiplexer_473_out), .sel(swift_2));  // open: en
  Multiplexer multiplexer_474 (
    .in0(multiplexer_443_out), .in1(X[7]), .out(multiplexer_474_out), .sel(swift_2));  // open: en
  Multiplexer multiplexer_475 (
    .in0(multiplexer_444_out), .in1(X[8]), .out(multiplexer_475_out), .sel(swift_2));  // open: en
  Multiplexer multiplexer_476 (
    .in0(multiplexer_445_out), .in1(X[9]), .out(multiplexer_476_out), .sel(swift_2));  // open: en
  Multiplexer multiplexer_477 (
    .in0(multiplexer_446_out), .in1(X[10]), .out(multiplexer_477_out), .sel(swift_2));  // open: en
  Multiplexer multiplexer_478 (
    .in0(multiplexer_447_out), .in1(X[11]), .out(multiplexer_478_out), .sel(swift_2));  // open: en
  Multiplexer multiplexer_479 (
    .in0(multiplexer_448_out), .in1(X[12]), .out(multiplexer_479_out), .sel(swift_2));  // open: en
  Multiplexer multiplexer_480 (
    .in0(multiplexer_449_out), .in1(X[13]), .out(multiplexer_480_out), .sel(swift_2));  // open: en
  Multiplexer multiplexer_481 (
    .in0(multiplexer_450_out), .in1(X[14]), .out(multiplexer_481_out), .sel(swift_2));  // open: en
  Multiplexer multiplexer_482 (
    .in0(multiplexer_451_out), .in1(X[15]), .out(multiplexer_482_out), .sel(swift_2));  // open: en
  Multiplexer multiplexer_483 (
    .in0(multiplexer_452_out), .in1(X[16]), .out(multiplexer_483_out), .sel(swift_2));  // open: en
  Multiplexer multiplexer_484 (
    .in0(multiplexer_453_out), .in1(X[17]), .out(multiplexer_484_out), .sel(swift_2));  // open: en
  Multiplexer multiplexer_485 (
    .in0(multiplexer_454_out), .in1(X[18]), .out(multiplexer_485_out), .sel(swift_2));  // open: en
  Multiplexer multiplexer_486 (
    .in0(multiplexer_455_out), .in1(X[19]), .out(multiplexer_486_out), .sel(swift_2));  // open: en
  Multiplexer multiplexer_487 (
    .in0(multiplexer_456_out), .in1(X[20]), .out(multiplexer_487_out), .sel(swift_2));  // open: en
  Multiplexer multiplexer_488 (
    .in0(multiplexer_457_out), .in1(X[21]), .out(multiplexer_488_out), .sel(swift_2));  // open: en
  Multiplexer multiplexer_489 (
    .in0(multiplexer_458_out), .in1(X[22]), .out(multiplexer_489_out), .sel(swift_2));  // open: en
  Multiplexer multiplexer_490 (
    .in0(multiplexer_459_out), .in1(X[23]), .out(multiplexer_490_out), .sel(swift_2));  // open: en
  Multiplexer multiplexer_491 (
    .in0(multiplexer_460_out), .in1(X[24]), .out(multiplexer_491_out), .sel(swift_2));  // open: en
  Multiplexer multiplexer_492 (
    .in0(multiplexer_461_out), .in1(X[25]), .out(multiplexer_492_out), .sel(swift_2));  // open: en
  Multiplexer multiplexer_493 (
    .in0(multiplexer_462_out), .in1(X[26]), .out(multiplexer_493_out), .sel(swift_2));  // open: en
  Multiplexer multiplexer_494 (
    .in0(multiplexer_463_out), .in1(X[27]), .out(multiplexer_494_out), .sel(swift_2));  // open: en
  Multiplexer multiplexer_495 (
    .in0(multiplexer_464_out), .in1(X[28]), .out(multiplexer_495_out), .sel(swift_2));  // open: en
  Multiplexer multiplexer_496 (
    .in0(multiplexer_465_out), .in1(X[29]), .out(multiplexer_496_out), .sel(swift_2));  // open: en
  Multiplexer multiplexer_497 (
    .in0(multiplexer_466_out), .in1(X[0]), .out(multiplexer_497_out), .sel(swift_1));  // open: en
  Multiplexer multiplexer_498 (
    .in0(multiplexer_467_out), .in1(X[1]), .out(multiplexer_498_out), .sel(swift_1));  // open: en
  Multiplexer multiplexer_499 (
    .in0(multiplexer_468_out), .in1(X[2]), .out(multiplexer_499_out), .sel(swift_1));  // open: en
  Multiplexer multiplexer_500 (
    .in0(multiplexer_469_out), .in1(X[3]), .out(multiplexer_500_out), .sel(swift_1));  // open: en
  Multiplexer multiplexer_501 (
    .in0(multiplexer_470_out), .in1(X[4]), .out(multiplexer_501_out), .sel(swift_1));  // open: en
  Multiplexer multiplexer_502 (
    .in0(multiplexer_471_out), .in1(X[5]), .out(multiplexer_502_out), .sel(swift_1));  // open: en
  Multiplexer multiplexer_503 (
    .in0(multiplexer_472_out), .in1(X[6]), .out(multiplexer_503_out), .sel(swift_1));  // open: en
  Multiplexer multiplexer_504 (
    .in0(multiplexer_473_out), .in1(X[7]), .out(multiplexer_504_out), .sel(swift_1));  // open: en
  Multiplexer multiplexer_505 (
    .in0(multiplexer_474_out), .in1(X[8]), .out(multiplexer_505_out), .sel(swift_1));  // open: en
  Multiplexer multiplexer_506 (
    .in0(multiplexer_475_out), .in1(X[9]), .out(multiplexer_506_out), .sel(swift_1));  // open: en
  Multiplexer multiplexer_507 (
    .in0(multiplexer_476_out), .in1(X[10]), .out(multiplexer_507_out), .sel(swift_1));  // open: en
  Multiplexer multiplexer_508 (
    .in0(multiplexer_477_out), .in1(X[11]), .out(multiplexer_508_out), .sel(swift_1));  // open: en
  Multiplexer multiplexer_509 (
    .in0(multiplexer_478_out), .in1(X[12]), .out(multiplexer_509_out), .sel(swift_1));  // open: en
  Multiplexer multiplexer_510 (
    .in0(multiplexer_479_out), .in1(X[13]), .out(multiplexer_510_out), .sel(swift_1));  // open: en
  Multiplexer multiplexer_511 (
    .in0(multiplexer_480_out), .in1(X[14]), .out(multiplexer_511_out), .sel(swift_1));  // open: en
  Multiplexer multiplexer_512 (
    .in0(multiplexer_481_out), .in1(X[15]), .out(multiplexer_512_out), .sel(swift_1));  // open: en
  Multiplexer multiplexer_513 (
    .in0(multiplexer_482_out), .in1(X[16]), .out(multiplexer_513_out), .sel(swift_1));  // open: en
  Multiplexer multiplexer_514 (
    .in0(multiplexer_483_out), .in1(X[17]), .out(multiplexer_514_out), .sel(swift_1));  // open: en
  Multiplexer multiplexer_515 (
    .in0(multiplexer_484_out), .in1(X[18]), .out(multiplexer_515_out), .sel(swift_1));  // open: en
  Multiplexer multiplexer_516 (
    .in0(multiplexer_485_out), .in1(X[19]), .out(multiplexer_516_out), .sel(swift_1));  // open: en
  Multiplexer multiplexer_517 (
    .in0(multiplexer_486_out), .in1(X[20]), .out(multiplexer_517_out), .sel(swift_1));  // open: en
  Multiplexer multiplexer_518 (
    .in0(multiplexer_487_out), .in1(X[21]), .out(multiplexer_518_out), .sel(swift_1));  // open: en
  Multiplexer multiplexer_519 (
    .in0(multiplexer_488_out), .in1(X[22]), .out(multiplexer_519_out), .sel(swift_1));  // open: en
  Multiplexer multiplexer_520 (
    .in0(multiplexer_489_out), .in1(X[23]), .out(multiplexer_520_out), .sel(swift_1));  // open: en
  Multiplexer multiplexer_521 (
    .in0(multiplexer_490_out), .in1(X[24]), .out(multiplexer_521_out), .sel(swift_1));  // open: en
  Multiplexer multiplexer_522 (
    .in0(multiplexer_491_out), .in1(X[25]), .out(multiplexer_522_out), .sel(swift_1));  // open: en
  Multiplexer multiplexer_523 (
    .in0(multiplexer_492_out), .in1(X[26]), .out(multiplexer_523_out), .sel(swift_1));  // open: en
  Multiplexer multiplexer_524 (
    .in0(multiplexer_493_out), .in1(X[27]), .out(multiplexer_524_out), .sel(swift_1));  // open: en
  Multiplexer multiplexer_525 (
    .in0(multiplexer_494_out), .in1(X[28]), .out(multiplexer_525_out), .sel(swift_1));  // open: en
  Multiplexer multiplexer_526 (
    .in0(multiplexer_495_out), .in1(X[29]), .out(multiplexer_526_out), .sel(swift_1));  // open: en
  Multiplexer multiplexer_527 (
    .in0(multiplexer_496_out), .in1(X[30]), .out(multiplexer_527_out), .sel(swift_1));  // open: en
  Multiplexer multiplexer_528 (.in0(1'b0), .in1(1'b1), .out(multiplexer_528_out), .sel(full_with_1));  // open: en
  Multiplexer multiplexer_529 (.in0(multiplexer_528_out), .in1(X[0]), .out(out[0]), .sel(swift_0));  // open: en
  Multiplexer multiplexer_530 (.in0(multiplexer_497_out), .in1(X[1]), .out(out[1]), .sel(swift_0));  // open: en
  Multiplexer multiplexer_531 (.in0(multiplexer_498_out), .in1(X[2]), .out(out[2]), .sel(swift_0));  // open: en
  Multiplexer multiplexer_532 (.in0(multiplexer_499_out), .in1(X[3]), .out(out[3]), .sel(swift_0));  // open: en
  Multiplexer multiplexer_533 (.in0(multiplexer_500_out), .in1(X[4]), .out(out[4]), .sel(swift_0));  // open: en
  Multiplexer multiplexer_534 (.in0(multiplexer_501_out), .in1(X[5]), .out(out[5]), .sel(swift_0));  // open: en
  Multiplexer multiplexer_535 (.in0(multiplexer_502_out), .in1(X[6]), .out(out[6]), .sel(swift_0));  // open: en
  Multiplexer multiplexer_536 (.in0(multiplexer_503_out), .in1(X[7]), .out(out[7]), .sel(swift_0));  // open: en
  Multiplexer multiplexer_537 (.in0(multiplexer_504_out), .in1(X[8]), .out(out[8]), .sel(swift_0));  // open: en
  Multiplexer multiplexer_538 (.in0(multiplexer_505_out), .in1(X[9]), .out(out[9]), .sel(swift_0));  // open: en
  Multiplexer multiplexer_539 (.in0(multiplexer_506_out), .in1(X[10]), .out(out[10]), .sel(swift_0));  // open: en
  Multiplexer multiplexer_540 (.in0(multiplexer_507_out), .in1(X[11]), .out(out[11]), .sel(swift_0));  // open: en
  Multiplexer multiplexer_541 (.in0(multiplexer_508_out), .in1(X[12]), .out(out[12]), .sel(swift_0));  // open: en
  Multiplexer multiplexer_542 (.in0(multiplexer_509_out), .in1(X[13]), .out(out[13]), .sel(swift_0));  // open: en
  Multiplexer multiplexer_543 (.in0(multiplexer_510_out), .in1(X[14]), .out(out[14]), .sel(swift_0));  // open: en
  Multiplexer multiplexer_544 (.in0(multiplexer_511_out), .in1(X[15]), .out(out[15]), .sel(swift_0));  // open: en
  Multiplexer multiplexer_545 (.in0(multiplexer_512_out), .in1(X[16]), .out(out[16]), .sel(swift_0));  // open: en
  Multiplexer multiplexer_546 (.in0(multiplexer_513_out), .in1(X[17]), .out(out[17]), .sel(swift_0));  // open: en
  Multiplexer multiplexer_547 (.in0(multiplexer_514_out), .in1(X[18]), .out(out[18]), .sel(swift_0));  // open: en
  Multiplexer multiplexer_548 (.in0(multiplexer_515_out), .in1(X[19]), .out(out[19]), .sel(swift_0));  // open: en
  Multiplexer multiplexer_549 (.in0(multiplexer_516_out), .in1(X[20]), .out(out[20]), .sel(swift_0));  // open: en
  Multiplexer multiplexer_550 (.in0(multiplexer_517_out), .in1(X[21]), .out(out[21]), .sel(swift_0));  // open: en
  Multiplexer multiplexer_551 (.in0(multiplexer_518_out), .in1(X[22]), .out(out[22]), .sel(swift_0));  // open: en
  Multiplexer multiplexer_552 (.in0(multiplexer_519_out), .in1(X[23]), .out(out[23]), .sel(swift_0));  // open: en
  Multiplexer multiplexer_553 (.in0(multiplexer_520_out), .in1(X[24]), .out(out[24]), .sel(swift_0));  // open: en
  Multiplexer multiplexer_554 (.in0(multiplexer_521_out), .in1(X[25]), .out(out[25]), .sel(swift_0));  // open: en
  Multiplexer multiplexer_555 (.in0(multiplexer_522_out), .in1(X[26]), .out(out[26]), .sel(swift_0));  // open: en
  Multiplexer multiplexer_556 (.in0(multiplexer_523_out), .in1(X[27]), .out(out[27]), .sel(swift_0));  // open: en
  Multiplexer multiplexer_557 (.in0(multiplexer_524_out), .in1(X[28]), .out(out[28]), .sel(swift_0));  // open: en
  Multiplexer multiplexer_558 (.in0(multiplexer_525_out), .in1(X[29]), .out(out[29]), .sel(swift_0));  // open: en
  Multiplexer multiplexer_559 (.in0(multiplexer_526_out), .in1(X[30]), .out(out[30]), .sel(swift_0));  // open: en
  Multiplexer multiplexer_560 (.in0(multiplexer_527_out), .in1(X[31]), .out(out[31]), .sel(swift_0));  // open: en
endmodule

module \先试试乘法电路  (
);

  wire clock_1_out, d_ff_1_q, d_ff_2_q, d_ff_4_q, d_ff_6_q, d_ff_9_q, d_ff_10_q, d_ff_11_q, d_ff_12_q,
       \n4位快速加法器_1_c4 ;
  wire [3:0] and_4_out, d_ff_8_q, \n4位快速加法器_1_s ;

  Clock clock_1 (.out(clock_1_out));
  D_Flip_Flop d_ff_1 (.clk(clock_1_out), .Q(d_ff_1_q));  // open: D, Qn, preset, en, reset
  and and_1 (and_4_out[3], d_ff_12_q, d_ff_1_q);
  D_Flip_Flop d_ff_2 (.clk(clock_1_out), .Q(d_ff_2_q));  // open: D, Qn, preset, en, reset
  and and_2 (and_4_out[2], d_ff_12_q, d_ff_2_q);
  \_4位快速加法器  \u_4位快速加法器_1  (
    .X(d_ff_8_q), .Y(and_4_out), .C0(1'b0), .S(\n4位快速加法器_1_s ), .C4(\n4位快速加法器_1_c4 ));  // open: G_star, P_star, C3
  D_Flip_Flop d_ff_3 (.clk(clock_1_out), .D(\n4位快速加法器_1_c4 ), .Q(d_ff_8_q[3]));  // open: Qn, preset, en, reset
  D_Flip_Flop d_ff_4 (.clk(clock_1_out), .Q(d_ff_4_q));  // open: D, Qn, preset, en, reset
  and and_3 (and_4_out[1], d_ff_12_q, d_ff_4_q);
  D_Flip_Flop d_ff_5 (.clk(clock_1_out), .D(\n4位快速加法器_1_s [3]), .Q(d_ff_8_q[2]));  // open: Qn, preset, en, reset
  D_Flip_Flop d_ff_6 (.clk(clock_1_out), .Q(d_ff_6_q));  // open: D, Qn, preset, en, reset
  and and_4 (and_4_out[0], d_ff_12_q, d_ff_6_q);
  D_Flip_Flop d_ff_7 (.clk(clock_1_out), .D(\n4位快速加法器_1_s [2]), .Q(d_ff_8_q[1]));  // open: Qn, preset, en, reset
  D_Flip_Flop d_ff_8 (.clk(clock_1_out), .D(\n4位快速加法器_1_s [1]), .Q(d_ff_8_q[0]));  // open: Qn, preset, en, reset
  D_Flip_Flop d_ff_9 (.clk(clock_1_out), .D(\n4位快速加法器_1_s [0]), .Q(d_ff_9_q));  // open: Qn, preset, en, reset
  D_Flip_Flop d_ff_10 (.clk(clock_1_out), .D(d_ff_9_q), .Q(d_ff_10_q));  // open: Qn, preset, en, reset
  D_Flip_Flop d_ff_11 (.clk(clock_1_out), .D(d_ff_10_q), .Q(d_ff_11_q));  // open: Qn, preset, en, reset
  D_Flip_Flop d_ff_12 (.clk(clock_1_out), .D(d_ff_11_q), .Q(d_ff_12_q));  // open: Qn, preset, en, reset
endmodule

module \弃用的与或非电路  (
);

  wire and0, and1, and2, and3, and4, and5, and6, and7, and8, and9, and10, and11, and12, and13, and14, and15,
       and16, and17, and18, and19, and20, and21, and22, and23, and24, and25, and26, and27, and28, and29,
       and30, and31, or0, or1, or2, or3, or4, or5, or6, or7, or8, or9, or10, or11, or12, or13, or14, or15,
       or16, or17, or18, or19, or20, or21, or22, or23, or24, or25, or26, or27, or28, or29, or30, or31,
       undriven, undriven_2, undriven_3, undriven_4, undriven_5, undriven_6, undriven_7, undriven_8,
       undriven_9, undriven_10, undriven_11, undriven_12, undriven_13, undriven_14, undriven_15, undriven_16,
       undriven_17, undriven_18, undriven_19, undriven_20, undriven_21, undriven_22, undriven_23,
       undriven_24, undriven_25, undriven_26, undriven_27, undriven_28, undriven_29, undriven_30,
       undriven_31, undriven_32, undriven_33, undriven_34, undriven_35, undriven_36, undriven_37,
       undriven_38, undriven_39, undriven_40, undriven_41, undriven_42, undriven_43, undriven_44,
       undriven_45, undriven_46, undriven_47, undriven_48, undriven_49, undriven_50, undriven_51,
       undriven_52, undriven_53, undriven_54, undriven_55, undriven_56, undriven_57, undriven_58,
       undriven_59, undriven_60, undriven_61, undriven_62, undriven_63, undriven_64, xor0, xor1, xor2, xor3,
       xor4, xor5, xor6, xor7, xor8, xor9, xor10, xor11, xor12, xor13, xor14, xor15, xor16, xor17, xor18,
       xor19, xor20, xor21, xor22, xor23, xor24, xor25, xor26, xor27, xor28, xor29, xor30, xor31;
  wire [3:0] not_1_out, not_5_out, not_9_out, not_13_out, not_17_out, not_21_out, not_25_out, not_29_out;

  and and_1 (and31, undriven_22, undriven_33);
  or or_1 (or31, undriven_22, undriven_33);
  xor xor_1 (xor31, undriven_22, undriven_33);
  and and_2 (and30, undriven_11, undriven_34);
  or or_2 (or30, undriven_11, undriven_34);
  xor xor_2 (xor30, undriven_11, undriven_34);
  and and_3 (and29, undriven_32, undriven_35);
  or or_3 (or29, undriven_32, undriven_35);
  xor xor_3 (xor29, undriven_32, undriven_35);
  and and_4 (and28, undriven_21, undriven_36);
  or or_4 (or28, undriven_21, undriven_36);
  xor xor_4 (xor28, undriven_21, undriven_36);
  and and_5 (and26, undriven_31, undriven_38);
  or or_5 (or26, undriven_31, undriven_38);
  xor xor_5 (xor26, undriven_31, undriven_38);
  and and_6 (and27, undriven_10, undriven_37);
  or or_6 (or27, undriven_10, undriven_37);
  xor xor_6 (xor27, undriven_10, undriven_37);
  and and_7 (and25, undriven_20, undriven_39);
  or or_7 (or25, undriven_20, undriven_39);
  xor xor_7 (xor25, undriven_20, undriven_39);
  and and_8 (and24, undriven_9, undriven_40);
  or or_8 (or24, undriven_9, undriven_40);
  xor xor_8 (xor24, undriven_9, undriven_40);
  and and_9 (and23, undriven_30, undriven_41);
  or or_9 (or23, undriven_30, undriven_41);
  xor xor_9 (xor23, undriven_30, undriven_41);
  and and_10 (and22, undriven_19, undriven_42);
  or or_10 (or22, undriven_19, undriven_42);
  xor xor_10 (xor22, undriven_19, undriven_42);
  and and_11 (and20, undriven_29, undriven_44);
  or or_11 (or20, undriven_29, undriven_44);
  xor xor_11 (xor20, undriven_29, undriven_44);
  and and_12 (and21, undriven_8, undriven_43);
  or or_12 (or21, undriven_8, undriven_43);
  xor xor_12 (xor21, undriven_8, undriven_43);
  and and_13 (and18, undriven_7, undriven_46);
  or or_13 (or18, undriven_7, undriven_46);
  xor xor_13 (xor18, undriven_7, undriven_46);
  and and_14 (and19, undriven_18, undriven_45);
  or or_14 (or19, undriven_18, undriven_45);
  xor xor_14 (xor19, undriven_18, undriven_45);
  and and_15 (and17, undriven_28, undriven_47);
  or or_15 (or17, undriven_28, undriven_47);
  xor xor_15 (xor17, undriven_28, undriven_47);
  and and_16 (and16, undriven_17, undriven_48);
  or or_16 (or16, undriven_17, undriven_48);
  xor xor_16 (xor16, undriven_17, undriven_48);
  and and_17 (and15, undriven_6, undriven_49);
  or or_17 (or15, undriven_6, undriven_49);
  xor xor_17 (xor15, undriven_6, undriven_49);
  and and_18 (and14, undriven_27, undriven_50);
  or or_18 (or14, undriven_27, undriven_50);
  xor xor_18 (xor14, undriven_27, undriven_50);
  and and_19 (and13, undriven_16, undriven_51);
  or or_19 (or13, undriven_16, undriven_51);
  xor xor_19 (xor13, undriven_16, undriven_51);
  and and_20 (and11, undriven_26, undriven_53);
  or or_20 (or11, undriven_26, undriven_53);
  xor xor_20 (xor11, undriven_26, undriven_53);
  and and_21 (and12, undriven_5, undriven_52);
  or or_21 (or12, undriven_5, undriven_52);
  xor xor_21 (xor12, undriven_5, undriven_52);
  and and_22 (and10, undriven_15, undriven_54);
  or or_22 (or10, undriven_15, undriven_54);
  xor xor_22 (xor10, undriven_15, undriven_54);
  and and_23 (and9, undriven_4, undriven_55);
  or or_23 (or9, undriven_4, undriven_55);
  xor xor_23 (xor9, undriven_4, undriven_55);
  and and_24 (and8, undriven_25, undriven_56);
  or or_24 (or8, undriven_25, undriven_56);
  xor xor_24 (xor8, undriven_25, undriven_56);
  and and_25 (and7, undriven_14, undriven_57);
  or or_25 (or7, undriven_14, undriven_57);
  xor xor_25 (xor7, undriven_14, undriven_57);
  and and_26 (and5, undriven_24, undriven_59);
  or or_26 (or5, undriven_24, undriven_59);
  and and_27 (and6, undriven_3, undriven_58);
  or or_27 (or6, undriven_3, undriven_58);
  xor xor_26 (xor6, undriven_3, undriven_58);
  xor xor_27 (xor5, undriven_24, undriven_59);
  and and_28 (and4, undriven_13, undriven_60);
  or or_28 (or4, undriven_13, undriven_60);
  xor xor_28 (xor4, undriven_13, undriven_60);
  and and_29 (and2, undriven_23, undriven_62);
  or or_29 (or2, undriven_23, undriven_62);
  and and_30 (and3, undriven_2, undriven_61);
  or or_30 (or3, undriven_2, undriven_61);
  xor xor_29 (xor3, undriven_2, undriven_61);
  and and_31 (and1, undriven_12, undriven_63);
  or or_31 (or1, undriven_12, undriven_63);
  xor xor_30 (xor1, undriven_12, undriven_63);
  xor xor_31 (xor2, undriven_23, undriven_62);
  and and_32 (and0, undriven, undriven_64);
  or or_32 (or0, undriven, undriven_64);
  xor xor_32 (xor0, undriven, undriven_64);
  not not_1 (not_1_out[0], or16);
  not not_2 (not_1_out[1], or17);
  not not_3 (not_1_out[2], or18);
  not not_4 (not_1_out[3], or19);
  not not_5 (not_5_out[0], or20);
  not not_6 (not_5_out[1], or21);
  not not_7 (not_5_out[2], or22);
  not not_8 (not_5_out[3], or23);
  not not_9 (not_9_out[0], or24);
  not not_10 (not_9_out[1], or25);
  not not_11 (not_9_out[2], or26);
  not not_12 (not_9_out[3], or27);
  not not_13 (not_13_out[0], or28);
  not not_14 (not_13_out[1], or29);
  not not_15 (not_13_out[2], or30);
  not not_16 (not_13_out[3], or31);
  not not_17 (not_17_out[0], or0);
  not not_18 (not_17_out[1], or1);
  not not_19 (not_17_out[2], or2);
  not not_20 (not_17_out[3], or3);
  not not_21 (not_21_out[0], or4);
  not not_22 (not_21_out[1], or5);
  not not_23 (not_21_out[2], or6);
  not not_24 (not_21_out[3], or7);
  not not_25 (not_25_out[0], or8);
  not not_26 (not_25_out[1], or9);
  not not_27 (not_25_out[2], or10);
  not not_28 (not_25_out[3], or11);
  not not_29 (not_29_out[0], or12);
  not not_30 (not_29_out[1], or13);
  not not_31 (not_29_out[2], or14);
  not not_32 (not_29_out[3], or15);
endmodule

module \自带加法器包装  (
  input  Cin,
  input  [31:0] x,
  input  [31:0] y,
  output [31:0] Out,
  output Cout
);

  Adder #(.width(32)) adder_1 (.a(x), .b(y), .out(Out), .cin(Cin), .cout(Cout));
endmodule
