// Logisim project cpu24.circ as structural Verilog: 16 circuits, main circuit ◇单周期MIPS
module \单周期MIPS  (
);

  wire and_1_out, and_4_out, and_5_out, CLK, comparator_1_eq, Go, JAL, mips_alu_1_equal, not_1_out,
       not_2_out, not_3_out, not_4_out, not_5_out, or_1_out, or_2_out, or_3_out, or_4_out, pause, RST,
       SignedExt, sys_show, syscall, \硬布线控制器_1_alu_src , \硬布线控制器_1_beq , \硬布线控制器_1_bne , \硬布线控制器_1_jmp ,
       \硬布线控制器_1_jr , \硬布线控制器_1_memtoreg , \硬布线控制器_1_memwrite , \硬布线控制器_1_regdst , \硬布线控制器_1_regwrite ;
  wire [3:0] \硬布线控制器_1_alu_op ;
  wire [4:0] multiplexer_4_out, multiplexer_5_out, multiplexer_6_out, multiplexer_7_out;
  wire [15:0] \总周期数 , \无条件分支数 , \条件分支成功数 ;
  wire [31:0] a0, adder_1_out, adder_2_out, bit_extender_1_out, bit_extender_2_out, LedData,
       mips_alu_1_result, mips_regifile_1_r1, multiplexer_1_out, multiplexer_2_out, multiplexer_3_out,
       multiplexer_8_out, multiplexer_9_out, multiplexer_10_out, multiplexer_11_out, PC_q, ram_1_data,
       rom_1_data;

  Button \u_总复位  (.out(RST));
  Button u_Go (.out(Go));
  Clock clock_1 (.out(CLK));
  Multiplexer #(.width(32)) multiplexer_1 (
    .in0(adder_1_out), .in1(mips_regifile_1_r1), .out(multiplexer_1_out), .sel(\硬布线控制器_1_jr ));  // open: en
  Hex_Digit_Display hex_digit_display_1 (.value(LedData[27:24]));  // open: dp
  Hex_Digit_Display hex_digit_display_2 (.value(LedData[31:28]));  // open: dp
  or or_1 (or_1_out, \硬布线控制器_1_jmp , JAL);
  Multiplexer #(.width(32)) multiplexer_2 (
    .in0(multiplexer_1_out), .in1(adder_2_out), .out(multiplexer_2_out), .sel(or_4_out));  // open: en
  Multiplexer #(.width(32)) multiplexer_3 (
    .in0(multiplexer_2_out), .in1({adder_1_out[31:28], rom_1_data[25:0], 2'b00}), .out(multiplexer_3_out),
    .sel(or_1_out));  // open: en
  Hex_Digit_Display hex_digit_display_3 (.value(LedData[23:20]));  // open: dp
  Hex_Digit_Display hex_digit_display_4 (.value(LedData[19:16]));  // open: dp
  or or_2 (or_2_out, Go, and_1_out);
  and and_1 (and_1_out, not_1_out, not_2_out);
  not not_1 (not_1_out, Go);
  not not_2 (not_2_out, pause);
  Hex_Digit_Display hex_digit_display_5 (.value(LedData[15:12]));  // open: dp
  Hex_Digit_Display hex_digit_display_6 (.value(LedData[11:8]));  // open: dp
  Register #(.width(32)) PC (.D(multiplexer_3_out), .en(or_2_out), .Q(PC_q), .clk(CLK), .clr(RST));
  Hex_Digit_Display hex_digit_display_7 (.value(LedData[3:0]));  // open: dp
  Hex_Digit_Display hex_digit_display_8 (.value(LedData[7:4]));  // open: dp
  Adder #(.width(32)) adder_1 (.a(PC_q), .b(32'h4), .out(adder_1_out));  // open: cin, cout
  ROM #(.addrWidth(10), .dataWidth(32)) rom_1 (.addr(PC_q[11:2]), .data(rom_1_data));  // open: sel
  // Probe on \总周期数 
  // Probe on \无条件分支数 
  // Probe on \条件分支成功数 
  Multiplexer #(.width(5)) multiplexer_4 (
    .in0(rom_1_data[25:21]), .in1(5'b00010), .out(multiplexer_4_out), .sel(syscall));  // open: en
  Multiplexer #(.width(5)) multiplexer_5 (
    .in0(rom_1_data[20:16]), .in1(5'b00100), .out(multiplexer_5_out), .sel(syscall));  // open: en
  Multiplexer #(.width(5)) multiplexer_6 (
    .in0(rom_1_data[15:11]), .in1(rom_1_data[20:16]), .out(multiplexer_6_out), .sel(\硬布线控制器_1_regdst ));  // open: en
  or or_3 (or_3_out, \硬布线控制器_1_jr , or_1_out);
  Multiplexer #(.width(5)) multiplexer_7 (
    .in0(multiplexer_6_out), .in1({5{1'b1}}), .out(multiplexer_7_out), .sel(JAL));  // open: en
  assign bit_extender_1_out = {{14{rom_1_data[15]}}, {rom_1_data[15:0], 2'b00}};  // Bit_Extender bit_extender_1
  Counter #(.width(16), .max('hffff)) counter_1 (
    .count(or_3_out), .Q(\无条件分支数 ), .clk(CLK), .clr(RST));  // open: load, D, carry
  \硬布线控制器  \u_硬布线控制器_1  (
    .Func(rom_1_data[5:0]), .OP(rom_1_data[31:26]), .ALU_OP(\硬布线控制器_1_alu_op ),
    .MemToReg(\硬布线控制器_1_memtoreg ), .MemWrite(\硬布线控制器_1_memwrite ), .ALU_SRC(\硬布线控制器_1_alu_src ),
    .RegWrite(\硬布线控制器_1_regwrite ), .SysCALL(syscall), .SignedExt(SignedExt), .RegDst(\硬布线控制器_1_regdst ),
    .JR(\硬布线控制器_1_jr ), .JMP(\硬布线控制器_1_jmp ), .Beq(\硬布线控制器_1_beq ), .JAL(JAL), .Bne(\硬布线控制器_1_bne ));
  MIPS_Regifile mips_regifile_1 (
    .Din(multiplexer_10_out), .Clk(CLK), .R1(mips_regifile_1_r1), .R2(a0), .WE(\硬布线控制器_1_regwrite ),
    .W_num(multiplexer_7_out), .R1_num(multiplexer_4_out), .R2_num(multiplexer_5_out));
  Adder #(.width(32)) adder_2 (.a(bit_extender_1_out), .b(adder_1_out), .out(adder_2_out));  // open: cin, cout
  Register #(.width(32)) register_1 (.D(a0), .en(sys_show), .Q(LedData), .clk(CLK), .clr(RST));
  and and_2 (pause, syscall, not_3_out);
  not not_3 (not_3_out, comparator_1_eq);
  Comparator #(.width(32)) comparator_1 (.a(32'h22), .b(mips_regifile_1_r1), .eq(comparator_1_eq));  // open: gt, lt
  assign bit_extender_2_out = {{16{rom_1_data[15]}}, rom_1_data[15:0]};  // Bit_Extender bit_extender_2
  and and_3 (sys_show, syscall, comparator_1_eq);
  Multiplexer #(.width(32)) multiplexer_8 (
    .in0({{16{1'b0}}, rom_1_data[15:0]}), .in1(bit_extender_2_out), .out(multiplexer_8_out), .sel(SignedExt));  // open: en
  Multiplexer #(.width(32)) multiplexer_9 (
    .in0(a0), .in1(multiplexer_8_out), .out(multiplexer_9_out), .sel(\硬布线控制器_1_alu_src ));  // open: en
  not not_4 (not_4_out, pause);
  MIPS_ALU mips_alu_1 (
    .X(mips_regifile_1_r1), .Y(multiplexer_9_out), .AluOP(\硬布线控制器_1_alu_op ), .Equal(mips_alu_1_equal),
    .Result(mips_alu_1_result), .shamt(rom_1_data[10:6]));  // open: Result_2
  Counter #(.width(16), .max('hffff)) counter_2 (
    .count(not_4_out), .Q(\总周期数 ), .clk(CLK), .clr(RST));  // open: load, D, carry
  and and_4 (and_4_out, \硬布线控制器_1_beq , mips_alu_1_equal);
  and and_5 (and_5_out, \硬布线控制器_1_bne , not_5_out);
  not not_5 (not_5_out, mips_alu_1_equal);
  Counter #(.width(16), .max('hffff)) counter_3 (
    .count(or_4_out), .Q(\条件分支成功数 ), .clk(CLK), .clr(RST));  // open: load, D, carry
  or or_4 (or_4_out, and_4_out, and_5_out);
  RAM #(.addrWidth(10), .dataWidth(32), .bus("separate")) ram_1 (
    .addr(mips_alu_1_result[11:2]), .din(a0), .data(ram_1_data), .str(\硬布线控制器_1_memwrite ), .clk(CLK),
    .clr(RST));  // open: sel, ld
  Multiplexer #(.width(32)) multiplexer_10 (
    .in0(multiplexer_11_out), .in1(adder_1_out), .out(multiplexer_10_out), .sel(JAL));  // open: en
  Multiplexer #(.width(32)) multiplexer_11 (
    .in0(mips_alu_1_result), .in1(ram_1_data), .out(multiplexer_11_out), .sel(\硬布线控制器_1_memtoreg ));  // open: en
  // Probe on nothing

  // Notes on the sheet:
  //   jr
  //   branch
  //   数码管输出应该用寄存器锁存，否则显示数据只能一闪而过
  //   jmp
  //   可以通过项目增加Logisim库的方式将前几次实验完成的电路作为子电路引入到本电路中使用
  //   数码管输出
  //   指令存储器
  //   指令字
  //   contents of rom_1 (hex, n*v repeats v):
  //   20110001 8000c05 20110001 20120002 20130003 8000c09 20110001 20120002 20130003 8000c0d 20110001
  //   20120002 20130003 8000c11 20110001 20120002 20130003 c000cb8 20100001 20110001 118fc0 112020
  //   20020022 c 118882 12200001 8000c15 112020 20020022 c 20110001 118880 112020 20020022 c 12200001
  //   8000c1f 20110001 118fc0 112020 20020022 c 1188c3 112020 20020022 c 118903 112020 20020022 c 118903
  //   112020 20020022 c 118903 112020 20020022 c 118903 112020 20020022 c 118903 112020 20020022 c 118903
  //   112020 20020022 c 118903 112020 20020022 c 20100001 109fc0 139fc3 8021 2012000c 24160003 26100001
  //   3210000f 20080008 20090001 139900 2709825 132020 20020022 c 1094022 1500fff9 22100001 2018000f
  //   2188024 108700 20080008 20090001 139902 2709825 132021 20020022 c 1094022 1500fff9 108702 2c9b022
  //   12c00001 8000c50 4020 1084027 84400 3508ffff 82021 20020022 c 2010ffff 20110000 ae300000 22100001
  //   22310004 ae300000 22100001 22310004 ae300000 22100001 22310004 ae300000 22100001 22310004 ae300000
  //   22100001 22310004 ae300000 22100001 22310004 ae300000 22100001 22310004 ae300000 22100001 22310004
  //   ae300000 22100001 22310004 ae300000 22100001 22310004 ae300000 22100001 22310004 ae300000 22100001
  //   22310004 ae300000 22100001 22310004 ae300000 22100001 22310004 ae300000 22100001 22310004 ae300000
  //   22100001 22310004 22100001 8020 2011003c 8e130000 8e340000 274402a 11000002 ae330000 ae140000
  //   2231fffc 1611fff8 102020 20020022 c 22100004 2011003c 1611fff2 20020032 c 20100000 22100001 102020
  //   20020022 c 22100002 102020 20020022 c 22100003 102020 20020022 c 22100004 102020 20020022 c 22100005
  //   102020 20020022 c 22100006 102020 20020022 c 22100007 102020 20020022 c 22100008 102020 20020022
  //   20020022 c 3e00008
  //   OP
  //   Func
  //   rs
  //   rt
  //   rd
  //   shamt
  //   imm
  //   addr
  //   总复位信号应将除ROM以外所有存储组件全部清零
  //   RegDst
  //   JMP
  //   JR
  //   OP
  //   Func
  //   Beq
  //   Bne
  //   MemToReg
  //   MemWrite
  //   AluOP
  //   AluSrcB
  //   RegWrite
  //   JAL
  //   RegDst
  //   Syscall
  //   AluSrcB
  //   MemToReg
endmodule

// 单周期硬布线控制器
module \硬布线控制器  (
  input  [5:0] OP,
  input  [5:0] Func,
  output [3:0] ALU_OP,
  output MemToReg,
  output MemWrite,
  output ALU_SRC,
  output RegWrite,
  output SysCALL,
  output SignedExt,
  output RegDst,
  output Beq,
  output Bne,
  output JR,
  output JMP,
  output JAL
);

  \运算控制器  \u_运算控制器_1  (
    .OP0(OP[0]), .OP1(OP[1]), .OP2(OP[2]), .OP3(OP[3]), .OP4(OP[4]), .OP5(OP[5]), .F0(Func[0]), .F1(Func[1]),
    .F2(Func[2]), .F3(Func[3]), .F4(Func[4]), .F5(Func[5]), .S0(ALU_OP[0]), .S1(ALU_OP[1]), .S2(ALU_OP[2]),
    .S3(ALU_OP[3]));
  \控制信号生成  \u_控制信号生成_1  (
    .OP0(OP[0]), .OP1(OP[1]), .OP2(OP[2]), .OP3(OP[3]), .OP4(OP[4]), .OP5(OP[5]), .F0(Func[0]), .F1(Func[1]),
    .F2(Func[2]), .F3(Func[3]), .F4(Func[4]), .F5(Func[5]), .MemToReg(MemToReg), .MemWrite(MemWrite),
    .ALU_SRC(ALU_SRC), .RegWrite(RegWrite), .SysCALL(SysCALL), .SignedExt(SignedExt), .RegDst(RegDst),
    .BEQ(Beq), .BNE(Bne), .JR(JR), .JMP(JMP), .JAL(JAL));

  // Other names for the same wires on the sheet: OP_CODE[5:0] = OP

  // Notes on the sheet:
  //   运算器控制器，根据指令生成运算器功能选择信号
  //   控制信号生成，产生数据通路需要的其他控制信号
endmodule

// 运算器控制器
module \运算控制器  (
  input  OP0,
  input  OP1,
  input  OP2,
  input  OP3,
  input  OP4,
  input  OP5,
  input  F0,
  input  F1,
  input  F2,
  input  F3,
  input  F4,
  input  F5,
  output S0,
  output S1,
  output S2,
  output S3
);

  wire and_1_out, and_2_out, and_3_out, and_4_out, and_5_out, and_6_out, and_7_out, and_8_out, and_9_out,
       and_10_out, and_11_out, and_12_out, and_13_out, and_14_out, and_15_out, and_16_out, and_17_out,
       and_18_out, and_19_out, and_20_out, and_21_out, and_22_out, and_23_out, and_24_out, and_25_out,
       not_1_out, not_2_out, not_3_out, not_4_out, not_5_out, not_6_out, not_7_out, not_8_out, not_9_out,
       not_10_out, not_11_out, not_12_out, not_13_out, not_14_out, not_15_out, not_16_out, not_17_out,
       not_18_out, not_19_out, not_20_out, not_21_out, not_22_out, not_23_out, not_24_out, not_25_out,
       not_26_out, not_27_out, not_28_out, not_29_out, not_30_out, not_31_out, not_32_out, not_33_out,
       not_34_out, not_35_out, not_36_out, not_37_out, not_38_out, not_39_out, not_40_out, not_41_out,
       not_42_out, not_43_out, not_44_out, not_45_out, not_46_out, not_47_out, not_48_out, not_49_out,
       not_50_out, not_51_out, not_52_out, not_53_out, not_54_out, not_55_out, not_56_out, not_57_out,
       not_58_out, not_59_out, not_60_out, not_61_out, not_62_out, not_63_out, not_64_out, not_65_out,
       not_66_out, not_67_out, not_68_out, not_69_out, not_70_out, not_71_out, not_72_out, not_73_out,
       not_74_out, not_75_out, not_76_out, not_77_out, not_78_out, not_79_out, not_80_out, not_81_out,
       not_82_out, not_83_out, not_84_out, not_85_out, not_86_out, not_87_out, not_88_out, not_89_out,
       not_90_out, not_91_out, not_92_out, not_93_out, not_94_out, not_95_out, not_96_out, not_97_out,
       not_98_out, not_99_out, not_100_out, not_101_out, not_102_out, not_103_out, not_104_out, not_105_out,
       not_106_out, not_107_out, not_108_out, not_109_out, not_110_out, not_111_out, not_112_out,
       not_113_out, not_114_out, not_115_out, not_116_out, not_117_out, not_118_out, not_119_out,
       not_120_out, not_121_out, not_122_out, not_123_out, not_124_out, not_125_out, not_126_out,
       not_127_out, not_128_out, not_129_out, not_130_out, not_131_out, not_132_out, not_133_out,
       not_134_out, not_135_out, not_136_out, not_137_out, not_138_out, not_139_out, not_140_out,
       not_141_out, not_142_out, not_143_out, not_144_out, not_145_out, not_146_out, not_147_out,
       not_148_out, not_149_out, not_150_out, not_151_out, not_152_out, not_153_out, not_154_out,
       not_155_out, not_156_out, not_157_out, not_158_out, not_159_out, not_160_out, not_161_out;

  not not_1 (not_1_out, OP0);
  not not_2 (not_2_out, OP1);
  not not_3 (not_3_out, OP2);
  not not_4 (not_4_out, OP4);
  not not_5 (not_5_out, OP5);
  not not_6 (not_6_out, F0);
  not not_7 (not_7_out, F1);
  not not_8 (not_8_out, F3);
  not not_9 (not_9_out, F4);
  not not_10 (not_10_out, OP0);
  not not_11 (not_11_out, OP1);
  not not_12 (not_12_out, OP2);
  not not_13 (not_13_out, OP4);
  not not_14 (not_14_out, OP5);
  not not_15 (not_15_out, F1);
  not not_16 (not_16_out, F2);
  not not_17 (not_17_out, F3);
  not not_18 (not_18_out, F4);
  not not_19 (not_19_out, OP0);
  not not_20 (not_20_out, OP1);
  not not_21 (not_21_out, OP2);
  not not_22 (not_22_out, OP4);
  not not_23 (not_23_out, OP5);
  not not_24 (not_24_out, F0);
  not not_25 (not_25_out, F2);
  not not_26 (not_26_out, F4);
  not not_27 (not_27_out, OP0);
  not not_28 (not_28_out, OP1);
  not not_29 (not_29_out, OP2);
  not not_30 (not_30_out, OP4);
  not not_31 (not_31_out, OP5);
  not not_32 (not_32_out, F2);
  not not_33 (not_33_out, F3);
  not not_34 (not_34_out, F4);
  not not_35 (not_35_out, F5);
  not not_36 (not_36_out, OP0);
  not not_37 (not_37_out, OP1);
  not not_38 (not_38_out, OP4);
  not not_39 (not_39_out, OP5);
  not not_40 (not_40_out, OP0);
  not not_41 (not_41_out, OP2);
  not not_42 (not_42_out, OP4);
  not not_43 (not_43_out, OP5);
  not not_44 (not_44_out, OP1);
  not not_45 (not_45_out, OP2);
  not not_46 (not_46_out, OP4);
  not not_47 (not_47_out, OP5);
  not not_48 (not_48_out, OP2);
  not not_49 (not_49_out, OP4);
  not not_50 (not_50_out, OP0);
  not not_51 (not_51_out, OP1);
  not not_52 (not_52_out, OP2);
  not not_53 (not_53_out, OP3);
  not not_54 (not_54_out, OP4);
  not not_55 (not_55_out, OP5);
  not not_56 (not_56_out, F0);
  not not_57 (not_57_out, F1);
  not not_58 (not_58_out, F3);
  not not_59 (not_59_out, F4);
  not not_60 (not_60_out, OP0);
  not not_61 (not_61_out, OP1);
  not not_62 (not_62_out, OP2);
  not not_63 (not_63_out, OP3);
  not not_64 (not_64_out, OP4);
  not not_65 (not_65_out, OP5);
  not not_66 (not_66_out, F0);
  not not_67 (not_67_out, F2);
  not not_68 (not_68_out, F3);
  not not_69 (not_69_out, F4);
  not not_70 (not_70_out, OP0);
  not not_71 (not_71_out, OP1);
  not not_72 (not_72_out, OP2);
  not not_73 (not_73_out, OP3);
  not not_74 (not_74_out, OP4);
  not not_75 (not_75_out, OP5);
  not not_76 (not_76_out, F0);
  not not_77 (not_77_out, F2);
  not not_78 (not_78_out, F4);
  not not_79 (not_79_out, OP0);
  not not_80 (not_80_out, OP1);
  not not_81 (not_81_out, OP2);
  not not_82 (not_82_out, OP3);
  not not_83 (not_83_out, OP4);
  not not_84 (not_84_out, OP5);
  not not_85 (not_85_out, F3);
  not not_86 (not_86_out, F4);
  not not_87 (not_87_out, OP0);
  not not_88 (not_88_out, OP1);
  not not_89 (not_89_out, OP4);
  not not_90 (not_90_out, OP5);
  not not_91 (not_91_out, OP0);
  not not_92 (not_92_out, OP2);
  not not_93 (not_93_out, OP4);
  not not_94 (not_94_out, OP5);
  not not_95 (not_95_out, OP0);
  not not_96 (not_96_out, OP1);
  not not_97 (not_97_out, OP2);
  not not_98 (not_98_out, OP4);
  not not_99 (not_99_out, OP5);
  not not_100 (not_100_out, F0);
  not not_101 (not_101_out, F1);
  not not_102 (not_102_out, F3);
  not not_103 (not_103_out, F4);
  not not_104 (not_104_out, OP0);
  not not_105 (not_105_out, OP1);
  not not_106 (not_106_out, OP2);
  not not_107 (not_107_out, OP4);
  not not_108 (not_108_out, OP5);
  not not_109 (not_109_out, F0);
  not not_110 (not_110_out, F2);
  not not_111 (not_111_out, F3);
  not not_112 (not_112_out, F4);
  not not_113 (not_113_out, OP0);
  not not_114 (not_114_out, OP1);
  not not_115 (not_115_out, OP2);
  not not_116 (not_116_out, OP4);
  not not_117 (not_117_out, OP5);
  not not_118 (not_118_out, F1);
  not not_119 (not_119_out, F2);
  not not_120 (not_120_out, F3);
  not not_121 (not_121_out, F4);
  not not_122 (not_122_out, OP0);
  not not_123 (not_123_out, OP1);
  not not_124 (not_124_out, OP2);
  not not_125 (not_125_out, OP4);
  not not_126 (not_126_out, OP5);
  not not_127 (not_127_out, F2);
  not not_128 (not_128_out, F4);
  not not_129 (not_129_out, OP0);
  not not_130 (not_130_out, OP1);
  not not_131 (not_131_out, OP4);
  not not_132 (not_132_out, OP5);
  not not_133 (not_133_out, OP1);
  not not_134 (not_134_out, OP2);
  not not_135 (not_135_out, OP4);
  not not_136 (not_136_out, OP5);
  not not_137 (not_137_out, OP2);
  not not_138 (not_138_out, OP4);
  not not_139 (not_139_out, OP0);
  not not_140 (not_140_out, OP1);
  not not_141 (not_141_out, OP2);
  not not_142 (not_142_out, OP3);
  not not_143 (not_143_out, OP4);
  not not_144 (not_144_out, OP5);
  not not_145 (not_145_out, F2);
  not not_146 (not_146_out, F4);
  not not_147 (not_147_out, OP0);
  not not_148 (not_148_out, OP1);
  not not_149 (not_149_out, OP2);
  not not_150 (not_150_out, OP3);
  not not_151 (not_151_out, OP4);
  not not_152 (not_152_out, OP5);
  not not_153 (not_153_out, F3);
  not not_154 (not_154_out, F4);
  not not_155 (not_155_out, OP0);
  not not_156 (not_156_out, OP2);
  not not_157 (not_157_out, OP4);
  not not_158 (not_158_out, OP5);
  not not_159 (not_159_out, OP1);
  not not_160 (not_160_out, OP4);
  not not_161 (not_161_out, OP5);
  and and_1 (and_1_out, not_1_out, not_2_out, not_3_out, not_4_out, not_5_out, not_6_out, not_7_out, not_8_out, not_9_out, F5);
  and and_2 (and_2_out, not_10_out, not_11_out, not_12_out, not_13_out, not_14_out, not_15_out, not_16_out, not_17_out, not_18_out, F5);
  and and_3 (and_3_out, not_19_out, not_20_out, not_21_out, not_22_out, not_23_out, not_24_out, F1, not_25_out, F3, not_26_out, F5);
  and and_4 (and_4_out, not_27_out, not_28_out, not_29_out, not_30_out, not_31_out, F0, F1, not_32_out, not_33_out, not_34_out, not_35_out);
  and and_5 (and_5_out, not_36_out, not_37_out, OP3, not_38_out, not_39_out);
  and and_6 (and_6_out, not_40_out, not_41_out, OP3, not_42_out, not_43_out);
  and and_7 (and_7_out, not_44_out, not_45_out, OP3, not_46_out, not_47_out);
  and and_8 (and_8_out, OP0, OP1, not_48_out, not_49_out, OP5);
  and and_9 (and_9_out, not_50_out, not_51_out, not_52_out, not_53_out, not_54_out, not_55_out, not_56_out, not_57_out, F2, not_58_out, not_59_out, F5);
  and and_10 (and_10_out, not_60_out, not_61_out, not_62_out, not_63_out, not_64_out, not_65_out, not_66_out, F1, not_67_out, not_68_out, not_69_out);
  and and_11 (and_11_out, not_70_out, not_71_out, not_72_out, not_73_out, not_74_out, not_75_out, not_76_out, F1, not_77_out, not_78_out, F5);
  and and_12 (and_12_out, not_79_out, not_80_out, not_81_out, not_82_out, not_83_out, not_84_out, F0, F1, F2, not_85_out, not_86_out, F5);
  and and_13 (and_13_out, not_87_out, not_88_out, OP2, OP3, not_89_out, not_90_out);
  and and_14 (and_14_out, not_91_out, OP1, not_92_out, OP3, not_93_out, not_94_out);
  and and_15 (and_15_out, not_95_out, not_96_out, not_97_out, not_98_out, not_99_out, not_100_out, not_101_out, not_102_out, not_103_out, F5);
  and and_16 (and_16_out, not_104_out, not_105_out, not_106_out, not_107_out, not_108_out, not_109_out, not_110_out, not_111_out, not_112_out, F5);
  and and_17 (and_17_out, not_113_out, not_114_out, not_115_out, not_116_out, not_117_out, not_118_out, not_119_out, not_120_out, not_121_out, F5);
  and and_18 (and_18_out, not_122_out, not_123_out, not_124_out, not_125_out, not_126_out, F0, F1, not_127_out, F3, not_128_out, F5);
  and and_19 (and_19_out, not_129_out, not_130_out, OP3, not_131_out, not_132_out);
  and and_20 (and_20_out, not_133_out, not_134_out, OP3, not_135_out, not_136_out);
  and and_21 (and_21_out, OP0, OP1, not_137_out, not_138_out, OP5);
  and and_22 (and_22_out, not_139_out, not_140_out, not_141_out, not_142_out, not_143_out, not_144_out, F1, not_145_out, F3, not_146_out, F5);
  and and_23 (and_23_out, not_147_out, not_148_out, not_149_out, not_150_out, not_151_out, not_152_out, F0, F2, not_153_out, not_154_out, F5);
  and and_24 (and_24_out, not_155_out, OP1, not_156_out, OP3, not_157_out, not_158_out);
  and and_25 (and_25_out, OP0, not_159_out, OP2, OP3, not_160_out, not_161_out);
  or or_1 (S0, and_1_out, and_2_out, and_3_out, and_4_out, and_5_out, and_6_out, and_7_out, and_8_out);
  or or_2 (S1, and_9_out, and_10_out, and_11_out, and_12_out, and_13_out, and_14_out);
  or or_3 (S2, and_15_out, and_16_out, and_17_out, and_18_out, and_19_out, and_20_out, and_21_out);
  or or_4 (S3, and_22_out, and_23_out, and_24_out, and_25_out);
endmodule

// 控制信号生成
module \控制信号生成  (
  input  OP0,
  input  OP1,
  input  OP2,
  input  OP3,
  input  OP4,
  input  OP5,
  input  F0,
  input  F1,
  input  F2,
  input  F3,
  input  F4,
  input  F5,
  output MemToReg,
  output MemWrite,
  output ALU_SRC,
  output RegWrite,
  output SysCALL,
  output SignedExt,
  output RegDst,
  output BEQ,
  output BNE,
  output JR,
  output JMP,
  output JAL
);

  wire and_3_out, and_4_out, and_5_out, and_6_out, and_7_out, and_8_out, and_9_out, and_10_out, and_11_out,
       and_12_out, and_13_out, and_15_out, and_16_out, and_17_out, and_18_out, and_19_out, and_20_out,
       not_1_out, not_2_out, not_3_out, not_4_out, not_5_out, not_6_out, not_7_out, not_8_out, not_9_out,
       not_10_out, not_11_out, not_12_out, not_13_out, not_14_out, not_15_out, not_16_out, not_17_out,
       not_18_out, not_19_out, not_20_out, not_21_out, not_22_out, not_23_out, not_24_out, not_25_out,
       not_26_out, not_27_out, not_28_out, not_29_out, not_30_out, not_31_out, not_32_out, not_33_out,
       not_34_out, not_35_out, not_36_out, not_37_out, not_38_out, not_39_out, not_40_out, not_41_out,
       not_42_out, not_43_out, not_44_out, not_45_out, not_46_out, not_47_out, not_48_out, not_49_out,
       not_50_out, not_51_out, not_52_out, not_53_out, not_54_out, not_55_out, not_56_out, not_57_out,
       not_58_out, not_59_out, not_60_out, not_61_out, not_62_out, not_63_out, not_64_out, not_65_out,
       not_66_out, not_67_out, not_68_out, not_69_out, not_70_out, not_71_out, not_72_out, not_73_out,
       not_74_out, not_75_out, not_76_out, not_77_out, not_78_out, not_79_out, not_80_out, not_81_out,
       not_82_out, not_83_out, not_84_out, not_85_out, not_86_out, not_87_out, not_88_out, not_89_out,
       not_90_out, not_91_out, not_92_out, not_93_out, not_94_out, not_95_out, not_96_out, not_97_out,
       not_98_out, not_99_out, not_100_out, not_101_out, not_102_out, not_103_out, not_104_out, not_105_out,
       not_106_out, not_107_out, not_108_out, not_109_out, not_110_out, not_111_out, not_112_out,
       not_113_out, not_114_out, not_115_out, not_116_out, not_117_out, not_118_out, not_119_out,
       not_120_out, not_121_out, not_122_out, not_123_out;

  not not_1 (not_1_out, OP2);
  not not_2 (not_2_out, OP3);
  not not_3 (not_3_out, OP4);
  not not_4 (not_4_out, OP2);
  not not_5 (not_5_out, OP4);
  not not_6 (not_6_out, OP0);
  not not_7 (not_7_out, OP2);
  not not_8 (not_8_out, OP4);
  not not_9 (not_9_out, OP5);
  not not_10 (not_10_out, OP1);
  not not_11 (not_11_out, OP4);
  not not_12 (not_12_out, OP5);
  not not_13 (not_13_out, OP2);
  not not_14 (not_14_out, OP4);
  not not_15 (not_15_out, OP0);
  not not_16 (not_16_out, OP1);
  not not_17 (not_17_out, OP2);
  not not_18 (not_18_out, OP4);
  not not_19 (not_19_out, OP5);
  not not_20 (not_20_out, F0);
  not not_21 (not_21_out, F2);
  not not_22 (not_22_out, F3);
  not not_23 (not_23_out, F4);
  not not_24 (not_24_out, OP0);
  not not_25 (not_25_out, OP1);
  not not_26 (not_26_out, OP2);
  not not_27 (not_27_out, OP4);
  not not_28 (not_28_out, OP5);
  not not_29 (not_29_out, F1);
  not not_30 (not_30_out, F3);
  not not_31 (not_31_out, F4);
  not not_32 (not_32_out, OP0);
  not not_33 (not_33_out, OP1);
  not not_34 (not_34_out, OP2);
  not not_35 (not_35_out, OP4);
  not not_36 (not_36_out, OP5);
  not not_37 (not_37_out, F2);
  not not_38 (not_38_out, F3);
  not not_39 (not_39_out, F4);
  not not_40 (not_40_out, F5);
  not not_41 (not_41_out, OP0);
  not not_42 (not_42_out, OP1);
  not not_43 (not_43_out, OP2);
  not not_44 (not_44_out, OP4);
  not not_45 (not_45_out, OP5);
  not not_46 (not_46_out, F2);
  not not_47 (not_47_out, F4);
  not not_48 (not_48_out, OP0);
  not not_49 (not_49_out, OP1);
  not not_50 (not_50_out, OP2);
  not not_51 (not_51_out, OP4);
  not not_52 (not_52_out, OP5);
  not not_53 (not_53_out, F3);
  not not_54 (not_54_out, F4);
  not not_55 (not_55_out, OP0);
  not not_56 (not_56_out, OP2);
  not not_57 (not_57_out, OP4);
  not not_58 (not_58_out, OP5);
  not not_59 (not_59_out, OP1);
  not not_60 (not_60_out, OP4);
  not not_61 (not_61_out, OP5);
  not not_62 (not_62_out, OP2);
  not not_63 (not_63_out, OP3);
  not not_64 (not_64_out, OP4);
  not not_65 (not_65_out, OP0);
  not not_66 (not_66_out, OP1);
  not not_67 (not_67_out, OP2);
  not not_68 (not_68_out, OP3);
  not not_69 (not_69_out, OP4);
  not not_70 (not_70_out, OP5);
  not not_71 (not_71_out, F0);
  not not_72 (not_72_out, F1);
  not not_73 (not_73_out, F4);
  not not_74 (not_74_out, F5);
  not not_75 (not_75_out, OP0);
  not not_76 (not_76_out, OP2);
  not not_77 (not_77_out, OP4);
  not not_78 (not_78_out, OP5);
  not not_79 (not_79_out, OP1);
  not not_80 (not_80_out, OP2);
  not not_81 (not_81_out, OP4);
  not not_82 (not_82_out, OP5);
  not not_83 (not_83_out, OP2);
  not not_84 (not_84_out, OP4);
  not not_85 (not_85_out, OP0);
  not not_86 (not_86_out, OP2);
  not not_87 (not_87_out, OP4);
  not not_88 (not_88_out, OP5);
  not not_89 (not_89_out, OP1);
  not not_90 (not_90_out, OP4);
  not not_91 (not_91_out, OP5);
  not not_92 (not_92_out, OP2);
  not not_93 (not_93_out, OP3);
  not not_94 (not_94_out, OP4);
  not not_95 (not_95_out, OP0);
  not not_96 (not_96_out, OP1);
  not not_97 (not_97_out, OP3);
  not not_98 (not_98_out, OP4);
  not not_99 (not_99_out, OP5);
  not not_100 (not_100_out, OP1);
  not not_101 (not_101_out, OP3);
  not not_102 (not_102_out, OP4);
  not not_103 (not_103_out, OP5);
  not not_104 (not_104_out, OP0);
  not not_105 (not_105_out, OP1);
  not not_106 (not_106_out, OP2);
  not not_107 (not_107_out, OP3);
  not not_108 (not_108_out, OP4);
  not not_109 (not_109_out, OP5);
  not not_110 (not_110_out, F0);
  not not_111 (not_111_out, F1);
  not not_112 (not_112_out, F2);
  not not_113 (not_113_out, F4);
  not not_114 (not_114_out, F5);
  not not_115 (not_115_out, OP0);
  not not_116 (not_116_out, OP2);
  not not_117 (not_117_out, OP3);
  not not_118 (not_118_out, OP4);
  not not_119 (not_119_out, OP5);
  not not_120 (not_120_out, OP2);
  not not_121 (not_121_out, OP3);
  not not_122 (not_122_out, OP4);
  not not_123 (not_123_out, OP5);
  and and_1 (MemToReg, OP0, OP1, not_1_out, not_2_out, not_3_out, OP5);
  and and_2 (MemWrite, OP0, OP1, not_4_out, OP3, not_5_out, OP5);
  and and_3 (and_3_out, not_6_out, not_7_out, OP3, not_8_out, not_9_out);
  or or_1 (ALU_SRC, and_3_out, and_4_out, and_5_out);
  and and_4 (and_4_out, not_10_out, OP3, not_11_out, not_12_out);
  and and_5 (and_5_out, OP0, OP1, not_13_out, not_14_out, OP5);
  and and_6 (and_6_out, not_15_out, not_16_out, not_17_out, not_18_out, not_19_out, not_20_out, not_21_out, not_22_out, not_23_out);
  and and_7 (and_7_out, not_24_out, not_25_out, not_26_out, not_27_out, not_28_out, not_29_out, not_30_out, not_31_out, F5);
  and and_8 (and_8_out, not_32_out, not_33_out, not_34_out, not_35_out, not_36_out, F1, not_37_out, not_38_out, not_39_out, not_40_out);
  and and_9 (and_9_out, not_41_out, not_42_out, not_43_out, not_44_out, not_45_out, F1, not_46_out, F3, not_47_out, F5);
  and and_10 (and_10_out, not_48_out, not_49_out, not_50_out, not_51_out, not_52_out, F0, F2, not_53_out, not_54_out, F5);
  and and_11 (and_11_out, not_55_out, not_56_out, OP3, not_57_out, not_58_out);
  and and_12 (and_12_out, not_59_out, OP3, not_60_out, not_61_out);
  and and_13 (and_13_out, OP0, OP1, not_62_out, not_63_out, not_64_out);
  and and_14 (SysCALL, not_65_out, not_66_out, not_67_out, not_68_out, not_69_out, not_70_out, not_71_out, not_72_out, F2, F3, not_73_out, not_74_out);
  and and_15 (and_15_out, not_75_out, not_76_out, OP3, not_77_out, not_78_out);
  and and_16 (and_16_out, not_79_out, not_80_out, OP3, not_81_out, not_82_out);
  or or_2 (SignedExt, and_15_out, and_16_out, and_17_out);
  and and_17 (and_17_out, OP0, OP1, not_83_out, not_84_out, OP5);
  and and_18 (and_18_out, not_85_out, not_86_out, OP3, not_87_out, not_88_out);
  and and_19 (and_19_out, not_89_out, OP3, not_90_out, not_91_out);
  and and_20 (and_20_out, OP0, OP1, not_92_out, not_93_out, not_94_out, OP5);
  and and_21 (BEQ, not_95_out, not_96_out, OP2, not_97_out, not_98_out, not_99_out);
  and and_22 (BNE, OP0, not_100_out, OP2, not_101_out, not_102_out, not_103_out);
  and and_23 (JR, not_104_out, not_105_out, not_106_out, not_107_out, not_108_out, not_109_out, not_110_out, not_111_out, not_112_out, F3, not_113_out, not_114_out);
  and and_24 (JMP, not_115_out, OP1, not_116_out, not_117_out, not_118_out, not_119_out);
  and and_25 (JAL, OP0, OP1, not_120_out, not_121_out, not_122_out, not_123_out);
  or or_3 (RegWrite, and_6_out, and_7_out, and_8_out, and_9_out, and_10_out, and_11_out, and_12_out, and_13_out);
  or or_4 (RegDst, and_18_out, and_19_out, and_20_out);
endmodule

// ALU
module MIPS_ALU (
  input  [4:0] shamt,
  input  [31:0] X,
  input  [31:0] Y,
  input  [3:0] AluOP,
  output Equal,
  output [31:0] Result,
  output [31:0] Result_2
);

  wire [0:0] comparator_1_lt, comparator_2_lt;
  wire [31:0] adder_1_out, AND_out, divider_1_out, divider_1_rem, multiplier_1_cout, multiplier_1_out,
       NOR_out, OR_out, shifter_1_out, shifter_2_out, shifter_3_out, subtractor_1_out, XOR_out;

  assign AND_out = X & Y;  // AND_Gate AND, 32 bits wide
  assign OR_out = X | Y;  // OR_Gate OR, 32 bits wide
  Shifter #(.width(32)) shifter_1 (.in(Y), .\dist (shamt), .out(shifter_1_out));
  Shifter #(.width(32), .shift("ar")) shifter_2 (.in(Y), .\dist (shamt), .out(shifter_2_out));
  Shifter #(.width(32), .shift("lr")) shifter_3 (.in(Y), .\dist (shamt), .out(shifter_3_out));
  Multiplier #(.width(32)) multiplier_1 (.a(X), .b(Y), .out(multiplier_1_out), .cout(multiplier_1_cout));  // open: cin
  Divider #(.width(32)) divider_1 (.a(X), .b(Y), .out(divider_1_out), .rem(divider_1_rem));  // open: upper
  Adder #(.width(32)) adder_1 (.a(X), .b(Y), .out(adder_1_out));  // open: cin, cout
  Subtractor #(.width(32)) subtractor_1 (.a(X), .b(Y), .out(subtractor_1_out));  // open: bin, bout
  assign XOR_out = X ^ Y;  // XOR_Gate XOR, 32 bits wide
  assign NOR_out = ~(X | Y);  // NOR_Gate NOR, 32 bits wide
  Comparator #(.width(32)) comparator_1 (.a(X), .b(Y), .eq(Equal), .lt(comparator_1_lt[0]));  // open: gt
  Comparator #(.width(32), .mode("unsigned")) comparator_2 (.a(X), .b(Y), .lt(comparator_2_lt[0]));  // open: gt, eq
  Multiplexer #(.select(4), .width(32), .enable("false")) multiplexer_1 (
    .in0(shifter_1_out), .in1(shifter_2_out), .in2(shifter_3_out), .in3(multiplier_1_out),
    .in4(divider_1_out), .in5(adder_1_out), .in6(subtractor_1_out), .in7(AND_out), .in8(OR_out),
    .in9(XOR_out), .in10(NOR_out), .in11({{31{1'b0}}, comparator_1_lt[0]}),
    .in12({{31{1'b0}}, comparator_2_lt[0]}), .in13({32{1'b0}}), .in14({32{1'b0}}), .in15({32{1'b0}}),
    .out(Result), .sel(AluOP));
  Multiplexer #(.select(4), .width(32), .enable("false")) multiplexer_2 (
    .in0({32{1'b0}}), .in1({32{1'b0}}), .in2({32{1'b0}}), .in3(multiplier_1_cout), .in4(divider_1_rem),
    .in5({32{1'b0}}), .in6({32{1'b0}}), .in7({32{1'b0}}), .in8({32{1'b0}}), .in9({32{1'b0}}),
    .in10({32{1'b0}}), .in11({32{1'b0}}), .in12({32{1'b0}}), .in13({32{1'b0}}), .in14({32{1'b0}}),
    .in15({32{1'b0}}), .out(Result_2), .sel(AluOP));

  // Other names for the same wires on the sheet: Result2[31:0] = Result_2; S[3:0] = AluOP

  // Notes on the sheet:
  //   不要改变此引脚区域内容，也不要改变ALU封装形式
  //   输入引脚
  //   输出引脚
endmodule

module MIPS_Regifile (
  input  [31:0] Din,
  input  Clk,
  input  WE,
  input  [4:0] R1_num,
  input  [4:0] W_num,
  input  [4:0] R2_num,
  output [31:0] R1,
  output [31:0] R2
);

  // RegisterFile registerfile_1: pin names not known; wires that end beside it: Din, Clk, WE, W_num, R1_num, R2_num, R1, R2
endmodule

module \_5段理想流水线MIPS  (
);

  wire CLK, comparator_1_eq, Go, mips_alu_1_equal, not_1_out, not_2_out, not_3_out, pause, RST, sys_show,
       syscall;
  wire [3:0] \硬布线控制器_1_alu_op ;
  wire [4:0] multiplexer_1_out, multiplexer_2_out, multiplexer_6_out;
  wire [10:0] \硬布线控制器_1_signedext ;
  wire [15:0] \总周期数 , \无条件分支数 , \条件分支成功数 , \流水部件_2_ir_2 , \流水部件_2_控制信号_2 , \流水部件_3_控制信号_2 , \流水部件_4_控制信号_2 ;
  wire [31:0] a0, adder_1_out, adder_2_out, bit_extender_1_out, bit_extender_2_out, LedData,
       mips_alu_1_result, mips_regifile_1_r1, mips_regifile_1_r2, multiplexer_3_out, multiplexer_4_out,
       multiplexer_5_out, PC_q, ram_1_data, rom_1_data, \流水部件_1_ir_2 , \流水部件_1_pc_2 , \流水部件_2_pc_2 ,
       \流水部件_2_r1_2 , \流水部件_3_ir_2 , \流水部件_3_r1_2 , \流水部件_3_r2_2 , \流水部件_4_ir_2 , \流水部件_4_r1_2 ;
  wire [31:16] \流水部件_2_ir_2_2 ;

  Button \u_总复位  (.out(RST));
  Button u_Go (.out(Go));
  Clock clock_1 (.out(CLK));
  not not_1 (not_1_out, syscall);
  Register #(.width(32)) PC (.D(adder_1_out), .en(not_1_out), .Q(PC_q), .clk(CLK), .clr(RST));
  Hex_Digit_Display hex_digit_display_1 (.value(LedData[31:28]));  // open: dp
  Hex_Digit_Display hex_digit_display_2 (.value(LedData[27:24]));  // open: dp
  Hex_Digit_Display hex_digit_display_3 (.value(LedData[23:20]));  // open: dp
  Hex_Digit_Display hex_digit_display_4 (.value(LedData[19:16]));  // open: dp
  Adder #(.width(32)) adder_1 (.a(PC_q), .b(32'h4), .out(adder_1_out));  // open: cin, cout
  Hex_Digit_Display hex_digit_display_5 (.value(LedData[15:12]));  // open: dp
  Hex_Digit_Display hex_digit_display_6 (.value(LedData[11:8]));  // open: dp
  ROM #(.addrWidth(10), .dataWidth(32)) rom_1 (.addr(PC_q[11:2]), .data(rom_1_data));  // open: sel
  not not_2 (not_2_out, syscall);
  Hex_Digit_Display hex_digit_display_7 (.value(LedData[7:4]));  // open: dp
  Hex_Digit_Display hex_digit_display_8 (.value(LedData[3:0]));  // open: dp
  \流水部件  \u_流水部件_1  (
    .PC(adder_1_out), .IR(rom_1_data), .enable(not_2_out), .clk(CLK), .PC_2(\流水部件_1_pc_2 ),
    .IR_2(\流水部件_1_ir_2 ));  // open: 控制信号, R1, R2, Valid_Bit, sync_cls, 控制信号_2, R1_2, R2_2, Valid_Bit_2
  // Probe on \总周期数 
  // Probe on \无条件分支数 
  // Probe on \条件分支成功数 
  Multiplexer #(.width(5)) multiplexer_1 (
    .in0(\流水部件_1_ir_2 [25:21]), .in1(5'b00010), .out(multiplexer_1_out), .sel(syscall));  // open: en
  Multiplexer #(.width(5)) multiplexer_2 (
    .in0(\流水部件_1_ir_2 [20:16]), .in1(5'b00100), .out(multiplexer_2_out), .sel(syscall));  // open: en
  assign bit_extender_1_out = {{14{\流水部件_1_ir_2 [15]}}, {\流水部件_1_ir_2 [15:0], 2'b00}};  // Bit_Extender bit_extender_1
  \硬布线控制器  \u_硬布线控制器_1  (
    .Func(\流水部件_1_ir_2 [5:0]), .OP(\流水部件_1_ir_2 [31:26]), .ALU_OP(\硬布线控制器_1_alu_op ),
    .MemToReg(\硬布线控制器_1_signedext [1]), .MemWrite(\硬布线控制器_1_signedext [2]),
    .ALU_SRC(\硬布线控制器_1_signedext [7]), .RegWrite(\硬布线控制器_1_signedext [8]), .SysCALL(syscall),
    .SignedExt(\硬布线控制器_1_signedext [0]), .RegDst(\硬布线控制器_1_signedext [9]), .JAL(\硬布线控制器_1_signedext [10]));  // open: JR, JMP, Beq, Bne
  MIPS_Regifile mips_regifile_1 (
    .Din(\流水部件_4_r1_2 ), .Clk(CLK), .R1(mips_regifile_1_r1), .R2(mips_regifile_1_r2),
    .WE(\流水部件_4_控制信号_2 [8]), .W_num(multiplexer_6_out), .R1_num(multiplexer_1_out), .R2_num(multiplexer_2_out));
  Adder #(.width(32)) adder_2 (.a(bit_extender_1_out), .b(\流水部件_1_pc_2 ), .out(adder_2_out));  // open: cin, cout
  Register #(.width(32)) register_1 (.D(a0), .en(sys_show), .Q(LedData), .clk(CLK), .clr(RST));
  \流水部件  \u_流水部件_2  (
    .\控制信号 ({{5{1'b0}}, \硬布线控制器_1_signedext [10:7], \硬布线控制器_1_alu_op , \硬布线控制器_1_signedext [2:0]}),
    .PC(\流水部件_1_pc_2 ), .IR(\流水部件_1_ir_2 ), .R1(mips_regifile_1_r1), .R2(mips_regifile_1_r2), .clk(CLK),
    .\控制信号_2 (\流水部件_2_控制信号_2 ), .PC_2(\流水部件_2_pc_2 ), .IR_2({\流水部件_2_ir_2_2 , \流水部件_2_ir_2 }),
    .R1_2(\流水部件_2_r1_2 ), .R2_2(a0));  // open: Valid_Bit, sync_cls, enable, Valid_Bit_2
  and and_1 (pause, syscall, not_3_out);
  Comparator #(.width(32)) comparator_1 (.a(32'h22), .b(\流水部件_2_r1_2 ), .eq(comparator_1_eq));  // open: gt, lt
  assign bit_extender_2_out = {{16{\流水部件_2_ir_2 [15]}}, \流水部件_2_ir_2 };  // Bit_Extender bit_extender_2
  and and_2 (sys_show, syscall, comparator_1_eq);
  not not_3 (not_3_out, comparator_1_eq);
  Multiplexer #(.width(32)) multiplexer_3 (
    .in0({{16{1'b0}}, \流水部件_2_ir_2 }), .in1(bit_extender_2_out), .out(multiplexer_3_out),
    .sel(\流水部件_2_控制信号_2 [0]));  // open: en
  Multiplexer #(.width(32)) multiplexer_4 (
    .in0(a0), .in1(multiplexer_3_out), .out(multiplexer_4_out), .sel(\流水部件_2_控制信号_2 [7]));  // open: en
  MIPS_ALU mips_alu_1 (
    .X(\流水部件_2_r1_2 ), .Y(multiplexer_4_out), .AluOP(\流水部件_2_控制信号_2 [6:3]), .Equal(mips_alu_1_equal),
    .Result(mips_alu_1_result), .shamt(\流水部件_2_ir_2 [10:6]));  // open: Result_2
  \流水部件  \u_流水部件_3  (
    .\控制信号 (\流水部件_2_控制信号_2 ), .PC(\流水部件_2_pc_2 ), .IR({\流水部件_2_ir_2_2 , \流水部件_2_ir_2 }),
    .R1(mips_alu_1_result), .R2(a0), .clk(CLK), .\控制信号_2 (\流水部件_3_控制信号_2 ), .IR_2(\流水部件_3_ir_2 ),
    .R1_2(\流水部件_3_r1_2 ), .R2_2(\流水部件_3_r2_2 ));  // open: Valid_Bit, sync_cls, enable, PC_2, Valid_Bit_2
  RAM #(.addrWidth(10), .dataWidth(32), .bus("separate")) ram_1 (
    .addr(\流水部件_3_r1_2 [11:2]), .din(\流水部件_3_r2_2 ), .data(ram_1_data), .str(\流水部件_3_控制信号_2 [2]), .clk(CLK),
    .clr(RST));  // open: sel, ld
  Multiplexer #(.width(32)) multiplexer_5 (
    .in0(\流水部件_3_r1_2 ), .in1(ram_1_data), .out(multiplexer_5_out), .sel(\流水部件_3_控制信号_2 [1]));  // open: en
  \流水部件  \u_流水部件_4  (
    .\控制信号 (\流水部件_3_控制信号_2 ), .IR(\流水部件_3_ir_2 ), .R1(multiplexer_5_out), .clk(CLK),
    .\控制信号_2 (\流水部件_4_控制信号_2 ), .IR_2(\流水部件_4_ir_2 ), .R1_2(\流水部件_4_r1_2 ));  // open: PC, R2, Valid_Bit, sync_cls, enable, PC_2, R2_2, Valid_Bit_2
  Multiplexer #(.width(5)) multiplexer_6 (
    .in0(\流水部件_4_ir_2 [15:11]), .in1(\流水部件_4_ir_2 [20:16]), .out(multiplexer_6_out), .sel(\流水部件_4_控制信号_2 [9]));  // open: en
  // Probe on nothing
  // Probe on nothing

  // Notes on the sheet:
  //   数码管输出应该用寄存器锁存，否则显示数据只能一闪而过
  //   可以通过项目增加Logisim库的方式将前几次实验完成的电路作为子电路引入到本电路中使用
  //   指令存储器
  //   contents of rom_1 (hex, n*v repeats v):
  //   20100000 20110000 20120000 20130000 36100000 36310001 36520002 36730003 ae100000 ae110004 ae120008
  //   ae13000c 2002000a 20110000 20120000 20130000 c
  //   数码管输出
  //   OP
  //   Func
  //   rs
  //   rt
  //   rd
  //   shamt
  //   imm
  //   addr
  //   总复位信号应将除ROM以外所有存储组件全部清零
  //   JMP
  //   JMP
  //   JR
  //   SignedExt
  //   OP
  //   Func
  //   Beq
  //   Bne
  //   MemToReg
  //   MemWrite
  //   AluOP
  //   AluSrcB
  //   RegWrite
  //   JAL
  //   RegDst
  //   Syscall
  //   Branch
  //   JR
  //   shamt
  //   imm
  //   AluSrcB
  //   MemToReg
  //   rt
  //   rd
  //   RegDst
endmodule

module \流水部件  (
  input  sync_cls,
  input  [15:0] \控制信号 ,
  input  [31:0] PC,
  input  [31:0] IR,
  input  [31:0] R1,
  input  [31:0] R2,
  input  Valid_Bit,
  input  enable,
  input  clk,
  output [15:0] \控制信号_2 ,
  output [31:0] PC_2,
  output [31:0] IR_2,
  output [31:0] R1_2,
  output [31:0] R2_2,
  output Valid_Bit_2
);

  wire multiplexer_6_out;
  wire [15:0] multiplexer_1_out;
  wire [31:0] multiplexer_2_out, multiplexer_3_out, multiplexer_4_out, multiplexer_5_out;

  Pull_Resistor pull_resistor_1 (.node(sync_cls));
  Pull_Resistor #(.pull(1)) pull_resistor_2 (.node(enable));
  Multiplexer #(.width(16)) multiplexer_1 (
    .in0(\控制信号 ), .in1({16{1'b0}}), .out(multiplexer_1_out), .sel(sync_cls));  // open: en
  Multiplexer #(.width(32)) multiplexer_2 (
    .in0(PC), .in1({32{1'b0}}), .out(multiplexer_2_out), .sel(sync_cls));  // open: en
  Multiplexer #(.width(32)) multiplexer_3 (
    .in0(IR), .in1({32{1'b0}}), .out(multiplexer_3_out), .sel(sync_cls));  // open: en
  Multiplexer #(.width(32)) multiplexer_4 (
    .in0(R1), .in1({32{1'b0}}), .out(multiplexer_4_out), .sel(sync_cls));  // open: en
  Multiplexer #(.width(32)) multiplexer_5 (
    .in0(R2), .in1({32{1'b0}}), .out(multiplexer_5_out), .sel(sync_cls));  // open: en
  Multiplexer multiplexer_6 (.in0(Valid_Bit), .in1(1'b0), .out(multiplexer_6_out), .sel(sync_cls));  // open: en
  Register #(.width(16)) register_1 (.D(multiplexer_1_out), .en(enable), .Q(\控制信号_2 ), .clk(clk));  // open: clr
  Register #(.width(32)) register_2 (.D(multiplexer_2_out), .en(enable), .Q(PC_2), .clk(clk));  // open: clr
  Register #(.width(32)) register_3 (.D(multiplexer_3_out), .en(enable), .Q(IR_2), .clk(clk));  // open: clr
  Register #(.width(32)) register_4 (.D(multiplexer_4_out), .en(enable), .Q(R1_2), .clk(clk));  // open: clr
  Register #(.width(32)) register_5 (.D(multiplexer_5_out), .en(enable), .Q(R2_2), .clk(clk));  // open: clr
  Register #(.width(1)) register_6 (.D(multiplexer_6_out), .en(enable), .Q(Valid_Bit_2), .clk(clk));  // open: clr
endmodule

module \_5段分支相关流水线MIPS  (
);

  wire and_3_out, and_4_out, and_5_out, and_6_out, BEQ, BNE, branch, CLK, comparator_1_eq, Go, JAL, JAL_WB,
       JMP, jmp_or_branch, JR, mips_alu_1_equal, not_1_out, not_2_out, not_3_out, not_4_out, not_5_out,
       not_6_out, not_7_out, or_1_out, or_2_out, pause, RST, sys_show, syscall;
  wire [3:0] \硬布线控制器_1_alu_op ;
  wire [4:0] multiplexer_4_out, multiplexer_5_out, multiplexer_10_out, multiplexer_11_out;
  wire [14:0] \硬布线控制器_1_signedext ;
  wire [15:0] \总周期数 , \无条件分支数 , \条件分支成功数 , \流水部件_2_控制信号_2 , \流水部件_3_控制信号_2 , \流水部件_4_控制信号_2 ;
  wire [27:0] \流水部件_2_pc_2 ;
  wire [31:0] a0, adder_1_out, bit_extender_1_out, bit_extender_2_out, branch_addr, jr_addr, LedData,
       mips_alu_1_result, mips_regifile_1_r1, multiplexer_1_out, multiplexer_2_out, multiplexer_3_out,
       multiplexer_6_out, multiplexer_7_out, multiplexer_8_out, multiplexer_9_out, PC_q, ram_1_data,
       rom_1_data, \流水部件_1_ir_2 , \流水部件_1_pc_2 , \流水部件_2_r2_2 , \流水部件_3_ir_2 , \流水部件_3_pc_2 , \流水部件_3_r1_2 ,
       \流水部件_3_r2_2 , \流水部件_4_ir_2 , \流水部件_4_pc_2 , \流水部件_4_r1_2 ;
  wire [31:2] jmp_addr;
  wire [31:26] \流水部件_2_ir_2 ;

  Button \u_总复位  (.out(RST));
  Button u_Go (.out(Go));
  Clock clock_1 (.out(CLK));
  Multiplexer #(.width(32)) multiplexer_1 (
    .in0(adder_1_out), .in1(jr_addr), .out(multiplexer_1_out), .sel(JR));  // open: en
  Multiplexer #(.width(32)) multiplexer_2 (
    .in0(multiplexer_1_out), .in1({jmp_addr, 2'b00}), .out(multiplexer_2_out), .sel(or_1_out));  // open: en
  not not_1 (not_1_out, pause);
  Register #(.width(32)) PC (.D(multiplexer_3_out), .en(not_1_out), .Q(PC_q), .clk(CLK), .clr(RST));
  Hex_Digit_Display hex_digit_display_1 (.value(LedData[31:28]));  // open: dp
  Hex_Digit_Display hex_digit_display_2 (.value(LedData[27:24]));  // open: dp
  not not_2 (not_2_out, pause);
  or or_1 (or_1_out, JAL, JMP);
  Multiplexer #(.width(32)) multiplexer_3 (
    .in0(multiplexer_2_out), .in1(branch_addr), .out(multiplexer_3_out), .sel(branch));  // open: en
  Hex_Digit_Display hex_digit_display_3 (.value(LedData[23:20]));  // open: dp
  Hex_Digit_Display hex_digit_display_4 (.value(LedData[19:16]));  // open: dp
  Counter #(.width(16), .max('hffff)) counter_1 (
    .count(not_2_out), .Q(\总周期数 ), .clk(CLK), .clr(RST));  // open: load, D, carry
  Adder #(.width(32)) adder_1 (.a(PC_q), .b(32'h4), .out(adder_1_out));  // open: cin, cout
  Hex_Digit_Display hex_digit_display_5 (.value(LedData[15:12]));  // open: dp
  Hex_Digit_Display hex_digit_display_6 (.value(LedData[11:8]));  // open: dp
  ROM #(.addrWidth(10), .dataWidth(32)) rom_1 (.addr(PC_q[11:2]), .data(rom_1_data));  // open: sel
  or or_2 (or_2_out, RST, not_3_out);
  not not_3 (not_3_out, pause);
  Hex_Digit_Display hex_digit_display_7 (.value(LedData[7:4]));  // open: dp
  Hex_Digit_Display hex_digit_display_8 (.value(LedData[3:0]));  // open: dp
  \流水部件  \u_流水部件_1  (
    .PC(adder_1_out), .IR(rom_1_data), .sync_cls(jmp_or_branch), .enable(or_2_out), .clk(CLK),
    .PC_2(\流水部件_1_pc_2 ), .IR_2(\流水部件_1_ir_2 ));  // open: 控制信号, R1, R2, Valid_Bit, 控制信号_2, R1_2, R2_2, Valid_Bit_2
  // Probe on \总周期数 
  // Probe on \无条件分支数 
  // Probe on \条件分支成功数 
  Multiplexer #(.width(5)) multiplexer_4 (
    .in0(\流水部件_1_ir_2 [25:21]), .in1(5'b00010), .out(multiplexer_4_out), .sel(syscall));  // open: en
  Multiplexer #(.width(5)) multiplexer_5 (
    .in0(\流水部件_1_ir_2 [20:16]), .in1(5'b00100), .out(multiplexer_5_out), .sel(syscall));  // open: en
  \硬布线控制器  \u_硬布线控制器_1  (
    .Func(\流水部件_1_ir_2 [5:0]), .OP(\流水部件_1_ir_2 [31:26]), .ALU_OP(\硬布线控制器_1_alu_op ),
    .MemToReg(\硬布线控制器_1_signedext [1]), .MemWrite(\硬布线控制器_1_signedext [2]),
    .ALU_SRC(\硬布线控制器_1_signedext [7]), .RegWrite(\硬布线控制器_1_signedext [8]), .SysCALL(syscall),
    .SignedExt(\硬布线控制器_1_signedext [0]), .RegDst(\硬布线控制器_1_signedext [9]), .JR(\硬布线控制器_1_signedext [13]),
    .JMP(\硬布线控制器_1_signedext [14]), .Beq(\硬布线控制器_1_signedext [12]), .JAL(\硬布线控制器_1_signedext [10]),
    .Bne(\硬布线控制器_1_signedext [11]));
  MIPS_Regifile mips_regifile_1 (
    .Din(multiplexer_9_out), .Clk(CLK), .R1(mips_regifile_1_r1), .R2(a0), .WE(\流水部件_4_控制信号_2 [8]),
    .W_num(multiplexer_11_out), .R1_num(multiplexer_4_out), .R2_num(multiplexer_5_out));
  and and_1 (pause, syscall, not_4_out);
  not not_4 (not_4_out, comparator_1_eq);
  Comparator #(.width(32)) comparator_1 (.a(32'h22), .b(mips_regifile_1_r1), .eq(comparator_1_eq));  // open: gt, lt
  and and_2 (sys_show, syscall, comparator_1_eq);
  Register #(.width(32)) register_1 (.D(a0), .en(sys_show), .Q(LedData), .clk(CLK), .clr(RST));
  \流水部件  \u_流水部件_2  (
    .\控制信号 ({1'b0, \硬布线控制器_1_signedext [14:7], \硬布线控制器_1_alu_op , \硬布线控制器_1_signedext [2:0]}),
    .PC(\流水部件_1_pc_2 ), .IR(\流水部件_1_ir_2 ), .R1(mips_regifile_1_r1), .R2(a0), .sync_cls(jmp_or_branch),
    .clk(CLK), .\控制信号_2 ({\流水部件_2_控制信号_2 [15], JMP, JR, BEQ, BNE, JAL, \流水部件_2_控制信号_2 [9:0]}),
    .PC_2({jmp_addr[31:28], \流水部件_2_pc_2 }), .IR_2({\流水部件_2_ir_2 , jmp_addr[27:2]}), .R1_2(jr_addr),
    .R2_2(\流水部件_2_r2_2 ));  // open: Valid_Bit, enable, Valid_Bit_2
  and and_3 (and_3_out, jmp_or_branch, not_5_out);
  not not_5 (not_5_out, branch);
  assign bit_extender_1_out = {{14{jmp_addr[17]}}, {jmp_addr[17:2], 2'b00}};  // Bit_Extender bit_extender_1
  assign bit_extender_2_out = {{16{jmp_addr[17]}}, jmp_addr[17:2]};  // Bit_Extender bit_extender_2
  Counter #(.width(16), .max('hffff)) counter_2 (
    .count(and_3_out), .Q(\无条件分支数 ), .clk(CLK), .clr(RST));  // open: load, D, carry
  Adder #(.width(32)) adder_2 (
    .a(bit_extender_1_out), .b({jmp_addr[31:28], \流水部件_2_pc_2 }), .out(branch_addr));  // open: cin, cout
  Multiplexer #(.width(32)) multiplexer_6 (
    .in0({{16{1'b0}}, jmp_addr[17:2]}), .in1(bit_extender_2_out), .out(multiplexer_6_out),
    .sel(\流水部件_2_控制信号_2 [0]));  // open: en
  and and_4 (and_4_out, branch, not_6_out);
  not not_6 (not_6_out, pause);
  Multiplexer #(.width(32)) multiplexer_7 (
    .in0(\流水部件_2_r2_2 ), .in1(multiplexer_6_out), .out(multiplexer_7_out), .sel(\流水部件_2_控制信号_2 [7]));  // open: en
  Counter #(.width(16), .max('hffff)) counter_3 (
    .count(and_4_out), .Q(\条件分支成功数 ), .clk(CLK), .clr(RST));  // open: load, D, carry
  or or_3 (jmp_or_branch, JAL, JMP, JR, branch);
  or or_4 (branch, and_6_out, and_5_out);
  and and_5 (and_5_out, mips_alu_1_equal, BEQ);
  and and_6 (and_6_out, BNE, not_7_out);
  not not_7 (not_7_out, mips_alu_1_equal);
  MIPS_ALU mips_alu_1 (
    .X(jr_addr), .Y(multiplexer_7_out), .AluOP(\流水部件_2_控制信号_2 [6:3]), .Equal(mips_alu_1_equal),
    .Result(mips_alu_1_result), .shamt(jmp_addr[12:8]));  // open: Result_2
  \流水部件  \u_流水部件_3  (
    .\控制信号 ({\流水部件_2_控制信号_2 [15], JMP, JR, BEQ, BNE, JAL, \流水部件_2_控制信号_2 [9:0]}),
    .PC({jmp_addr[31:28], \流水部件_2_pc_2 }), .IR({\流水部件_2_ir_2 , jmp_addr[27:2]}), .R1(mips_alu_1_result),
    .R2(\流水部件_2_r2_2 ), .clk(CLK), .\控制信号_2 (\流水部件_3_控制信号_2 ), .PC_2(\流水部件_3_pc_2 ), .IR_2(\流水部件_3_ir_2 ),
    .R1_2(\流水部件_3_r1_2 ), .R2_2(\流水部件_3_r2_2 ));  // open: Valid_Bit, sync_cls, enable, Valid_Bit_2
  RAM #(.addrWidth(10), .dataWidth(32), .bus("separate")) ram_1 (
    .addr(\流水部件_3_r1_2 [11:2]), .din(\流水部件_3_r2_2 ), .data(ram_1_data), .str(\流水部件_3_控制信号_2 [2]), .clk(CLK),
    .clr(RST));  // open: sel, ld
  Multiplexer #(.width(32)) multiplexer_8 (
    .in0(\流水部件_3_r1_2 ), .in1(ram_1_data), .out(multiplexer_8_out), .sel(\流水部件_3_控制信号_2 [1]));  // open: en
  \流水部件  \u_流水部件_4  (
    .\控制信号 (\流水部件_3_控制信号_2 ), .PC(\流水部件_3_pc_2 ), .IR(\流水部件_3_ir_2 ), .R1(multiplexer_8_out), .clk(CLK),
    .\控制信号_2 ({\流水部件_4_控制信号_2 [15:11], JAL_WB, \流水部件_4_控制信号_2 [9:0]}), .PC_2(\流水部件_4_pc_2 ),
    .IR_2(\流水部件_4_ir_2 ), .R1_2(\流水部件_4_r1_2 ));  // open: R2, Valid_Bit, sync_cls, enable, R2_2, Valid_Bit_2
  Multiplexer #(.width(32)) multiplexer_9 (
    .in0(\流水部件_4_r1_2 ), .in1(\流水部件_4_pc_2 ), .out(multiplexer_9_out), .sel(JAL_WB));  // open: en
  Multiplexer #(.width(5)) multiplexer_10 (
    .in0(\流水部件_4_ir_2 [15:11]), .in1(\流水部件_4_ir_2 [20:16]), .out(multiplexer_10_out), .sel(\流水部件_4_控制信号_2 [9]));  // open: en
  // Probe on nothing
  Multiplexer #(.width(5)) multiplexer_11 (
    .in0(multiplexer_10_out), .in1({5{1'b1}}), .out(multiplexer_11_out), .sel(JAL_WB));  // open: en
  // Probe on nothing

  // Notes on the sheet:
  //   数码管输出应该用寄存器锁存，否则显示数据只能一闪而过
  //   可以通过项目增加Logisim库的方式将前几次实验完成的电路作为子电路引入到本电路中使用
  //   指令存储器
  //   contents of rom_1 (hex, n*v repeats v):
  //   20110020 20020022 8000006 20110004 20120005 20130006 10000003 20110007 20120008 20130009 14110003
  //   2011000a 2012000b 2013000c c000014 2002000a 0 0 0 c 2231ffff 0 0 0 112020 0 0 0 c 1620fff6 3e00008
  //   数码管输出
  //   OP
  //   Func
  //   rs
  //   rt
  //   总复位信号应将除ROM以外所有存储组件全部清零
  //   JMP
  //   JR
  //   SignedExt
  //   OP
  //   Func
  //   Beq
  //   Bne
  //   MemToReg
  //   MemWrite
  //   AluOP
  //   AluSrcB
  //   RegWrite
  //   JAL
  //   RegDst
  //   Syscall
  //   addr
  //   imm
  //   shamt
  //   imm
  //   AluSrcB
  //   MemToReg
  //   rt
  //   rd
  //   RegDst
endmodule

module \数据相关流水线  (
);

  wire and_3_out, and_4_out, and_5_out, and_6_out, BEQ, BNE, branch, CLK, comparator_1_eq, EX_RegWrite, Go,
       JAL, JAL_WB, JMP, jmp_or_branch, JR, Mem_RegWrite, mips_alu_1_equal, not_1_out, not_2_out, not_3_out,
       not_4_out, not_5_out, not_6_out, not_7_out, or_1_out, or_2_out, or_3_out, or_4_out, or_5_out, pause,
       pipeline_pause, r1_used, r2_used, RST, sys_show, syscall;
  wire [3:0] \硬布线控制器_1_alu_op ;
  wire [4:0] EX_WriteDst, Mem_WriteDst, multiplexer_12_out, multiplexer_13_out, R1_num, R2_num;
  wire [14:0] \硬布线控制器_1_signedext ;
  wire [15:0] \总周期数 , \插入气泡数 , \无条件分支数 , \条件分支成功数 , \流水部件_2_控制信号_2 , \流水部件_3_控制信号_2 , \流水部件_4_控制信号_2 ;
  wire [27:0] \流水部件_2_pc_2 ;
  wire [31:0] a0, adder_1_out, bit_extender_1_out, bit_extender_2_out, branch_addr, jr_addr, LedData,
       mips_alu_1_result, mips_regifile_1_r1, multiplexer_1_out, multiplexer_2_out, multiplexer_3_out,
       multiplexer_7_out, multiplexer_8_out, multiplexer_10_out, multiplexer_11_out, PC_q, ram_1_data,
       rom_1_data, \流水部件_1_ir_2 , \流水部件_1_pc_2 , \流水部件_2_r2_2 , \流水部件_3_ir_2 , \流水部件_3_pc_2 , \流水部件_3_r1_2 ,
       \流水部件_3_r2_2 , \流水部件_4_ir_2 , \流水部件_4_pc_2 , \流水部件_4_r1_2 ;
  wire [31:2] jmp_addr;
  wire [31:26] \流水部件_2_ir_2 ;

  Button \u_总复位  (.out(RST));
  Button u_Go (.out(Go));
  Clock clock_1 (.out(CLK));
  Multiplexer #(.width(32)) multiplexer_1 (
    .in0(adder_1_out), .in1(jr_addr), .out(multiplexer_1_out), .sel(JR));  // open: en
  Multiplexer #(.width(32)) multiplexer_2 (
    .in0(multiplexer_1_out), .in1({jmp_addr, 2'b00}), .out(multiplexer_2_out), .sel(or_2_out));  // open: en
  or or_1 (or_1_out, pause, pipeline_pause);
  not not_1 (not_1_out, or_1_out);
  Register #(.width(32)) PC (.D(multiplexer_3_out), .en(not_1_out), .Q(PC_q), .clk(CLK), .clr(RST));
  Hex_Digit_Display hex_digit_display_1 (.value(LedData[31:28]));  // open: dp
  Hex_Digit_Display hex_digit_display_2 (.value(LedData[27:24]));  // open: dp
  not not_2 (not_2_out, pause);
  or or_2 (or_2_out, JAL, JMP);
  Multiplexer #(.width(32)) multiplexer_3 (
    .in0(multiplexer_2_out), .in1(branch_addr), .out(multiplexer_3_out), .sel(branch));  // open: en
  Hex_Digit_Display hex_digit_display_3 (.value(LedData[19:16]));  // open: dp
  Hex_Digit_Display hex_digit_display_4 (.value(LedData[23:20]));  // open: dp
  Counter #(.width(16), .max('hffff)) counter_1 (
    .count(not_2_out), .Q(\总周期数 ), .clk(CLK), .clr(RST));  // open: load, D, carry
  Adder #(.width(32)) adder_1 (.a(PC_q), .b(32'h4), .out(adder_1_out));  // open: cin, cout
  Hex_Digit_Display hex_digit_display_5 (.value(LedData[15:12]));  // open: dp
  Hex_Digit_Display hex_digit_display_6 (.value(LedData[11:8]));  // open: dp
  ROM #(.addrWidth(10), .dataWidth(32)) rom_1 (.addr(PC_q[11:2]), .data(rom_1_data));  // open: sel
  or or_3 (or_3_out, RST, not_3_out);
  not not_3 (not_3_out, or_4_out);
  or or_4 (or_4_out, pause, pipeline_pause);
  Hex_Digit_Display hex_digit_display_7 (.value(LedData[7:4]));  // open: dp
  Hex_Digit_Display hex_digit_display_8 (.value(LedData[3:0]));  // open: dp
  \流水部件  \u_流水部件_1  (
    .PC(adder_1_out), .IR(rom_1_data), .sync_cls(jmp_or_branch), .enable(or_3_out), .clk(CLK),
    .PC_2(\流水部件_1_pc_2 ), .IR_2(\流水部件_1_ir_2 ));  // open: 控制信号, R1, R2, Valid_Bit, 控制信号_2, R1_2, R2_2, Valid_Bit_2
  \源寄存器使用情况  \u_源寄存器使用情况_1  (
    .func(\流水部件_1_ir_2 [5:0]), .opcode(\流水部件_1_ir_2 [31:26]), .R1_USED(r1_used), .R2_USED(r2_used));
  // Probe on \总周期数 
  // Probe on \无条件分支数 
  // Probe on \条件分支成功数 
  // Probe on \插入气泡数 
  Multiplexer #(.width(5)) multiplexer_4 (
    .in0(\流水部件_1_ir_2 [25:21]), .in1(5'b00010), .out(R1_num), .sel(syscall));  // open: en
  Multiplexer #(.width(5)) multiplexer_5 (
    .in0(\流水部件_1_ir_2 [20:16]), .in1(5'b00100), .out(R2_num), .sel(syscall));  // open: en
  \硬布线控制器  \u_硬布线控制器_1  (
    .Func(\流水部件_1_ir_2 [5:0]), .OP(\流水部件_1_ir_2 [31:26]), .ALU_OP(\硬布线控制器_1_alu_op ),
    .MemToReg(\硬布线控制器_1_signedext [1]), .MemWrite(\硬布线控制器_1_signedext [2]),
    .ALU_SRC(\硬布线控制器_1_signedext [7]), .RegWrite(\硬布线控制器_1_signedext [8]), .SysCALL(syscall),
    .SignedExt(\硬布线控制器_1_signedext [0]), .RegDst(\硬布线控制器_1_signedext [9]), .JR(\硬布线控制器_1_signedext [13]),
    .JMP(\硬布线控制器_1_signedext [14]), .Beq(\硬布线控制器_1_signedext [12]), .JAL(\硬布线控制器_1_signedext [10]),
    .Bne(\硬布线控制器_1_signedext [11]));
  MIPS_Regifile mips_regifile_1 (
    .Din(multiplexer_11_out), .Clk(CLK), .R1(mips_regifile_1_r1), .R2(a0), .WE(\流水部件_4_控制信号_2 [8]),
    .W_num(multiplexer_13_out), .R1_num(R1_num), .R2_num(R2_num));
  and and_1 (pause, syscall, not_4_out);
  not not_4 (not_4_out, comparator_1_eq);
  Comparator #(.width(32)) comparator_1 (.a(32'h22), .b(mips_regifile_1_r1), .eq(comparator_1_eq));  // open: gt, lt
  and and_2 (sys_show, syscall, comparator_1_eq);
  Register #(.width(32)) register_1 (.D(a0), .en(sys_show), .Q(LedData), .clk(CLK), .clr(RST));
  Counter #(.width(16), .max('hffff)) counter_2 (
    .count(pipeline_pause), .Q(\插入气泡数 ), .clk(CLK), .clr(RST));  // open: load, D, carry
  or or_5 (or_5_out, jmp_or_branch, pipeline_pause);
  \流水部件  \u_流水部件_2  (
    .\控制信号 ({1'b0, \硬布线控制器_1_signedext [14:7], \硬布线控制器_1_alu_op , \硬布线控制器_1_signedext [2:0]}),
    .PC(\流水部件_1_pc_2 ), .IR(\流水部件_1_ir_2 ), .R1(mips_regifile_1_r1), .R2(a0), .sync_cls(or_5_out), .clk(CLK),
    .\控制信号_2 ({\流水部件_2_控制信号_2 [15], JMP, JR, BEQ, BNE, JAL, \流水部件_2_控制信号_2 [9], EX_RegWrite, \流水部件_2_控制信号_2 [7:0]}),
    .PC_2({jmp_addr[31:28], \流水部件_2_pc_2 }), .IR_2({\流水部件_2_ir_2 , jmp_addr[27:2]}), .R1_2(jr_addr),
    .R2_2(\流水部件_2_r2_2 ));  // open: Valid_Bit, enable, Valid_Bit_2
  and and_3 (and_3_out, jmp_or_branch, not_5_out);
  not not_5 (not_5_out, branch);
  assign bit_extender_1_out = {{14{jmp_addr[17]}}, {jmp_addr[17:2], 2'b00}};  // Bit_Extender bit_extender_1
  assign bit_extender_2_out = {{16{jmp_addr[17]}}, jmp_addr[17:2]};  // Bit_Extender bit_extender_2
  Counter #(.width(16), .max('hffff)) counter_3 (
    .count(and_3_out), .Q(\无条件分支数 ), .clk(CLK), .clr(RST));  // open: load, D, carry
  Adder #(.width(32)) adder_2 (
    .a(bit_extender_1_out), .b({jmp_addr[31:28], \流水部件_2_pc_2 }), .out(branch_addr));  // open: cin, cout
  Multiplexer #(.width(5)) multiplexer_6 (
    .in0(jmp_addr[17:13]), .in1(jmp_addr[22:18]), .out(EX_WriteDst), .sel(\流水部件_2_控制信号_2 [9]));  // open: en
  Multiplexer #(.width(32)) multiplexer_7 (
    .in0({{16{1'b0}}, jmp_addr[17:2]}), .in1(bit_extender_2_out), .out(multiplexer_7_out),
    .sel(\流水部件_2_控制信号_2 [0]));  // open: en
  and and_4 (and_4_out, branch, not_6_out);
  not not_6 (not_6_out, pause);
  Multiplexer #(.width(32)) multiplexer_8 (
    .in0(\流水部件_2_r2_2 ), .in1(multiplexer_7_out), .out(multiplexer_8_out), .sel(\流水部件_2_控制信号_2 [7]));  // open: en
  Counter #(.width(16), .max('hffff)) counter_4 (
    .count(and_4_out), .Q(\条件分支成功数 ), .clk(CLK), .clr(RST));  // open: load, D, carry
  or or_6 (jmp_or_branch, JAL, JMP, JR, branch);
  or or_7 (branch, and_6_out, and_5_out);
  and and_5 (and_5_out, mips_alu_1_equal, BEQ);
  and and_6 (and_6_out, BNE, not_7_out);
  not not_7 (not_7_out, mips_alu_1_equal);
  MIPS_ALU mips_alu_1 (
    .X(jr_addr), .Y(multiplexer_8_out), .AluOP(\流水部件_2_控制信号_2 [6:3]), .Equal(mips_alu_1_equal),
    .Result(mips_alu_1_result), .shamt(jmp_addr[12:8]));  // open: Result_2
  \流水部件  \u_流水部件_3  (
    .\控制信号 ({\流水部件_2_控制信号_2 [15], JMP, JR, BEQ, BNE, JAL, \流水部件_2_控制信号_2 [9], EX_RegWrite, \流水部件_2_控制信号_2 [7:0]}),
    .PC({jmp_addr[31:28], \流水部件_2_pc_2 }), .IR({\流水部件_2_ir_2 , jmp_addr[27:2]}), .R1(mips_alu_1_result),
    .R2(\流水部件_2_r2_2 ), .clk(CLK), .\控制信号_2 ({\流水部件_3_控制信号_2 [15:9], Mem_RegWrite, \流水部件_3_控制信号_2 [7:0]}),
    .PC_2(\流水部件_3_pc_2 ), .IR_2(\流水部件_3_ir_2 ), .R1_2(\流水部件_3_r1_2 ), .R2_2(\流水部件_3_r2_2 ));  // open: Valid_Bit, sync_cls, enable, Valid_Bit_2
  \数据相关检测  \u_数据相关检测_1  (
    .EX_RegWrite(EX_RegWrite), .r1_used(r1_used), .r2_used(r2_used), .R1_num(R1_num), .R2_num(R2_num),
    .EX_WriteDst(EX_WriteDst), .Mem_WriteDst(Mem_WriteDst), .Mem_RegWrite(Mem_RegWrite),
    .Pipeline_pause(pipeline_pause));
  Multiplexer #(.width(5)) multiplexer_9 (
    .in0(\流水部件_3_ir_2 [15:11]), .in1(\流水部件_3_ir_2 [20:16]), .out(Mem_WriteDst), .sel(\流水部件_3_控制信号_2 [9]));  // open: en
  RAM #(.addrWidth(10), .dataWidth(32), .bus("separate")) ram_1 (
    .addr(\流水部件_3_r1_2 [11:2]), .din(\流水部件_3_r2_2 ), .data(ram_1_data), .str(\流水部件_3_控制信号_2 [2]), .clk(CLK),
    .clr(RST));  // open: sel, ld
  Multiplexer #(.width(32)) multiplexer_10 (
    .in0(\流水部件_3_r1_2 ), .in1(ram_1_data), .out(multiplexer_10_out), .sel(\流水部件_3_控制信号_2 [1]));  // open: en
  \流水部件  \u_流水部件_4  (
    .\控制信号 ({\流水部件_3_控制信号_2 [15:9], Mem_RegWrite, \流水部件_3_控制信号_2 [7:0]}), .PC(\流水部件_3_pc_2 ),
    .IR(\流水部件_3_ir_2 ), .R1(multiplexer_10_out), .clk(CLK),
    .\控制信号_2 ({\流水部件_4_控制信号_2 [15:11], JAL_WB, \流水部件_4_控制信号_2 [9:0]}), .PC_2(\流水部件_4_pc_2 ),
    .IR_2(\流水部件_4_ir_2 ), .R1_2(\流水部件_4_r1_2 ));  // open: R2, Valid_Bit, sync_cls, enable, R2_2, Valid_Bit_2
  Multiplexer #(.width(32)) multiplexer_11 (
    .in0(\流水部件_4_r1_2 ), .in1(\流水部件_4_pc_2 ), .out(multiplexer_11_out), .sel(JAL_WB));  // open: en
  Multiplexer #(.width(5)) multiplexer_12 (
    .in0(\流水部件_4_ir_2 [15:11]), .in1(\流水部件_4_ir_2 [20:16]), .out(multiplexer_12_out), .sel(\流水部件_4_控制信号_2 [9]));  // open: en
  // Probe on nothing
  Multiplexer #(.width(5)) multiplexer_13 (
    .in0(multiplexer_12_out), .in1({5{1'b1}}), .out(multiplexer_13_out), .sel(JAL_WB));  // open: en
  // Probe on nothing

  // Notes on the sheet:
  //   数码管输出应该用寄存器锁存，否则显示数据只能一闪而过
  //   可以通过项目增加Logisim库的方式将前几次实验完成的电路作为子电路引入到本电路中使用
  //   指令存储器
  //   取指
  //   contents of rom_1 (hex, n*v repeats v):
  //   20110001 8000c05 20110001 20120002 20130003 8000c09 20110001 20120002 20130003 8000c0d 20110001
  //   20120002 20130003 8000c11 20110001 20120002 20130003 c000cb8 20100001 20110001 118fc0 112020
  //   20020022 c 118882 12200001 8000c15 112020 20020022 c 20110001 118880 112020 20020022 c 12200001
  //   8000c1f 20110001 118fc0 112020 20020022 c 1188c3 112020 20020022 c 118903 112020 20020022 c 118903
  //   112020 20020022 c 118903 112020 20020022 c 118903 112020 20020022 c 118903 112020 20020022 c 118903
  //   112020 20020022 c 118903 112020 20020022 c 20100001 109fc0 139fc3 8021 2012000c 24160003 26100001
  //   3210000f 20080008 20090001 139900 2709825 132020 20020022 c 1094022 1500fff9 22100001 2018000f
  //   2188024 108700 20080008 20090001 139902 2709825 132021 20020022 c 1094022 1500fff9 108702 2c9b022
  //   12c00001 8000c50 4020 1084027 84400 3508ffff 82021 20020022 c 2010ffff 20110000 ae300000 22100001
  //   22310004 ae300000 22100001 22310004 ae300000 22100001 22310004 ae300000 22100001 22310004 ae300000
  //   22100001 22310004 ae300000 22100001 22310004 ae300000 22100001 22310004 ae300000 22100001 22310004
  //   ae300000 22100001 22310004 ae300000 22100001 22310004 ae300000 22100001 22310004 ae300000 22100001
  //   22310004 ae300000 22100001 22310004 ae300000 22100001 22310004 ae300000 22100001 22310004 ae300000
  //   22100001 22310004 22100001 8020 2011003c 8e130000 8e340000 274402a 11000002 ae330000 ae140000
  //   2231fffc 1611fff8 102020 20020022 c 22100004 2011003c 1611fff2 20020032 c 20100000 22100001 102020
  //   20020022 c 22100002 102020 20020022 c 22100003 102020 20020022 c 22100004 102020 20020022 c 22100005
  //   102020 20020022 c 22100006 102020 20020022 c 22100007 102020 20020022 c 22100008 102020 20020022
  //   20020022 c 3e00008
  //   数码管输出
  //   OP
  //   Func
  //   rs
  //   rt
  //   总复位信号应将除ROM以外所有存储组件全部清零
  //   译码
  //   JMP
  //   JR
  //   SignedExt
  //   OP
  //   Func
  //   Beq
  //   Bne
  //   MemToReg
  //   MemWrite
  //   AluOP
  //   AluSrcB
  //   RegWrite
  //   JAL
  //   RegDst
  //   Syscall
  //   addr
  //   imm
  //   shamt
  //   imm
  //   rt
  //   rd
  //   RegDst
  //   执行
  //   EX.RegWrite
  //   EX.WriteDst
  //   AluSrcB
  //   rt
  //   rd
  //   RegDst
  //   Mem.RegWrite
  //   Mem.WriteDst
  //   访存
  //   MemToReg
  //   rt
  //   rd
  //   RegDst
  //   写回
endmodule

module \源寄存器使用情况  (
  input  [5:0] opcode,
  input  [5:0] func,
  output R1_USED,
  output R2_USED
);

  wire and_1_out, and_2_out, and_3_out, and_4_out, and_5_out, and_6_out, and_7_out, and_8_out, and_9_out,
       and_10_out, and_11_out, and_12_out, and_13_out, and_14_out, and_15_out, and_16_out, and_17_out,
       not_1_out, not_2_out, not_3_out, not_4_out, not_5_out, not_6_out, not_7_out, not_8_out, not_9_out,
       not_10_out, not_11_out, not_12_out, not_13_out, not_14_out, not_15_out, not_16_out, not_17_out,
       not_18_out, not_19_out, not_20_out, not_21_out, not_22_out, not_23_out, not_24_out, not_25_out,
       not_26_out, not_27_out, not_28_out, not_29_out, not_30_out, not_31_out, not_32_out, not_33_out,
       not_34_out, not_35_out, not_36_out, not_37_out, not_38_out, not_39_out, not_40_out, not_41_out,
       not_42_out, not_43_out, not_44_out, not_45_out, not_46_out, not_47_out, not_48_out, not_49_out,
       not_50_out, not_51_out, not_52_out, not_53_out, not_54_out, not_55_out, not_56_out, not_57_out,
       not_58_out, not_59_out, not_60_out, not_61_out, not_62_out, not_63_out, not_64_out, not_65_out,
       not_66_out, not_67_out, not_68_out, not_69_out, not_70_out, not_71_out, not_72_out, not_73_out,
       not_74_out, not_75_out, not_76_out, not_77_out, not_78_out, not_79_out, not_80_out, not_81_out,
       not_82_out, not_83_out, not_84_out, not_85_out, not_86_out, not_87_out, not_88_out, not_89_out,
       not_90_out, not_91_out, not_92_out, not_93_out, not_94_out, not_95_out, not_96_out, not_97_out,
       not_98_out, not_99_out, not_100_out, not_101_out, not_102_out;

  not not_1 (not_1_out, opcode[0]);
  not not_2 (not_2_out, opcode[1]);
  not not_3 (not_3_out, opcode[4]);
  not not_4 (not_4_out, opcode[5]);
  not not_5 (not_5_out, func[0]);
  not not_6 (not_6_out, func[2]);
  not not_7 (not_7_out, func[3]);
  not not_8 (not_8_out, func[4]);
  not not_9 (not_9_out, opcode[0]);
  not not_10 (not_10_out, opcode[1]);
  not not_11 (not_11_out, opcode[4]);
  not not_12 (not_12_out, opcode[5]);
  not not_13 (not_13_out, func[1]);
  not not_14 (not_14_out, func[3]);
  not not_15 (not_15_out, func[4]);
  not not_16 (not_16_out, opcode[0]);
  not not_17 (not_17_out, opcode[1]);
  not not_18 (not_18_out, opcode[4]);
  not not_19 (not_19_out, opcode[5]);
  not not_20 (not_20_out, func[0]);
  not not_21 (not_21_out, func[1]);
  not not_22 (not_22_out, func[4]);
  not not_23 (not_23_out, func[5]);
  not not_24 (not_24_out, opcode[0]);
  not not_25 (not_25_out, opcode[1]);
  not not_26 (not_26_out, opcode[4]);
  not not_27 (not_27_out, opcode[5]);
  not not_28 (not_28_out, func[2]);
  not not_29 (not_29_out, func[4]);
  not not_30 (not_30_out, opcode[0]);
  not not_31 (not_31_out, opcode[1]);
  not not_32 (not_32_out, opcode[4]);
  not not_33 (not_33_out, opcode[5]);
  not not_34 (not_34_out, func[3]);
  not not_35 (not_35_out, func[4]);
  not not_36 (not_36_out, opcode[0]);
  not not_37 (not_37_out, opcode[2]);
  not not_38 (not_38_out, opcode[4]);
  not not_39 (not_39_out, opcode[5]);
  not not_40 (not_40_out, opcode[1]);
  not not_41 (not_41_out, opcode[4]);
  not not_42 (not_42_out, opcode[5]);
  not not_43 (not_43_out, opcode[1]);
  not not_44 (not_44_out, opcode[4]);
  not not_45 (not_45_out, opcode[5]);
  not not_46 (not_46_out, opcode[2]);
  not not_47 (not_47_out, opcode[4]);
  not not_48 (not_48_out, opcode[0]);
  not not_49 (not_49_out, opcode[1]);
  not not_50 (not_50_out, opcode[3]);
  not not_51 (not_51_out, opcode[4]);
  not not_52 (not_52_out, opcode[5]);
  not not_53 (not_53_out, func[0]);
  not not_54 (not_54_out, func[2]);
  not not_55 (not_55_out, func[3]);
  not not_56 (not_56_out, func[4]);
  not not_57 (not_57_out, opcode[0]);
  not not_58 (not_58_out, opcode[1]);
  not not_59 (not_59_out, opcode[3]);
  not not_60 (not_60_out, opcode[4]);
  not not_61 (not_61_out, opcode[5]);
  not not_62 (not_62_out, func[1]);
  not not_63 (not_63_out, func[3]);
  not not_64 (not_64_out, func[4]);
  not not_65 (not_65_out, opcode[0]);
  not not_66 (not_66_out, opcode[1]);
  not not_67 (not_67_out, opcode[3]);
  not not_68 (not_68_out, opcode[4]);
  not not_69 (not_69_out, opcode[5]);
  not not_70 (not_70_out, func[0]);
  not not_71 (not_71_out, func[1]);
  not not_72 (not_72_out, func[4]);
  not not_73 (not_73_out, func[5]);
  not not_74 (not_74_out, opcode[0]);
  not not_75 (not_75_out, opcode[1]);
  not not_76 (not_76_out, opcode[3]);
  not not_77 (not_77_out, opcode[4]);
  not not_78 (not_78_out, opcode[5]);
  not not_79 (not_79_out, func[2]);
  not not_80 (not_80_out, func[3]);
  not not_81 (not_81_out, func[4]);
  not not_82 (not_82_out, func[5]);
  not not_83 (not_83_out, opcode[0]);
  not not_84 (not_84_out, opcode[1]);
  not not_85 (not_85_out, opcode[3]);
  not not_86 (not_86_out, opcode[4]);
  not not_87 (not_87_out, opcode[5]);
  not not_88 (not_88_out, func[2]);
  not not_89 (not_89_out, func[4]);
  not not_90 (not_90_out, opcode[0]);
  not not_91 (not_91_out, opcode[1]);
  not not_92 (not_92_out, opcode[3]);
  not not_93 (not_93_out, opcode[4]);
  not not_94 (not_94_out, opcode[5]);
  not not_95 (not_95_out, func[3]);
  not not_96 (not_96_out, func[4]);
  not not_97 (not_97_out, opcode[1]);
  not not_98 (not_98_out, opcode[3]);
  not not_99 (not_99_out, opcode[4]);
  not not_100 (not_100_out, opcode[5]);
  not not_101 (not_101_out, opcode[2]);
  not not_102 (not_102_out, opcode[4]);
  and and_1 (and_1_out, not_1_out, not_2_out, not_3_out, not_4_out, not_5_out, not_6_out, not_7_out, not_8_out, func[5]);
  and and_2 (and_2_out, not_9_out, not_10_out, not_11_out, not_12_out, not_13_out, not_14_out, not_15_out, func[5]);
  and and_3 (and_3_out, not_16_out, not_17_out, not_18_out, not_19_out, not_20_out, not_21_out, func[3], not_22_out, not_23_out);
  and and_4 (and_4_out, not_24_out, not_25_out, not_26_out, not_27_out, func[1], not_28_out, func[3], not_29_out, func[5]);
  and and_5 (and_5_out, not_30_out, not_31_out, not_32_out, not_33_out, func[0], func[2], not_34_out, not_35_out, func[5]);
  and and_6 (and_6_out, not_36_out, not_37_out, opcode[3], not_38_out, not_39_out);
  and and_7 (and_7_out, not_40_out, opcode[3], not_41_out, not_42_out);
  and and_8 (and_8_out, not_43_out, opcode[2], not_44_out, not_45_out);
  and and_9 (and_9_out, opcode[0], opcode[1], not_46_out, not_47_out, opcode[5]);
  and and_10 (and_10_out, not_48_out, not_49_out, not_50_out, not_51_out, not_52_out, not_53_out, not_54_out, not_55_out, not_56_out);
  and and_11 (and_11_out, not_57_out, not_58_out, not_59_out, not_60_out, not_61_out, not_62_out, not_63_out, not_64_out, func[5]);
  and and_12 (and_12_out, not_65_out, not_66_out, not_67_out, not_68_out, not_69_out, not_70_out, not_71_out, func[2], func[3], not_72_out, not_73_out);
  and and_13 (and_13_out, not_74_out, not_75_out, not_76_out, not_77_out, not_78_out, func[1], not_79_out, not_80_out, not_81_out, not_82_out);
  and and_14 (and_14_out, not_83_out, not_84_out, not_85_out, not_86_out, not_87_out, func[1], not_88_out, func[3], not_89_out, func[5]);
  and and_15 (and_15_out, not_90_out, not_91_out, not_92_out, not_93_out, not_94_out, func[0], func[2], not_95_out, not_96_out, func[5]);
  and and_16 (and_16_out, not_97_out, opcode[2], not_98_out, not_99_out, not_100_out);
  and and_17 (and_17_out, opcode[0], opcode[1], not_101_out, opcode[3], not_102_out, opcode[5]);
  or or_1 (R1_USED, and_1_out, and_2_out, and_3_out, and_4_out, and_5_out, and_6_out, and_7_out, and_8_out, and_9_out);
  or or_2 (R2_USED, and_10_out, and_11_out, and_12_out, and_13_out, and_14_out, and_15_out, and_16_out, and_17_out);
endmodule

module \数据相关检测  (
  input  EX_RegWrite,
  input  r1_used,
  input  r2_used,
  input  [4:0] R1_num,
  input  [4:0] R2_num,
  input  [4:0] EX_WriteDst,
  input  [4:0] Mem_WriteDst,
  input  Mem_RegWrite,
  output Pipeline_pause
);

  wire and_1_out, and_2_out, and_3_out, and_4_out, and_5_out, and_6_out, comparator_1_eq, comparator_2_eq,
       comparator_3_eq, comparator_4_eq, comparator_5_eq, comparator_6_eq, not_1_out, not_2_out, or_1_out,
       or_2_out;

  Comparator #(.width(5)) comparator_1 (.a(R1_num), .b(EX_WriteDst), .eq(comparator_1_eq));  // open: gt, lt
  Comparator #(.width(5)) comparator_2 (.a(R2_num), .b(EX_WriteDst), .eq(comparator_2_eq));  // open: gt, lt
  Comparator #(.width(5)) comparator_3 (.a(R1_num), .b({5{1'b0}}), .eq(comparator_3_eq));  // open: gt, lt
  not not_1 (not_1_out, comparator_3_eq);
  not not_2 (not_2_out, comparator_4_eq);
  Comparator #(.width(5)) comparator_4 (.a(R2_num), .b({5{1'b0}}), .eq(comparator_4_eq));  // open: gt, lt
  Comparator #(.width(5)) comparator_5 (.a(R1_num), .b(Mem_WriteDst), .eq(comparator_5_eq));  // open: gt, lt
  Comparator #(.width(5)) comparator_6 (.a(R2_num), .b(Mem_WriteDst), .eq(comparator_6_eq));  // open: gt, lt
  and and_1 (and_1_out, r1_used, comparator_1_eq, not_1_out);
  and and_2 (and_2_out, r2_used, comparator_2_eq, not_2_out);
  and and_3 (and_3_out, not_1_out, r1_used, comparator_5_eq);
  and and_4 (and_4_out, comparator_6_eq, r2_used, not_2_out);
  or or_1 (or_1_out, and_1_out, and_2_out);
  or or_2 (or_2_out, and_3_out, and_4_out);
  and and_5 (and_5_out, EX_RegWrite, or_1_out);
  and and_6 (and_6_out, or_2_out, Mem_RegWrite);
  or or_3 (Pipeline_pause, and_5_out, and_6_out);
endmodule

module \源寄存器使用情况1  (
  input  OP0,
  input  OP1,
  input  OP2,
  input  OP3,
  input  OP4,
  input  OP5,
  input  F0,
  input  F1,
  input  F2,
  input  F3,
  input  F4,
  input  F5,
  output R1_USED,
  output R2_USED
);

  wire and_1_out, and_2_out, and_3_out, and_4_out, and_5_out, and_6_out, and_7_out, and_8_out, and_9_out,
       and_10_out, and_11_out, and_12_out, and_13_out, and_14_out, and_15_out, and_16_out, and_17_out,
       not_1_out, not_2_out, not_3_out, not_4_out, not_5_out, not_6_out, not_7_out, not_8_out, not_9_out,
       not_10_out, not_11_out, not_12_out, not_13_out, not_14_out, not_15_out, not_16_out, not_17_out,
       not_18_out, not_19_out, not_20_out, not_21_out, not_22_out, not_23_out, not_24_out, not_25_out,
       not_26_out, not_27_out, not_28_out, not_29_out, not_30_out, not_31_out, not_32_out, not_33_out,
       not_34_out, not_35_out, not_36_out, not_37_out, not_38_out, not_39_out, not_40_out, not_41_out,
       not_42_out, not_43_out, not_44_out, not_45_out, not_46_out, not_47_out, not_48_out, not_49_out,
       not_50_out, not_51_out, not_52_out, not_53_out, not_54_out, not_55_out, not_56_out, not_57_out,
       not_58_out, not_59_out, not_60_out, not_61_out, not_62_out, not_63_out, not_64_out, not_65_out,
       not_66_out, not_67_out, not_68_out, not_69_out, not_70_out, not_71_out, not_72_out, not_73_out,
       not_74_out, not_75_out, not_76_out, not_77_out, not_78_out, not_79_out, not_80_out, not_81_out,
       not_82_out, not_83_out, not_84_out, not_85_out, not_86_out, not_87_out, not_88_out, not_89_out,
       not_90_out, not_91_out, not_92_out, not_93_out, not_94_out, not_95_out, not_96_out, not_97_out,
       not_98_out, not_99_out, not_100_out, not_101_out, not_102_out;

  not not_1 (not_1_out, OP0);
  not not_2 (not_2_out, OP1);
  not not_3 (not_3_out, OP4);
  not not_4 (not_4_out, OP5);
  not not_5 (not_5_out, F0);
  not not_6 (not_6_out, F2);
  not not_7 (not_7_out, F3);
  not not_8 (not_8_out, F4);
  not not_9 (not_9_out, OP0);
  not not_10 (not_10_out, OP1);
  not not_11 (not_11_out, OP4);
  not not_12 (not_12_out, OP5);
  not not_13 (not_13_out, F1);
  not not_14 (not_14_out, F3);
  not not_15 (not_15_out, F4);
  not not_16 (not_16_out, OP0);
  not not_17 (not_17_out, OP1);
  not not_18 (not_18_out, OP4);
  not not_19 (not_19_out, OP5);
  not not_20 (not_20_out, F0);
  not not_21 (not_21_out, F1);
  not not_22 (not_22_out, F4);
  not not_23 (not_23_out, F5);
  not not_24 (not_24_out, OP0);
  not not_25 (not_25_out, OP1);
  not not_26 (not_26_out, OP4);
  not not_27 (not_27_out, OP5);
  not not_28 (not_28_out, F2);
  not not_29 (not_29_out, F4);
  not not_30 (not_30_out, OP0);
  not not_31 (not_31_out, OP1);
  not not_32 (not_32_out, OP4);
  not not_33 (not_33_out, OP5);
  not not_34 (not_34_out, F3);
  not not_35 (not_35_out, F4);
  not not_36 (not_36_out, OP0);
  not not_37 (not_37_out, OP2);
  not not_38 (not_38_out, OP4);
  not not_39 (not_39_out, OP5);
  not not_40 (not_40_out, OP1);
  not not_41 (not_41_out, OP4);
  not not_42 (not_42_out, OP5);
  not not_43 (not_43_out, OP1);
  not not_44 (not_44_out, OP4);
  not not_45 (not_45_out, OP5);
  not not_46 (not_46_out, OP2);
  not not_47 (not_47_out, OP4);
  not not_48 (not_48_out, OP0);
  not not_49 (not_49_out, OP1);
  not not_50 (not_50_out, OP3);
  not not_51 (not_51_out, OP4);
  not not_52 (not_52_out, OP5);
  not not_53 (not_53_out, F0);
  not not_54 (not_54_out, F2);
  not not_55 (not_55_out, F3);
  not not_56 (not_56_out, F4);
  not not_57 (not_57_out, OP0);
  not not_58 (not_58_out, OP1);
  not not_59 (not_59_out, OP3);
  not not_60 (not_60_out, OP4);
  not not_61 (not_61_out, OP5);
  not not_62 (not_62_out, F1);
  not not_63 (not_63_out, F3);
  not not_64 (not_64_out, F4);
  not not_65 (not_65_out, OP0);
  not not_66 (not_66_out, OP1);
  not not_67 (not_67_out, OP3);
  not not_68 (not_68_out, OP4);
  not not_69 (not_69_out, OP5);
  not not_70 (not_70_out, F0);
  not not_71 (not_71_out, F1);
  not not_72 (not_72_out, F4);
  not not_73 (not_73_out, F5);
  not not_74 (not_74_out, OP0);
  not not_75 (not_75_out, OP1);
  not not_76 (not_76_out, OP3);
  not not_77 (not_77_out, OP4);
  not not_78 (not_78_out, OP5);
  not not_79 (not_79_out, F2);
  not not_80 (not_80_out, F3);
  not not_81 (not_81_out, F4);
  not not_82 (not_82_out, F5);
  not not_83 (not_83_out, OP0);
  not not_84 (not_84_out, OP1);
  not not_85 (not_85_out, OP3);
  not not_86 (not_86_out, OP4);
  not not_87 (not_87_out, OP5);
  not not_88 (not_88_out, F2);
  not not_89 (not_89_out, F4);
  not not_90 (not_90_out, OP0);
  not not_91 (not_91_out, OP1);
  not not_92 (not_92_out, OP3);
  not not_93 (not_93_out, OP4);
  not not_94 (not_94_out, OP5);
  not not_95 (not_95_out, F3);
  not not_96 (not_96_out, F4);
  not not_97 (not_97_out, OP1);
  not not_98 (not_98_out, OP3);
  not not_99 (not_99_out, OP4);
  not not_100 (not_100_out, OP5);
  not not_101 (not_101_out, OP2);
  not not_102 (not_102_out, OP4);
  and and_1 (and_1_out, not_1_out, not_2_out, not_3_out, not_4_out, not_5_out, not_6_out, not_7_out, not_8_out, F5);
  and and_2 (and_2_out, not_9_out, not_10_out, not_11_out, not_12_out, not_13_out, not_14_out, not_15_out, F5);
  and and_3 (and_3_out, not_16_out, not_17_out, not_18_out, not_19_out, not_20_out, not_21_out, F3, not_22_out, not_23_out);
  and and_4 (and_4_out, not_24_out, not_25_out, not_26_out, not_27_out, F1, not_28_out, F3, not_29_out, F5);
  and and_5 (and_5_out, not_30_out, not_31_out, not_32_out, not_33_out, F0, F2, not_34_out, not_35_out, F5);
  and and_6 (and_6_out, not_36_out, not_37_out, OP3, not_38_out, not_39_out);
  and and_7 (and_7_out, not_40_out, OP3, not_41_out, not_42_out);
  and and_8 (and_8_out, not_43_out, OP2, not_44_out, not_45_out);
  and and_9 (and_9_out, OP0, OP1, not_46_out, not_47_out, OP5);
  and and_10 (and_10_out, not_48_out, not_49_out, not_50_out, not_51_out, not_52_out, not_53_out, not_54_out, not_55_out, not_56_out);
  and and_11 (and_11_out, not_57_out, not_58_out, not_59_out, not_60_out, not_61_out, not_62_out, not_63_out, not_64_out, F5);
  and and_12 (and_12_out, not_65_out, not_66_out, not_67_out, not_68_out, not_69_out, not_70_out, not_71_out, F2, F3, not_72_out, not_73_out);
  and and_13 (and_13_out, not_74_out, not_75_out, not_76_out, not_77_out, not_78_out, F1, not_79_out, not_80_out, not_81_out, not_82_out);
  and and_14 (and_14_out, not_83_out, not_84_out, not_85_out, not_86_out, not_87_out, F1, not_88_out, F3, not_89_out, F5);
  and and_15 (and_15_out, not_90_out, not_91_out, not_92_out, not_93_out, not_94_out, F0, F2, not_95_out, not_96_out, F5);
  and and_16 (and_16_out, not_97_out, OP2, not_98_out, not_99_out, not_100_out);
  and and_17 (and_17_out, OP0, OP1, not_101_out, OP3, not_102_out, OP5);
  or or_1 (R1_USED, and_1_out, and_2_out, and_3_out, and_4_out, and_5_out, and_6_out, and_7_out, and_8_out, and_9_out);
  or or_2 (R2_USED, and_10_out, and_11_out, and_12_out, and_13_out, and_14_out, and_15_out, and_16_out, and_17_out);
endmodule

module \键盘测试  (
  input  in_1,
  input  in_2,
  output [6:0] out_3
);

  wire clock_1_out, keyboard_1_avail;

  RAM #(.bus("separate")) ram_1 ();  // open: addr, din, data, str, sel, clk, ld, clr
  Clock clock_1 (.out(clock_1_out));
  Keyboard keyboard_1 (.clk(clock_1_out), .re(in_1), .clr(in_2), .avail(keyboard_1_avail), .data(out_3));
  LED led_1 (.in(keyboard_1_avail));
  // Probe on out_3
endmodule

module \重定向流水线  (
);

  wire and_1_out, and_2_out, and_3_out, and_4_out, and_6_out, and_7_out, and_8_out, BEQ, BNE, branch, CLK,
       comparator_1_eq, comparator_2_eq, comparator_3_eq, comparator_4_eq, EX_r1_used, EX_r2_used, Go, JAL,
       JAL_WB, JMP, jmp_or_branch, JR, Mem_MemToReg, Mem_RegWrite, mips_alu_1_equal, not_1_out, not_2_out,
       not_3_out, not_4_out, not_5_out, not_6_out, not_7_out, not_8_out, not_9_out, not_10_out, not_11_out,
       or_1_out, or_2_out, or_3_out, or_4_out, or_5_out, or_6_out, or_8_out, or_10_out, or_11_out, or_13_out,
       pause, pipeline_pause, r1_used, r2_used, RST, sys_show, syscall, Wb_RegWrite;
  wire [1:0] EX_r1_redirect, EX_r2_redirect, or_12_out;
  wire [3:0] \硬布线控制器_1_alu_op ;
  wire [4:0] EX_R1_num, EX_R2_num, Mem_WriteDst, multiplexer_15_out, R1_num, R2_num, Wb_WriteDst;
  wire [5:0] EX_opcode;
  wire [9:0] \流水部件_2_控制信号_2 ;
  wire [15:0] \load_use插入气泡数 , \总周期数 , \无条件分支数 , \条件分支成功数 , \流水线重定向次数 , \流水部件_3_控制信号_2 , \流水部件_4_控制信号_2 ,
       \硬布线控制器_1_signedext ;
  wire [27:0] \流水部件_2_pc_2 ;
  wire [31:0] a0, adder_1_out, bit_extender_1_out, bit_extender_2_out, branch_addr, jr_addr, LedData,
       Mem_AluRslt, mips_alu_1_result, mips_regifile_1_r1, mips_regifile_1_r2, multiplexer_1_out,
       multiplexer_2_out, multiplexer_3_out, multiplexer_10_out, multiplexer_11_out, multiplexer_13_out,
       PC_q, ram_1_data, rom_1_data, v0, Wb_WriteData, \流水部件_1_ir_2 , \流水部件_1_pc_2 , \流水部件_2_r2_2 ,
       \流水部件_3_ir_2 , \流水部件_3_pc_2 , \流水部件_3_r2_2 , \流水部件_4_ir_2 , \流水部件_4_pc_2 , \流水部件_4_r1_2 ;
  wire [31:2] jmp_addr;

  Button \u_总复位  (.out(RST));
  Button u_Go (.out(Go));
  Clock clock_1 (.out(CLK));
  Multiplexer #(.width(32)) multiplexer_1 (
    .in0(adder_1_out), .in1(jr_addr), .out(multiplexer_1_out), .sel(JR));  // open: en
  Multiplexer #(.width(32)) multiplexer_2 (
    .in0(multiplexer_1_out), .in1({jmp_addr, 2'b00}), .out(multiplexer_2_out), .sel(or_2_out));  // open: en
  or or_1 (or_1_out, pause, pipeline_pause);
  not not_1 (not_1_out, or_1_out);
  Register #(.width(32)) PC (.D(multiplexer_3_out), .en(not_1_out), .Q(PC_q), .clk(CLK), .clr(RST));
  Hex_Digit_Display hex_digit_display_1 (.value(LedData[31:28]));  // open: dp
  Hex_Digit_Display hex_digit_display_2 (.value(LedData[27:24]));  // open: dp
  or or_2 (or_2_out, JAL, JMP);
  Multiplexer #(.width(32)) multiplexer_3 (
    .in0(multiplexer_2_out), .in1(branch_addr), .out(multiplexer_3_out), .sel(branch));  // open: en
  Hex_Digit_Display hex_digit_display_3 (.value(LedData[23:20]));  // open: dp
  Hex_Digit_Display hex_digit_display_4 (.value(LedData[19:16]));  // open: dp
  Adder #(.width(32)) adder_1 (.a(PC_q), .b(32'h4), .out(adder_1_out));  // open: cin, cout
  Hex_Digit_Display hex_digit_display_5 (.value(LedData[15:12]));  // open: dp
  Hex_Digit_Display hex_digit_display_6 (.value(LedData[11:8]));  // open: dp
  ROM #(.addrWidth(10), .dataWidth(32)) rom_1 (.addr(PC_q[11:2]), .data(rom_1_data));  // open: sel
  or or_3 (or_3_out, RST, not_2_out);
  not not_2 (not_2_out, or_4_out);
  or or_4 (or_4_out, pause, pipeline_pause);
  Hex_Digit_Display hex_digit_display_7 (.value(LedData[7:4]));  // open: dp
  Hex_Digit_Display hex_digit_display_8 (.value(LedData[3:0]));  // open: dp
  \流水部件  \u_流水部件_1  (
    .PC(adder_1_out), .IR(rom_1_data), .sync_cls(jmp_or_branch), .enable(or_3_out), .clk(CLK),
    .PC_2(\流水部件_1_pc_2 ), .IR_2(\流水部件_1_ir_2 ));  // open: 控制信号, R1, R2, Valid_Bit, 控制信号_2, R1_2, R2_2, Valid_Bit_2
  \源寄存器使用情况  \u_源寄存器使用情况_1  (
    .func(\流水部件_1_ir_2 [5:0]), .opcode(\流水部件_1_ir_2 [31:26]), .R1_USED(r1_used), .R2_USED(r2_used));
  // Probe on \总周期数 
  // Probe on \无条件分支数 
  // Probe on \条件分支成功数 
  // Probe on \load_use插入气泡数 
  // Probe on \流水线重定向次数 
  Multiplexer #(.width(5)) multiplexer_4 (
    .in0(\流水部件_1_ir_2 [25:21]), .in1(5'b00010), .out(R1_num), .sel(\硬布线控制器_1_signedext [15]));  // open: en
  Multiplexer #(.width(5)) multiplexer_5 (
    .in0(\流水部件_1_ir_2 [20:16]), .in1(5'b00100), .out(R2_num), .sel(\硬布线控制器_1_signedext [15]));  // open: en
  \硬布线控制器  \u_硬布线控制器_1  (
    .Func(\流水部件_1_ir_2 [5:0]), .OP(\流水部件_1_ir_2 [31:26]), .ALU_OP(\硬布线控制器_1_alu_op ),
    .MemToReg(\硬布线控制器_1_signedext [1]), .MemWrite(\硬布线控制器_1_signedext [2]),
    .ALU_SRC(\硬布线控制器_1_signedext [7]), .RegWrite(\硬布线控制器_1_signedext [8]),
    .SysCALL(\硬布线控制器_1_signedext [15]), .SignedExt(\硬布线控制器_1_signedext [0]),
    .RegDst(\硬布线控制器_1_signedext [9]), .JR(\硬布线控制器_1_signedext [13]), .JMP(\硬布线控制器_1_signedext [14]),
    .Beq(\硬布线控制器_1_signedext [12]), .JAL(\硬布线控制器_1_signedext [10]), .Bne(\硬布线控制器_1_signedext [11]));
  MIPS_Regifile mips_regifile_1 (
    .Din(Wb_WriteData), .Clk(CLK), .R1(mips_regifile_1_r1), .R2(mips_regifile_1_r2), .WE(Wb_RegWrite),
    .W_num(Wb_WriteDst), .R1_num(R1_num), .R2_num(R2_num));
  or or_5 (or_5_out, RST, not_3_out);
  or or_6 (or_6_out, jmp_or_branch, pipeline_pause);
  \流水部件  \u_流水部件_2  (
    .\控制信号 ({\硬布线控制器_1_signedext [15:7], \硬布线控制器_1_alu_op , \硬布线控制器_1_signedext [2:0]}), .PC(\流水部件_1_pc_2 ),
    .IR(\流水部件_1_ir_2 ), .R1(mips_regifile_1_r1), .R2(mips_regifile_1_r2), .sync_cls(or_6_out),
    .enable(or_5_out), .clk(CLK), .\控制信号_2 ({syscall, JMP, JR, BEQ, BNE, JAL, \流水部件_2_控制信号_2 }),
    .PC_2({jmp_addr[31:28], \流水部件_2_pc_2 }), .IR_2({EX_opcode, jmp_addr[27:2]}), .R1_2(jr_addr),
    .R2_2(\流水部件_2_r2_2 ));  // open: Valid_Bit, Valid_Bit_2
  not not_3 (not_3_out, pause);
  assign bit_extender_1_out = {{14{jmp_addr[17]}}, {jmp_addr[17:2], 2'b00}};  // Bit_Extender bit_extender_1
  Multiplexer #(.width(5)) multiplexer_6 (
    .in0(jmp_addr[27:23]), .in1(5'b00010), .out(EX_R1_num), .sel(syscall));  // open: en
  Multiplexer #(.width(5)) multiplexer_7 (
    .in0(jmp_addr[22:18]), .in1(5'b00100), .out(EX_R2_num), .sel(syscall));  // open: en
  assign bit_extender_2_out = {{16{jmp_addr[17]}}, jmp_addr[17:2]};  // Bit_Extender bit_extender_2
  Adder #(.width(32)) adder_2 (
    .a(bit_extender_1_out), .b({jmp_addr[31:28], \流水部件_2_pc_2 }), .out(branch_addr));  // open: cin, cout
  \源寄存器使用情况  \u_源寄存器使用情况_2  (.func(jmp_addr[7:2]), .opcode(EX_opcode), .R1_USED(EX_r1_used), .R2_USED(EX_r2_used));
  Multiplexer #(.select(2), .width(32)) multiplexer_8 (
    .in0(jr_addr), .in1(Wb_WriteData), .in2(Mem_AluRslt), .in3(Mem_AluRslt), .out(v0), .sel(EX_r1_redirect));  // open: en
  Multiplexer #(.select(2), .width(32)) multiplexer_9 (
    .in0(\流水部件_2_r2_2 ), .in1(Wb_WriteData), .in2(Mem_AluRslt), .in3(Mem_AluRslt), .out(a0),
    .sel(EX_r2_redirect));  // open: en
  Multiplexer #(.width(32)) multiplexer_10 (
    .in0({{16{1'b0}}, jmp_addr[17:2]}), .in1(bit_extender_2_out), .out(multiplexer_10_out),
    .sel(\流水部件_2_控制信号_2 [0]));  // open: en
  Multiplexer #(.width(32)) multiplexer_11 (
    .in0(a0), .in1(multiplexer_10_out), .out(multiplexer_11_out), .sel(\流水部件_2_控制信号_2 [7]));  // open: en
  or or_7 (branch, and_1_out, and_2_out);
  and and_1 (and_1_out, BNE, not_4_out);
  and and_2 (and_2_out, mips_alu_1_equal, BEQ);
  not not_4 (not_4_out, mips_alu_1_equal);
  MIPS_ALU mips_alu_1 (
    .X(v0), .Y(multiplexer_11_out), .AluOP(\流水部件_2_控制信号_2 [6:3]), .Equal(mips_alu_1_equal),
    .Result(mips_alu_1_result), .shamt(jmp_addr[12:8]));  // open: Result_2
  \流水部件  \u_流水部件_3  (
    .\控制信号 ({syscall, JMP, JR, BEQ, BNE, JAL, \流水部件_2_控制信号_2 }), .PC({jmp_addr[31:28], \流水部件_2_pc_2 }),
    .IR({EX_opcode, jmp_addr[27:2]}), .R1(mips_alu_1_result), .R2(\流水部件_2_r2_2 ), .enable(or_8_out),
    .clk(CLK),
    .\控制信号_2 ({\流水部件_3_控制信号_2 [15:9], Mem_RegWrite, \流水部件_3_控制信号_2 [7:2], Mem_MemToReg, \流水部件_3_控制信号_2 [0]}),
    .PC_2(\流水部件_3_pc_2 ), .IR_2(\流水部件_3_ir_2 ), .R1_2(Mem_AluRslt), .R2_2(\流水部件_3_r2_2 ));  // open: Valid_Bit, sync_cls, Valid_Bit_2
  or or_8 (or_8_out, RST, not_5_out);
  not not_5 (not_5_out, pause);
  or or_9 (jmp_or_branch, JAL, JMP, JR, branch);
  Multiplexer #(.width(5)) multiplexer_12 (
    .in0(\流水部件_3_ir_2 [15:11]), .in1(\流水部件_3_ir_2 [20:16]), .out(Mem_WriteDst), .sel(\流水部件_3_控制信号_2 [9]));  // open: en
  RAM #(.addrWidth(10), .dataWidth(32), .bus("separate")) ram_1 (
    .addr(Mem_AluRslt[11:2]), .din(\流水部件_3_r2_2 ), .data(ram_1_data), .str(\流水部件_3_控制信号_2 [2]), .clk(CLK),
    .clr(RST));  // open: sel, ld
  Comparator #(.width(6)) comparator_1 (.a(6'b100011), .b(EX_opcode), .eq(comparator_1_eq));  // open: gt, lt
  Comparator #(.width(5)) comparator_2 (.a(EX_R2_num), .b(R1_num), .eq(comparator_2_eq));  // open: gt, lt
  Comparator #(.width(5)) comparator_3 (.a(EX_R2_num), .b(R2_num), .eq(comparator_3_eq));  // open: gt, lt
  and and_3 (and_3_out, comparator_2_eq, r1_used);
  and and_4 (and_4_out, comparator_3_eq, r2_used);
  Multiplexer #(.width(32)) multiplexer_13 (
    .in0(Mem_AluRslt), .in1(ram_1_data), .out(multiplexer_13_out), .sel(Mem_MemToReg));  // open: en
  and and_5 (pipeline_pause, comparator_1_eq, or_10_out);
  or or_10 (or_10_out, and_3_out, and_4_out);
  \流水部件  \u_流水部件_4  (
    .\控制信号 ({\流水部件_3_控制信号_2 [15:9], Mem_RegWrite, \流水部件_3_控制信号_2 [7:2], Mem_MemToReg, \流水部件_3_控制信号_2 [0]}),
    .PC(\流水部件_3_pc_2 ), .IR(\流水部件_3_ir_2 ), .R1(multiplexer_13_out), .enable(or_11_out), .clk(CLK),
    .\控制信号_2 ({\流水部件_4_控制信号_2 [15:11], JAL_WB, \流水部件_4_控制信号_2 [9], Wb_RegWrite, \流水部件_4_控制信号_2 [7:0]}),
    .PC_2(\流水部件_4_pc_2 ), .IR_2(\流水部件_4_ir_2 ), .R1_2(\流水部件_4_r1_2 ));  // open: R2, Valid_Bit, sync_cls, R2_2, Valid_Bit_2
  or or_11 (or_11_out, RST, not_6_out);
  not not_6 (not_6_out, pause);
  Multiplexer #(.width(32)) multiplexer_14 (
    .in0(\流水部件_4_r1_2 ), .in1(\流水部件_4_pc_2 ), .out(Wb_WriteData), .sel(JAL_WB));  // open: en
  Multiplexer #(.width(5)) multiplexer_15 (
    .in0(\流水部件_4_ir_2 [15:11]), .in1(\流水部件_4_ir_2 [20:16]), .out(multiplexer_15_out), .sel(\流水部件_4_控制信号_2 [9]));  // open: en
  Multiplexer #(.width(5)) multiplexer_16 (
    .in0(multiplexer_15_out), .in1({5{1'b1}}), .out(Wb_WriteDst), .sel(JAL_WB));  // open: en
  Register #(.width(32)) register_1 (.D(a0), .en(sys_show), .Q(LedData), .clk(CLK), .clr(RST));
  Counter #(.width(16), .max('hffff)) counter_1 (
    .count(pipeline_pause), .Q(\load_use插入气泡数 ), .clk(CLK), .clr(RST));  // open: load, D, carry
  assign or_12_out = EX_r1_redirect | EX_r2_redirect;  // OR_Gate or_12, 2 bits wide
  not not_7 (not_7_out, pause);
  // Probe on nothing
  or or_13 (or_13_out, or_12_out[0], or_12_out[1]);
  and and_6 (and_6_out, or_13_out, not_7_out);
  \重定向数据相关检测  \u_重定向数据相关检测_1  (
    .EX_r1_used(EX_r1_used), .Mem_RegWrite(Mem_RegWrite), .Wb_RegWrite(Wb_RegWrite),
    .Mem_MemToReg(Mem_MemToReg), .EX_R1__redirect(EX_r1_redirect), .EX_R1_num(EX_R1_num),
    .Mem_WriteDst(Mem_WriteDst), .Wb_WriteDst(Wb_WriteDst), .EX_R2__redirect(EX_r2_redirect),
    .EX_r2_used(EX_r2_used), .EX_R2_num(EX_R2_num));
  Counter #(.width(16), .max('hffff)) counter_2 (
    .count(and_6_out), .Q(\流水线重定向次数 ), .clk(CLK), .clr(RST));  // open: load, D, carry
  and and_7 (and_7_out, jmp_or_branch, not_8_out);
  not not_8 (not_8_out, branch);
  // Probe on EX_r1_redirect
  // Probe on EX_r2_redirect
  Counter #(.width(16), .max('hffff)) counter_3 (
    .count(and_7_out), .Q(\无条件分支数 ), .clk(CLK), .clr(RST));  // open: load, D, carry
  Counter #(.width(16), .max('hffff)) counter_4 (
    .count(and_8_out), .Q(\条件分支成功数 ), .clk(CLK), .clr(RST));  // open: load, D, carry
  and and_8 (and_8_out, branch, not_9_out);
  not not_9 (not_9_out, pause);
  not not_10 (not_10_out, pause);
  Counter #(.width(16), .max('hffff)) counter_5 (
    .count(not_10_out), .Q(\总周期数 ), .clk(CLK), .clr(RST));  // open: load, D, carry
  and and_9 (pause, syscall, not_11_out);
  not not_11 (not_11_out, comparator_4_eq);
  Comparator #(.width(32)) comparator_4 (.a(32'h22), .b(v0), .eq(comparator_4_eq));  // open: gt, lt
  and and_10 (sys_show, syscall, comparator_4_eq);

  // Notes on the sheet:
  //   数码管输出应该用寄存器锁存，否则显示数据只能一闪而过
  //   可以通过项目增加Logisim库的方式将前几次实验完成的电路作为子电路引入到本电路中使用
  //   指令存储器
  //   取指
  //   contents of rom_1 (hex, n*v repeats v):
  //   20110001 8000c05 20110001 20120002 20130003 8000c09 20110001 20120002 20130003 8000c0d 20110001
  //   20120002 20130003 8000c11 20110001 20120002 20130003 c000cb8 20100001 20110001 118fc0 112020
  //   20020022 c 118882 12200001 8000c15 112020 20020022 c 20110001 118880 112020 20020022 c 12200001
  //   8000c1f 20110001 118fc0 112020 20020022 c 1188c3 112020 20020022 c 118903 112020 20020022 c 118903
  //   112020 20020022 c 118903 112020 20020022 c 118903 112020 20020022 c 118903 112020 20020022 c 118903
  //   112020 20020022 c 118903 112020 20020022 c 20100001 109fc0 139fc3 8021 2012000c 24160003 26100001
  //   3210000f 20080008 20090001 139900 2709825 132020 20020022 c 1094022 1500fff9 22100001 2018000f
  //   2188024 108700 20080008 20090001 139902 2709825 132021 20020022 c 1094022 1500fff9 108702 2c9b022
  //   12c00001 8000c50 4020 1084027 84400 3508ffff 82021 20020022 c 2010ffff 20110000 ae300000 22100001
  //   22310004 ae300000 22100001 22310004 ae300000 22100001 22310004 ae300000 22100001 22310004 ae300000
  //   22100001 22310004 ae300000 22100001 22310004 ae300000 22100001 22310004 ae300000 22100001 22310004
  //   ae300000 22100001 22310004 ae300000 22100001 22310004 ae300000 22100001 22310004 ae300000 22100001
  //   22310004 ae300000 22100001 22310004 ae300000 22100001 22310004 ae300000 22100001 22310004 ae300000
  //   22100001 22310004 22100001 8020 2011003c 8e130000 8e340000 274402a 11000002 ae330000 ae140000
  //   2231fffc 1611fff8 102020 20020022 c 22100004 2011003c 1611fff2 20020032 c 20100000 22100001 102020
  //   20020022 c 22100002 102020 20020022 c 22100003 102020 20020022 c 22100004 102020 20020022 c 22100005
  //   102020 20020022 c 22100006 102020 20020022 c 22100007 102020 20020022 c 22100008 102020 20020022
  //   20020022 c 3e00008
  //   数码管输出
  //   OP
  //   Func
  //   rs
  //   rt
  //   总复位信号应将除ROM以外所有存储组件全部清零
  //   译码
  //   JMP
  //   JR
  //   SignedExt
  //   OP
  //   Func
  //   Beq
  //   Bne
  //   MemToReg
  //   MemWrite
  //   AluOP
  //   AluSrcB
  //   RegWrite
  //   JAL
  //   RegDst
  //   Syscall
  //   addr
  //   imm
  //   OP
  //   Func
  //   rs
  //   rt
  //   shamt
  //   imm
  //   为syscall的数据重定向专门加两个mux
  //   AluSrcB
  //   执行
  //   PC跳转清空流水线逻辑
  //   rt
  //   rd
  //   RegDst
  //   Mem.RegWrite
  //   Mem.WriteDst
  //   访存
  //   load-use流水线暂停逻辑
  //   EX.lw
  //   MemToReg
  //   rt
  //   rd
  //   RegDst
  //   写回
  //   数据重定向判断逻辑
  //   计数和LED显示逻辑
  //   系统调用逻辑
endmodule

module \重定向数据相关检测  (
  input  EX_r1_used,
  input  Mem_RegWrite,
  input  Wb_RegWrite,
  input  [4:0] EX_R1_num,
  input  [4:0] Mem_WriteDst,
  input  [4:0] Wb_WriteDst,
  input  Mem_MemToReg,
  input  EX_r2_used,
  input  [4:0] EX_R2_num,
  output [1:0] EX_R1__redirect,
  output [1:0] EX_R2__redirect
);

  wire comparator_1_eq, comparator_2_eq, comparator_3_eq, comparator_4_eq, comparator_5_eq, comparator_6_eq,
       not_1_out, not_2_out, not_3_out, not_4_out;

  Comparator #(.width(5)) comparator_1 (.a(EX_R1_num), .b({5{1'b0}}), .eq(comparator_1_eq));  // open: gt, lt
  not not_1 (not_1_out, comparator_1_eq);
  Comparator #(.width(5)) comparator_2 (.a(EX_R1_num), .b(Mem_WriteDst), .eq(comparator_2_eq));  // open: gt, lt
  not not_2 (not_2_out, Mem_MemToReg);
  Comparator #(.width(5)) comparator_3 (.a(EX_R1_num), .b(Wb_WriteDst), .eq(comparator_3_eq));  // open: gt, lt
  not not_3 (not_3_out, comparator_4_eq);
  Comparator #(.width(5)) comparator_4 (.a(EX_R2_num), .b({5{1'b0}}), .eq(comparator_4_eq));  // open: gt, lt
  Comparator #(.width(5)) comparator_5 (.a(EX_R2_num), .b(Mem_WriteDst), .eq(comparator_5_eq));  // open: gt, lt
  not not_4 (not_4_out, Mem_MemToReg);
  Comparator #(.width(5)) comparator_6 (.a(EX_R2_num), .b(Wb_WriteDst), .eq(comparator_6_eq));  // open: gt, lt
  and and_1 (EX_R1__redirect[1], comparator_2_eq, Mem_RegWrite, not_1_out, EX_r1_used, not_2_out);
  and and_2 (EX_R1__redirect[0], not_1_out, comparator_3_eq, EX_r1_used, Wb_RegWrite);
  and and_3 (EX_R2__redirect[1], comparator_5_eq, Mem_RegWrite, not_3_out, EX_r2_used, not_4_out);
  and and_4 (EX_R2__redirect[0], not_3_out, comparator_6_eq, EX_r2_used, Wb_RegWrite);

  // Other names for the same wires on the sheet: Wb_WriteBackData_to_EX_R1_num = EX_R1__redirect[0];
  //   Mem_AluOut_to_EX_R1_num = EX_R1__redirect[1]; Wb_WriteBackData_to_EX_R2_num = EX_R2__redirect[0];
  //   Mem_AluOut_to_EX_R2_num = EX_R2__redirect[1]

  // Notes on the sheet:
  //   访存阶段 Alu结果 重定向至运算阶段R1#
  //   优先级更高
  //   写回阶段 寄存器写回数据 重定向至运算阶段R1#
  //   优先级更低
  //   访存阶段 Alu结果 重定向至运算阶段R1#
  //   优先级更高
  //   写回阶段 寄存器写回数据 重定向至运算阶段R1#
  //   优先级更低
  //   高电平：执行阶段R2端口重定向
  //   高电平：执行阶段R1端口重定向
endmodule
