// Logisim project 理论课的控制器设计.circ as structural Verilog: 4 circuits, main circuit 硬布线控制器
module \硬布线控制器  (
  input  in_1,
  input  in_2,
  input  in_3,
  input  in_4,
  input  in_5
);

  wire clock_1_out;
  wire [3:0] register_1_q, \硬布线控制器状态转换电路_1_n0 ;

  Clock clock_1 (.out(clock_1_out));
  Register #(.width(4)) register_1 (.D(\硬布线控制器状态转换电路_1_n0 ), .Q(register_1_q), .clk(clock_1_out));  // open: en, clr
  \硬布线控制器状态转换电路  \u_硬布线控制器状态转换电路_1  (
    .S3(register_1_q[3]), .S2(register_1_q[2]), .S1(register_1_q[1]), .S0(register_1_q[0]), .load(in_1),
    .move(in_2), .add(in_3), .store(in_4), .jmp(in_5), .N3(\硬布线控制器状态转换电路_1_n0 [3]),
    .N2(\硬布线控制器状态转换电路_1_n0 [2]), .N1(\硬布线控制器状态转换电路_1_n0 [1]), .N0(\硬布线控制器状态转换电路_1_n0 [0]));
  // Probe on \硬布线控制器状态转换电路_1_n0 
endmodule

module \硬布线控制器状态转换电路  (
  input  S3,
  input  S2,
  input  S1,
  input  S0,
  input  load,
  input  move,
  input  add,
  input  store,
  input  jmp,
  output N3,
  output N2,
  output N1,
  output N0
);

  wire and_1_out, and_2_out, and_3_out, and_4_out, and_5_out, and_6_out, and_7_out, and_8_out, and_9_out,
       and_10_out, and_11_out, and_12_out, and_13_out, and_14_out, and_15_out, and_16_out, and_17_out,
       and_18_out, and_19_out, and_20_out, and_21_out, not_1_out, not_2_out, not_3_out, not_4_out, not_5_out,
       not_6_out, not_7_out, not_8_out, not_9_out, not_10_out, not_11_out, not_12_out, not_13_out,
       not_14_out, not_15_out, not_16_out, not_17_out, not_18_out, not_19_out, not_20_out, not_21_out,
       not_22_out, not_23_out, not_24_out, not_25_out, not_26_out, not_27_out, not_28_out, not_29_out,
       not_30_out, not_31_out, not_32_out, not_33_out, not_34_out, not_35_out, not_36_out, not_37_out,
       not_38_out;

  not not_1 (not_1_out, S3);
  not not_2 (not_2_out, S2);
  not not_3 (not_3_out, S3);
  not not_4 (not_4_out, S2);
  not not_5 (not_5_out, S3);
  not not_6 (not_6_out, S2);
  not not_7 (not_7_out, S3);
  not not_8 (not_8_out, S2);
  not not_9 (not_9_out, S1);
  not not_10 (not_10_out, S2);
  not not_11 (not_11_out, S0);
  not not_12 (not_12_out, S1);
  not not_13 (not_13_out, S3);
  not not_14 (not_14_out, S2);
  not not_15 (not_15_out, S3);
  not not_16 (not_16_out, S2);
  not not_17 (not_17_out, S3);
  not not_18 (not_18_out, S2);
  not not_19 (not_19_out, S3);
  not not_20 (not_20_out, S0);
  not not_21 (not_21_out, S1);
  not not_22 (not_22_out, S1);
  not not_23 (not_23_out, S3);
  not not_24 (not_24_out, S0);
  not not_25 (not_25_out, S2);
  not not_26 (not_26_out, S0);
  not not_27 (not_27_out, S3);
  not not_28 (not_28_out, S2);
  not not_29 (not_29_out, S3);
  not not_30 (not_30_out, S0);
  not not_31 (not_31_out, S2);
  not not_32 (not_32_out, S0);
  not not_33 (not_33_out, S3);
  not not_34 (not_34_out, S2);
  not not_35 (not_35_out, S3);
  not not_36 (not_36_out, S2);
  not not_37 (not_37_out, S1);
  not not_38 (not_38_out, S0);
  and and_1 (and_1_out, not_1_out, not_2_out, S1, S0, jmp);
  and and_2 (and_2_out, not_3_out, not_4_out, S1, S0, store);
  and and_3 (and_3_out, not_5_out, not_6_out, S1, S0, add);
  and and_4 (and_4_out, not_7_out, not_8_out, S1, S0, move);
  and and_5 (and_5_out, S3, not_9_out, S0);
  and and_6 (and_6_out, S3, not_10_out, S1, not_11_out);
  and and_7 (and_7_out, S3, S2, not_12_out);
  and and_8 (and_8_out, not_13_out, not_14_out, S1, S0, jmp);
  and and_9 (and_9_out, not_15_out, not_16_out, S1, S0, store);
  and and_10 (and_10_out, not_17_out, not_18_out, S1, S0, load);
  and and_11 (and_11_out, not_19_out, S2, not_20_out);
  and and_12 (and_12_out, S2, not_21_out);
  and and_13 (and_13_out, not_22_out, S0);
  and and_14 (and_14_out, not_23_out, S1, not_24_out);
  and and_15 (and_15_out, not_25_out, S1, not_26_out);
  and and_16 (and_16_out, not_27_out, not_28_out, S1, jmp);
  and and_17 (and_17_out, not_29_out, not_30_out);
  and and_18 (and_18_out, not_31_out, S1, not_32_out);
  and and_19 (and_19_out, not_33_out, not_34_out, S1, jmp);
  and and_20 (and_20_out, not_35_out, not_36_out, S1, add);
  and and_21 (and_21_out, S2, not_37_out, not_38_out);
  or or_1 (N3, and_1_out, and_2_out, and_3_out, and_4_out, and_5_out, and_6_out, and_7_out);
  or or_2 (N2, and_8_out, and_9_out, and_10_out, and_11_out, and_12_out);
  or or_3 (N1, and_13_out, and_14_out, and_15_out, and_16_out);
  or or_4 (N0, and_17_out, and_18_out, and_19_out, and_20_out, and_21_out);
endmodule

module \微程序控制器  (
  input  in_1,
  input  in_2,
  input  in_3,
  input  in_4,
  input  in_5
);

  wire clock_1_out;
  wire [3:0] multiplexer_1_out, rom_1_data, \μPC_q , \微程序控制器状态转换电路_1_s ;
  wire [15:4] rom_1_data_2;

  \微程序控制器状态转换电路  \u_微程序控制器状态转换电路_1  (
    .load(in_1), .move(in_2), .add(in_3), .store(in_4), .jmp(in_5), .s(\微程序控制器状态转换电路_1_s ));
  // Probe on rom_1_data
  Multiplexer #(.width(4)) multiplexer_1 (
    .in0(rom_1_data), .in1(\微程序控制器状态转换电路_1_s ), .out(multiplexer_1_out), .sel(rom_1_data_2[4]));  // open: en
  // Probe on multiplexer_1_out
  Clock clock_1 (.out(clock_1_out));
  Register #(.width(4)) \u_μPC  (.D(multiplexer_1_out), .Q(\μPC_q ), .clk(clock_1_out));  // open: en, clr
  // Probe on \μPC_q 
  ROM #(.addrWidth(4), .dataWidth(16)) rom_1 (.addr(\μPC_q ), .data({rom_1_data_2, rom_1_data}));  // open: sel

  // Notes on the sheet:
  //   下址字段
  //   判别字段
  //   控制信号
  //   微程序存储器
  //   contents of rom_1 (hex, n*v repeats v):
  //   1 2 3 10 5 6 7 0 0 a b 0 d e
endmodule

module \微程序控制器状态转换电路  (
  input  load,
  input  move,
  input  add,
  input  store,
  input  jmp,
  output [3:0] s
);

  or or_1 (s[3], move, add, store, jmp);
  or or_2 (s[2], load, store, jmp);
  or or_3 (s[0], add, jmp);

  assign s[1] = jmp;
endmodule
